// Logisim project memory.circ as structural Verilog: 22 circuits, main circuit muxin8tor
module Mem (
  input  [15:0] I4,
  input  I1,
  input  [7:0] I5,
  input  I2,
  input  I3,
  output [7:0] out_6,
  output out_7
);

  wire and_1_out, and_2_out, and_3_out, and_4_out, and_5_out, and_6_out, and_107_out, and_137_out,
       and_138_out, and_139_out, and_140_out, buffer_1_out, buffer_2_out, buffer_3_out, buffer_4_out,
       buffer_5_out, buffer_6_out, buffer_7_out, buffer_8_out, buffer_9_out, buffer_10_out, buffer_11_out,
       buffer_12_out, buffer_13_out, buffer_14_out, buffer_15_out, buffer_16_out, buffer_17_out,
       buffer_18_out, buffer_19_out, buffer_20_out, buffer_21_out, buffer_22_out, buffer_23_out,
       buffer_24_out, buffer_25_out, buffer_26_out, buffer_27_out, buffer_28_out, buffer_29_out,
       buffer_30_out, buffer_31_out, buffer_32_out, buffer_33_out, buffer_34_out, buffer_35_out,
       buffer_36_out, buffer_37_out, buffer_38_out, buffer_39_out, buffer_75_out, buffer_76_out,
       buffer_77_out, buffer_78_out, buffer_79_out, buffer_80_out, buffer_81_out, buffer_82_out,
       buffer_86_out, buffer_87_out, clock_1_out, clock_2_out, controlled_buffer_38_out,
       controlled_buffer_46_out, controlled_buffer_57_out, controlled_inverter_1_out,
       controlled_inverter_3_out, controlled_inverter_5_out, controlled_inverter_7_out, d1_1_out_3,
       d1_2_out_3, d1_3_out_3, decoder_1_out0, decoder_1_out1, decoder_1_out2, decoder_1_out3,
       decoder_1_out4, decoder_1_out5, decoder_1_out6, decoder_1_out7, decoder_2_out0, decoder_2_out1,
       decoder_2_out2, decoder_2_out3, decoder_2_out4, decoder_2_out5, decoder_2_out6, decoder_2_out7,
       l0_1_out_9, l0_2_out_9, l0_3_out_9, l0_4_out_9, l0_5_out_9, l0_6_out_9, l0_7_out_9, l0_8_out_9,
       not_1_out, not_2_out, or_2_out, or_3_out, pull_resistor_7_node;
  wire [2:0] co8_1_out_2, co8_2_out_2, xor_12_out_2;
  wire [3:0] l0_1_out_8, l0_5_out_8;
  wire [3:3] controlled_buffer_69_out;
  wire [7:0] and_29_out, and_42_out, and_43_out, and_47_out, and_54_out, and_57_out, and_58_out, and_59_out,
       and_63_out, and_64_out, and_65_out, and_72_out, and_123_out, and_126_out, and_133_out, buffer_43_out,
       buffer_44_out, buffer_48_out, buffer_49_out, buffer_50_out, buffer_51_out, buffer_52_out,
       buffer_53_out, buffer_54_out, buffer_58_out, buffer_59_out, buffer_60_out, buffer_61_out,
       buffer_62_out, controlled_buffer_22_out, controlled_buffer_24_out, controlled_buffer_26_out,
       controlled_buffer_28_out, controlled_buffer_30_out, controlled_buffer_32_out,
       controlled_buffer_34_out, controlled_buffer_36_out, controlled_buffer_42_out, d8_1_out_3, l0_1_out_6,
       l0_1_out_10, l0_2_out_6, l0_2_out_10, l0_3_out_6, l0_3_out_10, l0_4_out_6, l0_4_out_10, l0_5_out_6,
       l0_5_out_10, l0_6_out_6, l0_6_out_10, l0_7_out_6, l0_7_out_10, l0_8_out_6, l0_8_out_10,
       multiplexer_1_out, multiplexer_4_out, multiplexer_4_out_2, multiplexer_4_out_3, multiplexer_4_out_4,
       nor_13_out, nor_14_out, nor_21_out, nor_22_out, not_6_out, not_13_out, not_14_out, not_21_out,
       or_12_out, or_14_out, or_15_out, or_25_out, or_26_out, or_27_out, pull_resistor_6_node, r4_1_out_7;
  wire [11:0] and_36_out, and_37_out, and_40_out, and_41_out, and_55_out, and_56_out, and_108_out,
       and_109_out, and_112_out, and_113_out, and_124_out, and_125_out, or_10_out, or_11_out, or_13_out,
       or_21_out, or_23_out, or_24_out;
  wire [12:0] xor_12_out;
  wire [13:0] and_23_out, and_24_out, and_27_out, and_28_out, and_38_out, and_39_out, and_98_out, and_99_out,
       and_102_out, and_103_out, and_110_out, and_111_out, or_6_out, or_8_out, or_9_out, or_18_out,
       or_20_out, or_22_out;
  wire [14:0] and_15_out, and_16_out, and_18_out, and_19_out, and_25_out, and_26_out, and_87_out, and_88_out,
       and_90_out, and_91_out, and_100_out, and_101_out, or_4_out, or_5_out, or_7_out, or_16_out, or_17_out,
       or_19_out, xor_1_out, xor_2_out, xor_3_out, xor_7_out, xor_8_out, xor_9_out;
  wire [14:14] xor_1_out_2, xor_2_out_2, xor_3_out_2, xor_7_out_2, xor_8_out_2, xor_9_out_2;
  wire [15:0] and_7_out, and_8_out, and_17_out, and_82_out, and_83_out, and_89_out, controlled_buffer_23_out,
       controlled_buffer_25_out, controlled_buffer_27_out, controlled_buffer_29_out,
       controlled_buffer_31_out, controlled_buffer_33_out, controlled_buffer_35_out,
       controlled_buffer_37_out, d16_1_out_3, d16_2_out_3, l0_1_out_7, l0_2_out_7, l0_3_out_7, l0_4_out_7,
       l0_5_out_7, l0_6_out_7, l0_7_out_7, l0_8_out_7, multiplexer_5_out, multiplexer_5_out_2,
       multiplexer_5_out_3, multiplexer_5_out_4, xor_4_out, xor_5_out, xor_6_out, xor_10_out, xor_11_out,
       xor_13_out, xor_14_out, xor_15_out, xor_16_out;
  wire [31:0] multiplexer_2_out;
  wire [63:0] and_9_out, and_10_out, and_11_out, and_12_out, and_13_out, and_14_out, and_20_out, and_21_out,
       and_22_out, and_30_out, and_31_out, and_32_out, and_33_out, and_34_out, and_35_out, and_44_out,
       and_45_out, and_46_out, and_48_out, and_49_out, and_50_out, and_51_out, and_52_out, and_53_out,
       and_60_out, and_61_out, and_62_out, and_66_out, and_67_out, and_68_out, and_69_out, and_70_out,
       and_71_out, and_73_out, and_74_out, and_75_out, and_76_out, and_77_out, and_78_out, and_79_out,
       and_80_out, and_81_out, and_84_out, and_85_out, and_86_out, and_92_out, and_93_out, and_94_out,
       and_95_out, and_96_out, and_97_out, and_104_out, and_105_out, and_106_out, and_114_out, and_115_out,
       and_116_out, and_117_out, and_118_out, and_119_out, and_120_out, and_121_out, and_122_out,
       and_127_out, and_128_out, and_129_out, and_130_out, and_131_out, and_132_out, and_134_out,
       and_135_out, and_136_out, buffer_40_out, buffer_41_out, buffer_42_out, buffer_45_out, buffer_46_out,
       buffer_47_out, buffer_55_out, buffer_56_out, buffer_57_out, buffer_63_out, buffer_64_out,
       buffer_65_out, buffer_66_out, buffer_67_out, buffer_68_out, buffer_69_out, buffer_70_out,
       buffer_71_out, buffer_72_out, buffer_73_out, buffer_74_out, buffer_83_out, buffer_84_out,
       buffer_85_out, multiplexer_3_out, nor_1_out, nor_2_out, nor_3_out, nor_4_out, nor_5_out, nor_6_out,
       nor_7_out, nor_8_out, nor_9_out, nor_10_out, nor_11_out, nor_12_out, nor_15_out, nor_16_out,
       nor_17_out, nor_18_out, nor_19_out, nor_20_out, nor_23_out, nor_24_out, nor_25_out, nor_26_out,
       nor_27_out, nor_28_out, nor_29_out, nor_30_out, nor_31_out, nor_32_out, nor_33_out, nor_34_out,
       nor_35_out, nor_36_out, nor_37_out, nor_38_out, nor_39_out, nor_40_out, nor_41_out, nor_42_out,
       nor_43_out, nor_44_out, nor_45_out, nor_46_out, nor_47_out, nor_48_out, nor_49_out, nor_50_out,
       nor_51_out, nor_52_out, not_3_out, not_4_out, not_5_out, not_7_out, not_8_out, not_9_out, not_10_out,
       not_11_out, not_12_out, not_15_out, not_16_out, not_17_out, not_18_out, not_19_out, not_20_out,
       not_22_out, not_23_out, not_24_out, not_25_out, not_26_out, not_27_out, not_28_out, not_29_out,
       not_30_out, not_31_out, not_32_out, not_33_out, not_34_out, not_35_out, not_36_out, not_37_out,
       not_38_out, not_39_out, not_40_out, not_41_out, not_42_out;

  assign I4 = d1_3_out_3 ? d16_2_out_3 : 16'bz;  // Controlled_Buffer controlled_buffer_1
  assign I5 = d1_3_out_3 ? r4_1_out_7 : 8'bz;  // Controlled_Buffer controlled_buffer_2
  Pull_Resistor pull_resistor_1 (.node(I1));
  or or_1 (out_7, d1_3_out_3, and_1_out);
  Pull_Resistor pull_resistor_2 (.node(I2));
  and and_1 (and_1_out, I1, or_3_out);
  not not_1 (not_1_out, or_3_out);
  and and_2 (and_2_out, I1, not_1_out);
  Pull_Resistor pull_resistor_3 (.node(out_6));
  assign out_6 = d1_3_out_3 ? r4_1_out_7 : 8'bz;  // Controlled_Buffer controlled_buffer_3
  assign I2 = d1_3_out_3 ? d1_3_out_3 : 1'bz;  // Controlled_Buffer controlled_buffer_4
  and and_3 (and_3_out, I2, and_6_out);
  assign out_6 = d1_1_out_3 ? d8_1_out_3 : 8'bz;  // Controlled_Buffer controlled_buffer_5
  Pull_Resistor pull_resistor_4 (.node(I5));
  or or_2 (or_2_out, I1, I2);
  and and_4 (and_4_out, I1, and_6_out);
  Decoder #(.select(3)) decoder_1 (
    .out0(decoder_1_out0), .out1(decoder_1_out1), .out2(decoder_1_out2), .out3(decoder_1_out3),
    .out4(decoder_1_out4), .out5(decoder_1_out5), .out6(decoder_1_out6), .out7(decoder_1_out7),
    .sel(xor_12_out_2), .en(and_4_out));
  Decoder #(.select(3)) decoder_2 (
    .out0(decoder_2_out0), .out1(decoder_2_out1), .out2(decoder_2_out2), .out3(decoder_2_out3),
    .out4(decoder_2_out4), .out5(decoder_2_out5), .out6(decoder_2_out6), .out7(decoder_2_out7),
    .sel(xor_12_out_2), .en(and_3_out));
  Clock clock_1 (.out(clock_1_out));
  D8 d8_1 (.in_2(multiplexer_1_out), .in_1(clock_1_out), .out_3(d8_1_out_3));
  D1 d1_1 (.in_2(or_3_out), .in_1(clock_1_out), .out_3(d1_1_out_3));
  Pull_Resistor pull_resistor_5 (.node(I4));
  or or_3 (or_3_out, and_5_out, pull_resistor_7_node);
  Multiplexer #(.enable("true"), .width(8)) multiplexer_1 (
    .in0(pull_resistor_6_node), .in1(controlled_buffer_42_out), .out(multiplexer_1_out), .sel(and_5_out),
    .en(or_3_out));
  and and_5 (and_5_out, and_107_out, not_2_out);
  not not_2 (not_2_out, pull_resistor_7_node);
  Pull_Resistor pull_resistor_6 (.node(pull_resistor_6_node));
  Pull_Resistor pull_resistor_7 (.node(pull_resistor_7_node));
  assign pull_resistor_7_node = l0_1_out_9 ? l0_1_out_9 : 1'bz;  // Controlled_Buffer controlled_buffer_6
  assign pull_resistor_6_node = l0_1_out_9 ? l0_1_out_10 : 8'bz;  // Controlled_Buffer controlled_buffer_7
  assign pull_resistor_7_node = l0_2_out_9 ? l0_2_out_9 : 1'bz;  // Controlled_Buffer controlled_buffer_8
  assign pull_resistor_6_node = l0_2_out_9 ? l0_2_out_10 : 8'bz;  // Controlled_Buffer controlled_buffer_9
  assign pull_resistor_7_node = l0_3_out_9 ? l0_3_out_9 : 1'bz;  // Controlled_Buffer controlled_buffer_10
  assign pull_resistor_6_node = l0_3_out_9 ? l0_3_out_10 : 8'bz;  // Controlled_Buffer controlled_buffer_11
  assign pull_resistor_7_node = l0_4_out_9 ? l0_4_out_9 : 1'bz;  // Controlled_Buffer controlled_buffer_12
  assign pull_resistor_6_node = l0_4_out_9 ? l0_4_out_10 : 8'bz;  // Controlled_Buffer controlled_buffer_13
  assign pull_resistor_7_node = l0_5_out_9 ? l0_5_out_9 : 1'bz;  // Controlled_Buffer controlled_buffer_14
  assign pull_resistor_6_node = l0_5_out_9 ? l0_5_out_10 : 8'bz;  // Controlled_Buffer controlled_buffer_15
  assign pull_resistor_7_node = l0_6_out_9 ? l0_6_out_9 : 1'bz;  // Controlled_Buffer controlled_buffer_16
  assign pull_resistor_6_node = l0_6_out_9 ? l0_6_out_10 : 8'bz;  // Controlled_Buffer controlled_buffer_17
  assign pull_resistor_7_node = l0_7_out_9 ? l0_7_out_9 : 1'bz;  // Controlled_Buffer controlled_buffer_18
  assign pull_resistor_6_node = l0_7_out_9 ? l0_7_out_10 : 8'bz;  // Controlled_Buffer controlled_buffer_19
  assign pull_resistor_7_node = l0_8_out_9 ? l0_8_out_9 : 1'bz;  // Controlled_Buffer controlled_buffer_20
  assign pull_resistor_6_node = l0_8_out_9 ? l0_8_out_10 : 8'bz;  // Controlled_Buffer controlled_buffer_21
  L0 l0_1 (
    .in_4(I5), .in_5(I4), .in_2(decoder_2_out0), .in_1(I3), .in_3(decoder_1_out0), .out_6(l0_1_out_6),
    .out_7(l0_1_out_7), .out_8(l0_1_out_8[0]), .out_9(l0_1_out_9), .out_10(l0_1_out_10));
  L0 l0_2 (
    .in_4(I5), .in_5(I4), .in_2(decoder_2_out1), .in_1(I3), .in_3(decoder_1_out1), .out_6(l0_2_out_6),
    .out_7(l0_2_out_7), .out_8(l0_1_out_8[1]), .out_9(l0_2_out_9), .out_10(l0_2_out_10));
  L0 l0_3 (
    .in_4(I5), .in_5(I4), .in_2(decoder_2_out2), .in_1(I3), .in_3(decoder_1_out2), .out_6(l0_3_out_6),
    .out_7(l0_3_out_7), .out_8(l0_1_out_8[2]), .out_9(l0_3_out_9), .out_10(l0_3_out_10));
  L0 l0_4 (
    .in_4(I5), .in_5(I4), .in_2(decoder_2_out3), .in_1(I3), .in_3(decoder_1_out3), .out_6(l0_4_out_6),
    .out_7(l0_4_out_7), .out_8(l0_1_out_8[3]), .out_9(l0_4_out_9), .out_10(l0_4_out_10));
  L0 l0_5 (
    .in_4(I5), .in_5(I4), .in_2(decoder_2_out4), .in_1(I3), .in_3(decoder_1_out4), .out_6(l0_5_out_6),
    .out_7(l0_5_out_7), .out_8(l0_5_out_8[0]), .out_9(l0_5_out_9), .out_10(l0_5_out_10));
  L0 l0_6 (
    .in_4(I5), .in_5(I4), .in_2(decoder_2_out5), .in_1(I3), .in_3(decoder_1_out5), .out_6(l0_6_out_6),
    .out_7(l0_6_out_7), .out_8(l0_5_out_8[1]), .out_9(l0_6_out_9), .out_10(l0_6_out_10));
  L0 l0_7 (
    .in_4(I5), .in_5(I4), .in_2(decoder_2_out6), .in_1(I3), .in_3(decoder_1_out6), .out_6(l0_7_out_6),
    .out_7(l0_7_out_7), .out_8(l0_5_out_8[2]), .out_9(l0_7_out_9), .out_10(l0_7_out_10));
  L0 l0_8 (
    .in_4(I5), .in_5(I4), .in_2(decoder_2_out7), .in_1(I3), .in_3(decoder_1_out7), .out_6(l0_8_out_6),
    .out_7(l0_8_out_7), .out_8(l0_5_out_8[3]), .out_9(l0_8_out_9), .out_10(l0_8_out_10));
  assign controlled_buffer_22_out = l0_1_out_8[0] ? l0_1_out_6 : 8'bz;  // Controlled_Buffer controlled_buffer_22
  assign controlled_buffer_23_out = l0_1_out_8[0] ? l0_1_out_7 : 16'bz;  // Controlled_Buffer controlled_buffer_23
  assign controlled_buffer_24_out = l0_1_out_8[1] ? l0_2_out_6 : 8'bz;  // Controlled_Buffer controlled_buffer_24
  assign controlled_buffer_25_out = l0_1_out_8[1] ? l0_2_out_7 : 16'bz;  // Controlled_Buffer controlled_buffer_25
  assign controlled_buffer_26_out = l0_1_out_8[2] ? l0_3_out_6 : 8'bz;  // Controlled_Buffer controlled_buffer_26
  assign controlled_buffer_27_out = l0_1_out_8[2] ? l0_3_out_7 : 16'bz;  // Controlled_Buffer controlled_buffer_27
  assign controlled_buffer_28_out = l0_1_out_8[3] ? l0_4_out_6 : 8'bz;  // Controlled_Buffer controlled_buffer_28
  assign controlled_buffer_29_out = l0_1_out_8[3] ? l0_4_out_7 : 16'bz;  // Controlled_Buffer controlled_buffer_29
  assign controlled_buffer_30_out = l0_5_out_8[0] ? l0_5_out_6 : 8'bz;  // Controlled_Buffer controlled_buffer_30
  assign controlled_buffer_31_out = l0_5_out_8[0] ? l0_5_out_7 : 16'bz;  // Controlled_Buffer controlled_buffer_31
  assign controlled_buffer_32_out = l0_5_out_8[1] ? l0_6_out_6 : 8'bz;  // Controlled_Buffer controlled_buffer_32
  assign controlled_buffer_33_out = l0_5_out_8[1] ? l0_6_out_7 : 16'bz;  // Controlled_Buffer controlled_buffer_33
  assign controlled_buffer_34_out = l0_5_out_8[2] ? l0_7_out_6 : 8'bz;  // Controlled_Buffer controlled_buffer_34
  assign controlled_buffer_35_out = l0_5_out_8[2] ? l0_7_out_7 : 16'bz;  // Controlled_Buffer controlled_buffer_35
  assign controlled_buffer_36_out = l0_5_out_8[3] ? l0_8_out_6 : 8'bz;  // Controlled_Buffer controlled_buffer_36
  assign controlled_buffer_37_out = l0_5_out_8[3] ? l0_8_out_7 : 16'bz;  // Controlled_Buffer controlled_buffer_37
  and and_6 (and_6_out, buffer_39_out, or_2_out);
  Pull_Resistor pull_resistor_8 (.node({controlled_buffer_29_out, controlled_buffer_27_out, controlled_buffer_25_out, controlled_buffer_23_out}));
  buf buffer_1 (buffer_1_out, or_2_out);
  buf buffer_2 (buffer_2_out, buffer_1_out);
  buf buffer_3 (buffer_3_out, buffer_2_out);
  buf buffer_4 (buffer_4_out, buffer_31_out);
  buf buffer_5 (buffer_5_out, buffer_4_out);
  buf buffer_6 (buffer_6_out, buffer_5_out);
  buf buffer_7 (buffer_7_out, buffer_34_out);
  buf buffer_8 (buffer_8_out, buffer_7_out);
  buf buffer_9 (buffer_9_out, buffer_8_out);
  buf buffer_10 (buffer_10_out, buffer_37_out);
  buf buffer_11 (buffer_11_out, buffer_10_out);
  buf buffer_12 (buffer_12_out, buffer_11_out);
  Pull_Resistor pull_resistor_9 (.node({controlled_buffer_36_out, controlled_buffer_34_out, controlled_buffer_32_out, controlled_buffer_30_out, controlled_buffer_28_out, controlled_buffer_26_out, controlled_buffer_24_out, controlled_buffer_22_out}));
  Pull_Resistor pull_resistor_10 (.node({controlled_buffer_37_out, controlled_buffer_35_out, controlled_buffer_33_out, controlled_buffer_31_out}));
  buf buffer_13 (buffer_13_out, buffer_3_out);
  buf buffer_14 (buffer_14_out, buffer_13_out);
  buf buffer_15 (buffer_15_out, buffer_14_out);
  buf buffer_16 (buffer_16_out, buffer_15_out);
  buf buffer_17 (buffer_17_out, buffer_6_out);
  buf buffer_18 (buffer_18_out, buffer_17_out);
  buf buffer_19 (buffer_19_out, buffer_18_out);
  buf buffer_20 (buffer_20_out, buffer_19_out);
  buf buffer_21 (buffer_21_out, buffer_9_out);
  buf buffer_22 (buffer_22_out, buffer_21_out);
  buf buffer_23 (buffer_23_out, buffer_22_out);
  buf buffer_24 (buffer_24_out, buffer_23_out);
  buf buffer_25 (buffer_25_out, buffer_12_out);
  buf buffer_26 (buffer_26_out, buffer_25_out);
  buf buffer_27 (buffer_27_out, buffer_26_out);
  buf buffer_28 (buffer_28_out, buffer_27_out);
  buf buffer_29 (buffer_29_out, buffer_16_out);
  buf buffer_30 (buffer_30_out, buffer_29_out);
  buf buffer_31 (buffer_31_out, buffer_30_out);
  buf buffer_32 (buffer_32_out, buffer_20_out);
  buf buffer_33 (buffer_33_out, buffer_32_out);
  buf buffer_34 (buffer_34_out, buffer_33_out);
  buf buffer_35 (buffer_35_out, buffer_24_out);
  buf buffer_36 (buffer_36_out, buffer_35_out);
  buf buffer_37 (buffer_37_out, buffer_36_out);
  buf buffer_38 (buffer_38_out, buffer_28_out);
  buf buffer_39 (buffer_39_out, buffer_38_out);
  assign and_7_out = {I4[8:0], {7{1'b0}}} & {I4[3:0], {12{1'b0}}};  // AND_Gate and_7, 16 bits wide
  assign {xor_1_out_2[14], xor_1_out} = {I4[8:0], {7{1'b0}}} ^ {I4[3:0], {12{1'b0}}};  // XOR_Gate xor_1, 16 bits wide
  assign and_8_out = {I4[13:0], 2'b00} & I4;  // AND_Gate and_8, 16 bits wide
  assign {xor_2_out_2[14], xor_2_out} = {I4[13:0], 2'b00} ^ I4;  // XOR_Gate xor_2, 16 bits wide
  assign buffer_40_out = {controlled_buffer_36_out, controlled_buffer_34_out, controlled_buffer_32_out, controlled_buffer_30_out, controlled_buffer_28_out, controlled_buffer_26_out, controlled_buffer_24_out, controlled_buffer_22_out};  // Buffer buffer_40, 64 bits wide
  assign not_3_out = ~{controlled_buffer_36_out, controlled_buffer_34_out, controlled_buffer_32_out, controlled_buffer_30_out, controlled_buffer_28_out, controlled_buffer_26_out, controlled_buffer_24_out, controlled_buffer_22_out};  // NOT_Gate not_3, 64 bits wide
  assign buffer_41_out = {controlled_buffer_29_out, controlled_buffer_27_out, controlled_buffer_25_out, controlled_buffer_23_out};  // Buffer buffer_41, 64 bits wide
  assign not_4_out = ~{controlled_buffer_29_out, controlled_buffer_27_out, controlled_buffer_25_out, controlled_buffer_23_out};  // NOT_Gate not_4, 64 bits wide
  assign buffer_42_out = {controlled_buffer_37_out, controlled_buffer_35_out, controlled_buffer_33_out, controlled_buffer_31_out};  // Buffer buffer_42, 64 bits wide
  assign not_5_out = ~{controlled_buffer_37_out, controlled_buffer_35_out, controlled_buffer_33_out, controlled_buffer_31_out};  // NOT_Gate not_5, 64 bits wide
  assign and_9_out = buffer_40_out & {{8{l0_5_out_8[3]}}, {8{l0_5_out_8[2]}}, {8{l0_5_out_8[1]}}, {8{l0_5_out_8[0]}}, {8{l0_1_out_8[3]}}, {8{l0_1_out_8[2]}}, {8{l0_1_out_8[1]}}, {8{l0_1_out_8[0]}}};  // AND_Gate and_9, 64 bits wide
  assign nor_1_out = ~(and_9_out | and_20_out);  // NOR_Gate nor_1, 64 bits wide
  assign nor_2_out = ~(nor_1_out | and_10_out);  // NOR_Gate nor_2, 64 bits wide
  assign and_10_out = {{8{l0_5_out_8[3]}}, {8{l0_5_out_8[2]}}, {8{l0_5_out_8[1]}}, {8{l0_5_out_8[0]}}, {8{l0_1_out_8[3]}}, {8{l0_1_out_8[2]}}, {8{l0_1_out_8[1]}}, {8{l0_1_out_8[0]}}} & not_3_out;  // AND_Gate and_10, 64 bits wide
  assign and_11_out = buffer_41_out & {{16{l0_1_out_8[3]}}, {16{l0_1_out_8[2]}}, {16{l0_1_out_8[1]}}, {16{l0_1_out_8[0]}}};  // AND_Gate and_11, 64 bits wide
  assign nor_3_out = ~(and_11_out | and_21_out);  // NOR_Gate nor_3, 64 bits wide
  assign nor_4_out = ~(nor_3_out | and_12_out);  // NOR_Gate nor_4, 64 bits wide
  assign and_12_out = {{16{l0_1_out_8[3]}}, {16{l0_1_out_8[2]}}, {16{l0_1_out_8[1]}}, {16{l0_1_out_8[0]}}} & not_4_out;  // AND_Gate and_12, 64 bits wide
  assign and_13_out = buffer_42_out & {{16{l0_5_out_8[3]}}, {16{l0_5_out_8[2]}}, {16{l0_5_out_8[1]}}, {16{l0_5_out_8[0]}}};  // AND_Gate and_13, 64 bits wide
  assign nor_5_out = ~(and_13_out | and_22_out);  // NOR_Gate nor_5, 64 bits wide
  assign nor_6_out = ~(nor_5_out | and_14_out);  // NOR_Gate nor_6, 64 bits wide
  assign and_14_out = {{16{l0_5_out_8[3]}}, {16{l0_5_out_8[2]}}, {16{l0_5_out_8[1]}}, {16{l0_5_out_8[0]}}} & not_5_out;  // AND_Gate and_14, 64 bits wide
  assign and_15_out = and_7_out[14:0] & {xor_1_out_2[14], xor_1_out[14:1]};  // AND_Gate and_15, 15 bits wide
  assign or_4_out = and_15_out | and_7_out[15:1];  // OR_Gate or_4, 15 bits wide
  assign and_16_out = xor_1_out & {xor_1_out_2[14], xor_1_out[14:1]};  // AND_Gate and_16, 15 bits wide
  assign and_17_out = xor_4_out & xor_5_out;  // AND_Gate and_17, 16 bits wide
  assign {xor_3_out_2[14], xor_3_out} = xor_4_out ^ xor_5_out;  // XOR_Gate xor_3, 16 bits wide
  assign and_18_out = and_8_out[14:0] & {xor_2_out_2[14], xor_2_out[14:1]};  // AND_Gate and_18, 15 bits wide
  assign or_5_out = and_18_out | and_8_out[15:1];  // OR_Gate or_5, 15 bits wide
  assign and_19_out = xor_2_out & {xor_2_out_2[14], xor_2_out[14:1]};  // AND_Gate and_19, 15 bits wide
  assign buffer_43_out = {l0_5_out_8, l0_1_out_8};  // Buffer buffer_43, 8 bits wide
  assign and_20_out = {not_13_out, not_13_out, not_13_out, not_13_out, not_13_out, not_13_out, not_13_out, not_13_out} & nor_2_out;  // AND_Gate and_20, 64 bits wide
  assign and_21_out = {not_13_out, not_13_out, not_13_out, not_13_out, not_13_out, not_13_out, not_13_out, not_13_out} & nor_4_out;  // AND_Gate and_21, 64 bits wide
  assign and_22_out = {not_13_out, not_13_out, not_13_out, not_13_out, not_13_out, not_13_out, not_13_out, not_13_out} & nor_6_out;  // AND_Gate and_22, 64 bits wide
  assign buffer_44_out = buffer_43_out;  // Buffer buffer_44, 8 bits wide
  assign not_6_out = ~buffer_44_out;  // NOT_Gate not_6, 8 bits wide
  assign buffer_45_out = and_20_out;  // Buffer buffer_45, 64 bits wide
  assign not_7_out = ~{{8{l0_5_out_8[3]}}, {8{l0_5_out_8[2]}}, {8{l0_5_out_8[1]}}, {8{l0_5_out_8[0]}}, {8{l0_1_out_8[3]}}, {8{l0_1_out_8[2]}}, {8{l0_1_out_8[1]}}, {8{l0_1_out_8[0]}}};  // NOT_Gate not_7, 64 bits wide
  assign not_8_out = ~and_20_out;  // NOT_Gate not_8, 64 bits wide
  assign buffer_46_out = and_21_out;  // Buffer buffer_46, 64 bits wide
  assign not_9_out = ~{{16{l0_1_out_8[3]}}, {16{l0_1_out_8[2]}}, {16{l0_1_out_8[1]}}, {16{l0_1_out_8[0]}}};  // NOT_Gate not_9, 64 bits wide
  assign not_10_out = ~and_21_out;  // NOT_Gate not_10, 64 bits wide
  assign buffer_47_out = and_22_out;  // Buffer buffer_47, 64 bits wide
  assign not_11_out = ~{{16{l0_5_out_8[3]}}, {16{l0_5_out_8[2]}}, {16{l0_5_out_8[1]}}, {16{l0_5_out_8[0]}}};  // NOT_Gate not_11, 64 bits wide
  assign not_12_out = ~and_22_out;  // NOT_Gate not_12, 64 bits wide
  assign and_23_out = {or_4_out[12:0], and_7_out[0]} & and_16_out[14:1];  // AND_Gate and_23, 14 bits wide
  assign or_6_out = and_23_out | or_4_out[14:1];  // OR_Gate or_6, 14 bits wide
  assign and_24_out = {and_16_out[12:0], xor_1_out[0]} & and_16_out[14:1];  // AND_Gate and_24, 14 bits wide
  assign and_25_out = and_17_out[14:0] & {xor_3_out_2[14], xor_3_out[14:1]};  // AND_Gate and_25, 15 bits wide
  assign or_7_out = and_25_out | and_17_out[15:1];  // OR_Gate or_7, 15 bits wide
  assign and_26_out = xor_3_out & {xor_3_out_2[14], xor_3_out[14:1]};  // AND_Gate and_26, 15 bits wide
  assign and_27_out = {or_5_out[12:0], and_8_out[0]} & and_19_out[14:1];  // AND_Gate and_27, 14 bits wide
  assign or_8_out = and_27_out | or_5_out[14:1];  // OR_Gate or_8, 14 bits wide
  assign and_28_out = {and_19_out[12:0], xor_2_out[0]} & and_19_out[14:1];  // AND_Gate and_28, 14 bits wide
  assign and_29_out = {l0_5_out_8, l0_1_out_8} & not_6_out;  // AND_Gate and_29, 8 bits wide
  assign buffer_48_out = {l0_5_out_8, l0_1_out_8};  // Buffer buffer_48, 8 bits wide
  assign and_30_out = buffer_45_out & not_7_out;  // AND_Gate and_30, 64 bits wide
  assign and_31_out = not_7_out & not_8_out;  // AND_Gate and_31, 64 bits wide
  assign and_32_out = buffer_46_out & not_9_out;  // AND_Gate and_32, 64 bits wide
  assign and_33_out = not_9_out & not_10_out;  // AND_Gate and_33, 64 bits wide
  assign and_34_out = buffer_47_out & not_11_out;  // AND_Gate and_34, 64 bits wide
  assign and_35_out = not_11_out & not_12_out;  // AND_Gate and_35, 64 bits wide
  assign not_13_out = ~{8{I3}};  // NOT_Gate not_13, 8 bits wide
  assign not_14_out = ~and_47_out;  // NOT_Gate not_14, 8 bits wide
  assign buffer_49_out = and_47_out;  // Buffer buffer_49, 8 bits wide
  assign buffer_50_out = buffer_48_out;  // Buffer buffer_50, 8 bits wide
  assign buffer_51_out = buffer_50_out;  // Buffer buffer_51, 8 bits wide
  assign buffer_52_out = buffer_51_out;  // Buffer buffer_52, 8 bits wide
  assign buffer_53_out = buffer_52_out;  // Buffer buffer_53, 8 bits wide
  assign nor_7_out = ~(and_30_out | and_44_out);  // NOR_Gate nor_7, 64 bits wide
  assign nor_8_out = ~(nor_7_out | and_31_out);  // NOR_Gate nor_8, 64 bits wide
  assign nor_9_out = ~(and_32_out | and_45_out);  // NOR_Gate nor_9, 64 bits wide
  assign nor_10_out = ~(nor_9_out | and_33_out);  // NOR_Gate nor_10, 64 bits wide
  assign nor_11_out = ~(and_34_out | and_46_out);  // NOR_Gate nor_11, 64 bits wide
  assign nor_12_out = ~(nor_11_out | and_35_out);  // NOR_Gate nor_12, 64 bits wide
  assign and_36_out = {or_6_out[9:0], or_4_out[0], and_7_out[0]} & and_24_out[13:2];  // AND_Gate and_36, 12 bits wide
  assign and_37_out = {and_24_out[9:0], and_16_out[0], xor_1_out[0]} & and_24_out[13:2];  // AND_Gate and_37, 12 bits wide
  assign and_38_out = {or_7_out[12:0], and_17_out[0]} & and_26_out[14:1];  // AND_Gate and_38, 14 bits wide
  assign or_9_out = and_38_out | or_7_out[14:1];  // OR_Gate or_9, 14 bits wide
  assign and_39_out = {and_26_out[12:0], xor_3_out[0]} & and_26_out[14:1];  // AND_Gate and_39, 14 bits wide
  assign and_40_out = {or_8_out[9:0], or_5_out[0], and_8_out[0]} & and_28_out[13:2];  // AND_Gate and_40, 12 bits wide
  assign and_41_out = {and_28_out[9:0], and_19_out[0], xor_2_out[0]} & and_28_out[13:2];  // AND_Gate and_41, 12 bits wide
  assign and_42_out = not_14_out & and_29_out;  // AND_Gate and_42, 8 bits wide
  assign and_43_out = and_29_out & buffer_49_out;  // AND_Gate and_43, 8 bits wide
  assign buffer_54_out = buffer_53_out;  // Buffer buffer_54, 8 bits wide
  assign and_44_out = {not_13_out, not_13_out, not_13_out, not_13_out, not_13_out, not_13_out, not_13_out, not_13_out} & nor_8_out;  // AND_Gate and_44, 64 bits wide
  assign and_45_out = {not_13_out, not_13_out, not_13_out, not_13_out, not_13_out, not_13_out, not_13_out, not_13_out} & nor_10_out;  // AND_Gate and_45, 64 bits wide
  assign and_46_out = {not_13_out, not_13_out, not_13_out, not_13_out, not_13_out, not_13_out, not_13_out, not_13_out} & nor_12_out;  // AND_Gate and_46, 64 bits wide
  assign or_10_out = and_36_out | or_6_out[13:2];  // OR_Gate or_10, 12 bits wide
  assign or_11_out = and_40_out | or_8_out[13:2];  // OR_Gate or_11, 12 bits wide
  assign nor_13_out = ~(and_42_out | and_47_out);  // NOR_Gate nor_13, 8 bits wide
  assign and_47_out = not_13_out & nor_14_out;  // AND_Gate and_47, 8 bits wide
  assign nor_14_out = ~(nor_13_out | and_43_out);  // NOR_Gate nor_14, 8 bits wide
  assign buffer_55_out = and_44_out;  // Buffer buffer_55, 64 bits wide
  assign and_48_out = buffer_55_out & {{8{l0_5_out_8[3]}}, {8{l0_5_out_8[2]}}, {8{l0_5_out_8[1]}}, {8{l0_5_out_8[0]}}, {8{l0_1_out_8[3]}}, {8{l0_1_out_8[2]}}, {8{l0_1_out_8[1]}}, {8{l0_1_out_8[0]}}};  // AND_Gate and_48, 64 bits wide
  assign and_49_out = {{8{l0_5_out_8[3]}}, {8{l0_5_out_8[2]}}, {8{l0_5_out_8[1]}}, {8{l0_5_out_8[0]}}, {8{l0_1_out_8[3]}}, {8{l0_1_out_8[2]}}, {8{l0_1_out_8[1]}}, {8{l0_1_out_8[0]}}} & not_15_out;  // AND_Gate and_49, 64 bits wide
  assign not_15_out = ~and_44_out;  // NOT_Gate not_15, 64 bits wide
  assign buffer_56_out = and_45_out;  // Buffer buffer_56, 64 bits wide
  assign and_50_out = buffer_56_out & {{16{l0_1_out_8[3]}}, {16{l0_1_out_8[2]}}, {16{l0_1_out_8[1]}}, {16{l0_1_out_8[0]}}};  // AND_Gate and_50, 64 bits wide
  assign and_51_out = {{16{l0_1_out_8[3]}}, {16{l0_1_out_8[2]}}, {16{l0_1_out_8[1]}}, {16{l0_1_out_8[0]}}} & not_16_out;  // AND_Gate and_51, 64 bits wide
  assign not_16_out = ~and_45_out;  // NOT_Gate not_16, 64 bits wide
  assign buffer_57_out = and_46_out;  // Buffer buffer_57, 64 bits wide
  assign and_52_out = buffer_57_out & {{16{l0_5_out_8[3]}}, {16{l0_5_out_8[2]}}, {16{l0_5_out_8[1]}}, {16{l0_5_out_8[0]}}};  // AND_Gate and_52, 64 bits wide
  assign and_53_out = {{16{l0_5_out_8[3]}}, {16{l0_5_out_8[2]}}, {16{l0_5_out_8[1]}}, {16{l0_5_out_8[0]}}} & not_17_out;  // AND_Gate and_53, 64 bits wide
  assign not_17_out = ~and_46_out;  // NOT_Gate not_17, 64 bits wide
  assign and_54_out = {or_10_out[3:0], or_6_out[1:0], or_4_out[0], and_7_out[0]} & and_37_out[11:4];  // AND_Gate and_54, 8 bits wide
  assign and_55_out = {or_9_out[9:0], or_7_out[0], and_17_out[0]} & and_39_out[13:2];  // AND_Gate and_55, 12 bits wide
  assign and_56_out = {and_39_out[9:0], and_26_out[0], xor_3_out[0]} & and_39_out[13:2];  // AND_Gate and_56, 12 bits wide
  assign and_57_out = {or_11_out[3:0], or_8_out[1:0], or_5_out[0], and_8_out[0]} & and_41_out[11:4];  // AND_Gate and_57, 8 bits wide
  assign buffer_58_out = and_47_out;  // Buffer buffer_58, 8 bits wide
  assign buffer_59_out = buffer_58_out;  // Buffer buffer_59, 8 bits wide
  assign buffer_60_out = buffer_59_out;  // Buffer buffer_60, 8 bits wide
  assign and_58_out = buffer_54_out & and_47_out & and_72_out;  // AND_Gate and_58, 8 bits wide
  assign nor_15_out = ~(and_48_out | and_60_out);  // NOR_Gate nor_15, 64 bits wide
  assign nor_16_out = ~(nor_15_out | and_49_out);  // NOR_Gate nor_16, 64 bits wide
  assign nor_17_out = ~(and_50_out | and_61_out);  // NOR_Gate nor_17, 64 bits wide
  assign nor_18_out = ~(nor_17_out | and_51_out);  // NOR_Gate nor_18, 64 bits wide
  assign nor_19_out = ~(and_52_out | and_62_out);  // NOR_Gate nor_19, 64 bits wide
  assign nor_20_out = ~(nor_19_out | and_53_out);  // NOR_Gate nor_20, 64 bits wide
  assign or_12_out = and_54_out | or_10_out[11:4];  // OR_Gate or_12, 8 bits wide
  assign or_13_out = and_55_out | or_9_out[13:2];  // OR_Gate or_13, 12 bits wide
  assign or_14_out = and_57_out | or_11_out[11:4];  // OR_Gate or_14, 8 bits wide
  assign and_59_out = nor_13_out & buffer_61_out;  // AND_Gate and_59, 8 bits wide
  assign buffer_61_out = buffer_60_out;  // Buffer buffer_61, 8 bits wide
  assign not_18_out = ~{{8{l0_5_out_8[3]}}, {8{l0_5_out_8[2]}}, {8{l0_5_out_8[1]}}, {8{l0_5_out_8[0]}}, {8{l0_1_out_8[3]}}, {8{l0_1_out_8[2]}}, {8{l0_1_out_8[1]}}, {8{l0_1_out_8[0]}}};  // NOT_Gate not_18, 64 bits wide
  assign and_60_out = {not_13_out, not_13_out, not_13_out, not_13_out, not_13_out, not_13_out, not_13_out, not_13_out} & nor_16_out;  // AND_Gate and_60, 64 bits wide
  assign not_19_out = ~{{16{l0_1_out_8[3]}}, {16{l0_1_out_8[2]}}, {16{l0_1_out_8[1]}}, {16{l0_1_out_8[0]}}};  // NOT_Gate not_19, 64 bits wide
  assign and_61_out = {not_13_out, not_13_out, not_13_out, not_13_out, not_13_out, not_13_out, not_13_out, not_13_out} & nor_18_out;  // AND_Gate and_61, 64 bits wide
  assign not_20_out = ~{{16{l0_5_out_8[3]}}, {16{l0_5_out_8[2]}}, {16{l0_5_out_8[1]}}, {16{l0_5_out_8[0]}}};  // NOT_Gate not_20, 64 bits wide
  assign and_62_out = {not_13_out, not_13_out, not_13_out, not_13_out, not_13_out, not_13_out, not_13_out, not_13_out} & nor_20_out;  // AND_Gate and_62, 64 bits wide
  assign xor_4_out = {or_12_out[6:0], or_10_out[3:0], or_6_out[1:0], or_4_out[0], and_7_out[0], 1'b0} ^ {xor_1_out_2[14], xor_1_out};  // XOR_Gate xor_4, 16 bits wide
  assign and_63_out = {or_13_out[3:0], or_9_out[1:0], or_7_out[0], and_17_out[0]} & and_56_out[11:4];  // AND_Gate and_63, 8 bits wide
  assign xor_5_out = {or_14_out[6:0], or_11_out[3:0], or_8_out[1:0], or_5_out[0], and_8_out[0], 1'b0} ^ {xor_2_out_2[14], xor_2_out};  // XOR_Gate xor_5, 16 bits wide
  assign not_21_out = ~and_72_out;  // NOT_Gate not_21, 8 bits wide
  assign buffer_62_out = and_72_out;  // Buffer buffer_62, 8 bits wide
  assign buffer_63_out = and_60_out;  // Buffer buffer_63, 64 bits wide
  assign not_22_out = ~and_60_out;  // NOT_Gate not_22, 64 bits wide
  assign buffer_64_out = and_61_out;  // Buffer buffer_64, 64 bits wide
  assign not_23_out = ~and_61_out;  // NOT_Gate not_23, 64 bits wide
  assign buffer_65_out = and_62_out;  // Buffer buffer_65, 64 bits wide
  assign not_24_out = ~and_62_out;  // NOT_Gate not_24, 64 bits wide
  // Probe on {xor_12_out, xor_12_out_2}
  assign or_15_out = and_63_out | or_13_out[11:4];  // OR_Gate or_15, 8 bits wide
  assign and_64_out = not_21_out & and_59_out;  // AND_Gate and_64, 8 bits wide
  assign nor_21_out = ~(and_64_out | and_72_out);  // NOR_Gate nor_21, 8 bits wide
  assign nor_22_out = ~(nor_21_out | and_65_out);  // NOR_Gate nor_22, 8 bits wide
  assign and_65_out = and_59_out & buffer_62_out;  // AND_Gate and_65, 8 bits wide
  assign and_66_out = buffer_63_out & not_18_out;  // AND_Gate and_66, 64 bits wide
  assign nor_23_out = ~(and_66_out | and_73_out);  // NOR_Gate nor_23, 64 bits wide
  assign nor_24_out = ~(nor_23_out | and_67_out);  // NOR_Gate nor_24, 64 bits wide
  assign and_67_out = not_18_out & not_22_out;  // AND_Gate and_67, 64 bits wide
  assign and_68_out = buffer_64_out & not_19_out;  // AND_Gate and_68, 64 bits wide
  assign nor_25_out = ~(and_68_out | and_74_out);  // NOR_Gate nor_25, 64 bits wide
  assign nor_26_out = ~(nor_25_out | and_69_out);  // NOR_Gate nor_26, 64 bits wide
  assign and_69_out = not_19_out & not_23_out;  // AND_Gate and_69, 64 bits wide
  assign and_70_out = buffer_65_out & not_20_out;  // AND_Gate and_70, 64 bits wide
  assign nor_27_out = ~(and_70_out | and_75_out);  // NOR_Gate nor_27, 64 bits wide
  assign nor_28_out = ~(nor_27_out | and_71_out);  // NOR_Gate nor_28, 64 bits wide
  assign and_71_out = not_20_out & not_24_out;  // AND_Gate and_71, 64 bits wide
  assign xor_6_out = {or_15_out[6:0], or_13_out[3:0], or_9_out[1:0], or_7_out[0], and_17_out[0], 1'b0} ^ {xor_3_out_2[14], xor_3_out};  // XOR_Gate xor_6, 16 bits wide
  assign and_72_out = not_13_out & nor_22_out;  // AND_Gate and_72, 8 bits wide
  assign and_73_out = {not_13_out, not_13_out, not_13_out, not_13_out, not_13_out, not_13_out, not_13_out, not_13_out} & nor_24_out;  // AND_Gate and_73, 64 bits wide
  assign and_74_out = {not_13_out, not_13_out, not_13_out, not_13_out, not_13_out, not_13_out, not_13_out, not_13_out} & nor_26_out;  // AND_Gate and_74, 64 bits wide
  assign and_75_out = {not_13_out, not_13_out, not_13_out, not_13_out, not_13_out, not_13_out, not_13_out, not_13_out} & nor_28_out;  // AND_Gate and_75, 64 bits wide
  assign buffer_66_out = and_73_out;  // Buffer buffer_66, 64 bits wide
  assign not_25_out = ~and_73_out;  // NOT_Gate not_25, 64 bits wide
  assign buffer_67_out = and_74_out;  // Buffer buffer_67, 64 bits wide
  assign not_26_out = ~and_74_out;  // NOT_Gate not_26, 64 bits wide
  assign buffer_68_out = and_75_out;  // Buffer buffer_68, 64 bits wide
  assign not_27_out = ~and_75_out;  // NOT_Gate not_27, 64 bits wide
  assign and_76_out = buffer_66_out & {{8{l0_5_out_8[3]}}, {8{l0_5_out_8[2]}}, {8{l0_5_out_8[1]}}, {8{l0_5_out_8[0]}}, {8{l0_1_out_8[3]}}, {8{l0_1_out_8[2]}}, {8{l0_1_out_8[1]}}, {8{l0_1_out_8[0]}}};  // AND_Gate and_76, 64 bits wide
  assign and_77_out = {{8{l0_5_out_8[3]}}, {8{l0_5_out_8[2]}}, {8{l0_5_out_8[1]}}, {8{l0_5_out_8[0]}}, {8{l0_1_out_8[3]}}, {8{l0_1_out_8[2]}}, {8{l0_1_out_8[1]}}, {8{l0_1_out_8[0]}}} & not_25_out;  // AND_Gate and_77, 64 bits wide
  assign and_78_out = buffer_67_out & {{16{l0_1_out_8[3]}}, {16{l0_1_out_8[2]}}, {16{l0_1_out_8[1]}}, {16{l0_1_out_8[0]}}};  // AND_Gate and_78, 64 bits wide
  assign and_79_out = {{16{l0_1_out_8[3]}}, {16{l0_1_out_8[2]}}, {16{l0_1_out_8[1]}}, {16{l0_1_out_8[0]}}} & not_26_out;  // AND_Gate and_79, 64 bits wide
  assign and_80_out = buffer_68_out & {{16{l0_5_out_8[3]}}, {16{l0_5_out_8[2]}}, {16{l0_5_out_8[1]}}, {16{l0_5_out_8[0]}}};  // AND_Gate and_80, 64 bits wide
  assign and_81_out = {{16{l0_5_out_8[3]}}, {16{l0_5_out_8[2]}}, {16{l0_5_out_8[1]}}, {16{l0_5_out_8[0]}}} & not_27_out;  // AND_Gate and_81, 64 bits wide
  assign and_82_out = {xor_6_out[2:1], xor_6_out[12:10], xor_6_out[0], xor_6_out[9:7], {7{1'b0}}} & {xor_6_out[0], xor_6_out[9:7], {12{1'b0}}};  // AND_Gate and_82, 16 bits wide
  assign {xor_7_out_2[14], xor_7_out} = {xor_6_out[2:1], xor_6_out[12:10], xor_6_out[0], xor_6_out[9:7], {7{1'b0}}} ^ {xor_6_out[0], xor_6_out[9:7], {12{1'b0}}};  // XOR_Gate xor_7, 16 bits wide
  assign and_83_out = {xor_6_out[5], xor_6_out[14], xor_6_out[4], xor_6_out[13], xor_6_out[3:1], xor_6_out[12:10], xor_6_out[0], xor_6_out[9:7], 2'b00} & {xor_6_out[15], xor_6_out[6:5], xor_6_out[14], xor_6_out[4], xor_6_out[13], xor_6_out[3:1], xor_6_out[12:10], xor_6_out[0], xor_6_out[9:7]};  // AND_Gate and_83, 16 bits wide
  assign {xor_8_out_2[14], xor_8_out} = {xor_6_out[5], xor_6_out[14], xor_6_out[4], xor_6_out[13], xor_6_out[3:1], xor_6_out[12:10], xor_6_out[0], xor_6_out[9:7], 2'b00} ^ {xor_6_out[15], xor_6_out[6:5], xor_6_out[14], xor_6_out[4], xor_6_out[13], xor_6_out[3:1], xor_6_out[12:10], xor_6_out[0], xor_6_out[9:7]};  // XOR_Gate xor_8, 16 bits wide
  assign nor_29_out = ~(and_76_out | and_84_out);  // NOR_Gate nor_29, 64 bits wide
  assign nor_30_out = ~(nor_29_out | and_77_out);  // NOR_Gate nor_30, 64 bits wide
  assign nor_31_out = ~(and_78_out | and_85_out);  // NOR_Gate nor_31, 64 bits wide
  assign nor_32_out = ~(nor_31_out | and_79_out);  // NOR_Gate nor_32, 64 bits wide
  assign nor_33_out = ~(and_80_out | and_86_out);  // NOR_Gate nor_33, 64 bits wide
  assign nor_34_out = ~(nor_33_out | and_81_out);  // NOR_Gate nor_34, 64 bits wide
  assign not_28_out = ~{{8{l0_5_out_8[3]}}, {8{l0_5_out_8[2]}}, {8{l0_5_out_8[1]}}, {8{l0_5_out_8[0]}}, {8{l0_1_out_8[3]}}, {8{l0_1_out_8[2]}}, {8{l0_1_out_8[1]}}, {8{l0_1_out_8[0]}}};  // NOT_Gate not_28, 64 bits wide
  assign and_84_out = {not_13_out, not_13_out, not_13_out, not_13_out, not_13_out, not_13_out, not_13_out, not_13_out} & nor_30_out;  // AND_Gate and_84, 64 bits wide
  assign not_29_out = ~{{16{l0_1_out_8[3]}}, {16{l0_1_out_8[2]}}, {16{l0_1_out_8[1]}}, {16{l0_1_out_8[0]}}};  // NOT_Gate not_29, 64 bits wide
  assign and_85_out = {not_13_out, not_13_out, not_13_out, not_13_out, not_13_out, not_13_out, not_13_out, not_13_out} & nor_32_out;  // AND_Gate and_85, 64 bits wide
  assign not_30_out = ~{{16{l0_5_out_8[3]}}, {16{l0_5_out_8[2]}}, {16{l0_5_out_8[1]}}, {16{l0_5_out_8[0]}}};  // NOT_Gate not_30, 64 bits wide
  assign and_86_out = {not_13_out, not_13_out, not_13_out, not_13_out, not_13_out, not_13_out, not_13_out, not_13_out} & nor_34_out;  // AND_Gate and_86, 64 bits wide
  assign and_87_out = and_82_out[14:0] & {xor_7_out_2[14], xor_7_out[14:1]};  // AND_Gate and_87, 15 bits wide
  assign or_16_out = and_87_out | and_82_out[15:1];  // OR_Gate or_16, 15 bits wide
  assign and_88_out = xor_7_out & {xor_7_out_2[14], xor_7_out[14:1]};  // AND_Gate and_88, 15 bits wide
  assign and_89_out = xor_10_out & xor_11_out;  // AND_Gate and_89, 16 bits wide
  assign {xor_9_out_2[14], xor_9_out} = xor_10_out ^ xor_11_out;  // XOR_Gate xor_9, 16 bits wide
  assign and_90_out = and_83_out[14:0] & {xor_8_out_2[14], xor_8_out[14:1]};  // AND_Gate and_90, 15 bits wide
  assign or_17_out = and_90_out | and_83_out[15:1];  // OR_Gate or_17, 15 bits wide
  assign and_91_out = xor_8_out & {xor_8_out_2[14], xor_8_out[14:1]};  // AND_Gate and_91, 15 bits wide
  assign buffer_69_out = and_84_out;  // Buffer buffer_69, 64 bits wide
  assign and_92_out = buffer_69_out & not_28_out;  // AND_Gate and_92, 64 bits wide
  assign and_93_out = not_28_out & not_31_out;  // AND_Gate and_93, 64 bits wide
  assign not_31_out = ~and_84_out;  // NOT_Gate not_31, 64 bits wide
  assign buffer_70_out = and_85_out;  // Buffer buffer_70, 64 bits wide
  assign and_94_out = buffer_70_out & not_29_out;  // AND_Gate and_94, 64 bits wide
  assign and_95_out = not_29_out & not_32_out;  // AND_Gate and_95, 64 bits wide
  assign not_32_out = ~and_85_out;  // NOT_Gate not_32, 64 bits wide
  assign buffer_71_out = and_86_out;  // Buffer buffer_71, 64 bits wide
  assign and_96_out = buffer_71_out & not_30_out;  // AND_Gate and_96, 64 bits wide
  assign and_97_out = not_30_out & not_33_out;  // AND_Gate and_97, 64 bits wide
  assign not_33_out = ~and_86_out;  // NOT_Gate not_33, 64 bits wide
  assign nor_35_out = ~(and_92_out | and_104_out);  // NOR_Gate nor_35, 64 bits wide
  assign nor_36_out = ~(nor_35_out | and_93_out);  // NOR_Gate nor_36, 64 bits wide
  assign nor_37_out = ~(and_94_out | and_105_out);  // NOR_Gate nor_37, 64 bits wide
  assign nor_38_out = ~(nor_37_out | and_95_out);  // NOR_Gate nor_38, 64 bits wide
  assign nor_39_out = ~(and_96_out | and_106_out);  // NOR_Gate nor_39, 64 bits wide
  assign nor_40_out = ~(nor_39_out | and_97_out);  // NOR_Gate nor_40, 64 bits wide
  assign and_98_out = {or_16_out[12:0], and_82_out[0]} & and_88_out[14:1];  // AND_Gate and_98, 14 bits wide
  assign or_18_out = and_98_out | or_16_out[14:1];  // OR_Gate or_18, 14 bits wide
  assign and_99_out = {and_88_out[12:0], xor_7_out[0]} & and_88_out[14:1];  // AND_Gate and_99, 14 bits wide
  assign and_100_out = and_89_out[14:0] & {xor_9_out_2[14], xor_9_out[14:1]};  // AND_Gate and_100, 15 bits wide
  assign or_19_out = and_100_out | and_89_out[15:1];  // OR_Gate or_19, 15 bits wide
  assign and_101_out = xor_9_out & {xor_9_out_2[14], xor_9_out[14:1]};  // AND_Gate and_101, 15 bits wide
  assign and_102_out = {or_17_out[12:0], and_83_out[0]} & and_91_out[14:1];  // AND_Gate and_102, 14 bits wide
  assign or_20_out = and_102_out | or_17_out[14:1];  // OR_Gate or_20, 14 bits wide
  assign and_103_out = {and_91_out[12:0], xor_8_out[0]} & and_91_out[14:1];  // AND_Gate and_103, 14 bits wide
  assign and_104_out = {not_13_out, not_13_out, not_13_out, not_13_out, not_13_out, not_13_out, not_13_out, not_13_out} & nor_36_out;  // AND_Gate and_104, 64 bits wide
  assign and_105_out = {not_13_out, not_13_out, not_13_out, not_13_out, not_13_out, not_13_out, not_13_out, not_13_out} & nor_38_out;  // AND_Gate and_105, 64 bits wide
  assign and_106_out = {not_13_out, not_13_out, not_13_out, not_13_out, not_13_out, not_13_out, not_13_out, not_13_out} & nor_40_out;  // AND_Gate and_106, 64 bits wide
  assign buffer_72_out = and_104_out;  // Buffer buffer_72, 64 bits wide
  assign not_34_out = ~and_104_out;  // NOT_Gate not_34, 64 bits wide
  assign buffer_73_out = and_105_out;  // Buffer buffer_73, 64 bits wide
  assign not_35_out = ~and_105_out;  // NOT_Gate not_35, 64 bits wide
  assign buffer_74_out = and_106_out;  // Buffer buffer_74, 64 bits wide
  assign not_36_out = ~and_106_out;  // NOT_Gate not_36, 64 bits wide
  and and_107 (and_107_out, buffer_75_out, controlled_buffer_38_out);
  assign and_108_out = {or_18_out[9:0], or_16_out[0], and_82_out[0]} & and_99_out[13:2];  // AND_Gate and_108, 12 bits wide
  assign or_21_out = and_108_out | or_18_out[13:2];  // OR_Gate or_21, 12 bits wide
  assign and_109_out = {and_99_out[9:0], and_88_out[0], xor_7_out[0]} & and_99_out[13:2];  // AND_Gate and_109, 12 bits wide
  assign and_110_out = {or_19_out[12:0], and_89_out[0]} & and_101_out[14:1];  // AND_Gate and_110, 14 bits wide
  assign or_22_out = and_110_out | or_19_out[14:1];  // OR_Gate or_22, 14 bits wide
  assign and_111_out = {and_101_out[12:0], xor_9_out[0]} & and_101_out[14:1];  // AND_Gate and_111, 14 bits wide
  assign and_112_out = {or_20_out[9:0], or_17_out[0], and_83_out[0]} & and_103_out[13:2];  // AND_Gate and_112, 12 bits wide
  assign or_23_out = and_112_out | or_20_out[13:2];  // OR_Gate or_23, 12 bits wide
  assign and_113_out = {and_103_out[9:0], and_91_out[0], xor_8_out[0]} & and_103_out[13:2];  // AND_Gate and_113, 12 bits wide
  assign and_114_out = buffer_72_out & {{8{l0_5_out_8[3]}}, {8{l0_5_out_8[2]}}, {8{l0_5_out_8[1]}}, {8{l0_5_out_8[0]}}, {8{l0_1_out_8[3]}}, {8{l0_1_out_8[2]}}, {8{l0_1_out_8[1]}}, {8{l0_1_out_8[0]}}};  // AND_Gate and_114, 64 bits wide
  assign and_115_out = {{8{l0_5_out_8[3]}}, {8{l0_5_out_8[2]}}, {8{l0_5_out_8[1]}}, {8{l0_5_out_8[0]}}, {8{l0_1_out_8[3]}}, {8{l0_1_out_8[2]}}, {8{l0_1_out_8[1]}}, {8{l0_1_out_8[0]}}} & not_34_out;  // AND_Gate and_115, 64 bits wide
  assign and_116_out = buffer_73_out & {{16{l0_1_out_8[3]}}, {16{l0_1_out_8[2]}}, {16{l0_1_out_8[1]}}, {16{l0_1_out_8[0]}}};  // AND_Gate and_116, 64 bits wide
  assign and_117_out = {{16{l0_1_out_8[3]}}, {16{l0_1_out_8[2]}}, {16{l0_1_out_8[1]}}, {16{l0_1_out_8[0]}}} & not_35_out;  // AND_Gate and_117, 64 bits wide
  assign and_118_out = buffer_74_out & {{16{l0_5_out_8[3]}}, {16{l0_5_out_8[2]}}, {16{l0_5_out_8[1]}}, {16{l0_5_out_8[0]}}};  // AND_Gate and_118, 64 bits wide
  assign and_119_out = {{16{l0_5_out_8[3]}}, {16{l0_5_out_8[2]}}, {16{l0_5_out_8[1]}}, {16{l0_5_out_8[0]}}} & not_36_out;  // AND_Gate and_119, 64 bits wide
  assign nor_41_out = ~(and_114_out | and_120_out);  // NOR_Gate nor_41, 64 bits wide
  assign and_120_out = {not_13_out, not_13_out, not_13_out, not_13_out, not_13_out, not_13_out, not_13_out, not_13_out} & nor_42_out;  // AND_Gate and_120, 64 bits wide
  assign nor_42_out = ~(nor_41_out | and_115_out);  // NOR_Gate nor_42, 64 bits wide
  assign nor_43_out = ~(and_116_out | and_121_out);  // NOR_Gate nor_43, 64 bits wide
  assign and_121_out = {not_13_out, not_13_out, not_13_out, not_13_out, not_13_out, not_13_out, not_13_out, not_13_out} & nor_44_out;  // AND_Gate and_121, 64 bits wide
  assign nor_44_out = ~(nor_43_out | and_117_out);  // NOR_Gate nor_44, 64 bits wide
  assign nor_45_out = ~(and_118_out | and_122_out);  // NOR_Gate nor_45, 64 bits wide
  assign and_122_out = {not_13_out, not_13_out, not_13_out, not_13_out, not_13_out, not_13_out, not_13_out, not_13_out} & nor_46_out;  // AND_Gate and_122, 64 bits wide
  assign nor_46_out = ~(nor_45_out | and_119_out);  // NOR_Gate nor_46, 64 bits wide
  buf buffer_75 (buffer_75_out, buffer_76_out);
  buf buffer_76 (buffer_76_out, buffer_77_out);
  buf buffer_77 (buffer_77_out, buffer_78_out);
  buf buffer_78 (buffer_78_out, buffer_79_out);
  assign and_123_out = {or_21_out[3:0], or_18_out[1:0], or_16_out[0], and_82_out[0]} & and_109_out[11:4];  // AND_Gate and_123, 8 bits wide
  assign and_124_out = {or_22_out[9:0], or_19_out[0], and_89_out[0]} & and_111_out[13:2];  // AND_Gate and_124, 12 bits wide
  assign or_24_out = and_124_out | or_22_out[13:2];  // OR_Gate or_24, 12 bits wide
  assign and_125_out = {and_111_out[9:0], and_101_out[0], xor_9_out[0]} & and_111_out[13:2];  // AND_Gate and_125, 12 bits wide
  assign and_126_out = {or_23_out[3:0], or_20_out[1:0], or_17_out[0], and_83_out[0]} & and_113_out[11:4];  // AND_Gate and_126, 8 bits wide
  assign not_37_out = ~{{8{l0_5_out_8[3]}}, {8{l0_5_out_8[2]}}, {8{l0_5_out_8[1]}}, {8{l0_5_out_8[0]}}, {8{l0_1_out_8[3]}}, {8{l0_1_out_8[2]}}, {8{l0_1_out_8[1]}}, {8{l0_1_out_8[0]}}};  // NOT_Gate not_37, 64 bits wide
  assign not_38_out = ~{{16{l0_1_out_8[3]}}, {16{l0_1_out_8[2]}}, {16{l0_1_out_8[1]}}, {16{l0_1_out_8[0]}}};  // NOT_Gate not_38, 64 bits wide
  assign not_39_out = ~{{16{l0_5_out_8[3]}}, {16{l0_5_out_8[2]}}, {16{l0_5_out_8[1]}}, {16{l0_5_out_8[0]}}};  // NOT_Gate not_39, 64 bits wide
  buf buffer_79 (buffer_79_out, buffer_80_out);
  buf buffer_80 (buffer_80_out, buffer_81_out);
  buf buffer_81 (buffer_81_out, buffer_82_out);
  buf buffer_82 (buffer_82_out, buffer_86_out);
  assign or_25_out = and_123_out | or_21_out[11:4];  // OR_Gate or_25, 8 bits wide
  assign or_26_out = and_126_out | or_23_out[11:4];  // OR_Gate or_26, 8 bits wide
  assign buffer_83_out = and_120_out;  // Buffer buffer_83, 64 bits wide
  assign and_127_out = buffer_83_out & not_37_out;  // AND_Gate and_127, 64 bits wide
  assign and_128_out = not_37_out & not_40_out;  // AND_Gate and_128, 64 bits wide
  assign not_40_out = ~and_120_out;  // NOT_Gate not_40, 64 bits wide
  assign buffer_84_out = and_121_out;  // Buffer buffer_84, 64 bits wide
  assign and_129_out = buffer_84_out & not_38_out;  // AND_Gate and_129, 64 bits wide
  assign and_130_out = not_38_out & not_41_out;  // AND_Gate and_130, 64 bits wide
  assign not_41_out = ~and_121_out;  // NOT_Gate not_41, 64 bits wide
  assign buffer_85_out = and_122_out;  // Buffer buffer_85, 64 bits wide
  assign and_131_out = buffer_85_out & not_39_out;  // AND_Gate and_131, 64 bits wide
  assign and_132_out = not_39_out & not_42_out;  // AND_Gate and_132, 64 bits wide
  assign not_42_out = ~and_122_out;  // NOT_Gate not_42, 64 bits wide
  buf buffer_86 (buffer_86_out, buffer_87_out);
  buf buffer_87 (buffer_87_out, controlled_buffer_38_out);
  assign xor_10_out = {or_25_out[6:0], or_21_out[3:0], or_18_out[1:0], or_16_out[0], and_82_out[0], 1'b0} ^ {xor_7_out_2[14], xor_7_out};  // XOR_Gate xor_10, 16 bits wide
  assign and_133_out = {or_24_out[3:0], or_22_out[1:0], or_19_out[0], and_89_out[0]} & and_125_out[11:4];  // AND_Gate and_133, 8 bits wide
  assign xor_11_out = {or_26_out[6:0], or_23_out[3:0], or_20_out[1:0], or_17_out[0], and_83_out[0], 1'b0} ^ {xor_8_out_2[14], xor_8_out};  // XOR_Gate xor_11, 16 bits wide
  assign nor_47_out = ~(and_127_out | and_134_out);  // NOR_Gate nor_47, 64 bits wide
  assign nor_48_out = ~(nor_47_out | and_128_out);  // NOR_Gate nor_48, 64 bits wide
  assign nor_49_out = ~(and_129_out | and_135_out);  // NOR_Gate nor_49, 64 bits wide
  assign nor_50_out = ~(nor_49_out | and_130_out);  // NOR_Gate nor_50, 64 bits wide
  assign nor_51_out = ~(and_131_out | and_136_out);  // NOR_Gate nor_51, 64 bits wide
  assign nor_52_out = ~(nor_51_out | and_132_out);  // NOR_Gate nor_52, 64 bits wide
  assign or_27_out = and_133_out | or_24_out[11:4];  // OR_Gate or_27, 8 bits wide
  assign and_134_out = {not_13_out, not_13_out, not_13_out, not_13_out, not_13_out, not_13_out, not_13_out, not_13_out} & nor_48_out;  // AND_Gate and_134, 64 bits wide
  assign and_135_out = {not_13_out, not_13_out, not_13_out, not_13_out, not_13_out, not_13_out, not_13_out, not_13_out} & nor_50_out;  // AND_Gate and_135, 64 bits wide
  assign and_136_out = {not_13_out, not_13_out, not_13_out, not_13_out, not_13_out, not_13_out, not_13_out, not_13_out} & nor_52_out;  // AND_Gate and_136, 64 bits wide
  assign {xor_12_out[12], xor_12_out[3:2], xor_12_out[11], xor_12_out[1], xor_12_out[10], xor_12_out[0], xor_12_out_2[2:1], xor_12_out[9:7], xor_12_out_2[0], xor_12_out[6:4]} = {or_27_out[6:0], or_24_out[3:0], or_22_out[1:0], or_19_out[0], and_89_out[0], 1'b0} ^ {xor_9_out_2[14], xor_9_out};  // XOR_Gate xor_12, 16 bits wide
  assign controlled_buffer_38_out = and_137_out ? and_137_out : 1'bz;  // Controlled_Buffer controlled_buffer_38
  Pull_Resistor pull_resistor_11 (.node(controlled_buffer_38_out));
  assign controlled_buffer_38_out = and_138_out ? and_138_out : 1'bz;  // Controlled_Buffer controlled_buffer_39
  assign controlled_buffer_38_out = and_139_out ? and_139_out : 1'bz;  // Controlled_Buffer controlled_buffer_40
  assign controlled_buffer_38_out = and_140_out ? and_140_out : 1'bz;  // Controlled_Buffer controlled_buffer_41
  assign controlled_buffer_42_out = and_139_out ? multiplexer_4_out_3 : 8'bz;  // Controlled_Buffer controlled_buffer_42
  assign controlled_buffer_42_out = and_140_out ? multiplexer_4_out_4 : 8'bz;  // Controlled_Buffer controlled_buffer_43
  Pull_Resistor pull_resistor_12 (.node(controlled_buffer_42_out));
  assign controlled_buffer_42_out = and_138_out ? multiplexer_4_out_2 : 8'bz;  // Controlled_Buffer controlled_buffer_44
  assign controlled_buffer_42_out = and_137_out ? multiplexer_4_out : 8'bz;  // Controlled_Buffer controlled_buffer_45
  and and_137 (and_137_out, controlled_buffer_46_out, controlled_inverter_1_out);
  and and_138 (and_138_out, controlled_buffer_46_out, controlled_inverter_3_out);
  and and_139 (and_139_out, controlled_buffer_46_out, controlled_inverter_5_out);
  and and_140 (and_140_out, controlled_buffer_46_out, controlled_inverter_7_out);
  assign controlled_inverter_1_out = xor_13_out[15] ? ~xor_13_out[15] : 1'bz;  // Controlled_Inverter controlled_inverter_1
  assign controlled_inverter_1_out = xor_13_out[14] ? ~xor_13_out[14] : 1'bz;  // Controlled_Inverter controlled_inverter_2
  assign controlled_inverter_3_out = xor_14_out[15] ? ~xor_14_out[15] : 1'bz;  // Controlled_Inverter controlled_inverter_3
  assign controlled_inverter_3_out = xor_14_out[14] ? ~xor_14_out[14] : 1'bz;  // Controlled_Inverter controlled_inverter_4
  assign controlled_inverter_5_out = xor_15_out[15] ? ~xor_15_out[15] : 1'bz;  // Controlled_Inverter controlled_inverter_5
  assign controlled_inverter_5_out = xor_15_out[14] ? ~xor_15_out[14] : 1'bz;  // Controlled_Inverter controlled_inverter_6
  assign controlled_inverter_7_out = xor_16_out[15] ? ~xor_16_out[15] : 1'bz;  // Controlled_Inverter controlled_inverter_7
  assign controlled_inverter_7_out = xor_16_out[14] ? ~xor_16_out[14] : 1'bz;  // Controlled_Inverter controlled_inverter_8
  assign controlled_buffer_46_out = I4[15] ? I4[15] : 1'bz;  // Controlled_Buffer controlled_buffer_46
  assign controlled_buffer_46_out = I4[14] ? I4[14] : 1'bz;  // Controlled_Buffer controlled_buffer_47
  assign controlled_buffer_46_out = I4[13] ? I4[13] : 1'bz;  // Controlled_Buffer controlled_buffer_48
  assign controlled_inverter_1_out = xor_13_out[13] ? ~xor_13_out[13] : 1'bz;  // Controlled_Inverter controlled_inverter_9
  assign controlled_inverter_1_out = xor_13_out[12] ? ~xor_13_out[12] : 1'bz;  // Controlled_Inverter controlled_inverter_10
  assign controlled_inverter_1_out = xor_13_out[11] ? ~xor_13_out[11] : 1'bz;  // Controlled_Inverter controlled_inverter_11
  assign controlled_inverter_1_out = xor_13_out[10] ? ~xor_13_out[10] : 1'bz;  // Controlled_Inverter controlled_inverter_12
  assign controlled_inverter_3_out = xor_14_out[13] ? ~xor_14_out[13] : 1'bz;  // Controlled_Inverter controlled_inverter_13
  assign controlled_inverter_3_out = xor_14_out[12] ? ~xor_14_out[12] : 1'bz;  // Controlled_Inverter controlled_inverter_14
  assign controlled_inverter_3_out = xor_14_out[11] ? ~xor_14_out[11] : 1'bz;  // Controlled_Inverter controlled_inverter_15
  assign controlled_inverter_3_out = xor_14_out[10] ? ~xor_14_out[10] : 1'bz;  // Controlled_Inverter controlled_inverter_16
  assign controlled_inverter_5_out = xor_15_out[13] ? ~xor_15_out[13] : 1'bz;  // Controlled_Inverter controlled_inverter_17
  assign controlled_inverter_5_out = xor_15_out[12] ? ~xor_15_out[12] : 1'bz;  // Controlled_Inverter controlled_inverter_18
  assign controlled_inverter_5_out = xor_15_out[11] ? ~xor_15_out[11] : 1'bz;  // Controlled_Inverter controlled_inverter_19
  assign controlled_inverter_5_out = xor_15_out[10] ? ~xor_15_out[10] : 1'bz;  // Controlled_Inverter controlled_inverter_20
  assign controlled_inverter_7_out = xor_16_out[13] ? ~xor_16_out[13] : 1'bz;  // Controlled_Inverter controlled_inverter_21
  assign controlled_inverter_7_out = xor_16_out[12] ? ~xor_16_out[12] : 1'bz;  // Controlled_Inverter controlled_inverter_22
  assign controlled_inverter_7_out = xor_16_out[11] ? ~xor_16_out[11] : 1'bz;  // Controlled_Inverter controlled_inverter_23
  assign controlled_inverter_7_out = xor_16_out[10] ? ~xor_16_out[10] : 1'bz;  // Controlled_Inverter controlled_inverter_24
  assign controlled_buffer_46_out = I4[12] ? I4[12] : 1'bz;  // Controlled_Buffer controlled_buffer_49
  assign controlled_buffer_46_out = I4[11] ? I4[11] : 1'bz;  // Controlled_Buffer controlled_buffer_50
  assign controlled_buffer_46_out = I4[10] ? I4[10] : 1'bz;  // Controlled_Buffer controlled_buffer_51
  assign controlled_buffer_46_out = I4[9] ? I4[9] : 1'bz;  // Controlled_Buffer controlled_buffer_52
  assign controlled_inverter_1_out = xor_13_out[9] ? ~xor_13_out[9] : 1'bz;  // Controlled_Inverter controlled_inverter_25
  assign controlled_inverter_1_out = xor_13_out[8] ? ~xor_13_out[8] : 1'bz;  // Controlled_Inverter controlled_inverter_26
  assign controlled_inverter_1_out = xor_13_out[7] ? ~xor_13_out[7] : 1'bz;  // Controlled_Inverter controlled_inverter_27
  assign controlled_inverter_1_out = xor_13_out[6] ? ~xor_13_out[6] : 1'bz;  // Controlled_Inverter controlled_inverter_28
  assign controlled_inverter_3_out = xor_14_out[9] ? ~xor_14_out[9] : 1'bz;  // Controlled_Inverter controlled_inverter_29
  assign controlled_inverter_3_out = xor_14_out[8] ? ~xor_14_out[8] : 1'bz;  // Controlled_Inverter controlled_inverter_30
  assign controlled_inverter_3_out = xor_14_out[7] ? ~xor_14_out[7] : 1'bz;  // Controlled_Inverter controlled_inverter_31
  assign controlled_inverter_3_out = xor_14_out[6] ? ~xor_14_out[6] : 1'bz;  // Controlled_Inverter controlled_inverter_32
  assign controlled_inverter_5_out = xor_15_out[9] ? ~xor_15_out[9] : 1'bz;  // Controlled_Inverter controlled_inverter_33
  assign controlled_inverter_5_out = xor_15_out[8] ? ~xor_15_out[8] : 1'bz;  // Controlled_Inverter controlled_inverter_34
  assign controlled_inverter_5_out = xor_15_out[7] ? ~xor_15_out[7] : 1'bz;  // Controlled_Inverter controlled_inverter_35
  assign controlled_inverter_5_out = xor_15_out[6] ? ~xor_15_out[6] : 1'bz;  // Controlled_Inverter controlled_inverter_36
  assign controlled_inverter_7_out = xor_16_out[9] ? ~xor_16_out[9] : 1'bz;  // Controlled_Inverter controlled_inverter_37
  assign controlled_inverter_7_out = xor_16_out[8] ? ~xor_16_out[8] : 1'bz;  // Controlled_Inverter controlled_inverter_38
  assign controlled_inverter_7_out = xor_16_out[7] ? ~xor_16_out[7] : 1'bz;  // Controlled_Inverter controlled_inverter_39
  assign controlled_inverter_7_out = xor_16_out[6] ? ~xor_16_out[6] : 1'bz;  // Controlled_Inverter controlled_inverter_40
  assign controlled_buffer_46_out = I4[8] ? I4[8] : 1'bz;  // Controlled_Buffer controlled_buffer_53
  assign controlled_buffer_46_out = I4[7] ? I4[7] : 1'bz;  // Controlled_Buffer controlled_buffer_54
  assign controlled_buffer_46_out = I4[6] ? I4[6] : 1'bz;  // Controlled_Buffer controlled_buffer_55
  assign controlled_buffer_46_out = I4[5] ? I4[5] : 1'bz;  // Controlled_Buffer controlled_buffer_56
  assign controlled_buffer_57_out = and_58_out[7] ? and_58_out[7] : 1'bz;  // Controlled_Buffer controlled_buffer_57
  assign controlled_buffer_57_out = and_58_out[6] ? and_58_out[6] : 1'bz;  // Controlled_Buffer controlled_buffer_58
  assign controlled_buffer_57_out = and_58_out[5] ? and_58_out[5] : 1'bz;  // Controlled_Buffer controlled_buffer_59
  assign controlled_buffer_57_out = and_58_out[4] ? and_58_out[4] : 1'bz;  // Controlled_Buffer controlled_buffer_60
  assign controlled_inverter_1_out = xor_13_out[5] ? ~xor_13_out[5] : 1'bz;  // Controlled_Inverter controlled_inverter_41
  assign controlled_inverter_1_out = xor_13_out[4] ? ~xor_13_out[4] : 1'bz;  // Controlled_Inverter controlled_inverter_42
  assign controlled_inverter_1_out = xor_13_out[3] ? ~xor_13_out[3] : 1'bz;  // Controlled_Inverter controlled_inverter_43
  assign controlled_inverter_1_out = xor_13_out[2] ? ~xor_13_out[2] : 1'bz;  // Controlled_Inverter controlled_inverter_44
  assign controlled_inverter_3_out = xor_14_out[5] ? ~xor_14_out[5] : 1'bz;  // Controlled_Inverter controlled_inverter_45
  assign controlled_inverter_3_out = xor_14_out[4] ? ~xor_14_out[4] : 1'bz;  // Controlled_Inverter controlled_inverter_46
  assign controlled_inverter_3_out = xor_14_out[3] ? ~xor_14_out[3] : 1'bz;  // Controlled_Inverter controlled_inverter_47
  assign controlled_inverter_3_out = xor_14_out[2] ? ~xor_14_out[2] : 1'bz;  // Controlled_Inverter controlled_inverter_48
  assign controlled_inverter_5_out = xor_15_out[5] ? ~xor_15_out[5] : 1'bz;  // Controlled_Inverter controlled_inverter_49
  assign controlled_inverter_5_out = xor_15_out[4] ? ~xor_15_out[4] : 1'bz;  // Controlled_Inverter controlled_inverter_50
  assign controlled_inverter_5_out = xor_15_out[3] ? ~xor_15_out[3] : 1'bz;  // Controlled_Inverter controlled_inverter_51
  assign controlled_inverter_5_out = xor_15_out[2] ? ~xor_15_out[2] : 1'bz;  // Controlled_Inverter controlled_inverter_52
  assign controlled_inverter_7_out = xor_16_out[5] ? ~xor_16_out[5] : 1'bz;  // Controlled_Inverter controlled_inverter_53
  assign controlled_inverter_7_out = xor_16_out[4] ? ~xor_16_out[4] : 1'bz;  // Controlled_Inverter controlled_inverter_54
  assign controlled_inverter_7_out = xor_16_out[3] ? ~xor_16_out[3] : 1'bz;  // Controlled_Inverter controlled_inverter_55
  assign controlled_inverter_7_out = xor_16_out[2] ? ~xor_16_out[2] : 1'bz;  // Controlled_Inverter controlled_inverter_56
  assign controlled_buffer_46_out = I4[4] ? I4[4] : 1'bz;  // Controlled_Buffer controlled_buffer_61
  assign controlled_buffer_46_out = I4[3] ? I4[3] : 1'bz;  // Controlled_Buffer controlled_buffer_62
  assign controlled_buffer_46_out = I4[2] ? I4[2] : 1'bz;  // Controlled_Buffer controlled_buffer_63
  assign controlled_buffer_46_out = I4[1] ? I4[1] : 1'bz;  // Controlled_Buffer controlled_buffer_64
  assign controlled_buffer_57_out = and_58_out[3] ? and_58_out[3] : 1'bz;  // Controlled_Buffer controlled_buffer_65
  assign controlled_buffer_57_out = and_58_out[2] ? and_58_out[2] : 1'bz;  // Controlled_Buffer controlled_buffer_66
  assign controlled_buffer_57_out = and_58_out[1] ? and_58_out[1] : 1'bz;  // Controlled_Buffer controlled_buffer_67
  assign controlled_buffer_57_out = and_58_out[0] ? and_58_out[0] : 1'bz;  // Controlled_Buffer controlled_buffer_68
  assign controlled_buffer_69_out[3] = and_58_out[7] ? and_58_out[7] : 1'bz;  // Controlled_Buffer controlled_buffer_69
  assign controlled_buffer_69_out[3] = and_58_out[6] ? and_58_out[6] : 1'bz;  // Controlled_Buffer controlled_buffer_70
  assign controlled_buffer_69_out[3] = and_58_out[5] ? and_58_out[5] : 1'bz;  // Controlled_Buffer controlled_buffer_71
  assign controlled_buffer_69_out[3] = and_58_out[4] ? and_58_out[4] : 1'bz;  // Controlled_Buffer controlled_buffer_72
  Pull_Resistor #(.pull(1)) pull_resistor_13 (.node(controlled_inverter_1_out));
  assign controlled_inverter_1_out = xor_13_out[1] ? ~xor_13_out[1] : 1'bz;  // Controlled_Inverter controlled_inverter_57
  assign controlled_inverter_1_out = xor_13_out[0] ? ~xor_13_out[0] : 1'bz;  // Controlled_Inverter controlled_inverter_58
  assign xor_13_out = I4 ^ multiplexer_5_out;  // XOR_Gate xor_13, 16 bits wide
  Pull_Resistor #(.pull(1)) pull_resistor_14 (.node(controlled_inverter_3_out));
  assign controlled_inverter_3_out = xor_14_out[1] ? ~xor_14_out[1] : 1'bz;  // Controlled_Inverter controlled_inverter_59
  assign controlled_inverter_3_out = xor_14_out[0] ? ~xor_14_out[0] : 1'bz;  // Controlled_Inverter controlled_inverter_60
  Pull_Resistor #(.pull(1)) pull_resistor_15 (.node(controlled_inverter_5_out));
  assign controlled_inverter_5_out = xor_15_out[1] ? ~xor_15_out[1] : 1'bz;  // Controlled_Inverter controlled_inverter_61
  assign controlled_inverter_5_out = xor_15_out[0] ? ~xor_15_out[0] : 1'bz;  // Controlled_Inverter controlled_inverter_62
  Pull_Resistor #(.pull(1)) pull_resistor_16 (.node(controlled_inverter_7_out));
  assign controlled_inverter_7_out = xor_16_out[1] ? ~xor_16_out[1] : 1'bz;  // Controlled_Inverter controlled_inverter_63
  assign controlled_inverter_7_out = xor_16_out[0] ? ~xor_16_out[0] : 1'bz;  // Controlled_Inverter controlled_inverter_64
  assign controlled_buffer_46_out = I4[0] ? I4[0] : 1'bz;  // Controlled_Buffer controlled_buffer_73
  Pull_Resistor pull_resistor_17 (.node(controlled_buffer_57_out));
  CO8 co8_1 (.in_1(and_58_out), .out_2(co8_1_out_2));
  assign controlled_buffer_69_out[3] = and_58_out[3] ? and_58_out[3] : 1'bz;  // Controlled_Buffer controlled_buffer_74
  assign controlled_buffer_69_out[3] = and_58_out[2] ? and_58_out[2] : 1'bz;  // Controlled_Buffer controlled_buffer_75
  assign controlled_buffer_69_out[3] = and_58_out[1] ? and_58_out[1] : 1'bz;  // Controlled_Buffer controlled_buffer_76
  assign controlled_buffer_69_out[3] = and_58_out[0] ? and_58_out[0] : 1'bz;  // Controlled_Buffer controlled_buffer_77
  CO8 co8_2 (.in_1(and_58_out), .out_2(co8_2_out_2));
  Clock clock_2 (.out(clock_2_out));
  assign xor_14_out = I4 ^ multiplexer_5_out_2;  // XOR_Gate xor_14, 16 bits wide
  assign xor_15_out = I4 ^ multiplexer_5_out_3;  // XOR_Gate xor_15, 16 bits wide
  assign xor_16_out = I4 ^ multiplexer_5_out_4;  // XOR_Gate xor_16, 16 bits wide
  Pull_Resistor pull_resistor_18 (.node(controlled_buffer_46_out));
  Multiplexer #(.enable("true"), .select(3), .width(32)) multiplexer_2 (
    .in0({and_44_out[7:0], and_73_out[7:0], and_104_out[7:0], and_134_out[7:0]}),
    .in1({and_44_out[15:8], and_73_out[15:8], and_104_out[15:8], and_134_out[15:8]}),
    .in2({and_44_out[23:16], and_73_out[23:16], and_104_out[23:16], and_134_out[23:16]}),
    .in3({and_44_out[31:24], and_73_out[31:24], and_104_out[31:24], and_134_out[31:24]}),
    .in4({and_44_out[39:32], and_73_out[39:32], and_104_out[39:32], and_134_out[39:32]}),
    .in5({and_44_out[47:40], and_73_out[47:40], and_104_out[47:40], and_134_out[47:40]}),
    .in6({and_44_out[55:48], and_73_out[55:48], and_104_out[55:48], and_134_out[55:48]}),
    .in7({and_44_out[63:56], and_73_out[63:56], and_104_out[63:56], and_134_out[63:56]}),
    .out(multiplexer_2_out));  // open: sel, en
  Pull_Resistor pull_resistor_19 (.node(controlled_buffer_69_out[3]));
  Multiplexer #(.enable("true"), .select(3), .width(64)) multiplexer_3 (
    .in0({and_45_out[15:0], and_74_out[15:0], and_105_out[15:0], and_135_out[15:0]}),
    .in1({and_45_out[31:16], and_74_out[31:16], and_105_out[31:16], and_135_out[31:16]}),
    .in2({and_45_out[47:32], and_74_out[47:32], and_105_out[47:32], and_135_out[47:32]}),
    .in3({and_45_out[63:48], and_74_out[63:48], and_105_out[63:48], and_135_out[63:48]}),
    .in4({and_46_out[15:0], and_75_out[15:0], and_106_out[15:0], and_136_out[15:0]}),
    .in5({and_46_out[31:16], and_75_out[31:16], and_106_out[31:16], and_136_out[31:16]}),
    .in6({and_46_out[47:32], and_75_out[47:32], and_106_out[47:32], and_136_out[47:32]}),
    .in7({and_46_out[63:48], and_75_out[63:48], and_106_out[63:48], and_136_out[63:48]}),
    .out(multiplexer_3_out));  // open: sel, en
  D1 d1_2 (.in_2(and_2_out), .in_1(clock_2_out), .out_3(d1_2_out_3));
  D1 d1_3 (.in_2(d1_2_out_3), .in_1(clock_2_out), .out_3(d1_3_out_3));
  Multiplexer #(.select(3), .width(32)) multiplexer_4 (
    .in0({and_44_out[7:0], and_73_out[7:0], and_104_out[7:0], and_134_out[7:0]}),
    .in1({and_44_out[15:8], and_73_out[15:8], and_104_out[15:8], and_134_out[15:8]}),
    .in2({and_44_out[23:16], and_73_out[23:16], and_104_out[23:16], and_134_out[23:16]}),
    .in3({and_44_out[31:24], and_73_out[31:24], and_104_out[31:24], and_134_out[31:24]}),
    .in4({and_44_out[39:32], and_73_out[39:32], and_104_out[39:32], and_134_out[39:32]}),
    .in5({and_44_out[47:40], and_73_out[47:40], and_104_out[47:40], and_134_out[47:40]}),
    .in6({and_44_out[55:48], and_73_out[55:48], and_104_out[55:48], and_134_out[55:48]}),
    .in7({and_44_out[63:56], and_73_out[63:56], and_104_out[63:56], and_134_out[63:56]}),
    .out({multiplexer_4_out_4, multiplexer_4_out_3, multiplexer_4_out_2, multiplexer_4_out}));  // open: sel
  Multiplexer #(.select(3), .width(64)) multiplexer_5 (
    .in0({and_45_out[15:0], and_74_out[15:0], and_105_out[15:0], and_135_out[15:0]}),
    .in1({and_45_out[31:16], and_74_out[31:16], and_105_out[31:16], and_135_out[31:16]}),
    .in2({and_45_out[47:32], and_74_out[47:32], and_105_out[47:32], and_135_out[47:32]}),
    .in3({and_45_out[63:48], and_74_out[63:48], and_105_out[63:48], and_135_out[63:48]}),
    .in4({and_46_out[15:0], and_75_out[15:0], and_106_out[15:0], and_136_out[15:0]}),
    .in5({and_46_out[31:16], and_75_out[31:16], and_106_out[31:16], and_136_out[31:16]}),
    .in6({and_46_out[47:32], and_75_out[47:32], and_106_out[47:32], and_136_out[47:32]}),
    .in7({and_46_out[63:48], and_75_out[63:48], and_106_out[63:48], and_136_out[63:48]}),
    .out({multiplexer_5_out_4, multiplexer_5_out_3, multiplexer_5_out_2, multiplexer_5_out}));  // open: sel
  D16 d16_1 (.in_2(I4), .in_1(clock_2_out), .out_3(d16_1_out_3));
  D16 d16_2 (.in_2(d16_1_out_3), .in_1(clock_2_out), .out_3(d16_2_out_3));
  R4 r4_1 (
    .in_1(multiplexer_2_out), .in_2(multiplexer_3_out), .in_3({4{controlled_buffer_69_out[3]}}), .in_4(I4),
    .in_5(and_2_out), .in_6(I3), .out_7(r4_1_out_7));

  // Notes on the sheet:
  //   LINE C1
  //   U6
endmodule

module muxin8tor (
  input  in_1,
  input  in_2,
  output [7:0] out_3,
  output [7:0] out_4
);

  wire buffer_2_out, not_2_out;
  wire [7:7] buffer_1_out, not_1_out;

  not not_1 (not_1_out[7], in_2);
  buf buffer_1 (buffer_1_out[7], in_2);
  buf buffer_2 (buffer_2_out, in_1);
  not not_2 (not_2_out, in_1);
  assign out_3 = not_2_out ? {8{not_1_out[7]}} : 8'bz;  // Controlled_Buffer controlled_buffer_1
  assign out_3 = buffer_2_out ? {8{1'b1}} : 8'bz;  // Controlled_Buffer controlled_buffer_2
  assign out_4 = buffer_2_out ? {8{1'b1}} : 8'bz;  // Controlled_Buffer controlled_buffer_3
  assign out_4 = not_2_out ? {8{buffer_1_out[7]}} : 8'bz;  // Controlled_Buffer controlled_buffer_4
endmodule

module muxin16tor (
  input  in_1,
  input  in_2,
  output [15:0] out_3,
  output [15:0] out_4
);

  wire buffer_2_out, not_2_out;
  wire [7:7] buffer_1_out, not_1_out;

  not not_1 (not_1_out[7], in_2);
  buf buffer_1 (buffer_1_out[7], in_2);
  buf buffer_2 (buffer_2_out, in_1);
  not not_2 (not_2_out, in_1);
  assign out_3 = not_2_out ? {16{not_1_out[7]}} : 16'bz;  // Controlled_Buffer controlled_buffer_1
  assign out_3 = buffer_2_out ? {16{1'b1}} : 16'bz;  // Controlled_Buffer controlled_buffer_2
  assign out_4 = buffer_2_out ? {16{1'b1}} : 16'bz;  // Controlled_Buffer controlled_buffer_3
  assign out_4 = not_2_out ? {16{buffer_1_out[7]}} : 16'bz;  // Controlled_Buffer controlled_buffer_4
endmodule

module demuxin8tor (
  input  in_1,
  input  [15:0] in_2,
  input  [7:0] in_3,
  output [15:0] out_4
);

  wire buffer_1_out, not_1_out;

  buf buffer_1 (buffer_1_out, in_1);
  not not_1 (not_1_out, in_1);
  assign out_4 = not_1_out ? in_2 : 16'bz;  // Controlled_Buffer controlled_buffer_1
  assign out_4 = buffer_1_out ? {{8{1'b0}}, in_3} : 16'bz;  // Controlled_Buffer controlled_buffer_2
endmodule
module L0 (
  input  in_1,
  input  in_2,
  input  in_3,
  input  [7:0] in_4,
  input  [15:0] in_5,
  output [7:0] out_6,
  output [15:0] out_7,
  output out_8,
  output out_9,
  output [7:0] out_10
);

  wire and_1_out, and_2_out, and_3_out, and_4_out, and_5_out, and_10_out, and_17_out, and_18_out, and_23_out,
       and_30_out, and_31_out, and_34_out, and_43_out, and_44_out, and_45_out, and_56_out, and_57_out,
       and_58_out, and_69_out, and_70_out, and_75_out, and_82_out, and_83_out, and_88_out, and_95_out,
       and_96_out, and_101_out, and_108_out, and_109_out, and_114_out, and_121_out, and_122_out, and_127_out,
       and_134_out, and_135_out, and_138_out, and_147_out, and_148_out, and_149_out, and_160_out,
       and_161_out, and_162_out, and_173_out, and_174_out, and_179_out, and_186_out, and_187_out,
       and_192_out, and_199_out, and_200_out, and_205_out, and_212_out, and_213_out, buffer_5_out,
       buffer_6_out, buffer_7_out, buffer_8_out, buffer_9_out, buffer_10_out, buffer_11_out, buffer_12_out,
       buffer_13_out, buffer_14_out, buffer_15_out, controlled_buffer_40_out, controlled_buffer_84_out,
       controlled_buffer_127_out, controlled_buffer_170_out, controlled_buffer_212_out,
       controlled_buffer_255_out, controlled_buffer_297_out, controlled_buffer_339_out,
       controlled_buffer_385_out, controlled_buffer_428_out, controlled_buffer_471_out,
       controlled_buffer_514_out, controlled_buffer_556_out, controlled_buffer_599_out,
       controlled_buffer_641_out, controlled_buffer_683_out, nor_1_out, nor_2_out, nor_3_out, nor_4_out,
       not_1_out, not_2_out, not_3_out, not_4_out, not_7_out, not_10_out, not_13_out, not_16_out, not_19_out,
       not_22_out, not_25_out, not_28_out, not_31_out, not_34_out, not_37_out, not_40_out, not_43_out,
       not_46_out, not_49_out, not_52_out, not_55_out, not_58_out, not_61_out, not_64_out, not_67_out,
       not_70_out, not_73_out, not_76_out, not_79_out, not_82_out, not_85_out, not_88_out, not_91_out,
       not_94_out, not_97_out, not_100_out, not_103_out, not_106_out, not_109_out, not_112_out, not_115_out,
       not_118_out, not_121_out, not_124_out, not_127_out, not_130_out, not_133_out, not_136_out,
       not_139_out, not_142_out, not_145_out, or_1_out, pull_resistor_3_node, pull_resistor_9_node,
       pull_resistor_10_node, pull_resistor_12_node, pull_resistor_13_node, pull_resistor_19_node,
       pull_resistor_20_node, pull_resistor_21_node, pull_resistor_23_node, pull_resistor_29_node,
       pull_resistor_30_node, pull_resistor_31_node, pull_resistor_33_node, pull_resistor_39_node,
       pull_resistor_40_node, pull_resistor_41_node, pull_resistor_43_node, pull_resistor_49_node,
       pull_resistor_50_node, pull_resistor_51_node, pull_resistor_53_node, pull_resistor_59_node,
       pull_resistor_60_node, pull_resistor_62_node, pull_resistor_63_node, pull_resistor_69_node,
       pull_resistor_70_node, pull_resistor_71_node, pull_resistor_73_node, pull_resistor_79_node,
       pull_resistor_80_node, pull_resistor_81_node, pull_resistor_83_node, pull_resistor_89_node,
       pull_resistor_90_node, pull_resistor_91_node, pull_resistor_93_node, pull_resistor_99_node,
       pull_resistor_100_node, pull_resistor_101_node, pull_resistor_103_node, pull_resistor_109_node,
       pull_resistor_110_node, pull_resistor_111_node, pull_resistor_113_node, pull_resistor_119_node,
       pull_resistor_120_node, pull_resistor_121_node, pull_resistor_123_node, pull_resistor_129_node,
       pull_resistor_130_node, pull_resistor_131_node, pull_resistor_133_node, pull_resistor_139_node,
       pull_resistor_140_node, pull_resistor_142_node, pull_resistor_143_node, pull_resistor_149_node,
       pull_resistor_150_node, pull_resistor_151_node, pull_resistor_153_node, pull_resistor_159_node,
       pull_resistor_160_node, pull_resistor_161_node;
  wire [2:0] controlled_buffer_25_out, controlled_buffer_29_out, controlled_buffer_68_out,
       controlled_buffer_72_out, controlled_buffer_106_out, controlled_buffer_115_out,
       controlled_buffer_149_out, controlled_buffer_158_out, controlled_buffer_192_out,
       controlled_buffer_201_out, controlled_buffer_240_out, controlled_buffer_244_out,
       controlled_buffer_278_out, controlled_buffer_287_out, controlled_buffer_321_out,
       controlled_buffer_330_out, controlled_buffer_364_out, controlled_buffer_373_out,
       controlled_buffer_412_out, controlled_buffer_416_out, controlled_buffer_450_out,
       controlled_buffer_459_out, controlled_buffer_493_out, controlled_buffer_502_out,
       controlled_buffer_536_out, controlled_buffer_545_out, controlled_buffer_584_out,
       controlled_buffer_588_out, controlled_buffer_622_out, controlled_buffer_631_out,
       controlled_buffer_665_out, controlled_buffer_674_out;
  wire [3:0] and_15_out, and_16_out, and_28_out, and_29_out, and_41_out, and_42_out, and_54_out, and_55_out,
       and_67_out, and_68_out, and_80_out, and_81_out, and_93_out, and_94_out, and_106_out, and_107_out,
       and_119_out, and_120_out, and_132_out, and_133_out, and_145_out, and_146_out, and_158_out,
       and_159_out, and_171_out, and_172_out, and_184_out, and_185_out, and_197_out, and_198_out,
       and_210_out, and_211_out, buffer_26_out, buffer_27_out, buffer_34_out, buffer_35_out, buffer_42_out,
       buffer_43_out, buffer_50_out, buffer_51_out, buffer_58_out, buffer_59_out, buffer_66_out,
       buffer_67_out, buffer_74_out, buffer_75_out, buffer_82_out, buffer_83_out, buffer_90_out,
       buffer_91_out, buffer_98_out, buffer_99_out, buffer_106_out, buffer_107_out, buffer_114_out,
       buffer_115_out, buffer_122_out, buffer_123_out, buffer_130_out, buffer_131_out, buffer_138_out,
       buffer_139_out, buffer_146_out, buffer_147_out, controlled_buffer_1_out, controlled_buffer_1_out_2,
       not_11_out, not_12_out, not_20_out, not_21_out, not_29_out, not_30_out, not_38_out, not_39_out,
       not_47_out, not_48_out, not_56_out, not_57_out, not_65_out, not_66_out, not_74_out, not_75_out,
       not_83_out, not_84_out, not_92_out, not_93_out, not_101_out, not_102_out, not_110_out, not_111_out,
       not_119_out, not_120_out, not_128_out, not_129_out, not_137_out, not_138_out, not_146_out,
       not_147_out, xor_1_out, xor_2_out, xor_4_out, xor_5_out, xor_7_out, xor_8_out, xor_10_out, xor_11_out,
       xor_13_out, xor_14_out, xor_16_out, xor_17_out, xor_19_out, xor_20_out, xor_22_out, xor_23_out,
       xor_25_out, xor_26_out, xor_28_out, xor_29_out, xor_31_out, xor_32_out, xor_34_out, xor_35_out,
       xor_37_out, xor_38_out, xor_40_out, xor_41_out, xor_43_out, xor_44_out, xor_46_out, xor_47_out;
  wire [7:0] and_6_out, and_7_out, and_11_out, and_12_out, and_19_out, and_20_out, and_26_out, and_27_out,
       and_35_out, and_36_out, and_37_out, and_38_out, and_46_out, and_47_out, and_50_out, and_51_out,
       and_59_out, and_60_out, and_63_out, and_64_out, and_71_out, and_72_out, and_76_out, and_77_out,
       and_84_out, and_85_out, and_89_out, and_90_out, and_97_out, and_98_out, and_102_out, and_103_out,
       and_110_out, and_111_out, and_117_out, and_118_out, and_123_out, and_124_out, and_130_out,
       and_131_out, and_139_out, and_140_out, and_141_out, and_142_out, and_150_out, and_151_out,
       and_154_out, and_155_out, and_163_out, and_164_out, and_167_out, and_168_out, and_175_out,
       and_176_out, and_180_out, and_181_out, and_188_out, and_189_out, and_193_out, and_194_out,
       and_201_out, and_202_out, and_206_out, and_207_out, buffer_1_out, buffer_3_out, buffer_16_out,
       buffer_18_out, buffer_20_out, buffer_21_out, buffer_22_out, buffer_24_out, buffer_28_out,
       buffer_29_out, buffer_30_out, buffer_32_out, buffer_36_out, buffer_37_out, buffer_38_out,
       buffer_40_out, buffer_44_out, buffer_45_out, buffer_46_out, buffer_48_out, buffer_52_out,
       buffer_53_out, buffer_54_out, buffer_56_out, buffer_60_out, buffer_61_out, buffer_62_out,
       buffer_64_out, buffer_68_out, buffer_69_out, buffer_70_out, buffer_72_out, buffer_76_out,
       buffer_77_out, buffer_78_out, buffer_80_out, buffer_84_out, buffer_85_out, buffer_86_out,
       buffer_88_out, buffer_92_out, buffer_93_out, buffer_94_out, buffer_96_out, buffer_100_out,
       buffer_101_out, buffer_102_out, buffer_104_out, buffer_108_out, buffer_109_out, buffer_110_out,
       buffer_112_out, buffer_116_out, buffer_117_out, buffer_118_out, buffer_120_out, buffer_124_out,
       buffer_125_out, buffer_126_out, buffer_128_out, buffer_132_out, buffer_133_out, buffer_134_out,
       buffer_136_out, buffer_140_out, buffer_141_out, buffer_142_out, buffer_144_out,
       controlled_buffer_136_out, controlled_buffer_179_out, controlled_buffer_480_out,
       controlled_buffer_523_out, multiplexer_1_out, muxin8tor_1_out_3, muxin8tor_1_out_4, muxin8tor_2_out_3,
       muxin8tor_2_out_4, muxin8tor_3_out_3, muxin8tor_3_out_4, muxin8tor_4_out_3, muxin8tor_4_out_4,
       muxin8tor_5_out_3, muxin8tor_5_out_4, muxin8tor_6_out_3, muxin8tor_6_out_4, muxin8tor_7_out_3,
       muxin8tor_7_out_4, muxin8tor_8_out_3, muxin8tor_8_out_4, muxin8tor_9_out_3, muxin8tor_9_out_4,
       muxin8tor_10_out_3, muxin8tor_10_out_4, muxin8tor_11_out_3, muxin8tor_11_out_4, muxin8tor_12_out_3,
       muxin8tor_12_out_4, muxin8tor_13_out_3, muxin8tor_13_out_4, muxin8tor_14_out_3, muxin8tor_14_out_4,
       muxin8tor_15_out_3, muxin8tor_15_out_4, muxin8tor_16_out_3, muxin8tor_16_out_4, nor_5_out, nor_6_out,
       nor_9_out, nor_10_out, nor_13_out, nor_14_out, nor_17_out, nor_18_out, nor_21_out, nor_22_out,
       nor_27_out, nor_28_out, nor_29_out, nor_30_out, nor_33_out, nor_34_out, nor_37_out, nor_38_out,
       nor_41_out, nor_42_out, nor_45_out, nor_46_out, nor_49_out, nor_50_out, nor_53_out, nor_54_out,
       nor_57_out, nor_58_out, nor_61_out, nor_62_out, nor_65_out, nor_66_out, nor_69_out, nor_70_out,
       nor_73_out, nor_74_out, nor_77_out, nor_78_out, nor_81_out, nor_82_out, nor_85_out, nor_86_out,
       nor_91_out, nor_92_out, nor_93_out, nor_94_out, nor_97_out, nor_98_out, nor_101_out, nor_102_out,
       nor_105_out, nor_106_out, nor_109_out, nor_110_out, nor_113_out, nor_114_out, nor_117_out,
       nor_118_out, nor_121_out, nor_122_out, nor_125_out, nor_126_out, nor_129_out, not_5_out, not_8_out,
       not_14_out, not_17_out, not_23_out, not_26_out, not_32_out, not_35_out, not_41_out, not_44_out,
       not_50_out, not_53_out, not_59_out, not_62_out, not_68_out, not_71_out, not_77_out, not_80_out,
       not_86_out, not_89_out, not_95_out, not_98_out, not_104_out, not_107_out, not_113_out, not_116_out,
       not_122_out, not_125_out, not_131_out, not_134_out, not_140_out, not_143_out, not_148_out,
       pull_resistor_4_node, pull_resistor_14_node, pull_resistor_24_node, pull_resistor_54_node,
       pull_resistor_64_node, pull_resistor_74_node, pull_resistor_84_node, pull_resistor_94_node,
       pull_resistor_104_node, pull_resistor_134_node, pull_resistor_144_node, pull_resistor_154_node;
  wire [15:0] and_8_out, and_9_out, and_13_out, and_14_out, and_21_out, and_22_out, and_24_out, and_25_out,
       and_32_out, and_33_out, and_39_out, and_40_out, and_48_out, and_49_out, and_52_out, and_53_out,
       and_61_out, and_62_out, and_65_out, and_66_out, and_73_out, and_74_out, and_78_out, and_79_out,
       and_86_out, and_87_out, and_91_out, and_92_out, and_99_out, and_100_out, and_104_out, and_105_out,
       and_112_out, and_113_out, and_115_out, and_116_out, and_125_out, and_126_out, and_128_out,
       and_129_out, and_136_out, and_137_out, and_143_out, and_144_out, and_152_out, and_153_out,
       and_156_out, and_157_out, and_165_out, and_166_out, and_169_out, and_170_out, and_177_out,
       and_178_out, and_182_out, and_183_out, and_190_out, and_191_out, and_195_out, and_196_out,
       and_203_out, and_204_out, and_208_out, and_209_out, buffer_2_out, buffer_4_out, buffer_17_out,
       buffer_19_out, buffer_23_out, buffer_25_out, buffer_31_out, buffer_33_out, buffer_39_out,
       buffer_41_out, buffer_47_out, buffer_49_out, buffer_55_out, buffer_57_out, buffer_63_out,
       buffer_65_out, buffer_71_out, buffer_73_out, buffer_79_out, buffer_81_out, buffer_87_out,
       buffer_89_out, buffer_95_out, buffer_97_out, buffer_103_out, buffer_105_out, buffer_111_out,
       buffer_113_out, buffer_119_out, buffer_121_out, buffer_127_out, buffer_129_out, buffer_135_out,
       buffer_137_out, buffer_143_out, buffer_145_out, demuxin8tor_1_out_4, demuxin8tor_2_out_4,
       demuxin8tor_3_out_4, demuxin8tor_4_out_4, demuxin8tor_5_out_4, demuxin8tor_6_out_4,
       demuxin8tor_7_out_4, demuxin8tor_8_out_4, demuxin8tor_9_out_4, demuxin8tor_10_out_4,
       demuxin8tor_11_out_4, demuxin8tor_12_out_4, demuxin8tor_13_out_4, demuxin8tor_14_out_4,
       demuxin8tor_15_out_4, demuxin8tor_16_out_4, multiplexer_2_out, muxin16tor_1_out_3, muxin16tor_1_out_4,
       muxin16tor_2_out_3, muxin16tor_2_out_4, muxin16tor_3_out_3, muxin16tor_3_out_4, muxin16tor_4_out_3,
       muxin16tor_4_out_4, muxin16tor_5_out_3, muxin16tor_5_out_4, muxin16tor_6_out_3, muxin16tor_6_out_4,
       muxin16tor_7_out_3, muxin16tor_7_out_4, muxin16tor_8_out_3, muxin16tor_8_out_4, muxin16tor_9_out_3,
       muxin16tor_9_out_4, muxin16tor_10_out_3, muxin16tor_10_out_4, muxin16tor_11_out_3,
       muxin16tor_11_out_4, muxin16tor_12_out_3, muxin16tor_12_out_4, muxin16tor_13_out_3,
       muxin16tor_13_out_4, muxin16tor_14_out_3, muxin16tor_14_out_4, muxin16tor_15_out_3,
       muxin16tor_15_out_4, muxin16tor_16_out_3, muxin16tor_16_out_4, nor_7_out, nor_8_out, nor_11_out,
       nor_12_out, nor_15_out, nor_16_out, nor_19_out, nor_20_out, nor_23_out, nor_24_out, nor_25_out,
       nor_26_out, nor_31_out, nor_32_out, nor_35_out, nor_36_out, nor_39_out, nor_40_out, nor_43_out,
       nor_44_out, nor_47_out, nor_48_out, nor_51_out, nor_52_out, nor_55_out, nor_56_out, nor_59_out,
       nor_60_out, nor_63_out, nor_64_out, nor_67_out, nor_68_out, nor_71_out, nor_72_out, nor_75_out,
       nor_76_out, nor_79_out, nor_80_out, nor_83_out, nor_84_out, nor_87_out, nor_88_out, nor_89_out,
       nor_90_out, nor_95_out, nor_96_out, nor_99_out, nor_100_out, nor_103_out, nor_104_out, nor_107_out,
       nor_108_out, nor_111_out, nor_112_out, nor_115_out, nor_116_out, nor_119_out, nor_120_out,
       nor_123_out, nor_124_out, nor_127_out, nor_128_out, nor_131_out, not_6_out, not_9_out, not_15_out,
       not_18_out, not_24_out, not_27_out, not_33_out, not_36_out, not_42_out, not_45_out, not_51_out,
       not_54_out, not_60_out, not_63_out, not_69_out, not_72_out, not_78_out, not_81_out, not_87_out,
       not_90_out, not_96_out, not_99_out, not_105_out, not_108_out, not_114_out, not_117_out, not_123_out,
       not_126_out, not_132_out, not_135_out, not_141_out, not_144_out, pull_resistor_1_node, xor_3_out,
       xor_6_out, xor_9_out, xor_12_out, xor_15_out, xor_18_out, xor_21_out, xor_24_out, xor_27_out,
       xor_30_out, xor_33_out, xor_36_out, xor_39_out, xor_42_out, xor_45_out, xor_48_out;

  assign buffer_1_out = in_4;  // Buffer buffer_1, 8 bits wide
  assign buffer_2_out = in_5;  // Buffer buffer_2, 16 bits wide
  or or_1 (or_1_out, in_2, in_3);
  assign buffer_3_out = buffer_1_out;  // Buffer buffer_3, 8 bits wide
  assign buffer_4_out = buffer_2_out;  // Buffer buffer_4, 16 bits wide
  buf buffer_5 (buffer_5_out, or_1_out);
  and and_1 (and_1_out, or_1_out, buffer_5_out);
  buf buffer_6 (buffer_6_out, in_2);
  not not_1 (not_1_out, out_9);
  buf buffer_7 (buffer_7_out, buffer_11_out);
  buf buffer_8 (buffer_8_out, buffer_7_out);
  not not_2 (not_2_out, and_5_out);
  not not_3 (not_3_out, and_4_out);
  buf buffer_9 (buffer_9_out, buffer_6_out);
  buf buffer_10 (buffer_10_out, buffer_9_out);
  buf buffer_11 (buffer_11_out, buffer_10_out);
  and and_2 (and_2_out, not_1_out, buffer_8_out, not_2_out);
  and and_3 (and_3_out, not_3_out, out_9, buffer_11_out);
  buf buffer_12 (buffer_12_out, buffer_6_out);
  buf buffer_13 (buffer_13_out, buffer_12_out);
  buf buffer_14 (buffer_14_out, buffer_13_out);
  buf buffer_15 (buffer_15_out, buffer_14_out);
  nor nor_1 (nor_1_out, and_2_out, and_4_out);
  nor nor_2 (nor_2_out, nor_1_out, 1'b0);
  nor nor_3 (nor_3_out, and_3_out, and_5_out);
  nor nor_4 (nor_4_out, nor_3_out, 1'b0);
  assign {controlled_buffer_1_out_2, controlled_buffer_1_out} = and_4_out ? {8{1'b1}} : 8'bz;  // Controlled_Buffer controlled_buffer_1
  and and_4 (and_4_out, buffer_6_out, nor_2_out);
  and and_5 (and_5_out, buffer_6_out, nor_4_out);
  Pull_Resistor pull_resistor_1 (.node(pull_resistor_1_node));
  Pull_Resistor pull_resistor_2 (.node(out_10));
  assign out_9 = and_4_out ? and_4_out : 1'bz;  // Controlled_Buffer controlled_buffer_2
  assign buffer_16_out = multiplexer_1_out;  // Buffer buffer_16, 8 bits wide
  Multiplexer #(.width(8)) multiplexer_1 (
    .in0(out_10), .in1(buffer_3_out), .out(multiplexer_1_out), .sel(buffer_15_out));
  assign buffer_17_out = multiplexer_2_out;  // Buffer buffer_17, 16 bits wide
  Multiplexer #(.width(16)) multiplexer_2 (
    .in0(pull_resistor_1_node), .in1(buffer_4_out), .out(multiplexer_2_out), .sel(buffer_15_out));
  assign out_9 = and_5_out ? and_5_out : 1'bz;  // Controlled_Buffer controlled_buffer_3
  assign buffer_18_out = buffer_16_out;  // Buffer buffer_18, 8 bits wide
  assign buffer_19_out = buffer_17_out;  // Buffer buffer_19, 16 bits wide
  Pull_Resistor pull_resistor_3 (.node(pull_resistor_3_node));
  assign pull_resistor_3_node = 1'b0 ? 1'b0 : 1'bz;  // Controlled_Buffer controlled_buffer_4
  assign pull_resistor_3_node = 1'b0 ? 1'b0 : 1'bz;  // Controlled_Buffer controlled_buffer_5
  not not_4 (not_4_out, in_1);
  assign pull_resistor_3_node = 1'b0 ? 1'b0 : 1'bz;  // Controlled_Buffer controlled_buffer_6
  assign pull_resistor_3_node = 1'b0 ? 1'b0 : 1'bz;  // Controlled_Buffer controlled_buffer_7
  assign pull_resistor_3_node = 1'b0 ? 1'b0 : 1'bz;  // Controlled_Buffer controlled_buffer_8
  assign pull_resistor_3_node = 1'b0 ? 1'b0 : 1'bz;  // Controlled_Buffer controlled_buffer_9
  muxin8tor muxin8tor_1 (.in_2(and_18_out), .in_1(in_1), .out_3(muxin8tor_1_out_3), .out_4(muxin8tor_1_out_4));
  Pull_Resistor pull_resistor_4 (.node(pull_resistor_4_node));
  assign pull_resistor_4_node = not_4_out ? buffer_18_out : 8'bz;  // Controlled_Buffer controlled_buffer_10
  assign buffer_20_out = pull_resistor_4_node;  // Buffer buffer_20, 8 bits wide
  assign buffer_21_out = buffer_20_out;  // Buffer buffer_21, 8 bits wide
  muxin16tor muxin16tor_1 (.in_2(and_18_out), .in_1(in_1), .out_3(muxin16tor_1_out_3), .out_4(muxin16tor_1_out_4));
  demuxin8tor demuxin8tor_1 (.in_2(buffer_19_out), .in_3({8{1'b0}}), .in_1(in_1), .out_4(demuxin8tor_1_out_4));
  assign {controlled_buffer_1_out_2, controlled_buffer_1_out} = and_10_out ? {8{1'b0}} : 8'bz;  // Controlled_Buffer controlled_buffer_11
  Pull_Resistor pull_resistor_5 (.node({controlled_buffer_1_out_2, controlled_buffer_1_out}));
  assign pull_resistor_3_node = 1'b0 ? 1'b0 : 1'bz;  // Controlled_Buffer controlled_buffer_12
  assign pull_resistor_3_node = 1'b0 ? 1'b0 : 1'bz;  // Controlled_Buffer controlled_buffer_13
  assign buffer_22_out = buffer_21_out;  // Buffer buffer_22, 8 bits wide
  assign not_5_out = ~buffer_21_out;  // NOT_Gate not_5, 8 bits wide
  assign buffer_23_out = demuxin8tor_1_out_4;  // Buffer buffer_23, 16 bits wide
  assign not_6_out = ~demuxin8tor_1_out_4;  // NOT_Gate not_6, 16 bits wide
  Pull_Resistor pull_resistor_6 (.node(out_9));
  assign out_9 = and_10_out ? and_10_out : 1'bz;  // Controlled_Buffer controlled_buffer_14
  assign xor_1_out = controlled_buffer_1_out_2 ^ 4'b0000;  // XOR_Gate xor_1, 4 bits wide
  assign xor_2_out = 4'b0000 ^ controlled_buffer_1_out;  // XOR_Gate xor_2, 4 bits wide
  assign and_6_out = buffer_22_out & muxin8tor_1_out_4;  // AND_Gate and_6, 8 bits wide
  assign and_7_out = muxin8tor_1_out_4 & not_5_out;  // AND_Gate and_7, 8 bits wide
  assign and_8_out = buffer_23_out & muxin16tor_1_out_4;  // AND_Gate and_8, 16 bits wide
  assign and_9_out = muxin16tor_1_out_4 & not_6_out;  // AND_Gate and_9, 16 bits wide
  and and_10 (and_10_out, pull_resistor_12_node, and_1_out);
  not not_7 (not_7_out, pull_resistor_3_node);
  assign nor_5_out = ~(and_6_out | nor_6_out);  // NOR_Gate nor_5, 8 bits wide
  assign buffer_24_out = nor_6_out;  // Buffer buffer_24, 8 bits wide
  assign nor_6_out = ~(nor_5_out | and_7_out);  // NOR_Gate nor_6, 8 bits wide
  assign buffer_25_out = nor_8_out;  // Buffer buffer_25, 16 bits wide
  assign nor_7_out = ~(and_8_out | nor_8_out);  // NOR_Gate nor_7, 16 bits wide
  assign nor_8_out = ~(nor_7_out | and_9_out);  // NOR_Gate nor_8, 16 bits wide
  assign controlled_buffer_25_out[1] = xor_1_out[1] ? xor_1_out[1] : 1'bz;  // Controlled_Buffer controlled_buffer_15
  assign controlled_buffer_25_out[1] = xor_1_out[2] ? xor_1_out[2] : 1'bz;  // Controlled_Buffer controlled_buffer_16
  assign controlled_buffer_25_out[1] = xor_1_out[3] ? xor_1_out[3] : 1'bz;  // Controlled_Buffer controlled_buffer_17
  assign controlled_buffer_25_out[2] = xor_1_out[2] ? xor_1_out[2] : 1'bz;  // Controlled_Buffer controlled_buffer_18
  assign controlled_buffer_25_out[2] = xor_1_out[3] ? xor_1_out[3] : 1'bz;  // Controlled_Buffer controlled_buffer_19
  assign controlled_buffer_29_out[1] = xor_2_out[1] ? xor_2_out[1] : 1'bz;  // Controlled_Buffer controlled_buffer_20
  assign controlled_buffer_29_out[1] = xor_2_out[2] ? xor_2_out[2] : 1'bz;  // Controlled_Buffer controlled_buffer_21
  assign controlled_buffer_29_out[1] = xor_2_out[3] ? xor_2_out[3] : 1'bz;  // Controlled_Buffer controlled_buffer_22
  assign controlled_buffer_29_out[2] = xor_2_out[2] ? xor_2_out[2] : 1'bz;  // Controlled_Buffer controlled_buffer_23
  assign controlled_buffer_29_out[2] = xor_2_out[3] ? xor_2_out[3] : 1'bz;  // Controlled_Buffer controlled_buffer_24
  assign and_11_out = buffer_24_out & muxin8tor_1_out_3;  // AND_Gate and_11, 8 bits wide
  assign and_12_out = muxin8tor_1_out_3 & not_8_out;  // AND_Gate and_12, 8 bits wide
  assign not_8_out = ~nor_6_out;  // NOT_Gate not_8, 8 bits wide
  assign and_13_out = buffer_25_out & muxin16tor_1_out_3;  // AND_Gate and_13, 16 bits wide
  assign and_14_out = muxin16tor_1_out_3 & not_9_out;  // AND_Gate and_14, 16 bits wide
  assign not_9_out = ~nor_8_out;  // NOT_Gate not_9, 16 bits wide
  assign controlled_buffer_25_out[0] = xor_1_out[0] ? xor_1_out[0] : 1'bz;  // Controlled_Buffer controlled_buffer_25
  assign controlled_buffer_25_out[0] = xor_1_out[1] ? xor_1_out[1] : 1'bz;  // Controlled_Buffer controlled_buffer_26
  assign controlled_buffer_25_out[0] = xor_1_out[2] ? xor_1_out[2] : 1'bz;  // Controlled_Buffer controlled_buffer_27
  assign controlled_buffer_25_out[0] = xor_1_out[3] ? xor_1_out[3] : 1'bz;  // Controlled_Buffer controlled_buffer_28
  not not_10 (not_10_out, controlled_buffer_25_out[0]);
  assign controlled_buffer_29_out[0] = xor_2_out[0] ? xor_2_out[0] : 1'bz;  // Controlled_Buffer controlled_buffer_29
  assign controlled_buffer_29_out[0] = xor_2_out[1] ? xor_2_out[1] : 1'bz;  // Controlled_Buffer controlled_buffer_30
  assign controlled_buffer_29_out[0] = xor_2_out[2] ? xor_2_out[2] : 1'bz;  // Controlled_Buffer controlled_buffer_31
  assign controlled_buffer_29_out[0] = xor_2_out[3] ? xor_2_out[3] : 1'bz;  // Controlled_Buffer controlled_buffer_32
  Pull_Resistor pull_resistor_7 (.node({xor_2_out[3], controlled_buffer_29_out}));
  assign nor_9_out = ~(and_11_out | nor_10_out);  // NOR_Gate nor_9, 8 bits wide
  assign nor_10_out = ~(nor_9_out | and_12_out);  // NOR_Gate nor_10, 8 bits wide
  assign nor_11_out = ~(and_13_out | nor_12_out);  // NOR_Gate nor_11, 16 bits wide
  assign nor_12_out = ~(nor_11_out | and_14_out);  // NOR_Gate nor_12, 16 bits wide
  assign buffer_26_out = {xor_1_out[3], controlled_buffer_25_out};  // Buffer buffer_26, 4 bits wide
  Pull_Resistor pull_resistor_8 (.node({xor_1_out[3], controlled_buffer_25_out}));
  Pull_Resistor pull_resistor_9 (.node(pull_resistor_9_node));
  assign not_11_out = ~{1'b0, xor_1_out[3], controlled_buffer_25_out[2:1]};  // NOT_Gate not_11, 4 bits wide
  assign and_15_out = buffer_27_out & not_12_out;  // AND_Gate and_15, 4 bits wide
  assign buffer_27_out = {xor_2_out[3], controlled_buffer_29_out};  // Buffer buffer_27, 4 bits wide
  Pull_Resistor pull_resistor_10 (.node(pull_resistor_10_node));
  assign pull_resistor_10_node = and_15_out[3] ? controlled_buffer_1_out[3] : 1'bz;  // Controlled_Buffer controlled_buffer_33
  assign pull_resistor_10_node = and_15_out[2] ? controlled_buffer_1_out[2] : 1'bz;  // Controlled_Buffer controlled_buffer_34
  assign pull_resistor_10_node = and_15_out[1] ? controlled_buffer_1_out[1] : 1'bz;  // Controlled_Buffer controlled_buffer_35
  assign not_12_out = ~{1'b0, xor_2_out[3], controlled_buffer_29_out[2:1]};  // NOT_Gate not_12, 4 bits wide
  assign xor_3_out = nor_12_out ^ buffer_2_out;  // XOR_Gate xor_3, 16 bits wide
  assign and_16_out = buffer_26_out & not_11_out;  // AND_Gate and_16, 4 bits wide
  assign pull_resistor_9_node = and_16_out[3] ? controlled_buffer_1_out_2[3] : 1'bz;  // Controlled_Buffer controlled_buffer_36
  assign pull_resistor_9_node = and_16_out[2] ? controlled_buffer_1_out_2[2] : 1'bz;  // Controlled_Buffer controlled_buffer_37
  assign pull_resistor_9_node = and_16_out[1] ? controlled_buffer_1_out_2[1] : 1'bz;  // Controlled_Buffer controlled_buffer_38
  assign pull_resistor_9_node = and_16_out[0] ? controlled_buffer_1_out_2[0] : 1'bz;  // Controlled_Buffer controlled_buffer_39
  assign controlled_buffer_40_out = pull_resistor_9_node ? pull_resistor_9_node : 1'bz;  // Controlled_Buffer controlled_buffer_40
  and and_17 (and_17_out, not_10_out, pull_resistor_10_node);
  assign controlled_buffer_40_out = and_17_out ? and_17_out : 1'bz;  // Controlled_Buffer controlled_buffer_41
  Pull_Resistor pull_resistor_11 (.node(controlled_buffer_40_out));
  assign pull_resistor_10_node = and_15_out[0] ? controlled_buffer_1_out[0] : 1'bz;  // Controlled_Buffer controlled_buffer_42
  Pull_Resistor #(.pull(1)) pull_resistor_12 (.node(pull_resistor_12_node));
  and and_18 (and_18_out, controlled_buffer_40_out, out_9);
  assign controlled_buffer_40_out = not_7_out ? not_7_out : 1'bz;  // Controlled_Buffer controlled_buffer_43
  assign out_10 = and_10_out ? nor_10_out : 8'bz;  // Controlled_Buffer controlled_buffer_44
  assign pull_resistor_12_node = xor_3_out[0] ? ~xor_3_out[0] : 1'bz;  // Controlled_Inverter controlled_inverter_1
  assign pull_resistor_12_node = xor_3_out[1] ? ~xor_3_out[1] : 1'bz;  // Controlled_Inverter controlled_inverter_2
  assign pull_resistor_12_node = xor_3_out[2] ? ~xor_3_out[2] : 1'bz;  // Controlled_Inverter controlled_inverter_3
  assign pull_resistor_12_node = xor_3_out[3] ? ~xor_3_out[3] : 1'bz;  // Controlled_Inverter controlled_inverter_4
  assign pull_resistor_12_node = xor_3_out[4] ? ~xor_3_out[4] : 1'bz;  // Controlled_Inverter controlled_inverter_5
  assign pull_resistor_12_node = xor_3_out[5] ? ~xor_3_out[5] : 1'bz;  // Controlled_Inverter controlled_inverter_6
  assign pull_resistor_12_node = xor_3_out[6] ? ~xor_3_out[6] : 1'bz;  // Controlled_Inverter controlled_inverter_7
  assign pull_resistor_12_node = xor_3_out[7] ? ~xor_3_out[7] : 1'bz;  // Controlled_Inverter controlled_inverter_8
  assign pull_resistor_12_node = xor_3_out[8] ? ~xor_3_out[8] : 1'bz;  // Controlled_Inverter controlled_inverter_9
  assign pull_resistor_12_node = xor_3_out[9] ? ~xor_3_out[9] : 1'bz;  // Controlled_Inverter controlled_inverter_10
  assign pull_resistor_12_node = xor_3_out[10] ? ~xor_3_out[10] : 1'bz;  // Controlled_Inverter controlled_inverter_11
  assign pull_resistor_12_node = xor_3_out[11] ? ~xor_3_out[11] : 1'bz;  // Controlled_Inverter controlled_inverter_12
  assign pull_resistor_12_node = xor_3_out[12] ? ~xor_3_out[12] : 1'bz;  // Controlled_Inverter controlled_inverter_13
  assign pull_resistor_12_node = xor_3_out[13] ? ~xor_3_out[13] : 1'bz;  // Controlled_Inverter controlled_inverter_14
  assign pull_resistor_12_node = xor_3_out[14] ? ~xor_3_out[14] : 1'bz;  // Controlled_Inverter controlled_inverter_15
  assign pull_resistor_12_node = xor_3_out[15] ? ~xor_3_out[15] : 1'bz;  // Controlled_Inverter controlled_inverter_16
  assign controlled_buffer_40_out = pull_resistor_12_node ? pull_resistor_12_node : 1'bz;  // Controlled_Buffer controlled_buffer_45
  assign pull_resistor_1_node = and_10_out ? nor_12_out : 16'bz;  // Controlled_Buffer controlled_buffer_46
  Pull_Resistor pull_resistor_13 (.node(pull_resistor_13_node));
  assign pull_resistor_13_node = 1'b0 ? 1'b0 : 1'bz;  // Controlled_Buffer controlled_buffer_47
  assign pull_resistor_13_node = 1'b0 ? 1'b0 : 1'bz;  // Controlled_Buffer controlled_buffer_48
  assign pull_resistor_13_node = 1'b0 ? 1'b0 : 1'bz;  // Controlled_Buffer controlled_buffer_49
  assign pull_resistor_13_node = 1'b0 ? 1'b0 : 1'bz;  // Controlled_Buffer controlled_buffer_50
  muxin8tor muxin8tor_2 (.in_2(and_30_out), .in_1(in_1), .out_3(muxin8tor_2_out_3), .out_4(muxin8tor_2_out_4));
  not not_13 (not_13_out, in_1);
  Pull_Resistor pull_resistor_14 (.node(pull_resistor_14_node));
  assign pull_resistor_14_node = not_13_out ? nor_10_out : 8'bz;  // Controlled_Buffer controlled_buffer_51
  muxin16tor muxin16tor_2 (.in_2(and_30_out), .in_1(in_1), .out_3(muxin16tor_2_out_3), .out_4(muxin16tor_2_out_4));
  demuxin8tor demuxin8tor_2 (.in_2(nor_12_out), .in_3(8'h1), .in_1(in_1), .out_4(demuxin8tor_2_out_4));
  assign pull_resistor_13_node = 1'b0 ? 1'b0 : 1'bz;  // Controlled_Buffer controlled_buffer_52
  assign pull_resistor_13_node = 1'b0 ? 1'b0 : 1'bz;  // Controlled_Buffer controlled_buffer_53
  assign pull_resistor_13_node = 1'b0 ? 1'b0 : 1'bz;  // Controlled_Buffer controlled_buffer_54
  assign pull_resistor_13_node = 1'b1 ? 1'b1 : 1'bz;  // Controlled_Buffer controlled_buffer_55
  assign buffer_28_out = pull_resistor_14_node;  // Buffer buffer_28, 8 bits wide
  assign buffer_29_out = buffer_28_out;  // Buffer buffer_29, 8 bits wide
  assign {controlled_buffer_1_out_2, controlled_buffer_1_out} = and_23_out ? 8'h1 : 8'bz;  // Controlled_Buffer controlled_buffer_56
  Pull_Resistor pull_resistor_15 (.node({controlled_buffer_1_out_2, controlled_buffer_1_out}));
  Pull_Resistor pull_resistor_16 (.node(out_9));
  assign out_9 = and_23_out ? and_23_out : 1'bz;  // Controlled_Buffer controlled_buffer_57
  assign and_19_out = buffer_30_out & muxin8tor_2_out_4;  // AND_Gate and_19, 8 bits wide
  assign buffer_30_out = buffer_29_out;  // Buffer buffer_30, 8 bits wide
  assign and_20_out = muxin8tor_2_out_4 & not_14_out;  // AND_Gate and_20, 8 bits wide
  assign not_14_out = ~buffer_29_out;  // NOT_Gate not_14, 8 bits wide
  assign buffer_31_out = demuxin8tor_2_out_4;  // Buffer buffer_31, 16 bits wide
  assign and_21_out = buffer_31_out & muxin16tor_2_out_4;  // AND_Gate and_21, 16 bits wide
  assign and_22_out = muxin16tor_2_out_4 & not_15_out;  // AND_Gate and_22, 16 bits wide
  assign not_15_out = ~demuxin8tor_2_out_4;  // NOT_Gate not_15, 16 bits wide
  and and_23 (and_23_out, pull_resistor_21_node, and_1_out);
  not not_16 (not_16_out, pull_resistor_13_node);
  assign xor_4_out = controlled_buffer_1_out_2 ^ 4'b0000;  // XOR_Gate xor_4, 4 bits wide
  assign xor_5_out = 4'b0001 ^ controlled_buffer_1_out;  // XOR_Gate xor_5, 4 bits wide
  assign nor_13_out = ~(and_19_out | nor_14_out);  // NOR_Gate nor_13, 8 bits wide
  assign nor_14_out = ~(nor_13_out | and_20_out);  // NOR_Gate nor_14, 8 bits wide
  assign nor_15_out = ~(and_21_out | nor_16_out);  // NOR_Gate nor_15, 16 bits wide
  assign nor_16_out = ~(nor_15_out | and_22_out);  // NOR_Gate nor_16, 16 bits wide
  assign controlled_buffer_68_out[1] = xor_5_out[1] ? xor_5_out[1] : 1'bz;  // Controlled_Buffer controlled_buffer_58
  assign controlled_buffer_68_out[1] = xor_5_out[2] ? xor_5_out[2] : 1'bz;  // Controlled_Buffer controlled_buffer_59
  assign controlled_buffer_68_out[1] = xor_5_out[3] ? xor_5_out[3] : 1'bz;  // Controlled_Buffer controlled_buffer_60
  assign controlled_buffer_68_out[2] = xor_5_out[2] ? xor_5_out[2] : 1'bz;  // Controlled_Buffer controlled_buffer_61
  assign controlled_buffer_68_out[2] = xor_5_out[3] ? xor_5_out[3] : 1'bz;  // Controlled_Buffer controlled_buffer_62
  assign buffer_32_out = nor_14_out;  // Buffer buffer_32, 8 bits wide
  assign not_17_out = ~nor_14_out;  // NOT_Gate not_17, 8 bits wide
  assign buffer_33_out = nor_16_out;  // Buffer buffer_33, 16 bits wide
  assign and_24_out = buffer_33_out & muxin16tor_2_out_3;  // AND_Gate and_24, 16 bits wide
  assign and_25_out = muxin16tor_2_out_3 & not_18_out;  // AND_Gate and_25, 16 bits wide
  assign not_18_out = ~nor_16_out;  // NOT_Gate not_18, 16 bits wide
  assign controlled_buffer_72_out[1] = xor_4_out[1] ? xor_4_out[1] : 1'bz;  // Controlled_Buffer controlled_buffer_63
  assign controlled_buffer_72_out[1] = xor_4_out[2] ? xor_4_out[2] : 1'bz;  // Controlled_Buffer controlled_buffer_64
  assign controlled_buffer_72_out[1] = xor_4_out[3] ? xor_4_out[3] : 1'bz;  // Controlled_Buffer controlled_buffer_65
  assign controlled_buffer_72_out[2] = xor_4_out[2] ? xor_4_out[2] : 1'bz;  // Controlled_Buffer controlled_buffer_66
  assign controlled_buffer_72_out[2] = xor_4_out[3] ? xor_4_out[3] : 1'bz;  // Controlled_Buffer controlled_buffer_67
  assign controlled_buffer_68_out[0] = xor_5_out[0] ? xor_5_out[0] : 1'bz;  // Controlled_Buffer controlled_buffer_68
  assign controlled_buffer_68_out[0] = xor_5_out[1] ? xor_5_out[1] : 1'bz;  // Controlled_Buffer controlled_buffer_69
  assign controlled_buffer_68_out[0] = xor_5_out[2] ? xor_5_out[2] : 1'bz;  // Controlled_Buffer controlled_buffer_70
  assign controlled_buffer_68_out[0] = xor_5_out[3] ? xor_5_out[3] : 1'bz;  // Controlled_Buffer controlled_buffer_71
  Pull_Resistor pull_resistor_17 (.node({xor_5_out[3], controlled_buffer_68_out}));
  assign and_26_out = buffer_32_out & muxin8tor_2_out_3;  // AND_Gate and_26, 8 bits wide
  assign nor_17_out = ~(and_26_out | nor_18_out);  // NOR_Gate nor_17, 8 bits wide
  assign and_27_out = muxin8tor_2_out_3 & not_17_out;  // AND_Gate and_27, 8 bits wide
  assign nor_18_out = ~(nor_17_out | and_27_out);  // NOR_Gate nor_18, 8 bits wide
  assign nor_19_out = ~(and_24_out | nor_20_out);  // NOR_Gate nor_19, 16 bits wide
  assign nor_20_out = ~(nor_19_out | and_25_out);  // NOR_Gate nor_20, 16 bits wide
  assign controlled_buffer_72_out[0] = xor_4_out[0] ? xor_4_out[0] : 1'bz;  // Controlled_Buffer controlled_buffer_72
  assign controlled_buffer_72_out[0] = xor_4_out[1] ? xor_4_out[1] : 1'bz;  // Controlled_Buffer controlled_buffer_73
  assign controlled_buffer_72_out[0] = xor_4_out[2] ? xor_4_out[2] : 1'bz;  // Controlled_Buffer controlled_buffer_74
  Pull_Resistor pull_resistor_18 (.node({xor_4_out[3], controlled_buffer_72_out}));
  assign controlled_buffer_72_out[0] = xor_4_out[3] ? xor_4_out[3] : 1'bz;  // Controlled_Buffer controlled_buffer_75
  not not_19 (not_19_out, controlled_buffer_72_out[0]);
  assign buffer_34_out = {xor_5_out[3], controlled_buffer_68_out};  // Buffer buffer_34, 4 bits wide
  Pull_Resistor pull_resistor_19 (.node(pull_resistor_19_node));
  assign pull_resistor_19_node = and_29_out[3] ? controlled_buffer_1_out[3] : 1'bz;  // Controlled_Buffer controlled_buffer_76
  assign xor_6_out = nor_20_out ^ buffer_2_out;  // XOR_Gate xor_6, 16 bits wide
  assign and_28_out = buffer_35_out & not_20_out;  // AND_Gate and_28, 4 bits wide
  assign buffer_35_out = {xor_4_out[3], controlled_buffer_72_out};  // Buffer buffer_35, 4 bits wide
  Pull_Resistor pull_resistor_20 (.node(pull_resistor_20_node));
  assign not_20_out = ~{1'b0, xor_4_out[3], controlled_buffer_72_out[2:1]};  // NOT_Gate not_20, 4 bits wide
  assign pull_resistor_20_node = and_28_out[3] ? controlled_buffer_1_out_2[3] : 1'bz;  // Controlled_Buffer controlled_buffer_77
  assign pull_resistor_20_node = and_28_out[2] ? controlled_buffer_1_out_2[2] : 1'bz;  // Controlled_Buffer controlled_buffer_78
  assign and_29_out = buffer_34_out & not_21_out;  // AND_Gate and_29, 4 bits wide
  assign pull_resistor_19_node = and_29_out[2] ? controlled_buffer_1_out[2] : 1'bz;  // Controlled_Buffer controlled_buffer_79
  assign pull_resistor_19_node = and_29_out[1] ? controlled_buffer_1_out[1] : 1'bz;  // Controlled_Buffer controlled_buffer_80
  assign pull_resistor_19_node = and_29_out[0] ? controlled_buffer_1_out[0] : 1'bz;  // Controlled_Buffer controlled_buffer_81
  assign not_21_out = ~{1'b0, xor_5_out[3], controlled_buffer_68_out[2:1]};  // NOT_Gate not_21, 4 bits wide
  Pull_Resistor #(.pull(1)) pull_resistor_21 (.node(pull_resistor_21_node));
  and and_30 (and_30_out, controlled_buffer_84_out, out_9);
  assign pull_resistor_20_node = and_28_out[1] ? controlled_buffer_1_out_2[1] : 1'bz;  // Controlled_Buffer controlled_buffer_82
  assign pull_resistor_20_node = and_28_out[0] ? controlled_buffer_1_out_2[0] : 1'bz;  // Controlled_Buffer controlled_buffer_83
  assign controlled_buffer_84_out = pull_resistor_20_node ? pull_resistor_20_node : 1'bz;  // Controlled_Buffer controlled_buffer_84
  and and_31 (and_31_out, not_19_out, pull_resistor_19_node);
  assign controlled_buffer_84_out = and_31_out ? and_31_out : 1'bz;  // Controlled_Buffer controlled_buffer_85
  assign controlled_buffer_84_out = not_16_out ? not_16_out : 1'bz;  // Controlled_Buffer controlled_buffer_86
  Pull_Resistor pull_resistor_22 (.node(controlled_buffer_84_out));
  assign pull_resistor_21_node = xor_6_out[0] ? ~xor_6_out[0] : 1'bz;  // Controlled_Inverter controlled_inverter_17
  assign pull_resistor_21_node = xor_6_out[1] ? ~xor_6_out[1] : 1'bz;  // Controlled_Inverter controlled_inverter_18
  assign pull_resistor_21_node = xor_6_out[2] ? ~xor_6_out[2] : 1'bz;  // Controlled_Inverter controlled_inverter_19
  assign pull_resistor_21_node = xor_6_out[3] ? ~xor_6_out[3] : 1'bz;  // Controlled_Inverter controlled_inverter_20
  assign pull_resistor_21_node = xor_6_out[4] ? ~xor_6_out[4] : 1'bz;  // Controlled_Inverter controlled_inverter_21
  assign pull_resistor_21_node = xor_6_out[5] ? ~xor_6_out[5] : 1'bz;  // Controlled_Inverter controlled_inverter_22
  assign pull_resistor_21_node = xor_6_out[6] ? ~xor_6_out[6] : 1'bz;  // Controlled_Inverter controlled_inverter_23
  assign pull_resistor_21_node = xor_6_out[7] ? ~xor_6_out[7] : 1'bz;  // Controlled_Inverter controlled_inverter_24
  assign pull_resistor_21_node = xor_6_out[8] ? ~xor_6_out[8] : 1'bz;  // Controlled_Inverter controlled_inverter_25
  assign pull_resistor_21_node = xor_6_out[9] ? ~xor_6_out[9] : 1'bz;  // Controlled_Inverter controlled_inverter_26
  assign pull_resistor_21_node = xor_6_out[10] ? ~xor_6_out[10] : 1'bz;  // Controlled_Inverter controlled_inverter_27
  assign pull_resistor_21_node = xor_6_out[11] ? ~xor_6_out[11] : 1'bz;  // Controlled_Inverter controlled_inverter_28
  assign pull_resistor_21_node = xor_6_out[12] ? ~xor_6_out[12] : 1'bz;  // Controlled_Inverter controlled_inverter_29
  assign pull_resistor_21_node = xor_6_out[13] ? ~xor_6_out[13] : 1'bz;  // Controlled_Inverter controlled_inverter_30
  assign pull_resistor_21_node = xor_6_out[14] ? ~xor_6_out[14] : 1'bz;  // Controlled_Inverter controlled_inverter_31
  assign pull_resistor_21_node = xor_6_out[15] ? ~xor_6_out[15] : 1'bz;  // Controlled_Inverter controlled_inverter_32
  assign controlled_buffer_84_out = pull_resistor_21_node ? pull_resistor_21_node : 1'bz;  // Controlled_Buffer controlled_buffer_87
  assign out_10 = and_23_out ? nor_18_out : 8'bz;  // Controlled_Buffer controlled_buffer_88
  assign pull_resistor_1_node = and_23_out ? nor_20_out : 16'bz;  // Controlled_Buffer controlled_buffer_89
  Pull_Resistor pull_resistor_23 (.node(pull_resistor_23_node));
  assign pull_resistor_23_node = 1'b0 ? 1'b0 : 1'bz;  // Controlled_Buffer controlled_buffer_90
  assign pull_resistor_23_node = 1'b0 ? 1'b0 : 1'bz;  // Controlled_Buffer controlled_buffer_91
  assign pull_resistor_23_node = 1'b0 ? 1'b0 : 1'bz;  // Controlled_Buffer controlled_buffer_92
  assign pull_resistor_23_node = 1'b0 ? 1'b0 : 1'bz;  // Controlled_Buffer controlled_buffer_93
  muxin8tor muxin8tor_3 (.in_2(and_43_out), .in_1(in_1), .out_3(muxin8tor_3_out_3), .out_4(muxin8tor_3_out_4));
  not not_22 (not_22_out, in_1);
  Pull_Resistor pull_resistor_24 (.node(pull_resistor_24_node));
  assign pull_resistor_24_node = not_22_out ? nor_18_out : 8'bz;  // Controlled_Buffer controlled_buffer_94
  muxin16tor muxin16tor_3 (.in_2(and_43_out), .in_1(in_1), .out_3(muxin16tor_3_out_3), .out_4(muxin16tor_3_out_4));
  demuxin8tor demuxin8tor_3 (.in_2(nor_20_out), .in_3(8'h2), .in_1(in_1), .out_4(demuxin8tor_3_out_4));
  assign pull_resistor_23_node = 1'b0 ? 1'b0 : 1'bz;  // Controlled_Buffer controlled_buffer_95
  assign pull_resistor_23_node = 1'b0 ? 1'b0 : 1'bz;  // Controlled_Buffer controlled_buffer_96
  assign pull_resistor_23_node = 1'b1 ? 1'b1 : 1'bz;  // Controlled_Buffer controlled_buffer_97
  assign pull_resistor_23_node = 1'b0 ? 1'b0 : 1'bz;  // Controlled_Buffer controlled_buffer_98
  assign buffer_36_out = pull_resistor_24_node;  // Buffer buffer_36, 8 bits wide
  assign buffer_37_out = buffer_36_out;  // Buffer buffer_37, 8 bits wide
  assign {controlled_buffer_1_out_2, controlled_buffer_1_out} = and_34_out ? 8'h2 : 8'bz;  // Controlled_Buffer controlled_buffer_99
  Pull_Resistor pull_resistor_25 (.node({controlled_buffer_1_out_2, controlled_buffer_1_out}));
  assign out_9 = and_34_out ? and_34_out : 1'bz;  // Controlled_Buffer controlled_buffer_100
  assign buffer_38_out = buffer_37_out;  // Buffer buffer_38, 8 bits wide
  assign not_23_out = ~buffer_37_out;  // NOT_Gate not_23, 8 bits wide
  assign buffer_39_out = demuxin8tor_3_out_4;  // Buffer buffer_39, 16 bits wide
  assign and_32_out = buffer_39_out & muxin16tor_3_out_4;  // AND_Gate and_32, 16 bits wide
  assign and_33_out = muxin16tor_3_out_4 & not_24_out;  // AND_Gate and_33, 16 bits wide
  assign not_24_out = ~demuxin8tor_3_out_4;  // NOT_Gate not_24, 16 bits wide
  and and_34 (and_34_out, pull_resistor_31_node, and_1_out);
  Pull_Resistor pull_resistor_26 (.node(out_9));
  not not_25 (not_25_out, pull_resistor_23_node);
  assign xor_7_out = controlled_buffer_1_out_2 ^ 4'b0000;  // XOR_Gate xor_7, 4 bits wide
  assign xor_8_out = 4'b0010 ^ controlled_buffer_1_out;  // XOR_Gate xor_8, 4 bits wide
  assign and_35_out = buffer_38_out & muxin8tor_3_out_4;  // AND_Gate and_35, 8 bits wide
  assign nor_21_out = ~(and_35_out | nor_22_out);  // NOR_Gate nor_21, 8 bits wide
  assign and_36_out = muxin8tor_3_out_4 & not_23_out;  // AND_Gate and_36, 8 bits wide
  assign nor_22_out = ~(nor_21_out | and_36_out);  // NOR_Gate nor_22, 8 bits wide
  assign nor_23_out = ~(and_32_out | nor_24_out);  // NOR_Gate nor_23, 16 bits wide
  assign nor_24_out = ~(nor_23_out | and_33_out);  // NOR_Gate nor_24, 16 bits wide
  assign buffer_40_out = nor_22_out;  // Buffer buffer_40, 8 bits wide
  assign not_26_out = ~nor_22_out;  // NOT_Gate not_26, 8 bits wide
  assign buffer_41_out = nor_24_out;  // Buffer buffer_41, 16 bits wide
  assign not_27_out = ~nor_24_out;  // NOT_Gate not_27, 16 bits wide
  assign controlled_buffer_115_out[1] = xor_7_out[1] ? xor_7_out[1] : 1'bz;  // Controlled_Buffer controlled_buffer_101
  assign controlled_buffer_115_out[1] = xor_7_out[2] ? xor_7_out[2] : 1'bz;  // Controlled_Buffer controlled_buffer_102
  assign controlled_buffer_115_out[1] = xor_7_out[3] ? xor_7_out[3] : 1'bz;  // Controlled_Buffer controlled_buffer_103
  assign controlled_buffer_115_out[2] = xor_7_out[2] ? xor_7_out[2] : 1'bz;  // Controlled_Buffer controlled_buffer_104
  assign controlled_buffer_115_out[2] = xor_7_out[3] ? xor_7_out[3] : 1'bz;  // Controlled_Buffer controlled_buffer_105
  assign controlled_buffer_106_out[0] = xor_8_out[0] ? xor_8_out[0] : 1'bz;  // Controlled_Buffer controlled_buffer_106
  assign controlled_buffer_106_out[1] = xor_8_out[1] ? xor_8_out[1] : 1'bz;  // Controlled_Buffer controlled_buffer_107
  assign controlled_buffer_106_out[0] = xor_8_out[1] ? xor_8_out[1] : 1'bz;  // Controlled_Buffer controlled_buffer_108
  assign controlled_buffer_106_out[1] = xor_8_out[2] ? xor_8_out[2] : 1'bz;  // Controlled_Buffer controlled_buffer_109
  assign controlled_buffer_106_out[0] = xor_8_out[2] ? xor_8_out[2] : 1'bz;  // Controlled_Buffer controlled_buffer_110
  assign controlled_buffer_106_out[1] = xor_8_out[3] ? xor_8_out[3] : 1'bz;  // Controlled_Buffer controlled_buffer_111
  assign controlled_buffer_106_out[0] = xor_8_out[3] ? xor_8_out[3] : 1'bz;  // Controlled_Buffer controlled_buffer_112
  assign controlled_buffer_106_out[2] = xor_8_out[2] ? xor_8_out[2] : 1'bz;  // Controlled_Buffer controlled_buffer_113
  Pull_Resistor pull_resistor_27 (.node({xor_8_out[3], controlled_buffer_106_out}));
  assign controlled_buffer_106_out[2] = xor_8_out[3] ? xor_8_out[3] : 1'bz;  // Controlled_Buffer controlled_buffer_114
  assign and_37_out = buffer_40_out & muxin8tor_3_out_3;  // AND_Gate and_37, 8 bits wide
  assign and_38_out = muxin8tor_3_out_3 & not_26_out;  // AND_Gate and_38, 8 bits wide
  assign nor_25_out = ~(and_39_out | nor_26_out);  // NOR_Gate nor_25, 16 bits wide
  assign and_39_out = buffer_41_out & muxin16tor_3_out_3;  // AND_Gate and_39, 16 bits wide
  assign and_40_out = muxin16tor_3_out_3 & not_27_out;  // AND_Gate and_40, 16 bits wide
  assign nor_26_out = ~(nor_25_out | and_40_out);  // NOR_Gate nor_26, 16 bits wide
  assign controlled_buffer_115_out[0] = xor_7_out[0] ? xor_7_out[0] : 1'bz;  // Controlled_Buffer controlled_buffer_115
  assign controlled_buffer_115_out[0] = xor_7_out[1] ? xor_7_out[1] : 1'bz;  // Controlled_Buffer controlled_buffer_116
  assign controlled_buffer_115_out[0] = xor_7_out[2] ? xor_7_out[2] : 1'bz;  // Controlled_Buffer controlled_buffer_117
  Pull_Resistor pull_resistor_28 (.node({xor_7_out[3], controlled_buffer_115_out}));
  assign controlled_buffer_115_out[0] = xor_7_out[3] ? xor_7_out[3] : 1'bz;  // Controlled_Buffer controlled_buffer_118
  not not_28 (not_28_out, controlled_buffer_115_out[0]);
  assign buffer_42_out = {xor_8_out[3], controlled_buffer_106_out};  // Buffer buffer_42, 4 bits wide
  Pull_Resistor pull_resistor_29 (.node(pull_resistor_29_node));
  assign nor_27_out = ~(and_37_out | nor_28_out);  // NOR_Gate nor_27, 8 bits wide
  assign nor_28_out = ~(nor_27_out | and_38_out);  // NOR_Gate nor_28, 8 bits wide
  assign xor_9_out = nor_26_out ^ buffer_2_out;  // XOR_Gate xor_9, 16 bits wide
  assign and_41_out = buffer_43_out & not_29_out;  // AND_Gate and_41, 4 bits wide
  assign buffer_43_out = {xor_7_out[3], controlled_buffer_115_out};  // Buffer buffer_43, 4 bits wide
  Pull_Resistor pull_resistor_30 (.node(pull_resistor_30_node));
  assign not_29_out = ~{1'b0, xor_7_out[3], controlled_buffer_115_out[2:1]};  // NOT_Gate not_29, 4 bits wide
  assign pull_resistor_30_node = and_41_out[3] ? controlled_buffer_1_out_2[3] : 1'bz;  // Controlled_Buffer controlled_buffer_119
  assign pull_resistor_30_node = and_41_out[2] ? controlled_buffer_1_out_2[2] : 1'bz;  // Controlled_Buffer controlled_buffer_120
  assign and_42_out = buffer_42_out & not_30_out;  // AND_Gate and_42, 4 bits wide
  assign pull_resistor_29_node = and_42_out[3] ? controlled_buffer_1_out[3] : 1'bz;  // Controlled_Buffer controlled_buffer_121
  assign pull_resistor_29_node = and_42_out[2] ? controlled_buffer_1_out[2] : 1'bz;  // Controlled_Buffer controlled_buffer_122
  assign pull_resistor_29_node = and_42_out[1] ? controlled_buffer_1_out[1] : 1'bz;  // Controlled_Buffer controlled_buffer_123
  assign pull_resistor_29_node = and_42_out[0] ? controlled_buffer_1_out[0] : 1'bz;  // Controlled_Buffer controlled_buffer_124
  assign not_30_out = ~{1'b0, xor_8_out[3], controlled_buffer_106_out[2:1]};  // NOT_Gate not_30, 4 bits wide
  Pull_Resistor #(.pull(1)) pull_resistor_31 (.node(pull_resistor_31_node));
  and and_43 (and_43_out, controlled_buffer_127_out, out_9);
  assign pull_resistor_30_node = and_41_out[1] ? controlled_buffer_1_out_2[1] : 1'bz;  // Controlled_Buffer controlled_buffer_125
  assign pull_resistor_30_node = and_41_out[0] ? controlled_buffer_1_out_2[0] : 1'bz;  // Controlled_Buffer controlled_buffer_126
  assign controlled_buffer_127_out = pull_resistor_30_node ? pull_resistor_30_node : 1'bz;  // Controlled_Buffer controlled_buffer_127
  and and_44 (and_44_out, not_28_out, pull_resistor_29_node);
  assign controlled_buffer_127_out = and_44_out ? and_44_out : 1'bz;  // Controlled_Buffer controlled_buffer_128
  assign controlled_buffer_127_out = not_25_out ? not_25_out : 1'bz;  // Controlled_Buffer controlled_buffer_129
  Pull_Resistor pull_resistor_32 (.node(controlled_buffer_127_out));
  assign pull_resistor_31_node = xor_9_out[0] ? ~xor_9_out[0] : 1'bz;  // Controlled_Inverter controlled_inverter_33
  assign pull_resistor_31_node = xor_9_out[1] ? ~xor_9_out[1] : 1'bz;  // Controlled_Inverter controlled_inverter_34
  assign pull_resistor_31_node = xor_9_out[2] ? ~xor_9_out[2] : 1'bz;  // Controlled_Inverter controlled_inverter_35
  assign pull_resistor_31_node = xor_9_out[3] ? ~xor_9_out[3] : 1'bz;  // Controlled_Inverter controlled_inverter_36
  assign pull_resistor_31_node = xor_9_out[4] ? ~xor_9_out[4] : 1'bz;  // Controlled_Inverter controlled_inverter_37
  assign pull_resistor_31_node = xor_9_out[5] ? ~xor_9_out[5] : 1'bz;  // Controlled_Inverter controlled_inverter_38
  assign pull_resistor_31_node = xor_9_out[6] ? ~xor_9_out[6] : 1'bz;  // Controlled_Inverter controlled_inverter_39
  assign pull_resistor_31_node = xor_9_out[7] ? ~xor_9_out[7] : 1'bz;  // Controlled_Inverter controlled_inverter_40
  assign pull_resistor_31_node = xor_9_out[8] ? ~xor_9_out[8] : 1'bz;  // Controlled_Inverter controlled_inverter_41
  assign pull_resistor_31_node = xor_9_out[9] ? ~xor_9_out[9] : 1'bz;  // Controlled_Inverter controlled_inverter_42
  assign pull_resistor_31_node = xor_9_out[10] ? ~xor_9_out[10] : 1'bz;  // Controlled_Inverter controlled_inverter_43
  assign pull_resistor_31_node = xor_9_out[11] ? ~xor_9_out[11] : 1'bz;  // Controlled_Inverter controlled_inverter_44
  assign pull_resistor_31_node = xor_9_out[12] ? ~xor_9_out[12] : 1'bz;  // Controlled_Inverter controlled_inverter_45
  assign pull_resistor_31_node = xor_9_out[13] ? ~xor_9_out[13] : 1'bz;  // Controlled_Inverter controlled_inverter_46
  assign pull_resistor_31_node = xor_9_out[14] ? ~xor_9_out[14] : 1'bz;  // Controlled_Inverter controlled_inverter_47
  assign pull_resistor_31_node = xor_9_out[15] ? ~xor_9_out[15] : 1'bz;  // Controlled_Inverter controlled_inverter_48
  assign out_10 = and_34_out ? nor_28_out : 8'bz;  // Controlled_Buffer controlled_buffer_130
  assign pull_resistor_1_node = and_34_out ? nor_26_out : 16'bz;  // Controlled_Buffer controlled_buffer_131
  assign controlled_buffer_127_out = pull_resistor_31_node ? pull_resistor_31_node : 1'bz;  // Controlled_Buffer controlled_buffer_132
  Pull_Resistor pull_resistor_33 (.node(pull_resistor_33_node));
  assign pull_resistor_33_node = 1'b0 ? 1'b0 : 1'bz;  // Controlled_Buffer controlled_buffer_133
  assign pull_resistor_33_node = 1'b0 ? 1'b0 : 1'bz;  // Controlled_Buffer controlled_buffer_134
  assign pull_resistor_33_node = 1'b0 ? 1'b0 : 1'bz;  // Controlled_Buffer controlled_buffer_135
  muxin8tor muxin8tor_4 (.in_2(and_56_out), .in_1(in_1), .out_3(muxin8tor_4_out_3), .out_4(muxin8tor_4_out_4));
  not not_31 (not_31_out, in_1);
  assign controlled_buffer_136_out = not_31_out ? nor_28_out : 8'bz;  // Controlled_Buffer controlled_buffer_136
  muxin16tor muxin16tor_4 (.in_2(and_56_out), .in_1(in_1), .out_3(muxin16tor_4_out_3), .out_4(muxin16tor_4_out_4));
  demuxin8tor demuxin8tor_4 (.in_2(nor_26_out), .in_3(8'h3), .in_1(in_1), .out_4(demuxin8tor_4_out_4));
  assign pull_resistor_33_node = 1'b0 ? 1'b0 : 1'bz;  // Controlled_Buffer controlled_buffer_137
  assign pull_resistor_33_node = 1'b0 ? 1'b0 : 1'bz;  // Controlled_Buffer controlled_buffer_138
  assign pull_resistor_33_node = 1'b0 ? 1'b0 : 1'bz;  // Controlled_Buffer controlled_buffer_139
  assign pull_resistor_33_node = 1'b1 ? 1'b1 : 1'bz;  // Controlled_Buffer controlled_buffer_140
  Pull_Resistor pull_resistor_34 (.node(controlled_buffer_136_out));
  assign buffer_44_out = controlled_buffer_136_out;  // Buffer buffer_44, 8 bits wide
  assign buffer_45_out = buffer_44_out;  // Buffer buffer_45, 8 bits wide
  assign {controlled_buffer_1_out_2, controlled_buffer_1_out} = and_45_out ? 8'h3 : 8'bz;  // Controlled_Buffer controlled_buffer_141
  Pull_Resistor pull_resistor_35 (.node({controlled_buffer_1_out_2, controlled_buffer_1_out}));
  assign out_9 = and_45_out ? and_45_out : 1'bz;  // Controlled_Buffer controlled_buffer_142
  assign pull_resistor_33_node = 1'b1 ? 1'b1 : 1'bz;  // Controlled_Buffer controlled_buffer_143
  assign buffer_46_out = buffer_45_out;  // Buffer buffer_46, 8 bits wide
  assign not_32_out = ~buffer_45_out;  // NOT_Gate not_32, 8 bits wide
  assign buffer_47_out = demuxin8tor_4_out_4;  // Buffer buffer_47, 16 bits wide
  assign not_33_out = ~demuxin8tor_4_out_4;  // NOT_Gate not_33, 16 bits wide
  and and_45 (and_45_out, pull_resistor_41_node, and_1_out);
  Pull_Resistor pull_resistor_36 (.node(out_9));
  not not_34 (not_34_out, pull_resistor_33_node);
  assign xor_10_out = controlled_buffer_1_out_2 ^ 4'b0000;  // XOR_Gate xor_10, 4 bits wide
  assign xor_11_out = 4'b0011 ^ controlled_buffer_1_out;  // XOR_Gate xor_11, 4 bits wide
  assign and_46_out = buffer_46_out & muxin8tor_4_out_4;  // AND_Gate and_46, 8 bits wide
  assign nor_29_out = ~(and_46_out | nor_30_out);  // NOR_Gate nor_29, 8 bits wide
  assign and_47_out = muxin8tor_4_out_4 & not_32_out;  // AND_Gate and_47, 8 bits wide
  assign nor_30_out = ~(nor_29_out | and_47_out);  // NOR_Gate nor_30, 8 bits wide
  assign nor_31_out = ~(and_48_out | nor_32_out);  // NOR_Gate nor_31, 16 bits wide
  assign and_48_out = buffer_47_out & muxin16tor_4_out_4;  // AND_Gate and_48, 16 bits wide
  assign nor_32_out = ~(nor_31_out | and_49_out);  // NOR_Gate nor_32, 16 bits wide
  assign and_49_out = muxin16tor_4_out_4 & not_33_out;  // AND_Gate and_49, 16 bits wide
  assign buffer_48_out = nor_30_out;  // Buffer buffer_48, 8 bits wide
  assign not_35_out = ~nor_30_out;  // NOT_Gate not_35, 8 bits wide
  assign buffer_49_out = nor_32_out;  // Buffer buffer_49, 16 bits wide
  assign not_36_out = ~nor_32_out;  // NOT_Gate not_36, 16 bits wide
  assign controlled_buffer_158_out[1] = xor_10_out[1] ? xor_10_out[1] : 1'bz;  // Controlled_Buffer controlled_buffer_144
  assign controlled_buffer_158_out[1] = xor_10_out[2] ? xor_10_out[2] : 1'bz;  // Controlled_Buffer controlled_buffer_145
  assign controlled_buffer_158_out[1] = xor_10_out[3] ? xor_10_out[3] : 1'bz;  // Controlled_Buffer controlled_buffer_146
  assign controlled_buffer_158_out[2] = xor_10_out[2] ? xor_10_out[2] : 1'bz;  // Controlled_Buffer controlled_buffer_147
  assign controlled_buffer_158_out[2] = xor_10_out[3] ? xor_10_out[3] : 1'bz;  // Controlled_Buffer controlled_buffer_148
  assign controlled_buffer_149_out[0] = xor_11_out[0] ? xor_11_out[0] : 1'bz;  // Controlled_Buffer controlled_buffer_149
  assign controlled_buffer_149_out[1] = xor_11_out[1] ? xor_11_out[1] : 1'bz;  // Controlled_Buffer controlled_buffer_150
  assign controlled_buffer_149_out[0] = xor_11_out[1] ? xor_11_out[1] : 1'bz;  // Controlled_Buffer controlled_buffer_151
  assign controlled_buffer_149_out[1] = xor_11_out[2] ? xor_11_out[2] : 1'bz;  // Controlled_Buffer controlled_buffer_152
  assign controlled_buffer_149_out[0] = xor_11_out[2] ? xor_11_out[2] : 1'bz;  // Controlled_Buffer controlled_buffer_153
  assign controlled_buffer_149_out[1] = xor_11_out[3] ? xor_11_out[3] : 1'bz;  // Controlled_Buffer controlled_buffer_154
  assign controlled_buffer_149_out[0] = xor_11_out[3] ? xor_11_out[3] : 1'bz;  // Controlled_Buffer controlled_buffer_155
  assign controlled_buffer_149_out[2] = xor_11_out[2] ? xor_11_out[2] : 1'bz;  // Controlled_Buffer controlled_buffer_156
  Pull_Resistor pull_resistor_37 (.node({xor_11_out[3], controlled_buffer_149_out}));
  assign controlled_buffer_149_out[2] = xor_11_out[3] ? xor_11_out[3] : 1'bz;  // Controlled_Buffer controlled_buffer_157
  assign and_50_out = buffer_48_out & muxin8tor_4_out_3;  // AND_Gate and_50, 8 bits wide
  assign and_51_out = muxin8tor_4_out_3 & not_35_out;  // AND_Gate and_51, 8 bits wide
  assign and_52_out = buffer_49_out & muxin16tor_4_out_3;  // AND_Gate and_52, 16 bits wide
  assign and_53_out = muxin16tor_4_out_3 & not_36_out;  // AND_Gate and_53, 16 bits wide
  assign controlled_buffer_158_out[0] = xor_10_out[0] ? xor_10_out[0] : 1'bz;  // Controlled_Buffer controlled_buffer_158
  assign controlled_buffer_158_out[0] = xor_10_out[1] ? xor_10_out[1] : 1'bz;  // Controlled_Buffer controlled_buffer_159
  assign controlled_buffer_158_out[0] = xor_10_out[2] ? xor_10_out[2] : 1'bz;  // Controlled_Buffer controlled_buffer_160
  Pull_Resistor pull_resistor_38 (.node({xor_10_out[3], controlled_buffer_158_out}));
  assign controlled_buffer_158_out[0] = xor_10_out[3] ? xor_10_out[3] : 1'bz;  // Controlled_Buffer controlled_buffer_161
  not not_37 (not_37_out, controlled_buffer_158_out[0]);
  assign buffer_50_out = {xor_11_out[3], controlled_buffer_149_out};  // Buffer buffer_50, 4 bits wide
  assign nor_33_out = ~(and_50_out | nor_34_out);  // NOR_Gate nor_33, 8 bits wide
  assign nor_34_out = ~(nor_33_out | and_51_out);  // NOR_Gate nor_34, 8 bits wide
  assign nor_35_out = ~(and_52_out | nor_36_out);  // NOR_Gate nor_35, 16 bits wide
  assign nor_36_out = ~(nor_35_out | and_53_out);  // NOR_Gate nor_36, 16 bits wide
  assign and_54_out = buffer_51_out & not_38_out;  // AND_Gate and_54, 4 bits wide
  assign buffer_51_out = {xor_10_out[3], controlled_buffer_158_out};  // Buffer buffer_51, 4 bits wide
  Pull_Resistor pull_resistor_39 (.node(pull_resistor_39_node));
  assign not_38_out = ~{1'b0, xor_10_out[3], controlled_buffer_158_out[2:1]};  // NOT_Gate not_38, 4 bits wide
  assign pull_resistor_39_node = and_54_out[3] ? controlled_buffer_1_out_2[3] : 1'bz;  // Controlled_Buffer controlled_buffer_162
  assign and_55_out = buffer_50_out & not_39_out;  // AND_Gate and_55, 4 bits wide
  Pull_Resistor pull_resistor_40 (.node(pull_resistor_40_node));
  assign pull_resistor_40_node = and_55_out[3] ? controlled_buffer_1_out[3] : 1'bz;  // Controlled_Buffer controlled_buffer_163
  assign pull_resistor_40_node = and_55_out[2] ? controlled_buffer_1_out[2] : 1'bz;  // Controlled_Buffer controlled_buffer_164
  assign pull_resistor_40_node = and_55_out[1] ? controlled_buffer_1_out[1] : 1'bz;  // Controlled_Buffer controlled_buffer_165
  assign pull_resistor_40_node = and_55_out[0] ? controlled_buffer_1_out[0] : 1'bz;  // Controlled_Buffer controlled_buffer_166
  assign not_39_out = ~{1'b0, xor_11_out[3], controlled_buffer_149_out[2:1]};  // NOT_Gate not_39, 4 bits wide
  assign xor_12_out = nor_36_out ^ buffer_2_out;  // XOR_Gate xor_12, 16 bits wide
  Pull_Resistor #(.pull(1)) pull_resistor_41 (.node(pull_resistor_41_node));
  and and_56 (and_56_out, controlled_buffer_170_out, out_9);
  assign pull_resistor_39_node = and_54_out[2] ? controlled_buffer_1_out_2[2] : 1'bz;  // Controlled_Buffer controlled_buffer_167
  assign pull_resistor_39_node = and_54_out[1] ? controlled_buffer_1_out_2[1] : 1'bz;  // Controlled_Buffer controlled_buffer_168
  assign pull_resistor_39_node = and_54_out[0] ? controlled_buffer_1_out_2[0] : 1'bz;  // Controlled_Buffer controlled_buffer_169
  assign controlled_buffer_170_out = pull_resistor_39_node ? pull_resistor_39_node : 1'bz;  // Controlled_Buffer controlled_buffer_170
  and and_57 (and_57_out, not_37_out, pull_resistor_40_node);
  assign controlled_buffer_170_out = and_57_out ? and_57_out : 1'bz;  // Controlled_Buffer controlled_buffer_171
  assign controlled_buffer_170_out = not_34_out ? not_34_out : 1'bz;  // Controlled_Buffer controlled_buffer_172
  Pull_Resistor pull_resistor_42 (.node(controlled_buffer_170_out));
  assign out_10 = and_45_out ? nor_34_out : 8'bz;  // Controlled_Buffer controlled_buffer_173
  assign pull_resistor_1_node = and_45_out ? nor_36_out : 16'bz;  // Controlled_Buffer controlled_buffer_174
  assign pull_resistor_41_node = xor_12_out[0] ? ~xor_12_out[0] : 1'bz;  // Controlled_Inverter controlled_inverter_49
  assign pull_resistor_41_node = xor_12_out[1] ? ~xor_12_out[1] : 1'bz;  // Controlled_Inverter controlled_inverter_50
  assign pull_resistor_41_node = xor_12_out[2] ? ~xor_12_out[2] : 1'bz;  // Controlled_Inverter controlled_inverter_51
  assign pull_resistor_41_node = xor_12_out[3] ? ~xor_12_out[3] : 1'bz;  // Controlled_Inverter controlled_inverter_52
  assign pull_resistor_41_node = xor_12_out[4] ? ~xor_12_out[4] : 1'bz;  // Controlled_Inverter controlled_inverter_53
  assign pull_resistor_41_node = xor_12_out[5] ? ~xor_12_out[5] : 1'bz;  // Controlled_Inverter controlled_inverter_54
  assign pull_resistor_41_node = xor_12_out[6] ? ~xor_12_out[6] : 1'bz;  // Controlled_Inverter controlled_inverter_55
  assign pull_resistor_41_node = xor_12_out[7] ? ~xor_12_out[7] : 1'bz;  // Controlled_Inverter controlled_inverter_56
  assign pull_resistor_41_node = xor_12_out[8] ? ~xor_12_out[8] : 1'bz;  // Controlled_Inverter controlled_inverter_57
  assign pull_resistor_41_node = xor_12_out[9] ? ~xor_12_out[9] : 1'bz;  // Controlled_Inverter controlled_inverter_58
  assign pull_resistor_41_node = xor_12_out[10] ? ~xor_12_out[10] : 1'bz;  // Controlled_Inverter controlled_inverter_59
  assign pull_resistor_41_node = xor_12_out[11] ? ~xor_12_out[11] : 1'bz;  // Controlled_Inverter controlled_inverter_60
  assign pull_resistor_41_node = xor_12_out[12] ? ~xor_12_out[12] : 1'bz;  // Controlled_Inverter controlled_inverter_61
  assign pull_resistor_41_node = xor_12_out[13] ? ~xor_12_out[13] : 1'bz;  // Controlled_Inverter controlled_inverter_62
  assign pull_resistor_41_node = xor_12_out[14] ? ~xor_12_out[14] : 1'bz;  // Controlled_Inverter controlled_inverter_63
  assign pull_resistor_41_node = xor_12_out[15] ? ~xor_12_out[15] : 1'bz;  // Controlled_Inverter controlled_inverter_64
  assign controlled_buffer_170_out = pull_resistor_41_node ? pull_resistor_41_node : 1'bz;  // Controlled_Buffer controlled_buffer_175
  Pull_Resistor pull_resistor_43 (.node(pull_resistor_43_node));
  assign pull_resistor_43_node = 1'b0 ? 1'b0 : 1'bz;  // Controlled_Buffer controlled_buffer_176
  assign pull_resistor_43_node = 1'b0 ? 1'b0 : 1'bz;  // Controlled_Buffer controlled_buffer_177
  assign pull_resistor_43_node = 1'b0 ? 1'b0 : 1'bz;  // Controlled_Buffer controlled_buffer_178
  not not_40 (not_40_out, in_1);
  assign controlled_buffer_179_out = not_40_out ? nor_34_out : 8'bz;  // Controlled_Buffer controlled_buffer_179
  assign pull_resistor_43_node = 1'b0 ? 1'b0 : 1'bz;  // Controlled_Buffer controlled_buffer_180
  assign pull_resistor_43_node = 1'b0 ? 1'b0 : 1'bz;  // Controlled_Buffer controlled_buffer_181
  assign pull_resistor_43_node = 1'b1 ? 1'b1 : 1'bz;  // Controlled_Buffer controlled_buffer_182
  assign pull_resistor_43_node = 1'b0 ? 1'b0 : 1'bz;  // Controlled_Buffer controlled_buffer_183
  muxin8tor muxin8tor_5 (.in_2(and_70_out), .in_1(in_1), .out_3(muxin8tor_5_out_3), .out_4(muxin8tor_5_out_4));
  Pull_Resistor pull_resistor_44 (.node(controlled_buffer_179_out));
  assign buffer_52_out = controlled_buffer_179_out;  // Buffer buffer_52, 8 bits wide
  assign buffer_53_out = buffer_52_out;  // Buffer buffer_53, 8 bits wide
  muxin16tor muxin16tor_5 (.in_2(and_70_out), .in_1(in_1), .out_3(muxin16tor_5_out_3), .out_4(muxin16tor_5_out_4));
  demuxin8tor demuxin8tor_5 (.in_2(nor_36_out), .in_3(8'h4), .in_1(in_1), .out_4(demuxin8tor_5_out_4));
  assign {controlled_buffer_1_out_2, controlled_buffer_1_out} = and_58_out ? 8'h4 : 8'bz;  // Controlled_Buffer controlled_buffer_184
  Pull_Resistor pull_resistor_45 (.node({controlled_buffer_1_out_2, controlled_buffer_1_out}));
  assign out_9 = and_58_out ? and_58_out : 1'bz;  // Controlled_Buffer controlled_buffer_185
  assign pull_resistor_43_node = 1'b0 ? 1'b0 : 1'bz;  // Controlled_Buffer controlled_buffer_186
  assign buffer_54_out = buffer_53_out;  // Buffer buffer_54, 8 bits wide
  assign not_41_out = ~buffer_53_out;  // NOT_Gate not_41, 8 bits wide
  assign buffer_55_out = demuxin8tor_5_out_4;  // Buffer buffer_55, 16 bits wide
  assign not_42_out = ~demuxin8tor_5_out_4;  // NOT_Gate not_42, 16 bits wide
  and and_58 (and_58_out, pull_resistor_51_node, and_1_out);
  Pull_Resistor pull_resistor_46 (.node(out_9));
  not not_43 (not_43_out, pull_resistor_43_node);
  assign xor_13_out = controlled_buffer_1_out_2 ^ 4'b0000;  // XOR_Gate xor_13, 4 bits wide
  assign xor_14_out = 4'b0100 ^ controlled_buffer_1_out;  // XOR_Gate xor_14, 4 bits wide
  assign and_59_out = buffer_54_out & muxin8tor_5_out_4;  // AND_Gate and_59, 8 bits wide
  assign and_60_out = muxin8tor_5_out_4 & not_41_out;  // AND_Gate and_60, 8 bits wide
  assign and_61_out = buffer_55_out & muxin16tor_5_out_4;  // AND_Gate and_61, 16 bits wide
  assign and_62_out = muxin16tor_5_out_4 & not_42_out;  // AND_Gate and_62, 16 bits wide
  assign nor_37_out = ~(and_59_out | nor_38_out);  // NOR_Gate nor_37, 8 bits wide
  assign buffer_56_out = nor_38_out;  // Buffer buffer_56, 8 bits wide
  assign nor_38_out = ~(nor_37_out | and_60_out);  // NOR_Gate nor_38, 8 bits wide
  assign not_44_out = ~nor_38_out;  // NOT_Gate not_44, 8 bits wide
  assign buffer_57_out = nor_40_out;  // Buffer buffer_57, 16 bits wide
  assign nor_39_out = ~(and_61_out | nor_40_out);  // NOR_Gate nor_39, 16 bits wide
  assign nor_40_out = ~(nor_39_out | and_62_out);  // NOR_Gate nor_40, 16 bits wide
  assign not_45_out = ~nor_40_out;  // NOT_Gate not_45, 16 bits wide
  assign controlled_buffer_201_out[1] = xor_13_out[1] ? xor_13_out[1] : 1'bz;  // Controlled_Buffer controlled_buffer_187
  assign controlled_buffer_201_out[1] = xor_13_out[2] ? xor_13_out[2] : 1'bz;  // Controlled_Buffer controlled_buffer_188
  assign controlled_buffer_201_out[1] = xor_13_out[3] ? xor_13_out[3] : 1'bz;  // Controlled_Buffer controlled_buffer_189
  assign controlled_buffer_201_out[2] = xor_13_out[2] ? xor_13_out[2] : 1'bz;  // Controlled_Buffer controlled_buffer_190
  assign controlled_buffer_201_out[2] = xor_13_out[3] ? xor_13_out[3] : 1'bz;  // Controlled_Buffer controlled_buffer_191
  assign controlled_buffer_192_out[0] = xor_14_out[0] ? xor_14_out[0] : 1'bz;  // Controlled_Buffer controlled_buffer_192
  assign controlled_buffer_192_out[1] = xor_14_out[1] ? xor_14_out[1] : 1'bz;  // Controlled_Buffer controlled_buffer_193
  assign controlled_buffer_192_out[0] = xor_14_out[1] ? xor_14_out[1] : 1'bz;  // Controlled_Buffer controlled_buffer_194
  assign controlled_buffer_192_out[1] = xor_14_out[2] ? xor_14_out[2] : 1'bz;  // Controlled_Buffer controlled_buffer_195
  assign controlled_buffer_192_out[0] = xor_14_out[2] ? xor_14_out[2] : 1'bz;  // Controlled_Buffer controlled_buffer_196
  assign controlled_buffer_192_out[1] = xor_14_out[3] ? xor_14_out[3] : 1'bz;  // Controlled_Buffer controlled_buffer_197
  assign controlled_buffer_192_out[0] = xor_14_out[3] ? xor_14_out[3] : 1'bz;  // Controlled_Buffer controlled_buffer_198
  assign controlled_buffer_192_out[2] = xor_14_out[2] ? xor_14_out[2] : 1'bz;  // Controlled_Buffer controlled_buffer_199
  Pull_Resistor pull_resistor_47 (.node({xor_14_out[3], controlled_buffer_192_out}));
  assign controlled_buffer_192_out[2] = xor_14_out[3] ? xor_14_out[3] : 1'bz;  // Controlled_Buffer controlled_buffer_200
  assign and_63_out = buffer_56_out & muxin8tor_5_out_3;  // AND_Gate and_63, 8 bits wide
  assign and_64_out = muxin8tor_5_out_3 & not_44_out;  // AND_Gate and_64, 8 bits wide
  assign and_65_out = buffer_57_out & muxin16tor_5_out_3;  // AND_Gate and_65, 16 bits wide
  assign and_66_out = muxin16tor_5_out_3 & not_45_out;  // AND_Gate and_66, 16 bits wide
  assign controlled_buffer_201_out[0] = xor_13_out[0] ? xor_13_out[0] : 1'bz;  // Controlled_Buffer controlled_buffer_201
  assign controlled_buffer_201_out[0] = xor_13_out[1] ? xor_13_out[1] : 1'bz;  // Controlled_Buffer controlled_buffer_202
  assign controlled_buffer_201_out[0] = xor_13_out[2] ? xor_13_out[2] : 1'bz;  // Controlled_Buffer controlled_buffer_203
  Pull_Resistor pull_resistor_48 (.node({xor_13_out[3], controlled_buffer_201_out}));
  assign controlled_buffer_201_out[0] = xor_13_out[3] ? xor_13_out[3] : 1'bz;  // Controlled_Buffer controlled_buffer_204
  not not_46 (not_46_out, controlled_buffer_201_out[0]);
  assign buffer_58_out = {xor_14_out[3], controlled_buffer_192_out};  // Buffer buffer_58, 4 bits wide
  assign nor_41_out = ~(and_63_out | nor_42_out);  // NOR_Gate nor_41, 8 bits wide
  assign nor_42_out = ~(nor_41_out | and_64_out);  // NOR_Gate nor_42, 8 bits wide
  assign nor_43_out = ~(and_65_out | nor_44_out);  // NOR_Gate nor_43, 16 bits wide
  assign nor_44_out = ~(nor_43_out | and_66_out);  // NOR_Gate nor_44, 16 bits wide
  assign and_67_out = buffer_59_out & not_47_out;  // AND_Gate and_67, 4 bits wide
  assign buffer_59_out = {xor_13_out[3], controlled_buffer_201_out};  // Buffer buffer_59, 4 bits wide
  Pull_Resistor pull_resistor_49 (.node(pull_resistor_49_node));
  assign not_47_out = ~{1'b0, xor_13_out[3], controlled_buffer_201_out[2:1]};  // NOT_Gate not_47, 4 bits wide
  assign pull_resistor_49_node = and_67_out[3] ? controlled_buffer_1_out_2[3] : 1'bz;  // Controlled_Buffer controlled_buffer_205
  assign and_68_out = buffer_58_out & not_48_out;  // AND_Gate and_68, 4 bits wide
  Pull_Resistor pull_resistor_50 (.node(pull_resistor_50_node));
  assign pull_resistor_50_node = and_68_out[3] ? controlled_buffer_1_out[3] : 1'bz;  // Controlled_Buffer controlled_buffer_206
  assign pull_resistor_50_node = and_68_out[2] ? controlled_buffer_1_out[2] : 1'bz;  // Controlled_Buffer controlled_buffer_207
  assign pull_resistor_50_node = and_68_out[1] ? controlled_buffer_1_out[1] : 1'bz;  // Controlled_Buffer controlled_buffer_208
  assign not_48_out = ~{1'b0, xor_14_out[3], controlled_buffer_192_out[2:1]};  // NOT_Gate not_48, 4 bits wide
  assign xor_15_out = nor_44_out ^ buffer_2_out;  // XOR_Gate xor_15, 16 bits wide
  Pull_Resistor #(.pull(1)) pull_resistor_51 (.node(pull_resistor_51_node));
  assign pull_resistor_49_node = and_67_out[2] ? controlled_buffer_1_out_2[2] : 1'bz;  // Controlled_Buffer controlled_buffer_209
  assign pull_resistor_49_node = and_67_out[1] ? controlled_buffer_1_out_2[1] : 1'bz;  // Controlled_Buffer controlled_buffer_210
  assign pull_resistor_49_node = and_67_out[0] ? controlled_buffer_1_out_2[0] : 1'bz;  // Controlled_Buffer controlled_buffer_211
  assign controlled_buffer_212_out = pull_resistor_49_node ? pull_resistor_49_node : 1'bz;  // Controlled_Buffer controlled_buffer_212
  and and_69 (and_69_out, not_46_out, pull_resistor_50_node);
  assign controlled_buffer_212_out = and_69_out ? and_69_out : 1'bz;  // Controlled_Buffer controlled_buffer_213
  assign controlled_buffer_212_out = not_43_out ? not_43_out : 1'bz;  // Controlled_Buffer controlled_buffer_214
  Pull_Resistor pull_resistor_52 (.node(controlled_buffer_212_out));
  assign pull_resistor_50_node = and_68_out[0] ? controlled_buffer_1_out[0] : 1'bz;  // Controlled_Buffer controlled_buffer_215
  and and_70 (and_70_out, controlled_buffer_212_out, out_9);
  assign out_10 = and_58_out ? nor_42_out : 8'bz;  // Controlled_Buffer controlled_buffer_216
  assign pull_resistor_51_node = xor_15_out[0] ? ~xor_15_out[0] : 1'bz;  // Controlled_Inverter controlled_inverter_65
  assign pull_resistor_51_node = xor_15_out[1] ? ~xor_15_out[1] : 1'bz;  // Controlled_Inverter controlled_inverter_66
  assign pull_resistor_51_node = xor_15_out[2] ? ~xor_15_out[2] : 1'bz;  // Controlled_Inverter controlled_inverter_67
  assign pull_resistor_51_node = xor_15_out[3] ? ~xor_15_out[3] : 1'bz;  // Controlled_Inverter controlled_inverter_68
  assign pull_resistor_51_node = xor_15_out[4] ? ~xor_15_out[4] : 1'bz;  // Controlled_Inverter controlled_inverter_69
  assign pull_resistor_51_node = xor_15_out[5] ? ~xor_15_out[5] : 1'bz;  // Controlled_Inverter controlled_inverter_70
  assign pull_resistor_51_node = xor_15_out[6] ? ~xor_15_out[6] : 1'bz;  // Controlled_Inverter controlled_inverter_71
  assign pull_resistor_51_node = xor_15_out[7] ? ~xor_15_out[7] : 1'bz;  // Controlled_Inverter controlled_inverter_72
  assign pull_resistor_51_node = xor_15_out[8] ? ~xor_15_out[8] : 1'bz;  // Controlled_Inverter controlled_inverter_73
  assign pull_resistor_51_node = xor_15_out[9] ? ~xor_15_out[9] : 1'bz;  // Controlled_Inverter controlled_inverter_74
  assign pull_resistor_51_node = xor_15_out[10] ? ~xor_15_out[10] : 1'bz;  // Controlled_Inverter controlled_inverter_75
  assign pull_resistor_51_node = xor_15_out[11] ? ~xor_15_out[11] : 1'bz;  // Controlled_Inverter controlled_inverter_76
  assign pull_resistor_51_node = xor_15_out[12] ? ~xor_15_out[12] : 1'bz;  // Controlled_Inverter controlled_inverter_77
  assign pull_resistor_51_node = xor_15_out[13] ? ~xor_15_out[13] : 1'bz;  // Controlled_Inverter controlled_inverter_78
  assign pull_resistor_51_node = xor_15_out[14] ? ~xor_15_out[14] : 1'bz;  // Controlled_Inverter controlled_inverter_79
  assign pull_resistor_51_node = xor_15_out[15] ? ~xor_15_out[15] : 1'bz;  // Controlled_Inverter controlled_inverter_80
  assign controlled_buffer_212_out = pull_resistor_51_node ? pull_resistor_51_node : 1'bz;  // Controlled_Buffer controlled_buffer_217
  assign pull_resistor_1_node = and_58_out ? nor_44_out : 16'bz;  // Controlled_Buffer controlled_buffer_218
  Pull_Resistor pull_resistor_53 (.node(pull_resistor_53_node));
  assign pull_resistor_53_node = 1'b0 ? 1'b0 : 1'bz;  // Controlled_Buffer controlled_buffer_219
  assign pull_resistor_53_node = 1'b0 ? 1'b0 : 1'bz;  // Controlled_Buffer controlled_buffer_220
  not not_49 (not_49_out, in_1);
  assign pull_resistor_53_node = 1'b0 ? 1'b0 : 1'bz;  // Controlled_Buffer controlled_buffer_221
  assign pull_resistor_53_node = 1'b0 ? 1'b0 : 1'bz;  // Controlled_Buffer controlled_buffer_222
  assign pull_resistor_53_node = 1'b0 ? 1'b0 : 1'bz;  // Controlled_Buffer controlled_buffer_223
  assign pull_resistor_53_node = 1'b1 ? 1'b1 : 1'bz;  // Controlled_Buffer controlled_buffer_224
  muxin8tor muxin8tor_6 (.in_2(and_83_out), .in_1(in_1), .out_3(muxin8tor_6_out_3), .out_4(muxin8tor_6_out_4));
  Pull_Resistor pull_resistor_54 (.node(pull_resistor_54_node));
  assign pull_resistor_54_node = not_49_out ? nor_42_out : 8'bz;  // Controlled_Buffer controlled_buffer_225
  assign buffer_60_out = pull_resistor_54_node;  // Buffer buffer_60, 8 bits wide
  assign buffer_61_out = buffer_60_out;  // Buffer buffer_61, 8 bits wide
  muxin16tor muxin16tor_6 (.in_2(and_83_out), .in_1(in_1), .out_3(muxin16tor_6_out_3), .out_4(muxin16tor_6_out_4));
  demuxin8tor demuxin8tor_6 (.in_2(nor_44_out), .in_3(8'h5), .in_1(in_1), .out_4(demuxin8tor_6_out_4));
  assign {controlled_buffer_1_out_2, controlled_buffer_1_out} = and_75_out ? 8'h5 : 8'bz;  // Controlled_Buffer controlled_buffer_226
  Pull_Resistor pull_resistor_55 (.node({controlled_buffer_1_out_2, controlled_buffer_1_out}));
  assign pull_resistor_53_node = 1'b0 ? 1'b0 : 1'bz;  // Controlled_Buffer controlled_buffer_227
  assign pull_resistor_53_node = 1'b1 ? 1'b1 : 1'bz;  // Controlled_Buffer controlled_buffer_228
  assign buffer_62_out = buffer_61_out;  // Buffer buffer_62, 8 bits wide
  assign not_50_out = ~buffer_61_out;  // NOT_Gate not_50, 8 bits wide
  assign buffer_63_out = demuxin8tor_6_out_4;  // Buffer buffer_63, 16 bits wide
  assign not_51_out = ~demuxin8tor_6_out_4;  // NOT_Gate not_51, 16 bits wide
  Pull_Resistor pull_resistor_56 (.node(out_9));
  assign out_9 = and_75_out ? and_75_out : 1'bz;  // Controlled_Buffer controlled_buffer_229
  assign xor_16_out = controlled_buffer_1_out_2 ^ 4'b0000;  // XOR_Gate xor_16, 4 bits wide
  assign xor_17_out = 4'b0101 ^ controlled_buffer_1_out;  // XOR_Gate xor_17, 4 bits wide
  assign and_71_out = buffer_62_out & muxin8tor_6_out_4;  // AND_Gate and_71, 8 bits wide
  assign and_72_out = muxin8tor_6_out_4 & not_50_out;  // AND_Gate and_72, 8 bits wide
  assign and_73_out = buffer_63_out & muxin16tor_6_out_4;  // AND_Gate and_73, 16 bits wide
  assign and_74_out = muxin16tor_6_out_4 & not_51_out;  // AND_Gate and_74, 16 bits wide
  and and_75 (and_75_out, pull_resistor_62_node, and_1_out);
  not not_52 (not_52_out, pull_resistor_53_node);
  assign nor_45_out = ~(and_71_out | nor_46_out);  // NOR_Gate nor_45, 8 bits wide
  assign buffer_64_out = nor_46_out;  // Buffer buffer_64, 8 bits wide
  assign nor_46_out = ~(nor_45_out | and_72_out);  // NOR_Gate nor_46, 8 bits wide
  assign buffer_65_out = nor_48_out;  // Buffer buffer_65, 16 bits wide
  assign nor_47_out = ~(and_73_out | nor_48_out);  // NOR_Gate nor_47, 16 bits wide
  assign nor_48_out = ~(nor_47_out | and_74_out);  // NOR_Gate nor_48, 16 bits wide
  assign controlled_buffer_240_out[1] = xor_16_out[1] ? xor_16_out[1] : 1'bz;  // Controlled_Buffer controlled_buffer_230
  assign controlled_buffer_240_out[1] = xor_16_out[2] ? xor_16_out[2] : 1'bz;  // Controlled_Buffer controlled_buffer_231
  assign controlled_buffer_240_out[1] = xor_16_out[3] ? xor_16_out[3] : 1'bz;  // Controlled_Buffer controlled_buffer_232
  assign controlled_buffer_240_out[2] = xor_16_out[2] ? xor_16_out[2] : 1'bz;  // Controlled_Buffer controlled_buffer_233
  assign controlled_buffer_240_out[2] = xor_16_out[3] ? xor_16_out[3] : 1'bz;  // Controlled_Buffer controlled_buffer_234
  assign controlled_buffer_244_out[1] = xor_17_out[1] ? xor_17_out[1] : 1'bz;  // Controlled_Buffer controlled_buffer_235
  assign controlled_buffer_244_out[1] = xor_17_out[2] ? xor_17_out[2] : 1'bz;  // Controlled_Buffer controlled_buffer_236
  assign controlled_buffer_244_out[1] = xor_17_out[3] ? xor_17_out[3] : 1'bz;  // Controlled_Buffer controlled_buffer_237
  assign controlled_buffer_244_out[2] = xor_17_out[2] ? xor_17_out[2] : 1'bz;  // Controlled_Buffer controlled_buffer_238
  assign controlled_buffer_244_out[2] = xor_17_out[3] ? xor_17_out[3] : 1'bz;  // Controlled_Buffer controlled_buffer_239
  assign and_76_out = buffer_64_out & muxin8tor_6_out_3;  // AND_Gate and_76, 8 bits wide
  assign and_77_out = muxin8tor_6_out_3 & not_53_out;  // AND_Gate and_77, 8 bits wide
  assign not_53_out = ~nor_46_out;  // NOT_Gate not_53, 8 bits wide
  assign and_78_out = buffer_65_out & muxin16tor_6_out_3;  // AND_Gate and_78, 16 bits wide
  assign and_79_out = muxin16tor_6_out_3 & not_54_out;  // AND_Gate and_79, 16 bits wide
  assign not_54_out = ~nor_48_out;  // NOT_Gate not_54, 16 bits wide
  assign controlled_buffer_240_out[0] = xor_16_out[0] ? xor_16_out[0] : 1'bz;  // Controlled_Buffer controlled_buffer_240
  assign controlled_buffer_240_out[0] = xor_16_out[1] ? xor_16_out[1] : 1'bz;  // Controlled_Buffer controlled_buffer_241
  assign controlled_buffer_240_out[0] = xor_16_out[2] ? xor_16_out[2] : 1'bz;  // Controlled_Buffer controlled_buffer_242
  assign controlled_buffer_240_out[0] = xor_16_out[3] ? xor_16_out[3] : 1'bz;  // Controlled_Buffer controlled_buffer_243
  not not_55 (not_55_out, controlled_buffer_240_out[0]);
  assign controlled_buffer_244_out[0] = xor_17_out[0] ? xor_17_out[0] : 1'bz;  // Controlled_Buffer controlled_buffer_244
  assign controlled_buffer_244_out[0] = xor_17_out[1] ? xor_17_out[1] : 1'bz;  // Controlled_Buffer controlled_buffer_245
  assign controlled_buffer_244_out[0] = xor_17_out[2] ? xor_17_out[2] : 1'bz;  // Controlled_Buffer controlled_buffer_246
  assign controlled_buffer_244_out[0] = xor_17_out[3] ? xor_17_out[3] : 1'bz;  // Controlled_Buffer controlled_buffer_247
  Pull_Resistor pull_resistor_57 (.node({xor_17_out[3], controlled_buffer_244_out}));
  assign nor_49_out = ~(and_76_out | nor_50_out);  // NOR_Gate nor_49, 8 bits wide
  assign nor_50_out = ~(nor_49_out | and_77_out);  // NOR_Gate nor_50, 8 bits wide
  assign nor_51_out = ~(and_78_out | nor_52_out);  // NOR_Gate nor_51, 16 bits wide
  assign nor_52_out = ~(nor_51_out | and_79_out);  // NOR_Gate nor_52, 16 bits wide
  assign buffer_66_out = {xor_16_out[3], controlled_buffer_240_out};  // Buffer buffer_66, 4 bits wide
  Pull_Resistor pull_resistor_58 (.node({xor_16_out[3], controlled_buffer_240_out}));
  Pull_Resistor pull_resistor_59 (.node(pull_resistor_59_node));
  assign not_56_out = ~{1'b0, xor_16_out[3], controlled_buffer_240_out[2:1]};  // NOT_Gate not_56, 4 bits wide
  assign and_80_out = buffer_67_out & not_57_out;  // AND_Gate and_80, 4 bits wide
  assign buffer_67_out = {xor_17_out[3], controlled_buffer_244_out};  // Buffer buffer_67, 4 bits wide
  Pull_Resistor pull_resistor_60 (.node(pull_resistor_60_node));
  assign pull_resistor_60_node = and_80_out[3] ? controlled_buffer_1_out[3] : 1'bz;  // Controlled_Buffer controlled_buffer_248
  assign pull_resistor_60_node = and_80_out[2] ? controlled_buffer_1_out[2] : 1'bz;  // Controlled_Buffer controlled_buffer_249
  assign pull_resistor_60_node = and_80_out[1] ? controlled_buffer_1_out[1] : 1'bz;  // Controlled_Buffer controlled_buffer_250
  assign not_57_out = ~{1'b0, xor_17_out[3], controlled_buffer_244_out[2:1]};  // NOT_Gate not_57, 4 bits wide
  assign xor_18_out = nor_52_out ^ buffer_2_out;  // XOR_Gate xor_18, 16 bits wide
  assign and_81_out = buffer_66_out & not_56_out;  // AND_Gate and_81, 4 bits wide
  assign pull_resistor_59_node = and_81_out[3] ? controlled_buffer_1_out_2[3] : 1'bz;  // Controlled_Buffer controlled_buffer_251
  assign pull_resistor_59_node = and_81_out[2] ? controlled_buffer_1_out_2[2] : 1'bz;  // Controlled_Buffer controlled_buffer_252
  assign pull_resistor_59_node = and_81_out[1] ? controlled_buffer_1_out_2[1] : 1'bz;  // Controlled_Buffer controlled_buffer_253
  assign pull_resistor_59_node = and_81_out[0] ? controlled_buffer_1_out_2[0] : 1'bz;  // Controlled_Buffer controlled_buffer_254
  assign controlled_buffer_255_out = pull_resistor_59_node ? pull_resistor_59_node : 1'bz;  // Controlled_Buffer controlled_buffer_255
  and and_82 (and_82_out, not_55_out, pull_resistor_60_node);
  assign controlled_buffer_255_out = and_82_out ? and_82_out : 1'bz;  // Controlled_Buffer controlled_buffer_256
  Pull_Resistor pull_resistor_61 (.node(controlled_buffer_255_out));
  assign pull_resistor_60_node = and_80_out[0] ? controlled_buffer_1_out[0] : 1'bz;  // Controlled_Buffer controlled_buffer_257
  Pull_Resistor #(.pull(1)) pull_resistor_62 (.node(pull_resistor_62_node));
  and and_83 (and_83_out, controlled_buffer_255_out, out_9);
  assign controlled_buffer_255_out = not_52_out ? not_52_out : 1'bz;  // Controlled_Buffer controlled_buffer_258
  assign out_10 = and_75_out ? nor_50_out : 8'bz;  // Controlled_Buffer controlled_buffer_259
  assign pull_resistor_62_node = xor_18_out[0] ? ~xor_18_out[0] : 1'bz;  // Controlled_Inverter controlled_inverter_81
  assign pull_resistor_62_node = xor_18_out[1] ? ~xor_18_out[1] : 1'bz;  // Controlled_Inverter controlled_inverter_82
  assign pull_resistor_62_node = xor_18_out[2] ? ~xor_18_out[2] : 1'bz;  // Controlled_Inverter controlled_inverter_83
  assign pull_resistor_62_node = xor_18_out[3] ? ~xor_18_out[3] : 1'bz;  // Controlled_Inverter controlled_inverter_84
  assign pull_resistor_62_node = xor_18_out[4] ? ~xor_18_out[4] : 1'bz;  // Controlled_Inverter controlled_inverter_85
  assign pull_resistor_62_node = xor_18_out[5] ? ~xor_18_out[5] : 1'bz;  // Controlled_Inverter controlled_inverter_86
  assign pull_resistor_62_node = xor_18_out[6] ? ~xor_18_out[6] : 1'bz;  // Controlled_Inverter controlled_inverter_87
  assign pull_resistor_62_node = xor_18_out[7] ? ~xor_18_out[7] : 1'bz;  // Controlled_Inverter controlled_inverter_88
  assign pull_resistor_62_node = xor_18_out[8] ? ~xor_18_out[8] : 1'bz;  // Controlled_Inverter controlled_inverter_89
  assign pull_resistor_62_node = xor_18_out[9] ? ~xor_18_out[9] : 1'bz;  // Controlled_Inverter controlled_inverter_90
  assign pull_resistor_62_node = xor_18_out[10] ? ~xor_18_out[10] : 1'bz;  // Controlled_Inverter controlled_inverter_91
  assign pull_resistor_62_node = xor_18_out[11] ? ~xor_18_out[11] : 1'bz;  // Controlled_Inverter controlled_inverter_92
  assign pull_resistor_62_node = xor_18_out[12] ? ~xor_18_out[12] : 1'bz;  // Controlled_Inverter controlled_inverter_93
  assign pull_resistor_62_node = xor_18_out[13] ? ~xor_18_out[13] : 1'bz;  // Controlled_Inverter controlled_inverter_94
  assign pull_resistor_62_node = xor_18_out[14] ? ~xor_18_out[14] : 1'bz;  // Controlled_Inverter controlled_inverter_95
  assign pull_resistor_62_node = xor_18_out[15] ? ~xor_18_out[15] : 1'bz;  // Controlled_Inverter controlled_inverter_96
  assign controlled_buffer_255_out = pull_resistor_62_node ? pull_resistor_62_node : 1'bz;  // Controlled_Buffer controlled_buffer_260
  assign pull_resistor_1_node = and_75_out ? nor_52_out : 16'bz;  // Controlled_Buffer controlled_buffer_261
  Pull_Resistor pull_resistor_63 (.node(pull_resistor_63_node));
  assign pull_resistor_63_node = 1'b0 ? 1'b0 : 1'bz;  // Controlled_Buffer controlled_buffer_262
  assign pull_resistor_63_node = 1'b0 ? 1'b0 : 1'bz;  // Controlled_Buffer controlled_buffer_263
  assign pull_resistor_63_node = 1'b0 ? 1'b0 : 1'bz;  // Controlled_Buffer controlled_buffer_264
  assign pull_resistor_63_node = 1'b0 ? 1'b0 : 1'bz;  // Controlled_Buffer controlled_buffer_265
  assign pull_resistor_63_node = 1'b0 ? 1'b0 : 1'bz;  // Controlled_Buffer controlled_buffer_266
  assign pull_resistor_63_node = 1'b1 ? 1'b1 : 1'bz;  // Controlled_Buffer controlled_buffer_267
  muxin8tor muxin8tor_7 (.in_2(and_96_out), .in_1(in_1), .out_3(muxin8tor_7_out_3), .out_4(muxin8tor_7_out_4));
  not not_58 (not_58_out, in_1);
  Pull_Resistor pull_resistor_64 (.node(pull_resistor_64_node));
  assign pull_resistor_64_node = not_58_out ? nor_50_out : 8'bz;  // Controlled_Buffer controlled_buffer_268
  assign buffer_68_out = pull_resistor_64_node;  // Buffer buffer_68, 8 bits wide
  muxin16tor muxin16tor_7 (.in_2(and_96_out), .in_1(in_1), .out_3(muxin16tor_7_out_3), .out_4(muxin16tor_7_out_4));
  demuxin8tor demuxin8tor_7 (.in_2(nor_52_out), .in_3(8'h6), .in_1(in_1), .out_4(demuxin8tor_7_out_4));
  Pull_Resistor pull_resistor_65 (.node({controlled_buffer_1_out_2, controlled_buffer_1_out}));
  assign pull_resistor_63_node = 1'b1 ? 1'b1 : 1'bz;  // Controlled_Buffer controlled_buffer_269
  assign pull_resistor_63_node = 1'b0 ? 1'b0 : 1'bz;  // Controlled_Buffer controlled_buffer_270
  assign buffer_69_out = buffer_68_out;  // Buffer buffer_69, 8 bits wide
  assign buffer_70_out = buffer_69_out;  // Buffer buffer_70, 8 bits wide
  assign not_59_out = ~buffer_69_out;  // NOT_Gate not_59, 8 bits wide
  assign buffer_71_out = demuxin8tor_7_out_4;  // Buffer buffer_71, 16 bits wide
  assign {controlled_buffer_1_out_2, controlled_buffer_1_out} = and_88_out ? 8'h6 : 8'bz;  // Controlled_Buffer controlled_buffer_271
  Pull_Resistor pull_resistor_66 (.node(out_9));
  assign out_9 = and_88_out ? and_88_out : 1'bz;  // Controlled_Buffer controlled_buffer_272
  assign xor_19_out = controlled_buffer_1_out_2 ^ 4'b0000;  // XOR_Gate xor_19, 4 bits wide
  assign xor_20_out = 4'b0110 ^ controlled_buffer_1_out;  // XOR_Gate xor_20, 4 bits wide
  assign and_84_out = buffer_70_out & muxin8tor_7_out_4;  // AND_Gate and_84, 8 bits wide
  assign and_85_out = muxin8tor_7_out_4 & not_59_out;  // AND_Gate and_85, 8 bits wide
  assign and_86_out = buffer_71_out & muxin16tor_7_out_4;  // AND_Gate and_86, 16 bits wide
  assign and_87_out = muxin16tor_7_out_4 & not_60_out;  // AND_Gate and_87, 16 bits wide
  assign not_60_out = ~demuxin8tor_7_out_4;  // NOT_Gate not_60, 16 bits wide
  and and_88 (and_88_out, pull_resistor_71_node, and_1_out);
  not not_61 (not_61_out, pull_resistor_63_node);
  assign nor_53_out = ~(and_84_out | nor_54_out);  // NOR_Gate nor_53, 8 bits wide
  assign nor_54_out = ~(nor_53_out | and_85_out);  // NOR_Gate nor_54, 8 bits wide
  assign nor_55_out = ~(and_86_out | nor_56_out);  // NOR_Gate nor_55, 16 bits wide
  assign nor_56_out = ~(nor_55_out | and_87_out);  // NOR_Gate nor_56, 16 bits wide
  assign controlled_buffer_287_out[1] = xor_20_out[1] ? xor_20_out[1] : 1'bz;  // Controlled_Buffer controlled_buffer_273
  assign controlled_buffer_287_out[1] = xor_20_out[2] ? xor_20_out[2] : 1'bz;  // Controlled_Buffer controlled_buffer_274
  assign controlled_buffer_287_out[1] = xor_20_out[3] ? xor_20_out[3] : 1'bz;  // Controlled_Buffer controlled_buffer_275
  assign controlled_buffer_287_out[2] = xor_20_out[2] ? xor_20_out[2] : 1'bz;  // Controlled_Buffer controlled_buffer_276
  assign controlled_buffer_287_out[2] = xor_20_out[3] ? xor_20_out[3] : 1'bz;  // Controlled_Buffer controlled_buffer_277
  assign and_89_out = buffer_72_out & muxin8tor_7_out_3;  // AND_Gate and_89, 8 bits wide
  assign buffer_72_out = nor_54_out;  // Buffer buffer_72, 8 bits wide
  assign and_90_out = muxin8tor_7_out_3 & not_62_out;  // AND_Gate and_90, 8 bits wide
  assign not_62_out = ~nor_54_out;  // NOT_Gate not_62, 8 bits wide
  assign buffer_73_out = nor_56_out;  // Buffer buffer_73, 16 bits wide
  assign and_91_out = buffer_73_out & muxin16tor_7_out_3;  // AND_Gate and_91, 16 bits wide
  assign and_92_out = muxin16tor_7_out_3 & not_63_out;  // AND_Gate and_92, 16 bits wide
  assign not_63_out = ~nor_56_out;  // NOT_Gate not_63, 16 bits wide
  assign controlled_buffer_278_out[0] = xor_19_out[0] ? xor_19_out[0] : 1'bz;  // Controlled_Buffer controlled_buffer_278
  assign controlled_buffer_278_out[1] = xor_19_out[1] ? xor_19_out[1] : 1'bz;  // Controlled_Buffer controlled_buffer_279
  assign controlled_buffer_278_out[0] = xor_19_out[1] ? xor_19_out[1] : 1'bz;  // Controlled_Buffer controlled_buffer_280
  assign controlled_buffer_278_out[1] = xor_19_out[2] ? xor_19_out[2] : 1'bz;  // Controlled_Buffer controlled_buffer_281
  assign controlled_buffer_278_out[0] = xor_19_out[2] ? xor_19_out[2] : 1'bz;  // Controlled_Buffer controlled_buffer_282
  assign controlled_buffer_278_out[1] = xor_19_out[3] ? xor_19_out[3] : 1'bz;  // Controlled_Buffer controlled_buffer_283
  assign controlled_buffer_278_out[0] = xor_19_out[3] ? xor_19_out[3] : 1'bz;  // Controlled_Buffer controlled_buffer_284
  assign controlled_buffer_278_out[2] = xor_19_out[2] ? xor_19_out[2] : 1'bz;  // Controlled_Buffer controlled_buffer_285
  assign controlled_buffer_278_out[2] = xor_19_out[3] ? xor_19_out[3] : 1'bz;  // Controlled_Buffer controlled_buffer_286
  not not_64 (not_64_out, controlled_buffer_278_out[0]);
  assign controlled_buffer_287_out[0] = xor_20_out[0] ? xor_20_out[0] : 1'bz;  // Controlled_Buffer controlled_buffer_287
  assign controlled_buffer_287_out[0] = xor_20_out[1] ? xor_20_out[1] : 1'bz;  // Controlled_Buffer controlled_buffer_288
  assign controlled_buffer_287_out[0] = xor_20_out[2] ? xor_20_out[2] : 1'bz;  // Controlled_Buffer controlled_buffer_289
  assign controlled_buffer_287_out[0] = xor_20_out[3] ? xor_20_out[3] : 1'bz;  // Controlled_Buffer controlled_buffer_290
  Pull_Resistor pull_resistor_67 (.node({xor_20_out[3], controlled_buffer_287_out}));
  assign nor_57_out = ~(and_89_out | nor_58_out);  // NOR_Gate nor_57, 8 bits wide
  assign nor_58_out = ~(nor_57_out | and_90_out);  // NOR_Gate nor_58, 8 bits wide
  assign nor_59_out = ~(and_91_out | nor_60_out);  // NOR_Gate nor_59, 16 bits wide
  assign nor_60_out = ~(nor_59_out | and_92_out);  // NOR_Gate nor_60, 16 bits wide
  assign buffer_74_out = {xor_19_out[3], controlled_buffer_278_out};  // Buffer buffer_74, 4 bits wide
  Pull_Resistor pull_resistor_68 (.node({xor_19_out[3], controlled_buffer_278_out}));
  Pull_Resistor pull_resistor_69 (.node(pull_resistor_69_node));
  assign not_65_out = ~{1'b0, xor_19_out[3], controlled_buffer_278_out[2:1]};  // NOT_Gate not_65, 4 bits wide
  assign and_93_out = buffer_75_out & not_66_out;  // AND_Gate and_93, 4 bits wide
  assign buffer_75_out = {xor_20_out[3], controlled_buffer_287_out};  // Buffer buffer_75, 4 bits wide
  Pull_Resistor pull_resistor_70 (.node(pull_resistor_70_node));
  assign pull_resistor_70_node = and_93_out[3] ? controlled_buffer_1_out[3] : 1'bz;  // Controlled_Buffer controlled_buffer_291
  assign pull_resistor_70_node = and_93_out[2] ? controlled_buffer_1_out[2] : 1'bz;  // Controlled_Buffer controlled_buffer_292
  assign not_66_out = ~{1'b0, xor_20_out[3], controlled_buffer_287_out[2:1]};  // NOT_Gate not_66, 4 bits wide
  assign xor_21_out = nor_60_out ^ buffer_2_out;  // XOR_Gate xor_21, 16 bits wide
  assign and_94_out = buffer_74_out & not_65_out;  // AND_Gate and_94, 4 bits wide
  assign pull_resistor_69_node = and_94_out[3] ? controlled_buffer_1_out_2[3] : 1'bz;  // Controlled_Buffer controlled_buffer_293
  assign pull_resistor_69_node = and_94_out[2] ? controlled_buffer_1_out_2[2] : 1'bz;  // Controlled_Buffer controlled_buffer_294
  assign pull_resistor_69_node = and_94_out[1] ? controlled_buffer_1_out_2[1] : 1'bz;  // Controlled_Buffer controlled_buffer_295
  assign pull_resistor_69_node = and_94_out[0] ? controlled_buffer_1_out_2[0] : 1'bz;  // Controlled_Buffer controlled_buffer_296
  assign controlled_buffer_297_out = pull_resistor_69_node ? pull_resistor_69_node : 1'bz;  // Controlled_Buffer controlled_buffer_297
  and and_95 (and_95_out, not_64_out, pull_resistor_70_node);
  assign controlled_buffer_297_out = and_95_out ? and_95_out : 1'bz;  // Controlled_Buffer controlled_buffer_298
  assign pull_resistor_70_node = and_93_out[1] ? controlled_buffer_1_out[1] : 1'bz;  // Controlled_Buffer controlled_buffer_299
  assign pull_resistor_70_node = and_93_out[0] ? controlled_buffer_1_out[0] : 1'bz;  // Controlled_Buffer controlled_buffer_300
  Pull_Resistor #(.pull(1)) pull_resistor_71 (.node(pull_resistor_71_node));
  and and_96 (and_96_out, controlled_buffer_297_out, out_9);
  assign controlled_buffer_297_out = not_61_out ? not_61_out : 1'bz;  // Controlled_Buffer controlled_buffer_301
  Pull_Resistor pull_resistor_72 (.node(controlled_buffer_297_out));
  assign pull_resistor_71_node = xor_21_out[0] ? ~xor_21_out[0] : 1'bz;  // Controlled_Inverter controlled_inverter_97
  assign pull_resistor_71_node = xor_21_out[1] ? ~xor_21_out[1] : 1'bz;  // Controlled_Inverter controlled_inverter_98
  assign pull_resistor_71_node = xor_21_out[2] ? ~xor_21_out[2] : 1'bz;  // Controlled_Inverter controlled_inverter_99
  assign pull_resistor_71_node = xor_21_out[3] ? ~xor_21_out[3] : 1'bz;  // Controlled_Inverter controlled_inverter_100
  assign pull_resistor_71_node = xor_21_out[4] ? ~xor_21_out[4] : 1'bz;  // Controlled_Inverter controlled_inverter_101
  assign pull_resistor_71_node = xor_21_out[5] ? ~xor_21_out[5] : 1'bz;  // Controlled_Inverter controlled_inverter_102
  assign pull_resistor_71_node = xor_21_out[6] ? ~xor_21_out[6] : 1'bz;  // Controlled_Inverter controlled_inverter_103
  assign pull_resistor_71_node = xor_21_out[7] ? ~xor_21_out[7] : 1'bz;  // Controlled_Inverter controlled_inverter_104
  assign pull_resistor_71_node = xor_21_out[8] ? ~xor_21_out[8] : 1'bz;  // Controlled_Inverter controlled_inverter_105
  assign pull_resistor_71_node = xor_21_out[9] ? ~xor_21_out[9] : 1'bz;  // Controlled_Inverter controlled_inverter_106
  assign pull_resistor_71_node = xor_21_out[10] ? ~xor_21_out[10] : 1'bz;  // Controlled_Inverter controlled_inverter_107
  assign pull_resistor_71_node = xor_21_out[11] ? ~xor_21_out[11] : 1'bz;  // Controlled_Inverter controlled_inverter_108
  assign pull_resistor_71_node = xor_21_out[12] ? ~xor_21_out[12] : 1'bz;  // Controlled_Inverter controlled_inverter_109
  assign pull_resistor_71_node = xor_21_out[13] ? ~xor_21_out[13] : 1'bz;  // Controlled_Inverter controlled_inverter_110
  assign pull_resistor_71_node = xor_21_out[14] ? ~xor_21_out[14] : 1'bz;  // Controlled_Inverter controlled_inverter_111
  assign pull_resistor_71_node = xor_21_out[15] ? ~xor_21_out[15] : 1'bz;  // Controlled_Inverter controlled_inverter_112
  assign controlled_buffer_297_out = pull_resistor_71_node ? pull_resistor_71_node : 1'bz;  // Controlled_Buffer controlled_buffer_302
  assign out_10 = and_88_out ? nor_58_out : 8'bz;  // Controlled_Buffer controlled_buffer_303
  assign pull_resistor_1_node = and_88_out ? nor_60_out : 16'bz;  // Controlled_Buffer controlled_buffer_304
  Pull_Resistor pull_resistor_73 (.node(pull_resistor_73_node));
  assign pull_resistor_73_node = 1'b0 ? 1'b0 : 1'bz;  // Controlled_Buffer controlled_buffer_305
  assign pull_resistor_73_node = 1'b0 ? 1'b0 : 1'bz;  // Controlled_Buffer controlled_buffer_306
  assign pull_resistor_73_node = 1'b0 ? 1'b0 : 1'bz;  // Controlled_Buffer controlled_buffer_307
  assign pull_resistor_73_node = 1'b0 ? 1'b0 : 1'bz;  // Controlled_Buffer controlled_buffer_308
  assign pull_resistor_73_node = 1'b0 ? 1'b0 : 1'bz;  // Controlled_Buffer controlled_buffer_309
  muxin8tor muxin8tor_8 (.in_2(and_109_out), .in_1(in_1), .out_3(muxin8tor_8_out_3), .out_4(muxin8tor_8_out_4));
  not not_67 (not_67_out, in_1);
  Pull_Resistor pull_resistor_74 (.node(pull_resistor_74_node));
  assign pull_resistor_74_node = not_67_out ? nor_58_out : 8'bz;  // Controlled_Buffer controlled_buffer_310
  assign buffer_76_out = pull_resistor_74_node;  // Buffer buffer_76, 8 bits wide
  muxin16tor muxin16tor_8 (.in_2(and_109_out), .in_1(in_1), .out_3(muxin16tor_8_out_3), .out_4(muxin16tor_8_out_4));
  demuxin8tor demuxin8tor_8 (.in_2(nor_60_out), .in_3(8'h7), .in_1(in_1), .out_4(demuxin8tor_8_out_4));
  Pull_Resistor pull_resistor_75 (.node({controlled_buffer_1_out_2, controlled_buffer_1_out}));
  assign pull_resistor_73_node = 1'b1 ? 1'b1 : 1'bz;  // Controlled_Buffer controlled_buffer_311
  assign pull_resistor_73_node = 1'b1 ? 1'b1 : 1'bz;  // Controlled_Buffer controlled_buffer_312
  assign pull_resistor_73_node = 1'b1 ? 1'b1 : 1'bz;  // Controlled_Buffer controlled_buffer_313
  assign buffer_77_out = buffer_76_out;  // Buffer buffer_77, 8 bits wide
  assign buffer_78_out = buffer_77_out;  // Buffer buffer_78, 8 bits wide
  assign {controlled_buffer_1_out_2, controlled_buffer_1_out} = and_101_out ? 8'h7 : 8'bz;  // Controlled_Buffer controlled_buffer_314
  Pull_Resistor pull_resistor_76 (.node(out_9));
  assign out_9 = and_101_out ? and_101_out : 1'bz;  // Controlled_Buffer controlled_buffer_315
  assign xor_22_out = controlled_buffer_1_out_2 ^ 4'b0000;  // XOR_Gate xor_22, 4 bits wide
  assign xor_23_out = 4'b0111 ^ controlled_buffer_1_out;  // XOR_Gate xor_23, 4 bits wide
  assign and_97_out = buffer_78_out & muxin8tor_8_out_4;  // AND_Gate and_97, 8 bits wide
  assign and_98_out = muxin8tor_8_out_4 & not_68_out;  // AND_Gate and_98, 8 bits wide
  assign not_68_out = ~buffer_77_out;  // NOT_Gate not_68, 8 bits wide
  assign buffer_79_out = demuxin8tor_8_out_4;  // Buffer buffer_79, 16 bits wide
  assign and_99_out = buffer_79_out & muxin16tor_8_out_4;  // AND_Gate and_99, 16 bits wide
  assign and_100_out = muxin16tor_8_out_4 & not_69_out;  // AND_Gate and_100, 16 bits wide
  assign not_69_out = ~demuxin8tor_8_out_4;  // NOT_Gate not_69, 16 bits wide
  and and_101 (and_101_out, pull_resistor_81_node, and_1_out);
  not not_70 (not_70_out, pull_resistor_73_node);
  assign nor_61_out = ~(and_97_out | nor_62_out);  // NOR_Gate nor_61, 8 bits wide
  assign nor_62_out = ~(nor_61_out | and_98_out);  // NOR_Gate nor_62, 8 bits wide
  assign nor_63_out = ~(and_99_out | nor_64_out);  // NOR_Gate nor_63, 16 bits wide
  assign nor_64_out = ~(nor_63_out | and_100_out);  // NOR_Gate nor_64, 16 bits wide
  assign controlled_buffer_330_out[1] = xor_23_out[1] ? xor_23_out[1] : 1'bz;  // Controlled_Buffer controlled_buffer_316
  assign controlled_buffer_330_out[1] = xor_23_out[2] ? xor_23_out[2] : 1'bz;  // Controlled_Buffer controlled_buffer_317
  assign controlled_buffer_330_out[1] = xor_23_out[3] ? xor_23_out[3] : 1'bz;  // Controlled_Buffer controlled_buffer_318
  assign controlled_buffer_330_out[2] = xor_23_out[2] ? xor_23_out[2] : 1'bz;  // Controlled_Buffer controlled_buffer_319
  assign controlled_buffer_330_out[2] = xor_23_out[3] ? xor_23_out[3] : 1'bz;  // Controlled_Buffer controlled_buffer_320
  assign and_102_out = buffer_80_out & muxin8tor_8_out_3;  // AND_Gate and_102, 8 bits wide
  assign buffer_80_out = nor_62_out;  // Buffer buffer_80, 8 bits wide
  assign and_103_out = muxin8tor_8_out_3 & not_71_out;  // AND_Gate and_103, 8 bits wide
  assign not_71_out = ~nor_62_out;  // NOT_Gate not_71, 8 bits wide
  assign buffer_81_out = nor_64_out;  // Buffer buffer_81, 16 bits wide
  assign and_104_out = buffer_81_out & muxin16tor_8_out_3;  // AND_Gate and_104, 16 bits wide
  assign and_105_out = muxin16tor_8_out_3 & not_72_out;  // AND_Gate and_105, 16 bits wide
  assign not_72_out = ~nor_64_out;  // NOT_Gate not_72, 16 bits wide
  assign controlled_buffer_321_out[0] = xor_22_out[0] ? xor_22_out[0] : 1'bz;  // Controlled_Buffer controlled_buffer_321
  assign controlled_buffer_321_out[1] = xor_22_out[1] ? xor_22_out[1] : 1'bz;  // Controlled_Buffer controlled_buffer_322
  assign controlled_buffer_321_out[0] = xor_22_out[1] ? xor_22_out[1] : 1'bz;  // Controlled_Buffer controlled_buffer_323
  assign controlled_buffer_321_out[1] = xor_22_out[2] ? xor_22_out[2] : 1'bz;  // Controlled_Buffer controlled_buffer_324
  assign controlled_buffer_321_out[0] = xor_22_out[2] ? xor_22_out[2] : 1'bz;  // Controlled_Buffer controlled_buffer_325
  assign controlled_buffer_321_out[1] = xor_22_out[3] ? xor_22_out[3] : 1'bz;  // Controlled_Buffer controlled_buffer_326
  assign controlled_buffer_321_out[0] = xor_22_out[3] ? xor_22_out[3] : 1'bz;  // Controlled_Buffer controlled_buffer_327
  assign controlled_buffer_321_out[2] = xor_22_out[2] ? xor_22_out[2] : 1'bz;  // Controlled_Buffer controlled_buffer_328
  assign controlled_buffer_321_out[2] = xor_22_out[3] ? xor_22_out[3] : 1'bz;  // Controlled_Buffer controlled_buffer_329
  not not_73 (not_73_out, controlled_buffer_321_out[0]);
  assign controlled_buffer_330_out[0] = xor_23_out[0] ? xor_23_out[0] : 1'bz;  // Controlled_Buffer controlled_buffer_330
  assign controlled_buffer_330_out[0] = xor_23_out[1] ? xor_23_out[1] : 1'bz;  // Controlled_Buffer controlled_buffer_331
  assign controlled_buffer_330_out[0] = xor_23_out[2] ? xor_23_out[2] : 1'bz;  // Controlled_Buffer controlled_buffer_332
  assign controlled_buffer_330_out[0] = xor_23_out[3] ? xor_23_out[3] : 1'bz;  // Controlled_Buffer controlled_buffer_333
  Pull_Resistor pull_resistor_77 (.node({xor_23_out[3], controlled_buffer_330_out}));
  assign nor_65_out = ~(and_102_out | nor_66_out);  // NOR_Gate nor_65, 8 bits wide
  assign nor_66_out = ~(nor_65_out | and_103_out);  // NOR_Gate nor_66, 8 bits wide
  assign nor_67_out = ~(and_104_out | nor_68_out);  // NOR_Gate nor_67, 16 bits wide
  assign nor_68_out = ~(nor_67_out | and_105_out);  // NOR_Gate nor_68, 16 bits wide
  assign buffer_82_out = {xor_22_out[3], controlled_buffer_321_out};  // Buffer buffer_82, 4 bits wide
  Pull_Resistor pull_resistor_78 (.node({xor_22_out[3], controlled_buffer_321_out}));
  assign not_74_out = ~{1'b0, xor_22_out[3], controlled_buffer_321_out[2:1]};  // NOT_Gate not_74, 4 bits wide
  assign and_106_out = buffer_83_out & not_75_out;  // AND_Gate and_106, 4 bits wide
  assign buffer_83_out = {xor_23_out[3], controlled_buffer_330_out};  // Buffer buffer_83, 4 bits wide
  Pull_Resistor pull_resistor_79 (.node(pull_resistor_79_node));
  assign pull_resistor_79_node = and_106_out[3] ? controlled_buffer_1_out[3] : 1'bz;  // Controlled_Buffer controlled_buffer_334
  assign pull_resistor_79_node = and_106_out[2] ? controlled_buffer_1_out[2] : 1'bz;  // Controlled_Buffer controlled_buffer_335
  assign not_75_out = ~{1'b0, xor_23_out[3], controlled_buffer_330_out[2:1]};  // NOT_Gate not_75, 4 bits wide
  assign xor_24_out = nor_68_out ^ buffer_2_out;  // XOR_Gate xor_24, 16 bits wide
  assign and_107_out = buffer_82_out & not_74_out;  // AND_Gate and_107, 4 bits wide
  Pull_Resistor pull_resistor_80 (.node(pull_resistor_80_node));
  assign pull_resistor_80_node = and_107_out[3] ? controlled_buffer_1_out_2[3] : 1'bz;  // Controlled_Buffer controlled_buffer_336
  assign pull_resistor_80_node = and_107_out[2] ? controlled_buffer_1_out_2[2] : 1'bz;  // Controlled_Buffer controlled_buffer_337
  assign pull_resistor_80_node = and_107_out[1] ? controlled_buffer_1_out_2[1] : 1'bz;  // Controlled_Buffer controlled_buffer_338
  and and_108 (and_108_out, not_73_out, pull_resistor_79_node);
  assign controlled_buffer_339_out = and_108_out ? and_108_out : 1'bz;  // Controlled_Buffer controlled_buffer_339
  assign pull_resistor_79_node = and_106_out[1] ? controlled_buffer_1_out[1] : 1'bz;  // Controlled_Buffer controlled_buffer_340
  assign pull_resistor_79_node = and_106_out[0] ? controlled_buffer_1_out[0] : 1'bz;  // Controlled_Buffer controlled_buffer_341
  Pull_Resistor #(.pull(1)) pull_resistor_81 (.node(pull_resistor_81_node));
  and and_109 (and_109_out, controlled_buffer_339_out, out_9);
  assign pull_resistor_80_node = and_107_out[0] ? controlled_buffer_1_out_2[0] : 1'bz;  // Controlled_Buffer controlled_buffer_342
  assign controlled_buffer_339_out = pull_resistor_80_node ? pull_resistor_80_node : 1'bz;  // Controlled_Buffer controlled_buffer_343
  assign controlled_buffer_339_out = not_70_out ? not_70_out : 1'bz;  // Controlled_Buffer controlled_buffer_344
  Pull_Resistor pull_resistor_82 (.node(controlled_buffer_339_out));
  assign pull_resistor_81_node = xor_24_out[0] ? ~xor_24_out[0] : 1'bz;  // Controlled_Inverter controlled_inverter_113
  assign pull_resistor_81_node = xor_24_out[1] ? ~xor_24_out[1] : 1'bz;  // Controlled_Inverter controlled_inverter_114
  assign pull_resistor_81_node = xor_24_out[2] ? ~xor_24_out[2] : 1'bz;  // Controlled_Inverter controlled_inverter_115
  assign pull_resistor_81_node = xor_24_out[3] ? ~xor_24_out[3] : 1'bz;  // Controlled_Inverter controlled_inverter_116
  assign pull_resistor_81_node = xor_24_out[4] ? ~xor_24_out[4] : 1'bz;  // Controlled_Inverter controlled_inverter_117
  assign pull_resistor_81_node = xor_24_out[5] ? ~xor_24_out[5] : 1'bz;  // Controlled_Inverter controlled_inverter_118
  assign pull_resistor_81_node = xor_24_out[6] ? ~xor_24_out[6] : 1'bz;  // Controlled_Inverter controlled_inverter_119
  assign pull_resistor_81_node = xor_24_out[7] ? ~xor_24_out[7] : 1'bz;  // Controlled_Inverter controlled_inverter_120
  assign pull_resistor_81_node = xor_24_out[8] ? ~xor_24_out[8] : 1'bz;  // Controlled_Inverter controlled_inverter_121
  assign pull_resistor_81_node = xor_24_out[9] ? ~xor_24_out[9] : 1'bz;  // Controlled_Inverter controlled_inverter_122
  assign pull_resistor_81_node = xor_24_out[10] ? ~xor_24_out[10] : 1'bz;  // Controlled_Inverter controlled_inverter_123
  assign pull_resistor_81_node = xor_24_out[11] ? ~xor_24_out[11] : 1'bz;  // Controlled_Inverter controlled_inverter_124
  assign pull_resistor_81_node = xor_24_out[12] ? ~xor_24_out[12] : 1'bz;  // Controlled_Inverter controlled_inverter_125
  assign pull_resistor_81_node = xor_24_out[13] ? ~xor_24_out[13] : 1'bz;  // Controlled_Inverter controlled_inverter_126
  assign pull_resistor_81_node = xor_24_out[14] ? ~xor_24_out[14] : 1'bz;  // Controlled_Inverter controlled_inverter_127
  assign pull_resistor_81_node = xor_24_out[15] ? ~xor_24_out[15] : 1'bz;  // Controlled_Inverter controlled_inverter_128
  assign controlled_buffer_339_out = pull_resistor_81_node ? pull_resistor_81_node : 1'bz;  // Controlled_Buffer controlled_buffer_345
  assign out_10 = and_101_out ? nor_66_out : 8'bz;  // Controlled_Buffer controlled_buffer_346
  assign pull_resistor_1_node = and_101_out ? nor_68_out : 16'bz;  // Controlled_Buffer controlled_buffer_347
  Pull_Resistor pull_resistor_83 (.node(pull_resistor_83_node));
  assign pull_resistor_83_node = 1'b0 ? 1'b0 : 1'bz;  // Controlled_Buffer controlled_buffer_348
  assign pull_resistor_83_node = 1'b0 ? 1'b0 : 1'bz;  // Controlled_Buffer controlled_buffer_349
  assign pull_resistor_83_node = 1'b0 ? 1'b0 : 1'bz;  // Controlled_Buffer controlled_buffer_350
  assign pull_resistor_83_node = 1'b0 ? 1'b0 : 1'bz;  // Controlled_Buffer controlled_buffer_351
  assign pull_resistor_83_node = 1'b1 ? 1'b1 : 1'bz;  // Controlled_Buffer controlled_buffer_352
  muxin8tor muxin8tor_9 (.in_2(and_122_out), .in_1(in_1), .out_3(muxin8tor_9_out_3), .out_4(muxin8tor_9_out_4));
  not not_76 (not_76_out, in_1);
  Pull_Resistor pull_resistor_84 (.node(pull_resistor_84_node));
  assign pull_resistor_84_node = not_76_out ? nor_66_out : 8'bz;  // Controlled_Buffer controlled_buffer_353
  muxin16tor muxin16tor_9 (.in_2(and_122_out), .in_1(in_1), .out_3(muxin16tor_9_out_3), .out_4(muxin16tor_9_out_4));
  demuxin8tor demuxin8tor_9 (.in_2(nor_68_out), .in_3(8'h8), .in_1(in_1), .out_4(demuxin8tor_9_out_4));
  assign pull_resistor_83_node = 1'b0 ? 1'b0 : 1'bz;  // Controlled_Buffer controlled_buffer_354
  assign pull_resistor_83_node = 1'b0 ? 1'b0 : 1'bz;  // Controlled_Buffer controlled_buffer_355
  assign pull_resistor_83_node = 1'b0 ? 1'b0 : 1'bz;  // Controlled_Buffer controlled_buffer_356
  assign buffer_84_out = pull_resistor_84_node;  // Buffer buffer_84, 8 bits wide
  assign buffer_85_out = buffer_84_out;  // Buffer buffer_85, 8 bits wide
  assign {controlled_buffer_1_out_2, controlled_buffer_1_out} = and_114_out ? 8'h8 : 8'bz;  // Controlled_Buffer controlled_buffer_357
  Pull_Resistor pull_resistor_85 (.node({controlled_buffer_1_out_2, controlled_buffer_1_out}));
  Pull_Resistor pull_resistor_86 (.node(out_9));
  assign out_9 = and_114_out ? and_114_out : 1'bz;  // Controlled_Buffer controlled_buffer_358
  assign and_110_out = buffer_86_out & muxin8tor_9_out_4;  // AND_Gate and_110, 8 bits wide
  assign buffer_86_out = buffer_85_out;  // Buffer buffer_86, 8 bits wide
  assign and_111_out = muxin8tor_9_out_4 & not_77_out;  // AND_Gate and_111, 8 bits wide
  assign not_77_out = ~buffer_85_out;  // NOT_Gate not_77, 8 bits wide
  assign buffer_87_out = demuxin8tor_9_out_4;  // Buffer buffer_87, 16 bits wide
  assign and_112_out = buffer_87_out & muxin16tor_9_out_4;  // AND_Gate and_112, 16 bits wide
  assign and_113_out = muxin16tor_9_out_4 & not_78_out;  // AND_Gate and_113, 16 bits wide
  assign not_78_out = ~demuxin8tor_9_out_4;  // NOT_Gate not_78, 16 bits wide
  and and_114 (and_114_out, pull_resistor_91_node, and_1_out);
  not not_79 (not_79_out, pull_resistor_83_node);
  assign xor_25_out = controlled_buffer_1_out_2 ^ 4'b0000;  // XOR_Gate xor_25, 4 bits wide
  assign xor_26_out = 4'b1000 ^ controlled_buffer_1_out;  // XOR_Gate xor_26, 4 bits wide
  assign nor_69_out = ~(and_110_out | nor_70_out);  // NOR_Gate nor_69, 8 bits wide
  assign nor_70_out = ~(nor_69_out | and_111_out);  // NOR_Gate nor_70, 8 bits wide
  assign nor_71_out = ~(and_112_out | nor_72_out);  // NOR_Gate nor_71, 16 bits wide
  assign nor_72_out = ~(nor_71_out | and_113_out);  // NOR_Gate nor_72, 16 bits wide
  assign controlled_buffer_373_out[1] = xor_26_out[1] ? xor_26_out[1] : 1'bz;  // Controlled_Buffer controlled_buffer_359
  assign controlled_buffer_373_out[1] = xor_26_out[2] ? xor_26_out[2] : 1'bz;  // Controlled_Buffer controlled_buffer_360
  assign controlled_buffer_373_out[1] = xor_26_out[3] ? xor_26_out[3] : 1'bz;  // Controlled_Buffer controlled_buffer_361
  assign controlled_buffer_373_out[2] = xor_26_out[2] ? xor_26_out[2] : 1'bz;  // Controlled_Buffer controlled_buffer_362
  assign controlled_buffer_373_out[2] = xor_26_out[3] ? xor_26_out[3] : 1'bz;  // Controlled_Buffer controlled_buffer_363
  assign buffer_88_out = nor_70_out;  // Buffer buffer_88, 8 bits wide
  assign not_80_out = ~nor_70_out;  // NOT_Gate not_80, 8 bits wide
  assign buffer_89_out = nor_72_out;  // Buffer buffer_89, 16 bits wide
  assign and_115_out = buffer_89_out & muxin16tor_9_out_3;  // AND_Gate and_115, 16 bits wide
  assign and_116_out = muxin16tor_9_out_3 & not_81_out;  // AND_Gate and_116, 16 bits wide
  assign not_81_out = ~nor_72_out;  // NOT_Gate not_81, 16 bits wide
  assign controlled_buffer_364_out[0] = xor_25_out[0] ? xor_25_out[0] : 1'bz;  // Controlled_Buffer controlled_buffer_364
  assign controlled_buffer_364_out[1] = xor_25_out[1] ? xor_25_out[1] : 1'bz;  // Controlled_Buffer controlled_buffer_365
  assign controlled_buffer_364_out[0] = xor_25_out[1] ? xor_25_out[1] : 1'bz;  // Controlled_Buffer controlled_buffer_366
  assign controlled_buffer_364_out[1] = xor_25_out[2] ? xor_25_out[2] : 1'bz;  // Controlled_Buffer controlled_buffer_367
  assign controlled_buffer_364_out[0] = xor_25_out[2] ? xor_25_out[2] : 1'bz;  // Controlled_Buffer controlled_buffer_368
  assign controlled_buffer_364_out[1] = xor_25_out[3] ? xor_25_out[3] : 1'bz;  // Controlled_Buffer controlled_buffer_369
  assign controlled_buffer_364_out[0] = xor_25_out[3] ? xor_25_out[3] : 1'bz;  // Controlled_Buffer controlled_buffer_370
  assign controlled_buffer_364_out[2] = xor_25_out[2] ? xor_25_out[2] : 1'bz;  // Controlled_Buffer controlled_buffer_371
  assign controlled_buffer_364_out[2] = xor_25_out[3] ? xor_25_out[3] : 1'bz;  // Controlled_Buffer controlled_buffer_372
  not not_82 (not_82_out, controlled_buffer_364_out[0]);
  assign controlled_buffer_373_out[0] = xor_26_out[0] ? xor_26_out[0] : 1'bz;  // Controlled_Buffer controlled_buffer_373
  assign controlled_buffer_373_out[0] = xor_26_out[1] ? xor_26_out[1] : 1'bz;  // Controlled_Buffer controlled_buffer_374
  assign controlled_buffer_373_out[0] = xor_26_out[2] ? xor_26_out[2] : 1'bz;  // Controlled_Buffer controlled_buffer_375
  assign controlled_buffer_373_out[0] = xor_26_out[3] ? xor_26_out[3] : 1'bz;  // Controlled_Buffer controlled_buffer_376
  Pull_Resistor pull_resistor_87 (.node({xor_26_out[3], controlled_buffer_373_out}));
  assign and_117_out = buffer_88_out & muxin8tor_9_out_3;  // AND_Gate and_117, 8 bits wide
  assign nor_73_out = ~(and_117_out | nor_74_out);  // NOR_Gate nor_73, 8 bits wide
  assign and_118_out = muxin8tor_9_out_3 & not_80_out;  // AND_Gate and_118, 8 bits wide
  assign nor_74_out = ~(nor_73_out | and_118_out);  // NOR_Gate nor_74, 8 bits wide
  assign nor_75_out = ~(and_115_out | nor_76_out);  // NOR_Gate nor_75, 16 bits wide
  assign nor_76_out = ~(nor_75_out | and_116_out);  // NOR_Gate nor_76, 16 bits wide
  assign buffer_90_out = {xor_25_out[3], controlled_buffer_364_out};  // Buffer buffer_90, 4 bits wide
  Pull_Resistor pull_resistor_88 (.node({xor_25_out[3], controlled_buffer_364_out}));
  assign and_119_out = buffer_91_out & not_84_out;  // AND_Gate and_119, 4 bits wide
  assign buffer_91_out = {xor_26_out[3], controlled_buffer_373_out};  // Buffer buffer_91, 4 bits wide
  Pull_Resistor pull_resistor_89 (.node(pull_resistor_89_node));
  assign pull_resistor_89_node = and_119_out[3] ? controlled_buffer_1_out[3] : 1'bz;  // Controlled_Buffer controlled_buffer_377
  assign xor_27_out = nor_76_out ^ buffer_2_out;  // XOR_Gate xor_27, 16 bits wide
  assign and_120_out = buffer_90_out & not_83_out;  // AND_Gate and_120, 4 bits wide
  Pull_Resistor pull_resistor_90 (.node(pull_resistor_90_node));
  assign not_83_out = ~{1'b0, xor_25_out[3], controlled_buffer_364_out[2:1]};  // NOT_Gate not_83, 4 bits wide
  assign pull_resistor_90_node = and_120_out[3] ? controlled_buffer_1_out_2[3] : 1'bz;  // Controlled_Buffer controlled_buffer_378
  assign pull_resistor_90_node = and_120_out[2] ? controlled_buffer_1_out_2[2] : 1'bz;  // Controlled_Buffer controlled_buffer_379
  assign pull_resistor_90_node = and_120_out[1] ? controlled_buffer_1_out_2[1] : 1'bz;  // Controlled_Buffer controlled_buffer_380
  and and_121 (and_121_out, not_82_out, pull_resistor_89_node);
  assign pull_resistor_89_node = and_119_out[2] ? controlled_buffer_1_out[2] : 1'bz;  // Controlled_Buffer controlled_buffer_381
  assign pull_resistor_89_node = and_119_out[1] ? controlled_buffer_1_out[1] : 1'bz;  // Controlled_Buffer controlled_buffer_382
  assign pull_resistor_89_node = and_119_out[0] ? controlled_buffer_1_out[0] : 1'bz;  // Controlled_Buffer controlled_buffer_383
  assign not_84_out = ~{1'b0, xor_26_out[3], controlled_buffer_373_out[2:1]};  // NOT_Gate not_84, 4 bits wide
  Pull_Resistor #(.pull(1)) pull_resistor_91 (.node(pull_resistor_91_node));
  and and_122 (and_122_out, controlled_buffer_385_out, out_9);
  assign pull_resistor_90_node = and_120_out[0] ? controlled_buffer_1_out_2[0] : 1'bz;  // Controlled_Buffer controlled_buffer_384
  assign controlled_buffer_385_out = pull_resistor_90_node ? pull_resistor_90_node : 1'bz;  // Controlled_Buffer controlled_buffer_385
  assign controlled_buffer_385_out = and_121_out ? and_121_out : 1'bz;  // Controlled_Buffer controlled_buffer_386
  assign controlled_buffer_385_out = not_79_out ? not_79_out : 1'bz;  // Controlled_Buffer controlled_buffer_387
  Pull_Resistor pull_resistor_92 (.node(controlled_buffer_385_out));
  assign pull_resistor_91_node = xor_27_out[0] ? ~xor_27_out[0] : 1'bz;  // Controlled_Inverter controlled_inverter_129
  assign pull_resistor_91_node = xor_27_out[1] ? ~xor_27_out[1] : 1'bz;  // Controlled_Inverter controlled_inverter_130
  assign pull_resistor_91_node = xor_27_out[2] ? ~xor_27_out[2] : 1'bz;  // Controlled_Inverter controlled_inverter_131
  assign pull_resistor_91_node = xor_27_out[3] ? ~xor_27_out[3] : 1'bz;  // Controlled_Inverter controlled_inverter_132
  assign pull_resistor_91_node = xor_27_out[4] ? ~xor_27_out[4] : 1'bz;  // Controlled_Inverter controlled_inverter_133
  assign pull_resistor_91_node = xor_27_out[5] ? ~xor_27_out[5] : 1'bz;  // Controlled_Inverter controlled_inverter_134
  assign pull_resistor_91_node = xor_27_out[6] ? ~xor_27_out[6] : 1'bz;  // Controlled_Inverter controlled_inverter_135
  assign pull_resistor_91_node = xor_27_out[7] ? ~xor_27_out[7] : 1'bz;  // Controlled_Inverter controlled_inverter_136
  assign pull_resistor_91_node = xor_27_out[8] ? ~xor_27_out[8] : 1'bz;  // Controlled_Inverter controlled_inverter_137
  assign pull_resistor_91_node = xor_27_out[9] ? ~xor_27_out[9] : 1'bz;  // Controlled_Inverter controlled_inverter_138
  assign pull_resistor_91_node = xor_27_out[10] ? ~xor_27_out[10] : 1'bz;  // Controlled_Inverter controlled_inverter_139
  assign pull_resistor_91_node = xor_27_out[11] ? ~xor_27_out[11] : 1'bz;  // Controlled_Inverter controlled_inverter_140
  assign pull_resistor_91_node = xor_27_out[12] ? ~xor_27_out[12] : 1'bz;  // Controlled_Inverter controlled_inverter_141
  assign pull_resistor_91_node = xor_27_out[13] ? ~xor_27_out[13] : 1'bz;  // Controlled_Inverter controlled_inverter_142
  assign pull_resistor_91_node = xor_27_out[14] ? ~xor_27_out[14] : 1'bz;  // Controlled_Inverter controlled_inverter_143
  assign pull_resistor_91_node = xor_27_out[15] ? ~xor_27_out[15] : 1'bz;  // Controlled_Inverter controlled_inverter_144
  assign controlled_buffer_385_out = pull_resistor_91_node ? pull_resistor_91_node : 1'bz;  // Controlled_Buffer controlled_buffer_388
  assign out_10 = and_114_out ? nor_74_out : 8'bz;  // Controlled_Buffer controlled_buffer_389
  assign pull_resistor_1_node = and_114_out ? nor_76_out : 16'bz;  // Controlled_Buffer controlled_buffer_390
  Pull_Resistor pull_resistor_93 (.node(pull_resistor_93_node));
  assign pull_resistor_93_node = 1'b0 ? 1'b0 : 1'bz;  // Controlled_Buffer controlled_buffer_391
  assign pull_resistor_93_node = 1'b0 ? 1'b0 : 1'bz;  // Controlled_Buffer controlled_buffer_392
  assign pull_resistor_93_node = 1'b0 ? 1'b0 : 1'bz;  // Controlled_Buffer controlled_buffer_393
  assign pull_resistor_93_node = 1'b0 ? 1'b0 : 1'bz;  // Controlled_Buffer controlled_buffer_394
  muxin8tor muxin8tor_10 (.in_2(and_134_out), .in_1(in_1), .out_3(muxin8tor_10_out_3), .out_4(muxin8tor_10_out_4));
  not not_85 (not_85_out, in_1);
  Pull_Resistor pull_resistor_94 (.node(pull_resistor_94_node));
  assign pull_resistor_94_node = not_85_out ? nor_74_out : 8'bz;  // Controlled_Buffer controlled_buffer_395
  muxin16tor muxin16tor_10 (.in_2(and_134_out), .in_1(in_1), .out_3(muxin16tor_10_out_3), .out_4(muxin16tor_10_out_4));
  demuxin8tor demuxin8tor_10 (.in_2(nor_76_out), .in_3(8'h9), .in_1(in_1), .out_4(demuxin8tor_10_out_4));
  assign pull_resistor_93_node = 1'b1 ? 1'b1 : 1'bz;  // Controlled_Buffer controlled_buffer_396
  assign pull_resistor_93_node = 1'b0 ? 1'b0 : 1'bz;  // Controlled_Buffer controlled_buffer_397
  assign pull_resistor_93_node = 1'b0 ? 1'b0 : 1'bz;  // Controlled_Buffer controlled_buffer_398
  assign pull_resistor_93_node = 1'b1 ? 1'b1 : 1'bz;  // Controlled_Buffer controlled_buffer_399
  assign buffer_92_out = pull_resistor_94_node;  // Buffer buffer_92, 8 bits wide
  assign buffer_93_out = buffer_92_out;  // Buffer buffer_93, 8 bits wide
  assign {controlled_buffer_1_out_2, controlled_buffer_1_out} = and_127_out ? 8'h9 : 8'bz;  // Controlled_Buffer controlled_buffer_400
  Pull_Resistor pull_resistor_95 (.node({controlled_buffer_1_out_2, controlled_buffer_1_out}));
  Pull_Resistor pull_resistor_96 (.node(out_9));
  assign out_9 = and_127_out ? and_127_out : 1'bz;  // Controlled_Buffer controlled_buffer_401
  assign and_123_out = buffer_94_out & muxin8tor_10_out_4;  // AND_Gate and_123, 8 bits wide
  assign buffer_94_out = buffer_93_out;  // Buffer buffer_94, 8 bits wide
  assign and_124_out = muxin8tor_10_out_4 & not_86_out;  // AND_Gate and_124, 8 bits wide
  assign not_86_out = ~buffer_93_out;  // NOT_Gate not_86, 8 bits wide
  assign buffer_95_out = demuxin8tor_10_out_4;  // Buffer buffer_95, 16 bits wide
  assign and_125_out = buffer_95_out & muxin16tor_10_out_4;  // AND_Gate and_125, 16 bits wide
  assign and_126_out = muxin16tor_10_out_4 & not_87_out;  // AND_Gate and_126, 16 bits wide
  assign not_87_out = ~demuxin8tor_10_out_4;  // NOT_Gate not_87, 16 bits wide
  and and_127 (and_127_out, pull_resistor_101_node, and_1_out);
  not not_88 (not_88_out, pull_resistor_93_node);
  assign xor_28_out = controlled_buffer_1_out_2 ^ 4'b0000;  // XOR_Gate xor_28, 4 bits wide
  assign xor_29_out = 4'b1001 ^ controlled_buffer_1_out;  // XOR_Gate xor_29, 4 bits wide
  assign nor_77_out = ~(and_123_out | nor_78_out);  // NOR_Gate nor_77, 8 bits wide
  assign nor_78_out = ~(nor_77_out | and_124_out);  // NOR_Gate nor_78, 8 bits wide
  assign nor_79_out = ~(and_125_out | nor_80_out);  // NOR_Gate nor_79, 16 bits wide
  assign nor_80_out = ~(nor_79_out | and_126_out);  // NOR_Gate nor_80, 16 bits wide
  assign controlled_buffer_412_out[1] = xor_29_out[1] ? xor_29_out[1] : 1'bz;  // Controlled_Buffer controlled_buffer_402
  assign controlled_buffer_412_out[1] = xor_29_out[2] ? xor_29_out[2] : 1'bz;  // Controlled_Buffer controlled_buffer_403
  assign controlled_buffer_412_out[1] = xor_29_out[3] ? xor_29_out[3] : 1'bz;  // Controlled_Buffer controlled_buffer_404
  assign controlled_buffer_412_out[2] = xor_29_out[2] ? xor_29_out[2] : 1'bz;  // Controlled_Buffer controlled_buffer_405
  assign controlled_buffer_412_out[2] = xor_29_out[3] ? xor_29_out[3] : 1'bz;  // Controlled_Buffer controlled_buffer_406
  assign buffer_96_out = nor_78_out;  // Buffer buffer_96, 8 bits wide
  assign not_89_out = ~nor_78_out;  // NOT_Gate not_89, 8 bits wide
  assign buffer_97_out = nor_80_out;  // Buffer buffer_97, 16 bits wide
  assign and_128_out = buffer_97_out & muxin16tor_10_out_3;  // AND_Gate and_128, 16 bits wide
  assign and_129_out = muxin16tor_10_out_3 & not_90_out;  // AND_Gate and_129, 16 bits wide
  assign not_90_out = ~nor_80_out;  // NOT_Gate not_90, 16 bits wide
  assign controlled_buffer_416_out[1] = xor_28_out[1] ? xor_28_out[1] : 1'bz;  // Controlled_Buffer controlled_buffer_407
  assign controlled_buffer_416_out[1] = xor_28_out[2] ? xor_28_out[2] : 1'bz;  // Controlled_Buffer controlled_buffer_408
  assign controlled_buffer_416_out[1] = xor_28_out[3] ? xor_28_out[3] : 1'bz;  // Controlled_Buffer controlled_buffer_409
  assign controlled_buffer_416_out[2] = xor_28_out[2] ? xor_28_out[2] : 1'bz;  // Controlled_Buffer controlled_buffer_410
  assign controlled_buffer_416_out[2] = xor_28_out[3] ? xor_28_out[3] : 1'bz;  // Controlled_Buffer controlled_buffer_411
  assign controlled_buffer_412_out[0] = xor_29_out[0] ? xor_29_out[0] : 1'bz;  // Controlled_Buffer controlled_buffer_412
  assign controlled_buffer_412_out[0] = xor_29_out[1] ? xor_29_out[1] : 1'bz;  // Controlled_Buffer controlled_buffer_413
  assign controlled_buffer_412_out[0] = xor_29_out[2] ? xor_29_out[2] : 1'bz;  // Controlled_Buffer controlled_buffer_414
  assign controlled_buffer_412_out[0] = xor_29_out[3] ? xor_29_out[3] : 1'bz;  // Controlled_Buffer controlled_buffer_415
  Pull_Resistor pull_resistor_97 (.node({xor_29_out[3], controlled_buffer_412_out}));
  assign and_130_out = buffer_96_out & muxin8tor_10_out_3;  // AND_Gate and_130, 8 bits wide
  assign nor_81_out = ~(and_130_out | nor_82_out);  // NOR_Gate nor_81, 8 bits wide
  assign and_131_out = muxin8tor_10_out_3 & not_89_out;  // AND_Gate and_131, 8 bits wide
  assign nor_82_out = ~(nor_81_out | and_131_out);  // NOR_Gate nor_82, 8 bits wide
  assign nor_83_out = ~(and_128_out | nor_84_out);  // NOR_Gate nor_83, 16 bits wide
  assign nor_84_out = ~(nor_83_out | and_129_out);  // NOR_Gate nor_84, 16 bits wide
  assign controlled_buffer_416_out[0] = xor_28_out[0] ? xor_28_out[0] : 1'bz;  // Controlled_Buffer controlled_buffer_416
  assign controlled_buffer_416_out[0] = xor_28_out[1] ? xor_28_out[1] : 1'bz;  // Controlled_Buffer controlled_buffer_417
  assign controlled_buffer_416_out[0] = xor_28_out[2] ? xor_28_out[2] : 1'bz;  // Controlled_Buffer controlled_buffer_418
  Pull_Resistor pull_resistor_98 (.node({xor_28_out[3], controlled_buffer_416_out}));
  assign controlled_buffer_416_out[0] = xor_28_out[3] ? xor_28_out[3] : 1'bz;  // Controlled_Buffer controlled_buffer_419
  not not_91 (not_91_out, controlled_buffer_416_out[0]);
  assign buffer_98_out = {xor_29_out[3], controlled_buffer_412_out};  // Buffer buffer_98, 4 bits wide
  Pull_Resistor pull_resistor_99 (.node(pull_resistor_99_node));
  assign pull_resistor_99_node = and_133_out[3] ? controlled_buffer_1_out[3] : 1'bz;  // Controlled_Buffer controlled_buffer_420
  assign xor_30_out = nor_84_out ^ buffer_2_out;  // XOR_Gate xor_30, 16 bits wide
  assign and_132_out = buffer_99_out & not_92_out;  // AND_Gate and_132, 4 bits wide
  assign buffer_99_out = {xor_28_out[3], controlled_buffer_416_out};  // Buffer buffer_99, 4 bits wide
  Pull_Resistor pull_resistor_100 (.node(pull_resistor_100_node));
  assign not_92_out = ~{1'b0, xor_28_out[3], controlled_buffer_416_out[2:1]};  // NOT_Gate not_92, 4 bits wide
  assign pull_resistor_100_node = and_132_out[3] ? controlled_buffer_1_out_2[3] : 1'bz;  // Controlled_Buffer controlled_buffer_421
  assign pull_resistor_100_node = and_132_out[2] ? controlled_buffer_1_out_2[2] : 1'bz;  // Controlled_Buffer controlled_buffer_422
  assign and_133_out = buffer_98_out & not_93_out;  // AND_Gate and_133, 4 bits wide
  assign pull_resistor_99_node = and_133_out[2] ? controlled_buffer_1_out[2] : 1'bz;  // Controlled_Buffer controlled_buffer_423
  assign pull_resistor_99_node = and_133_out[1] ? controlled_buffer_1_out[1] : 1'bz;  // Controlled_Buffer controlled_buffer_424
  assign pull_resistor_99_node = and_133_out[0] ? controlled_buffer_1_out[0] : 1'bz;  // Controlled_Buffer controlled_buffer_425
  assign not_93_out = ~{1'b0, xor_29_out[3], controlled_buffer_412_out[2:1]};  // NOT_Gate not_93, 4 bits wide
  Pull_Resistor #(.pull(1)) pull_resistor_101 (.node(pull_resistor_101_node));
  and and_134 (and_134_out, controlled_buffer_428_out, out_9);
  assign pull_resistor_100_node = and_132_out[1] ? controlled_buffer_1_out_2[1] : 1'bz;  // Controlled_Buffer controlled_buffer_426
  assign pull_resistor_100_node = and_132_out[0] ? controlled_buffer_1_out_2[0] : 1'bz;  // Controlled_Buffer controlled_buffer_427
  assign controlled_buffer_428_out = pull_resistor_100_node ? pull_resistor_100_node : 1'bz;  // Controlled_Buffer controlled_buffer_428
  and and_135 (and_135_out, not_91_out, pull_resistor_99_node);
  assign controlled_buffer_428_out = and_135_out ? and_135_out : 1'bz;  // Controlled_Buffer controlled_buffer_429
  assign controlled_buffer_428_out = not_88_out ? not_88_out : 1'bz;  // Controlled_Buffer controlled_buffer_430
  Pull_Resistor pull_resistor_102 (.node(controlled_buffer_428_out));
  assign pull_resistor_101_node = xor_30_out[0] ? ~xor_30_out[0] : 1'bz;  // Controlled_Inverter controlled_inverter_145
  assign pull_resistor_101_node = xor_30_out[1] ? ~xor_30_out[1] : 1'bz;  // Controlled_Inverter controlled_inverter_146
  assign pull_resistor_101_node = xor_30_out[2] ? ~xor_30_out[2] : 1'bz;  // Controlled_Inverter controlled_inverter_147
  assign pull_resistor_101_node = xor_30_out[3] ? ~xor_30_out[3] : 1'bz;  // Controlled_Inverter controlled_inverter_148
  assign pull_resistor_101_node = xor_30_out[4] ? ~xor_30_out[4] : 1'bz;  // Controlled_Inverter controlled_inverter_149
  assign pull_resistor_101_node = xor_30_out[5] ? ~xor_30_out[5] : 1'bz;  // Controlled_Inverter controlled_inverter_150
  assign pull_resistor_101_node = xor_30_out[6] ? ~xor_30_out[6] : 1'bz;  // Controlled_Inverter controlled_inverter_151
  assign pull_resistor_101_node = xor_30_out[7] ? ~xor_30_out[7] : 1'bz;  // Controlled_Inverter controlled_inverter_152
  assign pull_resistor_101_node = xor_30_out[8] ? ~xor_30_out[8] : 1'bz;  // Controlled_Inverter controlled_inverter_153
  assign pull_resistor_101_node = xor_30_out[9] ? ~xor_30_out[9] : 1'bz;  // Controlled_Inverter controlled_inverter_154
  assign pull_resistor_101_node = xor_30_out[10] ? ~xor_30_out[10] : 1'bz;  // Controlled_Inverter controlled_inverter_155
  assign pull_resistor_101_node = xor_30_out[11] ? ~xor_30_out[11] : 1'bz;  // Controlled_Inverter controlled_inverter_156
  assign pull_resistor_101_node = xor_30_out[12] ? ~xor_30_out[12] : 1'bz;  // Controlled_Inverter controlled_inverter_157
  assign pull_resistor_101_node = xor_30_out[13] ? ~xor_30_out[13] : 1'bz;  // Controlled_Inverter controlled_inverter_158
  assign pull_resistor_101_node = xor_30_out[14] ? ~xor_30_out[14] : 1'bz;  // Controlled_Inverter controlled_inverter_159
  assign pull_resistor_101_node = xor_30_out[15] ? ~xor_30_out[15] : 1'bz;  // Controlled_Inverter controlled_inverter_160
  assign controlled_buffer_428_out = pull_resistor_101_node ? pull_resistor_101_node : 1'bz;  // Controlled_Buffer controlled_buffer_431
  assign out_10 = and_127_out ? nor_82_out : 8'bz;  // Controlled_Buffer controlled_buffer_432
  assign pull_resistor_1_node = and_127_out ? nor_84_out : 16'bz;  // Controlled_Buffer controlled_buffer_433
  Pull_Resistor pull_resistor_103 (.node(pull_resistor_103_node));
  assign pull_resistor_103_node = 1'b0 ? 1'b0 : 1'bz;  // Controlled_Buffer controlled_buffer_434
  assign pull_resistor_103_node = 1'b0 ? 1'b0 : 1'bz;  // Controlled_Buffer controlled_buffer_435
  assign pull_resistor_103_node = 1'b0 ? 1'b0 : 1'bz;  // Controlled_Buffer controlled_buffer_436
  assign pull_resistor_103_node = 1'b0 ? 1'b0 : 1'bz;  // Controlled_Buffer controlled_buffer_437
  muxin8tor muxin8tor_11 (.in_2(and_147_out), .in_1(in_1), .out_3(muxin8tor_11_out_3), .out_4(muxin8tor_11_out_4));
  not not_94 (not_94_out, in_1);
  Pull_Resistor pull_resistor_104 (.node(pull_resistor_104_node));
  assign pull_resistor_104_node = not_94_out ? nor_82_out : 8'bz;  // Controlled_Buffer controlled_buffer_438
  muxin16tor muxin16tor_11 (.in_2(and_147_out), .in_1(in_1), .out_3(muxin16tor_11_out_3), .out_4(muxin16tor_11_out_4));
  demuxin8tor demuxin8tor_11 (.in_2(nor_84_out), .in_3(8'ha), .in_1(in_1), .out_4(demuxin8tor_11_out_4));
  assign pull_resistor_103_node = 1'b1 ? 1'b1 : 1'bz;  // Controlled_Buffer controlled_buffer_439
  assign pull_resistor_103_node = 1'b0 ? 1'b0 : 1'bz;  // Controlled_Buffer controlled_buffer_440
  assign pull_resistor_103_node = 1'b1 ? 1'b1 : 1'bz;  // Controlled_Buffer controlled_buffer_441
  assign pull_resistor_103_node = 1'b0 ? 1'b0 : 1'bz;  // Controlled_Buffer controlled_buffer_442
  assign buffer_100_out = pull_resistor_104_node;  // Buffer buffer_100, 8 bits wide
  assign buffer_101_out = buffer_100_out;  // Buffer buffer_101, 8 bits wide
  assign {controlled_buffer_1_out_2, controlled_buffer_1_out} = and_138_out ? 8'ha : 8'bz;  // Controlled_Buffer controlled_buffer_443
  Pull_Resistor pull_resistor_105 (.node({controlled_buffer_1_out_2, controlled_buffer_1_out}));
  assign out_9 = and_138_out ? and_138_out : 1'bz;  // Controlled_Buffer controlled_buffer_444
  assign buffer_102_out = buffer_101_out;  // Buffer buffer_102, 8 bits wide
  assign not_95_out = ~buffer_101_out;  // NOT_Gate not_95, 8 bits wide
  assign buffer_103_out = demuxin8tor_11_out_4;  // Buffer buffer_103, 16 bits wide
  assign and_136_out = buffer_103_out & muxin16tor_11_out_4;  // AND_Gate and_136, 16 bits wide
  assign and_137_out = muxin16tor_11_out_4 & not_96_out;  // AND_Gate and_137, 16 bits wide
  assign not_96_out = ~demuxin8tor_11_out_4;  // NOT_Gate not_96, 16 bits wide
  and and_138 (and_138_out, pull_resistor_111_node, and_1_out);
  Pull_Resistor pull_resistor_106 (.node(out_9));
  not not_97 (not_97_out, pull_resistor_103_node);
  assign xor_31_out = controlled_buffer_1_out_2 ^ 4'b0000;  // XOR_Gate xor_31, 4 bits wide
  assign xor_32_out = 4'b1010 ^ controlled_buffer_1_out;  // XOR_Gate xor_32, 4 bits wide
  assign and_139_out = buffer_102_out & muxin8tor_11_out_4;  // AND_Gate and_139, 8 bits wide
  assign nor_85_out = ~(and_139_out | nor_86_out);  // NOR_Gate nor_85, 8 bits wide
  assign and_140_out = muxin8tor_11_out_4 & not_95_out;  // AND_Gate and_140, 8 bits wide
  assign nor_86_out = ~(nor_85_out | and_140_out);  // NOR_Gate nor_86, 8 bits wide
  assign nor_87_out = ~(and_136_out | nor_88_out);  // NOR_Gate nor_87, 16 bits wide
  assign nor_88_out = ~(nor_87_out | and_137_out);  // NOR_Gate nor_88, 16 bits wide
  assign buffer_104_out = nor_86_out;  // Buffer buffer_104, 8 bits wide
  assign not_98_out = ~nor_86_out;  // NOT_Gate not_98, 8 bits wide
  assign buffer_105_out = nor_88_out;  // Buffer buffer_105, 16 bits wide
  assign not_99_out = ~nor_88_out;  // NOT_Gate not_99, 16 bits wide
  assign controlled_buffer_459_out[1] = xor_31_out[1] ? xor_31_out[1] : 1'bz;  // Controlled_Buffer controlled_buffer_445
  assign controlled_buffer_459_out[1] = xor_31_out[2] ? xor_31_out[2] : 1'bz;  // Controlled_Buffer controlled_buffer_446
  assign controlled_buffer_459_out[1] = xor_31_out[3] ? xor_31_out[3] : 1'bz;  // Controlled_Buffer controlled_buffer_447
  assign controlled_buffer_459_out[2] = xor_31_out[2] ? xor_31_out[2] : 1'bz;  // Controlled_Buffer controlled_buffer_448
  assign controlled_buffer_459_out[2] = xor_31_out[3] ? xor_31_out[3] : 1'bz;  // Controlled_Buffer controlled_buffer_449
  assign controlled_buffer_450_out[0] = xor_32_out[0] ? xor_32_out[0] : 1'bz;  // Controlled_Buffer controlled_buffer_450
  assign controlled_buffer_450_out[1] = xor_32_out[1] ? xor_32_out[1] : 1'bz;  // Controlled_Buffer controlled_buffer_451
  assign controlled_buffer_450_out[0] = xor_32_out[1] ? xor_32_out[1] : 1'bz;  // Controlled_Buffer controlled_buffer_452
  assign controlled_buffer_450_out[1] = xor_32_out[2] ? xor_32_out[2] : 1'bz;  // Controlled_Buffer controlled_buffer_453
  assign controlled_buffer_450_out[0] = xor_32_out[2] ? xor_32_out[2] : 1'bz;  // Controlled_Buffer controlled_buffer_454
  assign controlled_buffer_450_out[1] = xor_32_out[3] ? xor_32_out[3] : 1'bz;  // Controlled_Buffer controlled_buffer_455
  assign controlled_buffer_450_out[0] = xor_32_out[3] ? xor_32_out[3] : 1'bz;  // Controlled_Buffer controlled_buffer_456
  assign controlled_buffer_450_out[2] = xor_32_out[2] ? xor_32_out[2] : 1'bz;  // Controlled_Buffer controlled_buffer_457
  Pull_Resistor pull_resistor_107 (.node({xor_32_out[3], controlled_buffer_450_out}));
  assign controlled_buffer_450_out[2] = xor_32_out[3] ? xor_32_out[3] : 1'bz;  // Controlled_Buffer controlled_buffer_458
  assign and_141_out = buffer_104_out & muxin8tor_11_out_3;  // AND_Gate and_141, 8 bits wide
  assign and_142_out = muxin8tor_11_out_3 & not_98_out;  // AND_Gate and_142, 8 bits wide
  assign nor_89_out = ~(and_143_out | nor_90_out);  // NOR_Gate nor_89, 16 bits wide
  assign and_143_out = buffer_105_out & muxin16tor_11_out_3;  // AND_Gate and_143, 16 bits wide
  assign and_144_out = muxin16tor_11_out_3 & not_99_out;  // AND_Gate and_144, 16 bits wide
  assign nor_90_out = ~(nor_89_out | and_144_out);  // NOR_Gate nor_90, 16 bits wide
  assign controlled_buffer_459_out[0] = xor_31_out[0] ? xor_31_out[0] : 1'bz;  // Controlled_Buffer controlled_buffer_459
  assign controlled_buffer_459_out[0] = xor_31_out[1] ? xor_31_out[1] : 1'bz;  // Controlled_Buffer controlled_buffer_460
  assign controlled_buffer_459_out[0] = xor_31_out[2] ? xor_31_out[2] : 1'bz;  // Controlled_Buffer controlled_buffer_461
  Pull_Resistor pull_resistor_108 (.node({xor_31_out[3], controlled_buffer_459_out}));
  assign controlled_buffer_459_out[0] = xor_31_out[3] ? xor_31_out[3] : 1'bz;  // Controlled_Buffer controlled_buffer_462
  not not_100 (not_100_out, controlled_buffer_459_out[0]);
  assign buffer_106_out = {xor_32_out[3], controlled_buffer_450_out};  // Buffer buffer_106, 4 bits wide
  Pull_Resistor pull_resistor_109 (.node(pull_resistor_109_node));
  assign nor_91_out = ~(and_141_out | nor_92_out);  // NOR_Gate nor_91, 8 bits wide
  assign nor_92_out = ~(nor_91_out | and_142_out);  // NOR_Gate nor_92, 8 bits wide
  assign xor_33_out = nor_90_out ^ buffer_2_out;  // XOR_Gate xor_33, 16 bits wide
  assign and_145_out = buffer_107_out & not_101_out;  // AND_Gate and_145, 4 bits wide
  assign buffer_107_out = {xor_31_out[3], controlled_buffer_459_out};  // Buffer buffer_107, 4 bits wide
  Pull_Resistor pull_resistor_110 (.node(pull_resistor_110_node));
  assign not_101_out = ~{1'b0, xor_31_out[3], controlled_buffer_459_out[2:1]};  // NOT_Gate not_101, 4 bits wide
  assign pull_resistor_110_node = and_145_out[3] ? controlled_buffer_1_out_2[3] : 1'bz;  // Controlled_Buffer controlled_buffer_463
  assign pull_resistor_110_node = and_145_out[2] ? controlled_buffer_1_out_2[2] : 1'bz;  // Controlled_Buffer controlled_buffer_464
  assign and_146_out = buffer_106_out & not_102_out;  // AND_Gate and_146, 4 bits wide
  assign pull_resistor_109_node = and_146_out[3] ? controlled_buffer_1_out[3] : 1'bz;  // Controlled_Buffer controlled_buffer_465
  assign pull_resistor_109_node = and_146_out[2] ? controlled_buffer_1_out[2] : 1'bz;  // Controlled_Buffer controlled_buffer_466
  assign pull_resistor_109_node = and_146_out[1] ? controlled_buffer_1_out[1] : 1'bz;  // Controlled_Buffer controlled_buffer_467
  assign pull_resistor_109_node = and_146_out[0] ? controlled_buffer_1_out[0] : 1'bz;  // Controlled_Buffer controlled_buffer_468
  assign not_102_out = ~{1'b0, xor_32_out[3], controlled_buffer_450_out[2:1]};  // NOT_Gate not_102, 4 bits wide
  Pull_Resistor #(.pull(1)) pull_resistor_111 (.node(pull_resistor_111_node));
  and and_147 (and_147_out, controlled_buffer_471_out, out_9);
  assign pull_resistor_110_node = and_145_out[1] ? controlled_buffer_1_out_2[1] : 1'bz;  // Controlled_Buffer controlled_buffer_469
  assign pull_resistor_110_node = and_145_out[0] ? controlled_buffer_1_out_2[0] : 1'bz;  // Controlled_Buffer controlled_buffer_470
  assign controlled_buffer_471_out = pull_resistor_110_node ? pull_resistor_110_node : 1'bz;  // Controlled_Buffer controlled_buffer_471
  and and_148 (and_148_out, not_100_out, pull_resistor_109_node);
  assign controlled_buffer_471_out = and_148_out ? and_148_out : 1'bz;  // Controlled_Buffer controlled_buffer_472
  assign controlled_buffer_471_out = not_97_out ? not_97_out : 1'bz;  // Controlled_Buffer controlled_buffer_473
  Pull_Resistor pull_resistor_112 (.node(controlled_buffer_471_out));
  assign pull_resistor_111_node = xor_33_out[0] ? ~xor_33_out[0] : 1'bz;  // Controlled_Inverter controlled_inverter_161
  assign pull_resistor_111_node = xor_33_out[1] ? ~xor_33_out[1] : 1'bz;  // Controlled_Inverter controlled_inverter_162
  assign pull_resistor_111_node = xor_33_out[2] ? ~xor_33_out[2] : 1'bz;  // Controlled_Inverter controlled_inverter_163
  assign pull_resistor_111_node = xor_33_out[3] ? ~xor_33_out[3] : 1'bz;  // Controlled_Inverter controlled_inverter_164
  assign pull_resistor_111_node = xor_33_out[4] ? ~xor_33_out[4] : 1'bz;  // Controlled_Inverter controlled_inverter_165
  assign pull_resistor_111_node = xor_33_out[5] ? ~xor_33_out[5] : 1'bz;  // Controlled_Inverter controlled_inverter_166
  assign pull_resistor_111_node = xor_33_out[6] ? ~xor_33_out[6] : 1'bz;  // Controlled_Inverter controlled_inverter_167
  assign pull_resistor_111_node = xor_33_out[7] ? ~xor_33_out[7] : 1'bz;  // Controlled_Inverter controlled_inverter_168
  assign pull_resistor_111_node = xor_33_out[8] ? ~xor_33_out[8] : 1'bz;  // Controlled_Inverter controlled_inverter_169
  assign pull_resistor_111_node = xor_33_out[9] ? ~xor_33_out[9] : 1'bz;  // Controlled_Inverter controlled_inverter_170
  assign pull_resistor_111_node = xor_33_out[10] ? ~xor_33_out[10] : 1'bz;  // Controlled_Inverter controlled_inverter_171
  assign pull_resistor_111_node = xor_33_out[11] ? ~xor_33_out[11] : 1'bz;  // Controlled_Inverter controlled_inverter_172
  assign pull_resistor_111_node = xor_33_out[12] ? ~xor_33_out[12] : 1'bz;  // Controlled_Inverter controlled_inverter_173
  assign pull_resistor_111_node = xor_33_out[13] ? ~xor_33_out[13] : 1'bz;  // Controlled_Inverter controlled_inverter_174
  assign pull_resistor_111_node = xor_33_out[14] ? ~xor_33_out[14] : 1'bz;  // Controlled_Inverter controlled_inverter_175
  assign pull_resistor_111_node = xor_33_out[15] ? ~xor_33_out[15] : 1'bz;  // Controlled_Inverter controlled_inverter_176
  assign out_10 = and_138_out ? nor_92_out : 8'bz;  // Controlled_Buffer controlled_buffer_474
  assign pull_resistor_1_node = and_138_out ? nor_90_out : 16'bz;  // Controlled_Buffer controlled_buffer_475
  assign controlled_buffer_471_out = pull_resistor_111_node ? pull_resistor_111_node : 1'bz;  // Controlled_Buffer controlled_buffer_476
  Pull_Resistor pull_resistor_113 (.node(pull_resistor_113_node));
  assign pull_resistor_113_node = 1'b0 ? 1'b0 : 1'bz;  // Controlled_Buffer controlled_buffer_477
  assign pull_resistor_113_node = 1'b0 ? 1'b0 : 1'bz;  // Controlled_Buffer controlled_buffer_478
  assign pull_resistor_113_node = 1'b0 ? 1'b0 : 1'bz;  // Controlled_Buffer controlled_buffer_479
  muxin8tor muxin8tor_12 (.in_2(and_160_out), .in_1(in_1), .out_3(muxin8tor_12_out_3), .out_4(muxin8tor_12_out_4));
  not not_103 (not_103_out, in_1);
  assign controlled_buffer_480_out = not_103_out ? nor_92_out : 8'bz;  // Controlled_Buffer controlled_buffer_480
  muxin16tor muxin16tor_12 (.in_2(and_160_out), .in_1(in_1), .out_3(muxin16tor_12_out_3), .out_4(muxin16tor_12_out_4));
  demuxin8tor demuxin8tor_12 (.in_2(nor_90_out), .in_3(8'hb), .in_1(in_1), .out_4(demuxin8tor_12_out_4));
  assign pull_resistor_113_node = 1'b0 ? 1'b0 : 1'bz;  // Controlled_Buffer controlled_buffer_481
  assign pull_resistor_113_node = 1'b1 ? 1'b1 : 1'bz;  // Controlled_Buffer controlled_buffer_482
  assign pull_resistor_113_node = 1'b0 ? 1'b0 : 1'bz;  // Controlled_Buffer controlled_buffer_483
  assign pull_resistor_113_node = 1'b1 ? 1'b1 : 1'bz;  // Controlled_Buffer controlled_buffer_484
  Pull_Resistor pull_resistor_114 (.node(controlled_buffer_480_out));
  assign buffer_108_out = controlled_buffer_480_out;  // Buffer buffer_108, 8 bits wide
  assign buffer_109_out = buffer_108_out;  // Buffer buffer_109, 8 bits wide
  assign {controlled_buffer_1_out_2, controlled_buffer_1_out} = and_149_out ? 8'hb : 8'bz;  // Controlled_Buffer controlled_buffer_485
  Pull_Resistor pull_resistor_115 (.node({controlled_buffer_1_out_2, controlled_buffer_1_out}));
  assign out_9 = and_149_out ? and_149_out : 1'bz;  // Controlled_Buffer controlled_buffer_486
  assign pull_resistor_113_node = 1'b1 ? 1'b1 : 1'bz;  // Controlled_Buffer controlled_buffer_487
  assign buffer_110_out = buffer_109_out;  // Buffer buffer_110, 8 bits wide
  assign not_104_out = ~buffer_109_out;  // NOT_Gate not_104, 8 bits wide
  assign buffer_111_out = demuxin8tor_12_out_4;  // Buffer buffer_111, 16 bits wide
  assign not_105_out = ~demuxin8tor_12_out_4;  // NOT_Gate not_105, 16 bits wide
  and and_149 (and_149_out, pull_resistor_121_node, and_1_out);
  Pull_Resistor pull_resistor_116 (.node(out_9));
  not not_106 (not_106_out, pull_resistor_113_node);
  assign xor_34_out = controlled_buffer_1_out_2 ^ 4'b0000;  // XOR_Gate xor_34, 4 bits wide
  assign xor_35_out = 4'b1011 ^ controlled_buffer_1_out;  // XOR_Gate xor_35, 4 bits wide
  assign and_150_out = buffer_110_out & muxin8tor_12_out_4;  // AND_Gate and_150, 8 bits wide
  assign nor_93_out = ~(and_150_out | nor_94_out);  // NOR_Gate nor_93, 8 bits wide
  assign and_151_out = muxin8tor_12_out_4 & not_104_out;  // AND_Gate and_151, 8 bits wide
  assign nor_94_out = ~(nor_93_out | and_151_out);  // NOR_Gate nor_94, 8 bits wide
  assign nor_95_out = ~(and_152_out | nor_96_out);  // NOR_Gate nor_95, 16 bits wide
  assign and_152_out = buffer_111_out & muxin16tor_12_out_4;  // AND_Gate and_152, 16 bits wide
  assign nor_96_out = ~(nor_95_out | and_153_out);  // NOR_Gate nor_96, 16 bits wide
  assign and_153_out = muxin16tor_12_out_4 & not_105_out;  // AND_Gate and_153, 16 bits wide
  assign buffer_112_out = nor_94_out;  // Buffer buffer_112, 8 bits wide
  assign not_107_out = ~nor_94_out;  // NOT_Gate not_107, 8 bits wide
  assign buffer_113_out = nor_96_out;  // Buffer buffer_113, 16 bits wide
  assign not_108_out = ~nor_96_out;  // NOT_Gate not_108, 16 bits wide
  assign controlled_buffer_502_out[1] = xor_34_out[1] ? xor_34_out[1] : 1'bz;  // Controlled_Buffer controlled_buffer_488
  assign controlled_buffer_502_out[1] = xor_34_out[2] ? xor_34_out[2] : 1'bz;  // Controlled_Buffer controlled_buffer_489
  assign controlled_buffer_502_out[1] = xor_34_out[3] ? xor_34_out[3] : 1'bz;  // Controlled_Buffer controlled_buffer_490
  assign controlled_buffer_502_out[2] = xor_34_out[2] ? xor_34_out[2] : 1'bz;  // Controlled_Buffer controlled_buffer_491
  assign controlled_buffer_502_out[2] = xor_34_out[3] ? xor_34_out[3] : 1'bz;  // Controlled_Buffer controlled_buffer_492
  assign controlled_buffer_493_out[0] = xor_35_out[0] ? xor_35_out[0] : 1'bz;  // Controlled_Buffer controlled_buffer_493
  assign controlled_buffer_493_out[1] = xor_35_out[1] ? xor_35_out[1] : 1'bz;  // Controlled_Buffer controlled_buffer_494
  assign controlled_buffer_493_out[0] = xor_35_out[1] ? xor_35_out[1] : 1'bz;  // Controlled_Buffer controlled_buffer_495
  assign controlled_buffer_493_out[1] = xor_35_out[2] ? xor_35_out[2] : 1'bz;  // Controlled_Buffer controlled_buffer_496
  assign controlled_buffer_493_out[0] = xor_35_out[2] ? xor_35_out[2] : 1'bz;  // Controlled_Buffer controlled_buffer_497
  assign controlled_buffer_493_out[1] = xor_35_out[3] ? xor_35_out[3] : 1'bz;  // Controlled_Buffer controlled_buffer_498
  assign controlled_buffer_493_out[0] = xor_35_out[3] ? xor_35_out[3] : 1'bz;  // Controlled_Buffer controlled_buffer_499
  assign controlled_buffer_493_out[2] = xor_35_out[2] ? xor_35_out[2] : 1'bz;  // Controlled_Buffer controlled_buffer_500
  Pull_Resistor pull_resistor_117 (.node({xor_35_out[3], controlled_buffer_493_out}));
  assign controlled_buffer_493_out[2] = xor_35_out[3] ? xor_35_out[3] : 1'bz;  // Controlled_Buffer controlled_buffer_501
  assign and_154_out = buffer_112_out & muxin8tor_12_out_3;  // AND_Gate and_154, 8 bits wide
  assign and_155_out = muxin8tor_12_out_3 & not_107_out;  // AND_Gate and_155, 8 bits wide
  assign and_156_out = buffer_113_out & muxin16tor_12_out_3;  // AND_Gate and_156, 16 bits wide
  assign and_157_out = muxin16tor_12_out_3 & not_108_out;  // AND_Gate and_157, 16 bits wide
  assign controlled_buffer_502_out[0] = xor_34_out[0] ? xor_34_out[0] : 1'bz;  // Controlled_Buffer controlled_buffer_502
  assign controlled_buffer_502_out[0] = xor_34_out[1] ? xor_34_out[1] : 1'bz;  // Controlled_Buffer controlled_buffer_503
  assign controlled_buffer_502_out[0] = xor_34_out[2] ? xor_34_out[2] : 1'bz;  // Controlled_Buffer controlled_buffer_504
  Pull_Resistor pull_resistor_118 (.node({xor_34_out[3], controlled_buffer_502_out}));
  assign controlled_buffer_502_out[0] = xor_34_out[3] ? xor_34_out[3] : 1'bz;  // Controlled_Buffer controlled_buffer_505
  not not_109 (not_109_out, controlled_buffer_502_out[0]);
  assign buffer_114_out = {xor_35_out[3], controlled_buffer_493_out};  // Buffer buffer_114, 4 bits wide
  assign nor_97_out = ~(and_154_out | nor_98_out);  // NOR_Gate nor_97, 8 bits wide
  assign nor_98_out = ~(nor_97_out | and_155_out);  // NOR_Gate nor_98, 8 bits wide
  assign nor_99_out = ~(and_156_out | nor_100_out);  // NOR_Gate nor_99, 16 bits wide
  assign nor_100_out = ~(nor_99_out | and_157_out);  // NOR_Gate nor_100, 16 bits wide
  assign and_158_out = buffer_115_out & not_110_out;  // AND_Gate and_158, 4 bits wide
  assign buffer_115_out = {xor_34_out[3], controlled_buffer_502_out};  // Buffer buffer_115, 4 bits wide
  Pull_Resistor pull_resistor_119 (.node(pull_resistor_119_node));
  assign not_110_out = ~{1'b0, xor_34_out[3], controlled_buffer_502_out[2:1]};  // NOT_Gate not_110, 4 bits wide
  assign pull_resistor_119_node = and_158_out[3] ? controlled_buffer_1_out_2[3] : 1'bz;  // Controlled_Buffer controlled_buffer_506
  assign and_159_out = buffer_114_out & not_111_out;  // AND_Gate and_159, 4 bits wide
  Pull_Resistor pull_resistor_120 (.node(pull_resistor_120_node));
  assign pull_resistor_120_node = and_159_out[3] ? controlled_buffer_1_out[3] : 1'bz;  // Controlled_Buffer controlled_buffer_507
  assign pull_resistor_120_node = and_159_out[2] ? controlled_buffer_1_out[2] : 1'bz;  // Controlled_Buffer controlled_buffer_508
  assign pull_resistor_120_node = and_159_out[1] ? controlled_buffer_1_out[1] : 1'bz;  // Controlled_Buffer controlled_buffer_509
  assign pull_resistor_120_node = and_159_out[0] ? controlled_buffer_1_out[0] : 1'bz;  // Controlled_Buffer controlled_buffer_510
  assign not_111_out = ~{1'b0, xor_35_out[3], controlled_buffer_493_out[2:1]};  // NOT_Gate not_111, 4 bits wide
  assign xor_36_out = nor_100_out ^ buffer_2_out;  // XOR_Gate xor_36, 16 bits wide
  Pull_Resistor #(.pull(1)) pull_resistor_121 (.node(pull_resistor_121_node));
  and and_160 (and_160_out, controlled_buffer_514_out, out_9);
  assign pull_resistor_119_node = and_158_out[2] ? controlled_buffer_1_out_2[2] : 1'bz;  // Controlled_Buffer controlled_buffer_511
  assign pull_resistor_119_node = and_158_out[1] ? controlled_buffer_1_out_2[1] : 1'bz;  // Controlled_Buffer controlled_buffer_512
  assign pull_resistor_119_node = and_158_out[0] ? controlled_buffer_1_out_2[0] : 1'bz;  // Controlled_Buffer controlled_buffer_513
  assign controlled_buffer_514_out = pull_resistor_119_node ? pull_resistor_119_node : 1'bz;  // Controlled_Buffer controlled_buffer_514
  and and_161 (and_161_out, not_109_out, pull_resistor_120_node);
  assign controlled_buffer_514_out = and_161_out ? and_161_out : 1'bz;  // Controlled_Buffer controlled_buffer_515
  assign controlled_buffer_514_out = not_106_out ? not_106_out : 1'bz;  // Controlled_Buffer controlled_buffer_516
  Pull_Resistor pull_resistor_122 (.node(controlled_buffer_514_out));
  assign out_10 = and_149_out ? nor_98_out : 8'bz;  // Controlled_Buffer controlled_buffer_517
  assign pull_resistor_1_node = and_149_out ? nor_100_out : 16'bz;  // Controlled_Buffer controlled_buffer_518
  assign pull_resistor_121_node = xor_36_out[0] ? ~xor_36_out[0] : 1'bz;  // Controlled_Inverter controlled_inverter_177
  assign pull_resistor_121_node = xor_36_out[1] ? ~xor_36_out[1] : 1'bz;  // Controlled_Inverter controlled_inverter_178
  assign pull_resistor_121_node = xor_36_out[2] ? ~xor_36_out[2] : 1'bz;  // Controlled_Inverter controlled_inverter_179
  assign pull_resistor_121_node = xor_36_out[3] ? ~xor_36_out[3] : 1'bz;  // Controlled_Inverter controlled_inverter_180
  assign pull_resistor_121_node = xor_36_out[4] ? ~xor_36_out[4] : 1'bz;  // Controlled_Inverter controlled_inverter_181
  assign pull_resistor_121_node = xor_36_out[5] ? ~xor_36_out[5] : 1'bz;  // Controlled_Inverter controlled_inverter_182
  assign pull_resistor_121_node = xor_36_out[6] ? ~xor_36_out[6] : 1'bz;  // Controlled_Inverter controlled_inverter_183
  assign pull_resistor_121_node = xor_36_out[7] ? ~xor_36_out[7] : 1'bz;  // Controlled_Inverter controlled_inverter_184
  assign pull_resistor_121_node = xor_36_out[8] ? ~xor_36_out[8] : 1'bz;  // Controlled_Inverter controlled_inverter_185
  assign pull_resistor_121_node = xor_36_out[9] ? ~xor_36_out[9] : 1'bz;  // Controlled_Inverter controlled_inverter_186
  assign pull_resistor_121_node = xor_36_out[10] ? ~xor_36_out[10] : 1'bz;  // Controlled_Inverter controlled_inverter_187
  assign pull_resistor_121_node = xor_36_out[11] ? ~xor_36_out[11] : 1'bz;  // Controlled_Inverter controlled_inverter_188
  assign pull_resistor_121_node = xor_36_out[12] ? ~xor_36_out[12] : 1'bz;  // Controlled_Inverter controlled_inverter_189
  assign pull_resistor_121_node = xor_36_out[13] ? ~xor_36_out[13] : 1'bz;  // Controlled_Inverter controlled_inverter_190
  assign pull_resistor_121_node = xor_36_out[14] ? ~xor_36_out[14] : 1'bz;  // Controlled_Inverter controlled_inverter_191
  assign pull_resistor_121_node = xor_36_out[15] ? ~xor_36_out[15] : 1'bz;  // Controlled_Inverter controlled_inverter_192
  assign controlled_buffer_514_out = pull_resistor_121_node ? pull_resistor_121_node : 1'bz;  // Controlled_Buffer controlled_buffer_519
  Pull_Resistor pull_resistor_123 (.node(pull_resistor_123_node));
  assign pull_resistor_123_node = 1'b0 ? 1'b0 : 1'bz;  // Controlled_Buffer controlled_buffer_520
  assign pull_resistor_123_node = 1'b0 ? 1'b0 : 1'bz;  // Controlled_Buffer controlled_buffer_521
  assign pull_resistor_123_node = 1'b0 ? 1'b0 : 1'bz;  // Controlled_Buffer controlled_buffer_522
  not not_112 (not_112_out, in_1);
  assign controlled_buffer_523_out = not_112_out ? nor_98_out : 8'bz;  // Controlled_Buffer controlled_buffer_523
  assign pull_resistor_123_node = 1'b0 ? 1'b0 : 1'bz;  // Controlled_Buffer controlled_buffer_524
  assign pull_resistor_123_node = 1'b1 ? 1'b1 : 1'bz;  // Controlled_Buffer controlled_buffer_525
  assign pull_resistor_123_node = 1'b1 ? 1'b1 : 1'bz;  // Controlled_Buffer controlled_buffer_526
  assign pull_resistor_123_node = 1'b0 ? 1'b0 : 1'bz;  // Controlled_Buffer controlled_buffer_527
  muxin8tor muxin8tor_13 (.in_2(and_174_out), .in_1(in_1), .out_3(muxin8tor_13_out_3), .out_4(muxin8tor_13_out_4));
  Pull_Resistor pull_resistor_124 (.node(controlled_buffer_523_out));
  assign buffer_116_out = controlled_buffer_523_out;  // Buffer buffer_116, 8 bits wide
  assign buffer_117_out = buffer_116_out;  // Buffer buffer_117, 8 bits wide
  muxin16tor muxin16tor_13 (.in_2(and_174_out), .in_1(in_1), .out_3(muxin16tor_13_out_3), .out_4(muxin16tor_13_out_4));
  demuxin8tor demuxin8tor_13 (.in_2(nor_100_out), .in_3(8'hc), .in_1(in_1), .out_4(demuxin8tor_13_out_4));
  assign {controlled_buffer_1_out_2, controlled_buffer_1_out} = and_162_out ? 8'hc : 8'bz;  // Controlled_Buffer controlled_buffer_528
  Pull_Resistor pull_resistor_125 (.node({controlled_buffer_1_out_2, controlled_buffer_1_out}));
  assign out_9 = and_162_out ? and_162_out : 1'bz;  // Controlled_Buffer controlled_buffer_529
  assign pull_resistor_123_node = 1'b0 ? 1'b0 : 1'bz;  // Controlled_Buffer controlled_buffer_530
  assign buffer_118_out = buffer_117_out;  // Buffer buffer_118, 8 bits wide
  assign not_113_out = ~buffer_117_out;  // NOT_Gate not_113, 8 bits wide
  assign buffer_119_out = demuxin8tor_13_out_4;  // Buffer buffer_119, 16 bits wide
  assign not_114_out = ~demuxin8tor_13_out_4;  // NOT_Gate not_114, 16 bits wide
  and and_162 (and_162_out, pull_resistor_131_node, and_1_out);
  Pull_Resistor pull_resistor_126 (.node(out_9));
  not not_115 (not_115_out, pull_resistor_123_node);
  assign xor_37_out = controlled_buffer_1_out_2 ^ 4'b0000;  // XOR_Gate xor_37, 4 bits wide
  assign xor_38_out = 4'b1100 ^ controlled_buffer_1_out;  // XOR_Gate xor_38, 4 bits wide
  assign and_163_out = buffer_118_out & muxin8tor_13_out_4;  // AND_Gate and_163, 8 bits wide
  assign and_164_out = muxin8tor_13_out_4 & not_113_out;  // AND_Gate and_164, 8 bits wide
  assign and_165_out = buffer_119_out & muxin16tor_13_out_4;  // AND_Gate and_165, 16 bits wide
  assign and_166_out = muxin16tor_13_out_4 & not_114_out;  // AND_Gate and_166, 16 bits wide
  assign nor_101_out = ~(and_163_out | nor_102_out);  // NOR_Gate nor_101, 8 bits wide
  assign buffer_120_out = nor_102_out;  // Buffer buffer_120, 8 bits wide
  assign nor_102_out = ~(nor_101_out | and_164_out);  // NOR_Gate nor_102, 8 bits wide
  assign not_116_out = ~nor_102_out;  // NOT_Gate not_116, 8 bits wide
  assign buffer_121_out = nor_104_out;  // Buffer buffer_121, 16 bits wide
  assign nor_103_out = ~(and_165_out | nor_104_out);  // NOR_Gate nor_103, 16 bits wide
  assign nor_104_out = ~(nor_103_out | and_166_out);  // NOR_Gate nor_104, 16 bits wide
  assign not_117_out = ~nor_104_out;  // NOT_Gate not_117, 16 bits wide
  assign controlled_buffer_545_out[1] = xor_37_out[1] ? xor_37_out[1] : 1'bz;  // Controlled_Buffer controlled_buffer_531
  assign controlled_buffer_545_out[1] = xor_37_out[2] ? xor_37_out[2] : 1'bz;  // Controlled_Buffer controlled_buffer_532
  assign controlled_buffer_545_out[1] = xor_37_out[3] ? xor_37_out[3] : 1'bz;  // Controlled_Buffer controlled_buffer_533
  assign controlled_buffer_545_out[2] = xor_37_out[2] ? xor_37_out[2] : 1'bz;  // Controlled_Buffer controlled_buffer_534
  assign controlled_buffer_545_out[2] = xor_37_out[3] ? xor_37_out[3] : 1'bz;  // Controlled_Buffer controlled_buffer_535
  assign controlled_buffer_536_out[0] = xor_38_out[0] ? xor_38_out[0] : 1'bz;  // Controlled_Buffer controlled_buffer_536
  assign controlled_buffer_536_out[1] = xor_38_out[1] ? xor_38_out[1] : 1'bz;  // Controlled_Buffer controlled_buffer_537
  assign controlled_buffer_536_out[0] = xor_38_out[1] ? xor_38_out[1] : 1'bz;  // Controlled_Buffer controlled_buffer_538
  assign controlled_buffer_536_out[1] = xor_38_out[2] ? xor_38_out[2] : 1'bz;  // Controlled_Buffer controlled_buffer_539
  assign controlled_buffer_536_out[0] = xor_38_out[2] ? xor_38_out[2] : 1'bz;  // Controlled_Buffer controlled_buffer_540
  assign controlled_buffer_536_out[1] = xor_38_out[3] ? xor_38_out[3] : 1'bz;  // Controlled_Buffer controlled_buffer_541
  assign controlled_buffer_536_out[0] = xor_38_out[3] ? xor_38_out[3] : 1'bz;  // Controlled_Buffer controlled_buffer_542
  assign controlled_buffer_536_out[2] = xor_38_out[2] ? xor_38_out[2] : 1'bz;  // Controlled_Buffer controlled_buffer_543
  Pull_Resistor pull_resistor_127 (.node({xor_38_out[3], controlled_buffer_536_out}));
  assign controlled_buffer_536_out[2] = xor_38_out[3] ? xor_38_out[3] : 1'bz;  // Controlled_Buffer controlled_buffer_544
  assign and_167_out = buffer_120_out & muxin8tor_13_out_3;  // AND_Gate and_167, 8 bits wide
  assign and_168_out = muxin8tor_13_out_3 & not_116_out;  // AND_Gate and_168, 8 bits wide
  assign and_169_out = buffer_121_out & muxin16tor_13_out_3;  // AND_Gate and_169, 16 bits wide
  assign and_170_out = muxin16tor_13_out_3 & not_117_out;  // AND_Gate and_170, 16 bits wide
  assign controlled_buffer_545_out[0] = xor_37_out[0] ? xor_37_out[0] : 1'bz;  // Controlled_Buffer controlled_buffer_545
  assign controlled_buffer_545_out[0] = xor_37_out[1] ? xor_37_out[1] : 1'bz;  // Controlled_Buffer controlled_buffer_546
  assign controlled_buffer_545_out[0] = xor_37_out[2] ? xor_37_out[2] : 1'bz;  // Controlled_Buffer controlled_buffer_547
  Pull_Resistor pull_resistor_128 (.node({xor_37_out[3], controlled_buffer_545_out}));
  assign controlled_buffer_545_out[0] = xor_37_out[3] ? xor_37_out[3] : 1'bz;  // Controlled_Buffer controlled_buffer_548
  not not_118 (not_118_out, controlled_buffer_545_out[0]);
  assign buffer_122_out = {xor_38_out[3], controlled_buffer_536_out};  // Buffer buffer_122, 4 bits wide
  assign nor_105_out = ~(and_167_out | nor_106_out);  // NOR_Gate nor_105, 8 bits wide
  assign nor_106_out = ~(nor_105_out | and_168_out);  // NOR_Gate nor_106, 8 bits wide
  assign nor_107_out = ~(and_169_out | nor_108_out);  // NOR_Gate nor_107, 16 bits wide
  assign nor_108_out = ~(nor_107_out | and_170_out);  // NOR_Gate nor_108, 16 bits wide
  assign and_171_out = buffer_123_out & not_119_out;  // AND_Gate and_171, 4 bits wide
  assign buffer_123_out = {xor_37_out[3], controlled_buffer_545_out};  // Buffer buffer_123, 4 bits wide
  Pull_Resistor pull_resistor_129 (.node(pull_resistor_129_node));
  assign not_119_out = ~{1'b0, xor_37_out[3], controlled_buffer_545_out[2:1]};  // NOT_Gate not_119, 4 bits wide
  assign pull_resistor_129_node = and_171_out[3] ? controlled_buffer_1_out_2[3] : 1'bz;  // Controlled_Buffer controlled_buffer_549
  assign and_172_out = buffer_122_out & not_120_out;  // AND_Gate and_172, 4 bits wide
  Pull_Resistor pull_resistor_130 (.node(pull_resistor_130_node));
  assign pull_resistor_130_node = and_172_out[3] ? controlled_buffer_1_out[3] : 1'bz;  // Controlled_Buffer controlled_buffer_550
  assign pull_resistor_130_node = and_172_out[2] ? controlled_buffer_1_out[2] : 1'bz;  // Controlled_Buffer controlled_buffer_551
  assign pull_resistor_130_node = and_172_out[1] ? controlled_buffer_1_out[1] : 1'bz;  // Controlled_Buffer controlled_buffer_552
  assign not_120_out = ~{1'b0, xor_38_out[3], controlled_buffer_536_out[2:1]};  // NOT_Gate not_120, 4 bits wide
  assign xor_39_out = nor_108_out ^ buffer_2_out;  // XOR_Gate xor_39, 16 bits wide
  Pull_Resistor #(.pull(1)) pull_resistor_131 (.node(pull_resistor_131_node));
  assign pull_resistor_129_node = and_171_out[2] ? controlled_buffer_1_out_2[2] : 1'bz;  // Controlled_Buffer controlled_buffer_553
  assign pull_resistor_129_node = and_171_out[1] ? controlled_buffer_1_out_2[1] : 1'bz;  // Controlled_Buffer controlled_buffer_554
  assign pull_resistor_129_node = and_171_out[0] ? controlled_buffer_1_out_2[0] : 1'bz;  // Controlled_Buffer controlled_buffer_555
  assign controlled_buffer_556_out = pull_resistor_129_node ? pull_resistor_129_node : 1'bz;  // Controlled_Buffer controlled_buffer_556
  and and_173 (and_173_out, not_118_out, pull_resistor_130_node);
  assign controlled_buffer_556_out = and_173_out ? and_173_out : 1'bz;  // Controlled_Buffer controlled_buffer_557
  assign controlled_buffer_556_out = not_115_out ? not_115_out : 1'bz;  // Controlled_Buffer controlled_buffer_558
  Pull_Resistor pull_resistor_132 (.node(controlled_buffer_556_out));
  assign pull_resistor_130_node = and_172_out[0] ? controlled_buffer_1_out[0] : 1'bz;  // Controlled_Buffer controlled_buffer_559
  and and_174 (and_174_out, controlled_buffer_556_out, out_9);
  assign out_10 = and_162_out ? nor_106_out : 8'bz;  // Controlled_Buffer controlled_buffer_560
  assign pull_resistor_131_node = xor_39_out[0] ? ~xor_39_out[0] : 1'bz;  // Controlled_Inverter controlled_inverter_193
  assign pull_resistor_131_node = xor_39_out[1] ? ~xor_39_out[1] : 1'bz;  // Controlled_Inverter controlled_inverter_194
  assign pull_resistor_131_node = xor_39_out[2] ? ~xor_39_out[2] : 1'bz;  // Controlled_Inverter controlled_inverter_195
  assign pull_resistor_131_node = xor_39_out[3] ? ~xor_39_out[3] : 1'bz;  // Controlled_Inverter controlled_inverter_196
  assign pull_resistor_131_node = xor_39_out[4] ? ~xor_39_out[4] : 1'bz;  // Controlled_Inverter controlled_inverter_197
  assign pull_resistor_131_node = xor_39_out[5] ? ~xor_39_out[5] : 1'bz;  // Controlled_Inverter controlled_inverter_198
  assign pull_resistor_131_node = xor_39_out[6] ? ~xor_39_out[6] : 1'bz;  // Controlled_Inverter controlled_inverter_199
  assign pull_resistor_131_node = xor_39_out[7] ? ~xor_39_out[7] : 1'bz;  // Controlled_Inverter controlled_inverter_200
  assign pull_resistor_131_node = xor_39_out[8] ? ~xor_39_out[8] : 1'bz;  // Controlled_Inverter controlled_inverter_201
  assign pull_resistor_131_node = xor_39_out[9] ? ~xor_39_out[9] : 1'bz;  // Controlled_Inverter controlled_inverter_202
  assign pull_resistor_131_node = xor_39_out[10] ? ~xor_39_out[10] : 1'bz;  // Controlled_Inverter controlled_inverter_203
  assign pull_resistor_131_node = xor_39_out[11] ? ~xor_39_out[11] : 1'bz;  // Controlled_Inverter controlled_inverter_204
  assign pull_resistor_131_node = xor_39_out[12] ? ~xor_39_out[12] : 1'bz;  // Controlled_Inverter controlled_inverter_205
  assign pull_resistor_131_node = xor_39_out[13] ? ~xor_39_out[13] : 1'bz;  // Controlled_Inverter controlled_inverter_206
  assign pull_resistor_131_node = xor_39_out[14] ? ~xor_39_out[14] : 1'bz;  // Controlled_Inverter controlled_inverter_207
  assign pull_resistor_131_node = xor_39_out[15] ? ~xor_39_out[15] : 1'bz;  // Controlled_Inverter controlled_inverter_208
  assign controlled_buffer_556_out = pull_resistor_131_node ? pull_resistor_131_node : 1'bz;  // Controlled_Buffer controlled_buffer_561
  assign pull_resistor_1_node = and_162_out ? nor_108_out : 16'bz;  // Controlled_Buffer controlled_buffer_562
  Pull_Resistor pull_resistor_133 (.node(pull_resistor_133_node));
  assign pull_resistor_133_node = 1'b0 ? 1'b0 : 1'bz;  // Controlled_Buffer controlled_buffer_563
  assign pull_resistor_133_node = 1'b0 ? 1'b0 : 1'bz;  // Controlled_Buffer controlled_buffer_564
  not not_121 (not_121_out, in_1);
  assign pull_resistor_133_node = 1'b0 ? 1'b0 : 1'bz;  // Controlled_Buffer controlled_buffer_565
  assign pull_resistor_133_node = 1'b0 ? 1'b0 : 1'bz;  // Controlled_Buffer controlled_buffer_566
  assign pull_resistor_133_node = 1'b1 ? 1'b1 : 1'bz;  // Controlled_Buffer controlled_buffer_567
  assign pull_resistor_133_node = 1'b1 ? 1'b1 : 1'bz;  // Controlled_Buffer controlled_buffer_568
  muxin8tor muxin8tor_14 (.in_2(and_187_out), .in_1(in_1), .out_3(muxin8tor_14_out_3), .out_4(muxin8tor_14_out_4));
  Pull_Resistor pull_resistor_134 (.node(pull_resistor_134_node));
  assign pull_resistor_134_node = not_121_out ? nor_106_out : 8'bz;  // Controlled_Buffer controlled_buffer_569
  assign buffer_124_out = pull_resistor_134_node;  // Buffer buffer_124, 8 bits wide
  assign buffer_125_out = buffer_124_out;  // Buffer buffer_125, 8 bits wide
  muxin16tor muxin16tor_14 (.in_2(and_187_out), .in_1(in_1), .out_3(muxin16tor_14_out_3), .out_4(muxin16tor_14_out_4));
  demuxin8tor demuxin8tor_14 (.in_2(nor_108_out), .in_3(8'hd), .in_1(in_1), .out_4(demuxin8tor_14_out_4));
  assign {controlled_buffer_1_out_2, controlled_buffer_1_out} = and_179_out ? 8'hd : 8'bz;  // Controlled_Buffer controlled_buffer_570
  Pull_Resistor pull_resistor_135 (.node({controlled_buffer_1_out_2, controlled_buffer_1_out}));
  assign pull_resistor_133_node = 1'b0 ? 1'b0 : 1'bz;  // Controlled_Buffer controlled_buffer_571
  assign pull_resistor_133_node = 1'b1 ? 1'b1 : 1'bz;  // Controlled_Buffer controlled_buffer_572
  assign buffer_126_out = buffer_125_out;  // Buffer buffer_126, 8 bits wide
  assign not_122_out = ~buffer_125_out;  // NOT_Gate not_122, 8 bits wide
  assign buffer_127_out = demuxin8tor_14_out_4;  // Buffer buffer_127, 16 bits wide
  assign not_123_out = ~demuxin8tor_14_out_4;  // NOT_Gate not_123, 16 bits wide
  Pull_Resistor pull_resistor_136 (.node(out_9));
  assign out_9 = and_179_out ? and_179_out : 1'bz;  // Controlled_Buffer controlled_buffer_573
  assign xor_40_out = controlled_buffer_1_out_2 ^ 4'b0000;  // XOR_Gate xor_40, 4 bits wide
  assign xor_41_out = 4'b1101 ^ controlled_buffer_1_out;  // XOR_Gate xor_41, 4 bits wide
  assign and_175_out = buffer_126_out & muxin8tor_14_out_4;  // AND_Gate and_175, 8 bits wide
  assign and_176_out = muxin8tor_14_out_4 & not_122_out;  // AND_Gate and_176, 8 bits wide
  assign and_177_out = buffer_127_out & muxin16tor_14_out_4;  // AND_Gate and_177, 16 bits wide
  assign and_178_out = muxin16tor_14_out_4 & not_123_out;  // AND_Gate and_178, 16 bits wide
  and and_179 (and_179_out, pull_resistor_142_node, and_1_out);
  not not_124 (not_124_out, pull_resistor_133_node);
  assign nor_109_out = ~(and_175_out | nor_110_out);  // NOR_Gate nor_109, 8 bits wide
  assign buffer_128_out = nor_110_out;  // Buffer buffer_128, 8 bits wide
  assign nor_110_out = ~(nor_109_out | and_176_out);  // NOR_Gate nor_110, 8 bits wide
  assign buffer_129_out = nor_112_out;  // Buffer buffer_129, 16 bits wide
  assign nor_111_out = ~(and_177_out | nor_112_out);  // NOR_Gate nor_111, 16 bits wide
  assign nor_112_out = ~(nor_111_out | and_178_out);  // NOR_Gate nor_112, 16 bits wide
  assign controlled_buffer_584_out[1] = xor_40_out[1] ? xor_40_out[1] : 1'bz;  // Controlled_Buffer controlled_buffer_574
  assign controlled_buffer_584_out[1] = xor_40_out[2] ? xor_40_out[2] : 1'bz;  // Controlled_Buffer controlled_buffer_575
  assign controlled_buffer_584_out[1] = xor_40_out[3] ? xor_40_out[3] : 1'bz;  // Controlled_Buffer controlled_buffer_576
  assign controlled_buffer_584_out[2] = xor_40_out[2] ? xor_40_out[2] : 1'bz;  // Controlled_Buffer controlled_buffer_577
  assign controlled_buffer_584_out[2] = xor_40_out[3] ? xor_40_out[3] : 1'bz;  // Controlled_Buffer controlled_buffer_578
  assign controlled_buffer_588_out[1] = xor_41_out[1] ? xor_41_out[1] : 1'bz;  // Controlled_Buffer controlled_buffer_579
  assign controlled_buffer_588_out[1] = xor_41_out[2] ? xor_41_out[2] : 1'bz;  // Controlled_Buffer controlled_buffer_580
  assign controlled_buffer_588_out[1] = xor_41_out[3] ? xor_41_out[3] : 1'bz;  // Controlled_Buffer controlled_buffer_581
  assign controlled_buffer_588_out[2] = xor_41_out[2] ? xor_41_out[2] : 1'bz;  // Controlled_Buffer controlled_buffer_582
  assign controlled_buffer_588_out[2] = xor_41_out[3] ? xor_41_out[3] : 1'bz;  // Controlled_Buffer controlled_buffer_583
  assign and_180_out = buffer_128_out & muxin8tor_14_out_3;  // AND_Gate and_180, 8 bits wide
  assign and_181_out = muxin8tor_14_out_3 & not_125_out;  // AND_Gate and_181, 8 bits wide
  assign not_125_out = ~nor_110_out;  // NOT_Gate not_125, 8 bits wide
  assign and_182_out = buffer_129_out & muxin16tor_14_out_3;  // AND_Gate and_182, 16 bits wide
  assign and_183_out = muxin16tor_14_out_3 & not_126_out;  // AND_Gate and_183, 16 bits wide
  assign not_126_out = ~nor_112_out;  // NOT_Gate not_126, 16 bits wide
  assign controlled_buffer_584_out[0] = xor_40_out[0] ? xor_40_out[0] : 1'bz;  // Controlled_Buffer controlled_buffer_584
  assign controlled_buffer_584_out[0] = xor_40_out[1] ? xor_40_out[1] : 1'bz;  // Controlled_Buffer controlled_buffer_585
  assign controlled_buffer_584_out[0] = xor_40_out[2] ? xor_40_out[2] : 1'bz;  // Controlled_Buffer controlled_buffer_586
  assign controlled_buffer_584_out[0] = xor_40_out[3] ? xor_40_out[3] : 1'bz;  // Controlled_Buffer controlled_buffer_587
  not not_127 (not_127_out, controlled_buffer_584_out[0]);
  assign controlled_buffer_588_out[0] = xor_41_out[0] ? xor_41_out[0] : 1'bz;  // Controlled_Buffer controlled_buffer_588
  assign controlled_buffer_588_out[0] = xor_41_out[1] ? xor_41_out[1] : 1'bz;  // Controlled_Buffer controlled_buffer_589
  assign controlled_buffer_588_out[0] = xor_41_out[2] ? xor_41_out[2] : 1'bz;  // Controlled_Buffer controlled_buffer_590
  assign controlled_buffer_588_out[0] = xor_41_out[3] ? xor_41_out[3] : 1'bz;  // Controlled_Buffer controlled_buffer_591
  Pull_Resistor pull_resistor_137 (.node({xor_41_out[3], controlled_buffer_588_out}));
  assign nor_113_out = ~(and_180_out | nor_114_out);  // NOR_Gate nor_113, 8 bits wide
  assign nor_114_out = ~(nor_113_out | and_181_out);  // NOR_Gate nor_114, 8 bits wide
  assign nor_115_out = ~(and_182_out | nor_116_out);  // NOR_Gate nor_115, 16 bits wide
  assign nor_116_out = ~(nor_115_out | and_183_out);  // NOR_Gate nor_116, 16 bits wide
  assign buffer_130_out = {xor_40_out[3], controlled_buffer_584_out};  // Buffer buffer_130, 4 bits wide
  Pull_Resistor pull_resistor_138 (.node({xor_40_out[3], controlled_buffer_584_out}));
  Pull_Resistor pull_resistor_139 (.node(pull_resistor_139_node));
  assign not_128_out = ~{1'b0, xor_40_out[3], controlled_buffer_584_out[2:1]};  // NOT_Gate not_128, 4 bits wide
  assign and_184_out = buffer_131_out & not_129_out;  // AND_Gate and_184, 4 bits wide
  assign buffer_131_out = {xor_41_out[3], controlled_buffer_588_out};  // Buffer buffer_131, 4 bits wide
  Pull_Resistor pull_resistor_140 (.node(pull_resistor_140_node));
  assign pull_resistor_140_node = and_184_out[3] ? controlled_buffer_1_out[3] : 1'bz;  // Controlled_Buffer controlled_buffer_592
  assign pull_resistor_140_node = and_184_out[2] ? controlled_buffer_1_out[2] : 1'bz;  // Controlled_Buffer controlled_buffer_593
  assign pull_resistor_140_node = and_184_out[1] ? controlled_buffer_1_out[1] : 1'bz;  // Controlled_Buffer controlled_buffer_594
  assign not_129_out = ~{1'b0, xor_41_out[3], controlled_buffer_588_out[2:1]};  // NOT_Gate not_129, 4 bits wide
  assign xor_42_out = nor_116_out ^ buffer_2_out;  // XOR_Gate xor_42, 16 bits wide
  assign and_185_out = buffer_130_out & not_128_out;  // AND_Gate and_185, 4 bits wide
  assign pull_resistor_139_node = and_185_out[3] ? controlled_buffer_1_out_2[3] : 1'bz;  // Controlled_Buffer controlled_buffer_595
  assign pull_resistor_139_node = and_185_out[2] ? controlled_buffer_1_out_2[2] : 1'bz;  // Controlled_Buffer controlled_buffer_596
  assign pull_resistor_139_node = and_185_out[1] ? controlled_buffer_1_out_2[1] : 1'bz;  // Controlled_Buffer controlled_buffer_597
  assign pull_resistor_139_node = and_185_out[0] ? controlled_buffer_1_out_2[0] : 1'bz;  // Controlled_Buffer controlled_buffer_598
  assign controlled_buffer_599_out = pull_resistor_139_node ? pull_resistor_139_node : 1'bz;  // Controlled_Buffer controlled_buffer_599
  and and_186 (and_186_out, not_127_out, pull_resistor_140_node);
  assign controlled_buffer_599_out = and_186_out ? and_186_out : 1'bz;  // Controlled_Buffer controlled_buffer_600
  Pull_Resistor pull_resistor_141 (.node(controlled_buffer_599_out));
  assign pull_resistor_140_node = and_184_out[0] ? controlled_buffer_1_out[0] : 1'bz;  // Controlled_Buffer controlled_buffer_601
  Pull_Resistor #(.pull(1)) pull_resistor_142 (.node(pull_resistor_142_node));
  and and_187 (and_187_out, controlled_buffer_599_out, out_9);
  assign controlled_buffer_599_out = not_124_out ? not_124_out : 1'bz;  // Controlled_Buffer controlled_buffer_602
  assign out_10 = and_179_out ? nor_114_out : 8'bz;  // Controlled_Buffer controlled_buffer_603
  assign pull_resistor_142_node = xor_42_out[0] ? ~xor_42_out[0] : 1'bz;  // Controlled_Inverter controlled_inverter_209
  assign pull_resistor_142_node = xor_42_out[1] ? ~xor_42_out[1] : 1'bz;  // Controlled_Inverter controlled_inverter_210
  assign pull_resistor_142_node = xor_42_out[2] ? ~xor_42_out[2] : 1'bz;  // Controlled_Inverter controlled_inverter_211
  assign pull_resistor_142_node = xor_42_out[3] ? ~xor_42_out[3] : 1'bz;  // Controlled_Inverter controlled_inverter_212
  assign pull_resistor_142_node = xor_42_out[4] ? ~xor_42_out[4] : 1'bz;  // Controlled_Inverter controlled_inverter_213
  assign pull_resistor_142_node = xor_42_out[5] ? ~xor_42_out[5] : 1'bz;  // Controlled_Inverter controlled_inverter_214
  assign pull_resistor_142_node = xor_42_out[6] ? ~xor_42_out[6] : 1'bz;  // Controlled_Inverter controlled_inverter_215
  assign pull_resistor_142_node = xor_42_out[7] ? ~xor_42_out[7] : 1'bz;  // Controlled_Inverter controlled_inverter_216
  assign pull_resistor_142_node = xor_42_out[8] ? ~xor_42_out[8] : 1'bz;  // Controlled_Inverter controlled_inverter_217
  assign pull_resistor_142_node = xor_42_out[9] ? ~xor_42_out[9] : 1'bz;  // Controlled_Inverter controlled_inverter_218
  assign pull_resistor_142_node = xor_42_out[10] ? ~xor_42_out[10] : 1'bz;  // Controlled_Inverter controlled_inverter_219
  assign pull_resistor_142_node = xor_42_out[11] ? ~xor_42_out[11] : 1'bz;  // Controlled_Inverter controlled_inverter_220
  assign pull_resistor_142_node = xor_42_out[12] ? ~xor_42_out[12] : 1'bz;  // Controlled_Inverter controlled_inverter_221
  assign pull_resistor_142_node = xor_42_out[13] ? ~xor_42_out[13] : 1'bz;  // Controlled_Inverter controlled_inverter_222
  assign pull_resistor_142_node = xor_42_out[14] ? ~xor_42_out[14] : 1'bz;  // Controlled_Inverter controlled_inverter_223
  assign pull_resistor_142_node = xor_42_out[15] ? ~xor_42_out[15] : 1'bz;  // Controlled_Inverter controlled_inverter_224
  assign controlled_buffer_599_out = pull_resistor_142_node ? pull_resistor_142_node : 1'bz;  // Controlled_Buffer controlled_buffer_604
  assign pull_resistor_1_node = and_179_out ? nor_116_out : 16'bz;  // Controlled_Buffer controlled_buffer_605
  Pull_Resistor pull_resistor_143 (.node(pull_resistor_143_node));
  assign pull_resistor_143_node = 1'b0 ? 1'b0 : 1'bz;  // Controlled_Buffer controlled_buffer_606
  assign pull_resistor_143_node = 1'b0 ? 1'b0 : 1'bz;  // Controlled_Buffer controlled_buffer_607
  assign pull_resistor_143_node = 1'b0 ? 1'b0 : 1'bz;  // Controlled_Buffer controlled_buffer_608
  assign pull_resistor_143_node = 1'b0 ? 1'b0 : 1'bz;  // Controlled_Buffer controlled_buffer_609
  assign pull_resistor_143_node = 1'b1 ? 1'b1 : 1'bz;  // Controlled_Buffer controlled_buffer_610
  assign pull_resistor_143_node = 1'b1 ? 1'b1 : 1'bz;  // Controlled_Buffer controlled_buffer_611
  muxin8tor muxin8tor_15 (.in_2(and_200_out), .in_1(in_1), .out_3(muxin8tor_15_out_3), .out_4(muxin8tor_15_out_4));
  not not_130 (not_130_out, in_1);
  Pull_Resistor pull_resistor_144 (.node(pull_resistor_144_node));
  assign pull_resistor_144_node = not_130_out ? nor_114_out : 8'bz;  // Controlled_Buffer controlled_buffer_612
  assign buffer_132_out = pull_resistor_144_node;  // Buffer buffer_132, 8 bits wide
  muxin16tor muxin16tor_15 (.in_2(and_200_out), .in_1(in_1), .out_3(muxin16tor_15_out_3), .out_4(muxin16tor_15_out_4));
  demuxin8tor demuxin8tor_15 (.in_2(nor_116_out), .in_3(8'he), .in_1(in_1), .out_4(demuxin8tor_15_out_4));
  Pull_Resistor pull_resistor_145 (.node({controlled_buffer_1_out_2, controlled_buffer_1_out}));
  assign pull_resistor_143_node = 1'b1 ? 1'b1 : 1'bz;  // Controlled_Buffer controlled_buffer_613
  assign pull_resistor_143_node = 1'b0 ? 1'b0 : 1'bz;  // Controlled_Buffer controlled_buffer_614
  assign buffer_133_out = buffer_132_out;  // Buffer buffer_133, 8 bits wide
  assign buffer_134_out = buffer_133_out;  // Buffer buffer_134, 8 bits wide
  assign not_131_out = ~buffer_133_out;  // NOT_Gate not_131, 8 bits wide
  assign buffer_135_out = demuxin8tor_15_out_4;  // Buffer buffer_135, 16 bits wide
  assign {controlled_buffer_1_out_2, controlled_buffer_1_out} = and_192_out ? 8'he : 8'bz;  // Controlled_Buffer controlled_buffer_615
  Pull_Resistor pull_resistor_146 (.node(out_9));
  assign out_9 = and_192_out ? and_192_out : 1'bz;  // Controlled_Buffer controlled_buffer_616
  assign xor_43_out = controlled_buffer_1_out_2 ^ 4'b0000;  // XOR_Gate xor_43, 4 bits wide
  assign xor_44_out = 4'b1110 ^ controlled_buffer_1_out;  // XOR_Gate xor_44, 4 bits wide
  assign and_188_out = buffer_134_out & muxin8tor_15_out_4;  // AND_Gate and_188, 8 bits wide
  assign and_189_out = muxin8tor_15_out_4 & not_131_out;  // AND_Gate and_189, 8 bits wide
  assign and_190_out = buffer_135_out & muxin16tor_15_out_4;  // AND_Gate and_190, 16 bits wide
  assign and_191_out = muxin16tor_15_out_4 & not_132_out;  // AND_Gate and_191, 16 bits wide
  assign not_132_out = ~demuxin8tor_15_out_4;  // NOT_Gate not_132, 16 bits wide
  and and_192 (and_192_out, pull_resistor_151_node, and_1_out);
  not not_133 (not_133_out, pull_resistor_143_node);
  assign nor_117_out = ~(and_188_out | nor_118_out);  // NOR_Gate nor_117, 8 bits wide
  assign nor_118_out = ~(nor_117_out | and_189_out);  // NOR_Gate nor_118, 8 bits wide
  assign nor_119_out = ~(and_190_out | nor_120_out);  // NOR_Gate nor_119, 16 bits wide
  assign nor_120_out = ~(nor_119_out | and_191_out);  // NOR_Gate nor_120, 16 bits wide
  assign controlled_buffer_631_out[1] = xor_44_out[1] ? xor_44_out[1] : 1'bz;  // Controlled_Buffer controlled_buffer_617
  assign controlled_buffer_631_out[1] = xor_44_out[2] ? xor_44_out[2] : 1'bz;  // Controlled_Buffer controlled_buffer_618
  assign controlled_buffer_631_out[1] = xor_44_out[3] ? xor_44_out[3] : 1'bz;  // Controlled_Buffer controlled_buffer_619
  assign controlled_buffer_631_out[2] = xor_44_out[2] ? xor_44_out[2] : 1'bz;  // Controlled_Buffer controlled_buffer_620
  assign controlled_buffer_631_out[2] = xor_44_out[3] ? xor_44_out[3] : 1'bz;  // Controlled_Buffer controlled_buffer_621
  assign and_193_out = buffer_136_out & muxin8tor_15_out_3;  // AND_Gate and_193, 8 bits wide
  assign buffer_136_out = nor_118_out;  // Buffer buffer_136, 8 bits wide
  assign and_194_out = muxin8tor_15_out_3 & not_134_out;  // AND_Gate and_194, 8 bits wide
  assign not_134_out = ~nor_118_out;  // NOT_Gate not_134, 8 bits wide
  assign buffer_137_out = nor_120_out;  // Buffer buffer_137, 16 bits wide
  assign and_195_out = buffer_137_out & muxin16tor_15_out_3;  // AND_Gate and_195, 16 bits wide
  assign and_196_out = muxin16tor_15_out_3 & not_135_out;  // AND_Gate and_196, 16 bits wide
  assign not_135_out = ~nor_120_out;  // NOT_Gate not_135, 16 bits wide
  assign controlled_buffer_622_out[0] = xor_43_out[0] ? xor_43_out[0] : 1'bz;  // Controlled_Buffer controlled_buffer_622
  assign controlled_buffer_622_out[1] = xor_43_out[1] ? xor_43_out[1] : 1'bz;  // Controlled_Buffer controlled_buffer_623
  assign controlled_buffer_622_out[0] = xor_43_out[1] ? xor_43_out[1] : 1'bz;  // Controlled_Buffer controlled_buffer_624
  assign controlled_buffer_622_out[1] = xor_43_out[2] ? xor_43_out[2] : 1'bz;  // Controlled_Buffer controlled_buffer_625
  assign controlled_buffer_622_out[0] = xor_43_out[2] ? xor_43_out[2] : 1'bz;  // Controlled_Buffer controlled_buffer_626
  assign controlled_buffer_622_out[1] = xor_43_out[3] ? xor_43_out[3] : 1'bz;  // Controlled_Buffer controlled_buffer_627
  assign controlled_buffer_622_out[0] = xor_43_out[3] ? xor_43_out[3] : 1'bz;  // Controlled_Buffer controlled_buffer_628
  assign controlled_buffer_622_out[2] = xor_43_out[2] ? xor_43_out[2] : 1'bz;  // Controlled_Buffer controlled_buffer_629
  assign controlled_buffer_622_out[2] = xor_43_out[3] ? xor_43_out[3] : 1'bz;  // Controlled_Buffer controlled_buffer_630
  not not_136 (not_136_out, controlled_buffer_622_out[0]);
  assign controlled_buffer_631_out[0] = xor_44_out[0] ? xor_44_out[0] : 1'bz;  // Controlled_Buffer controlled_buffer_631
  assign controlled_buffer_631_out[0] = xor_44_out[1] ? xor_44_out[1] : 1'bz;  // Controlled_Buffer controlled_buffer_632
  assign controlled_buffer_631_out[0] = xor_44_out[2] ? xor_44_out[2] : 1'bz;  // Controlled_Buffer controlled_buffer_633
  assign controlled_buffer_631_out[0] = xor_44_out[3] ? xor_44_out[3] : 1'bz;  // Controlled_Buffer controlled_buffer_634
  Pull_Resistor pull_resistor_147 (.node({xor_44_out[3], controlled_buffer_631_out}));
  assign nor_121_out = ~(and_193_out | nor_122_out);  // NOR_Gate nor_121, 8 bits wide
  assign nor_122_out = ~(nor_121_out | and_194_out);  // NOR_Gate nor_122, 8 bits wide
  assign nor_123_out = ~(and_195_out | nor_124_out);  // NOR_Gate nor_123, 16 bits wide
  assign nor_124_out = ~(nor_123_out | and_196_out);  // NOR_Gate nor_124, 16 bits wide
  assign buffer_138_out = {xor_43_out[3], controlled_buffer_622_out};  // Buffer buffer_138, 4 bits wide
  Pull_Resistor pull_resistor_148 (.node({xor_43_out[3], controlled_buffer_622_out}));
  Pull_Resistor pull_resistor_149 (.node(pull_resistor_149_node));
  assign not_137_out = ~{1'b0, xor_43_out[3], controlled_buffer_622_out[2:1]};  // NOT_Gate not_137, 4 bits wide
  assign and_197_out = buffer_139_out & not_138_out;  // AND_Gate and_197, 4 bits wide
  assign buffer_139_out = {xor_44_out[3], controlled_buffer_631_out};  // Buffer buffer_139, 4 bits wide
  Pull_Resistor pull_resistor_150 (.node(pull_resistor_150_node));
  assign pull_resistor_150_node = and_197_out[3] ? controlled_buffer_1_out[3] : 1'bz;  // Controlled_Buffer controlled_buffer_635
  assign pull_resistor_150_node = and_197_out[2] ? controlled_buffer_1_out[2] : 1'bz;  // Controlled_Buffer controlled_buffer_636
  assign not_138_out = ~{1'b0, xor_44_out[3], controlled_buffer_631_out[2:1]};  // NOT_Gate not_138, 4 bits wide
  assign xor_45_out = nor_124_out ^ buffer_2_out;  // XOR_Gate xor_45, 16 bits wide
  assign and_198_out = buffer_138_out & not_137_out;  // AND_Gate and_198, 4 bits wide
  assign pull_resistor_149_node = and_198_out[3] ? controlled_buffer_1_out_2[3] : 1'bz;  // Controlled_Buffer controlled_buffer_637
  assign pull_resistor_149_node = and_198_out[2] ? controlled_buffer_1_out_2[2] : 1'bz;  // Controlled_Buffer controlled_buffer_638
  assign pull_resistor_149_node = and_198_out[1] ? controlled_buffer_1_out_2[1] : 1'bz;  // Controlled_Buffer controlled_buffer_639
  assign pull_resistor_149_node = and_198_out[0] ? controlled_buffer_1_out_2[0] : 1'bz;  // Controlled_Buffer controlled_buffer_640
  assign controlled_buffer_641_out = pull_resistor_149_node ? pull_resistor_149_node : 1'bz;  // Controlled_Buffer controlled_buffer_641
  and and_199 (and_199_out, not_136_out, pull_resistor_150_node);
  assign controlled_buffer_641_out = and_199_out ? and_199_out : 1'bz;  // Controlled_Buffer controlled_buffer_642
  assign pull_resistor_150_node = and_197_out[1] ? controlled_buffer_1_out[1] : 1'bz;  // Controlled_Buffer controlled_buffer_643
  assign pull_resistor_150_node = and_197_out[0] ? controlled_buffer_1_out[0] : 1'bz;  // Controlled_Buffer controlled_buffer_644
  Pull_Resistor #(.pull(1)) pull_resistor_151 (.node(pull_resistor_151_node));
  and and_200 (and_200_out, controlled_buffer_641_out, out_9);
  assign controlled_buffer_641_out = not_133_out ? not_133_out : 1'bz;  // Controlled_Buffer controlled_buffer_645
  Pull_Resistor pull_resistor_152 (.node(controlled_buffer_641_out));
  assign pull_resistor_151_node = xor_45_out[0] ? ~xor_45_out[0] : 1'bz;  // Controlled_Inverter controlled_inverter_225
  assign pull_resistor_151_node = xor_45_out[1] ? ~xor_45_out[1] : 1'bz;  // Controlled_Inverter controlled_inverter_226
  assign pull_resistor_151_node = xor_45_out[2] ? ~xor_45_out[2] : 1'bz;  // Controlled_Inverter controlled_inverter_227
  assign pull_resistor_151_node = xor_45_out[3] ? ~xor_45_out[3] : 1'bz;  // Controlled_Inverter controlled_inverter_228
  assign pull_resistor_151_node = xor_45_out[4] ? ~xor_45_out[4] : 1'bz;  // Controlled_Inverter controlled_inverter_229
  assign pull_resistor_151_node = xor_45_out[5] ? ~xor_45_out[5] : 1'bz;  // Controlled_Inverter controlled_inverter_230
  assign pull_resistor_151_node = xor_45_out[6] ? ~xor_45_out[6] : 1'bz;  // Controlled_Inverter controlled_inverter_231
  assign pull_resistor_151_node = xor_45_out[7] ? ~xor_45_out[7] : 1'bz;  // Controlled_Inverter controlled_inverter_232
  assign pull_resistor_151_node = xor_45_out[8] ? ~xor_45_out[8] : 1'bz;  // Controlled_Inverter controlled_inverter_233
  assign pull_resistor_151_node = xor_45_out[9] ? ~xor_45_out[9] : 1'bz;  // Controlled_Inverter controlled_inverter_234
  assign pull_resistor_151_node = xor_45_out[10] ? ~xor_45_out[10] : 1'bz;  // Controlled_Inverter controlled_inverter_235
  assign pull_resistor_151_node = xor_45_out[11] ? ~xor_45_out[11] : 1'bz;  // Controlled_Inverter controlled_inverter_236
  assign pull_resistor_151_node = xor_45_out[12] ? ~xor_45_out[12] : 1'bz;  // Controlled_Inverter controlled_inverter_237
  assign pull_resistor_151_node = xor_45_out[13] ? ~xor_45_out[13] : 1'bz;  // Controlled_Inverter controlled_inverter_238
  assign pull_resistor_151_node = xor_45_out[14] ? ~xor_45_out[14] : 1'bz;  // Controlled_Inverter controlled_inverter_239
  assign pull_resistor_151_node = xor_45_out[15] ? ~xor_45_out[15] : 1'bz;  // Controlled_Inverter controlled_inverter_240
  assign controlled_buffer_641_out = pull_resistor_151_node ? pull_resistor_151_node : 1'bz;  // Controlled_Buffer controlled_buffer_646
  assign out_10 = and_192_out ? nor_122_out : 8'bz;  // Controlled_Buffer controlled_buffer_647
  assign pull_resistor_1_node = and_192_out ? nor_124_out : 16'bz;  // Controlled_Buffer controlled_buffer_648
  Pull_Resistor pull_resistor_153 (.node(pull_resistor_153_node));
  assign pull_resistor_153_node = 1'b0 ? 1'b0 : 1'bz;  // Controlled_Buffer controlled_buffer_649
  assign pull_resistor_153_node = 1'b0 ? 1'b0 : 1'bz;  // Controlled_Buffer controlled_buffer_650
  assign pull_resistor_153_node = 1'b0 ? 1'b0 : 1'bz;  // Controlled_Buffer controlled_buffer_651
  assign pull_resistor_153_node = 1'b0 ? 1'b0 : 1'bz;  // Controlled_Buffer controlled_buffer_652
  assign pull_resistor_153_node = 1'b1 ? 1'b1 : 1'bz;  // Controlled_Buffer controlled_buffer_653
  muxin8tor muxin8tor_16 (.in_2(and_213_out), .in_1(in_1), .out_3(muxin8tor_16_out_3), .out_4(muxin8tor_16_out_4));
  not not_139 (not_139_out, in_1);
  Pull_Resistor pull_resistor_154 (.node(pull_resistor_154_node));
  assign pull_resistor_154_node = not_139_out ? nor_122_out : 8'bz;  // Controlled_Buffer controlled_buffer_654
  assign buffer_140_out = pull_resistor_154_node;  // Buffer buffer_140, 8 bits wide
  muxin16tor muxin16tor_16 (.in_2(and_213_out), .in_1(in_1), .out_3(muxin16tor_16_out_3), .out_4(muxin16tor_16_out_4));
  demuxin8tor demuxin8tor_16 (.in_2(nor_124_out), .in_3(8'hf), .in_1(in_1), .out_4(demuxin8tor_16_out_4));
  Pull_Resistor pull_resistor_155 (.node({controlled_buffer_1_out_2, controlled_buffer_1_out}));
  assign pull_resistor_153_node = 1'b1 ? 1'b1 : 1'bz;  // Controlled_Buffer controlled_buffer_655
  assign pull_resistor_153_node = 1'b1 ? 1'b1 : 1'bz;  // Controlled_Buffer controlled_buffer_656
  assign pull_resistor_153_node = 1'b1 ? 1'b1 : 1'bz;  // Controlled_Buffer controlled_buffer_657
  assign buffer_141_out = buffer_140_out;  // Buffer buffer_141, 8 bits wide
  assign buffer_142_out = buffer_141_out;  // Buffer buffer_142, 8 bits wide
  assign {controlled_buffer_1_out_2, controlled_buffer_1_out} = and_205_out ? 8'hf : 8'bz;  // Controlled_Buffer controlled_buffer_658
  Pull_Resistor pull_resistor_156 (.node(out_9));
  assign out_9 = and_205_out ? and_205_out : 1'bz;  // Controlled_Buffer controlled_buffer_659
  assign xor_46_out = controlled_buffer_1_out_2 ^ 4'b0000;  // XOR_Gate xor_46, 4 bits wide
  assign xor_47_out = 4'b1111 ^ controlled_buffer_1_out;  // XOR_Gate xor_47, 4 bits wide
  assign and_201_out = buffer_142_out & muxin8tor_16_out_4;  // AND_Gate and_201, 8 bits wide
  assign and_202_out = muxin8tor_16_out_4 & not_140_out;  // AND_Gate and_202, 8 bits wide
  assign not_140_out = ~buffer_141_out;  // NOT_Gate not_140, 8 bits wide
  assign buffer_143_out = demuxin8tor_16_out_4;  // Buffer buffer_143, 16 bits wide
  assign and_203_out = buffer_143_out & muxin16tor_16_out_4;  // AND_Gate and_203, 16 bits wide
  assign and_204_out = muxin16tor_16_out_4 & not_141_out;  // AND_Gate and_204, 16 bits wide
  assign not_141_out = ~demuxin8tor_16_out_4;  // NOT_Gate not_141, 16 bits wide
  and and_205 (and_205_out, pull_resistor_161_node, and_1_out);
  not not_142 (not_142_out, pull_resistor_153_node);
  assign nor_125_out = ~(and_201_out | nor_126_out);  // NOR_Gate nor_125, 8 bits wide
  assign nor_126_out = ~(nor_125_out | and_202_out);  // NOR_Gate nor_126, 8 bits wide
  assign nor_127_out = ~(and_203_out | nor_128_out);  // NOR_Gate nor_127, 16 bits wide
  assign nor_128_out = ~(nor_127_out | and_204_out);  // NOR_Gate nor_128, 16 bits wide
  assign controlled_buffer_674_out[1] = xor_47_out[1] ? xor_47_out[1] : 1'bz;  // Controlled_Buffer controlled_buffer_660
  assign controlled_buffer_674_out[1] = xor_47_out[2] ? xor_47_out[2] : 1'bz;  // Controlled_Buffer controlled_buffer_661
  assign controlled_buffer_674_out[1] = xor_47_out[3] ? xor_47_out[3] : 1'bz;  // Controlled_Buffer controlled_buffer_662
  assign controlled_buffer_674_out[2] = xor_47_out[2] ? xor_47_out[2] : 1'bz;  // Controlled_Buffer controlled_buffer_663
  assign controlled_buffer_674_out[2] = xor_47_out[3] ? xor_47_out[3] : 1'bz;  // Controlled_Buffer controlled_buffer_664
  assign and_206_out = buffer_144_out & muxin8tor_16_out_3;  // AND_Gate and_206, 8 bits wide
  assign buffer_144_out = nor_126_out;  // Buffer buffer_144, 8 bits wide
  assign and_207_out = muxin8tor_16_out_3 & not_143_out;  // AND_Gate and_207, 8 bits wide
  assign not_143_out = ~nor_126_out;  // NOT_Gate not_143, 8 bits wide
  assign buffer_145_out = nor_128_out;  // Buffer buffer_145, 16 bits wide
  assign and_208_out = buffer_145_out & muxin16tor_16_out_3;  // AND_Gate and_208, 16 bits wide
  assign and_209_out = muxin16tor_16_out_3 & not_144_out;  // AND_Gate and_209, 16 bits wide
  assign not_144_out = ~nor_128_out;  // NOT_Gate not_144, 16 bits wide
  assign controlled_buffer_665_out[0] = xor_46_out[0] ? xor_46_out[0] : 1'bz;  // Controlled_Buffer controlled_buffer_665
  assign controlled_buffer_665_out[1] = xor_46_out[1] ? xor_46_out[1] : 1'bz;  // Controlled_Buffer controlled_buffer_666
  assign controlled_buffer_665_out[0] = xor_46_out[1] ? xor_46_out[1] : 1'bz;  // Controlled_Buffer controlled_buffer_667
  assign controlled_buffer_665_out[1] = xor_46_out[2] ? xor_46_out[2] : 1'bz;  // Controlled_Buffer controlled_buffer_668
  assign controlled_buffer_665_out[0] = xor_46_out[2] ? xor_46_out[2] : 1'bz;  // Controlled_Buffer controlled_buffer_669
  assign controlled_buffer_665_out[1] = xor_46_out[3] ? xor_46_out[3] : 1'bz;  // Controlled_Buffer controlled_buffer_670
  assign controlled_buffer_665_out[0] = xor_46_out[3] ? xor_46_out[3] : 1'bz;  // Controlled_Buffer controlled_buffer_671
  assign controlled_buffer_665_out[2] = xor_46_out[2] ? xor_46_out[2] : 1'bz;  // Controlled_Buffer controlled_buffer_672
  assign controlled_buffer_665_out[2] = xor_46_out[3] ? xor_46_out[3] : 1'bz;  // Controlled_Buffer controlled_buffer_673
  not not_145 (not_145_out, controlled_buffer_665_out[0]);
  assign controlled_buffer_674_out[0] = xor_47_out[0] ? xor_47_out[0] : 1'bz;  // Controlled_Buffer controlled_buffer_674
  assign controlled_buffer_674_out[0] = xor_47_out[1] ? xor_47_out[1] : 1'bz;  // Controlled_Buffer controlled_buffer_675
  assign controlled_buffer_674_out[0] = xor_47_out[2] ? xor_47_out[2] : 1'bz;  // Controlled_Buffer controlled_buffer_676
  assign controlled_buffer_674_out[0] = xor_47_out[3] ? xor_47_out[3] : 1'bz;  // Controlled_Buffer controlled_buffer_677
  Pull_Resistor pull_resistor_157 (.node({xor_47_out[3], controlled_buffer_674_out}));
  assign nor_129_out = ~(and_206_out | out_6);  // NOR_Gate nor_129, 8 bits wide
  assign out_6 = ~(nor_129_out | and_207_out);  // NOR_Gate nor_130, 8 bits wide
  assign nor_131_out = ~(and_208_out | out_7);  // NOR_Gate nor_131, 16 bits wide
  assign out_7 = ~(nor_131_out | and_209_out);  // NOR_Gate nor_132, 16 bits wide
  assign buffer_146_out = {xor_46_out[3], controlled_buffer_665_out};  // Buffer buffer_146, 4 bits wide
  Pull_Resistor pull_resistor_158 (.node({xor_46_out[3], controlled_buffer_665_out}));
  assign not_146_out = ~{1'b0, xor_46_out[3], controlled_buffer_665_out[2:1]};  // NOT_Gate not_146, 4 bits wide
  assign and_210_out = buffer_147_out & not_147_out;  // AND_Gate and_210, 4 bits wide
  assign buffer_147_out = {xor_47_out[3], controlled_buffer_674_out};  // Buffer buffer_147, 4 bits wide
  Pull_Resistor pull_resistor_159 (.node(pull_resistor_159_node));
  assign pull_resistor_159_node = and_210_out[3] ? controlled_buffer_1_out[3] : 1'bz;  // Controlled_Buffer controlled_buffer_678
  assign pull_resistor_159_node = and_210_out[2] ? controlled_buffer_1_out[2] : 1'bz;  // Controlled_Buffer controlled_buffer_679
  assign not_147_out = ~{1'b0, xor_47_out[3], controlled_buffer_674_out[2:1]};  // NOT_Gate not_147, 4 bits wide
  assign xor_48_out = out_7 ^ buffer_2_out;  // XOR_Gate xor_48, 16 bits wide
  assign and_211_out = buffer_146_out & not_146_out;  // AND_Gate and_211, 4 bits wide
  Pull_Resistor pull_resistor_160 (.node(pull_resistor_160_node));
  assign pull_resistor_160_node = and_211_out[3] ? controlled_buffer_1_out_2[3] : 1'bz;  // Controlled_Buffer controlled_buffer_680
  assign pull_resistor_160_node = and_211_out[2] ? controlled_buffer_1_out_2[2] : 1'bz;  // Controlled_Buffer controlled_buffer_681
  assign pull_resistor_160_node = and_211_out[1] ? controlled_buffer_1_out_2[1] : 1'bz;  // Controlled_Buffer controlled_buffer_682
  and and_212 (and_212_out, not_145_out, pull_resistor_159_node);
  assign controlled_buffer_683_out = and_212_out ? and_212_out : 1'bz;  // Controlled_Buffer controlled_buffer_683
  assign pull_resistor_159_node = and_210_out[1] ? controlled_buffer_1_out[1] : 1'bz;  // Controlled_Buffer controlled_buffer_684
  assign pull_resistor_159_node = and_210_out[0] ? controlled_buffer_1_out[0] : 1'bz;  // Controlled_Buffer controlled_buffer_685
  Pull_Resistor #(.pull(1)) pull_resistor_161 (.node(pull_resistor_161_node));
  and and_213 (and_213_out, controlled_buffer_683_out, out_9);
  assign pull_resistor_160_node = and_211_out[0] ? controlled_buffer_1_out_2[0] : 1'bz;  // Controlled_Buffer controlled_buffer_686
  assign controlled_buffer_683_out = pull_resistor_160_node ? pull_resistor_160_node : 1'bz;  // Controlled_Buffer controlled_buffer_687
  assign controlled_buffer_683_out = not_142_out ? not_142_out : 1'bz;  // Controlled_Buffer controlled_buffer_688
  Pull_Resistor pull_resistor_162 (.node(controlled_buffer_683_out));
  assign pull_resistor_161_node = xor_48_out[0] ? ~xor_48_out[0] : 1'bz;  // Controlled_Inverter controlled_inverter_241
  assign pull_resistor_161_node = xor_48_out[1] ? ~xor_48_out[1] : 1'bz;  // Controlled_Inverter controlled_inverter_242
  assign pull_resistor_161_node = xor_48_out[2] ? ~xor_48_out[2] : 1'bz;  // Controlled_Inverter controlled_inverter_243
  assign pull_resistor_161_node = xor_48_out[3] ? ~xor_48_out[3] : 1'bz;  // Controlled_Inverter controlled_inverter_244
  assign pull_resistor_161_node = xor_48_out[4] ? ~xor_48_out[4] : 1'bz;  // Controlled_Inverter controlled_inverter_245
  assign pull_resistor_161_node = xor_48_out[5] ? ~xor_48_out[5] : 1'bz;  // Controlled_Inverter controlled_inverter_246
  assign pull_resistor_161_node = xor_48_out[6] ? ~xor_48_out[6] : 1'bz;  // Controlled_Inverter controlled_inverter_247
  assign pull_resistor_161_node = xor_48_out[7] ? ~xor_48_out[7] : 1'bz;  // Controlled_Inverter controlled_inverter_248
  assign pull_resistor_161_node = xor_48_out[8] ? ~xor_48_out[8] : 1'bz;  // Controlled_Inverter controlled_inverter_249
  assign pull_resistor_161_node = xor_48_out[9] ? ~xor_48_out[9] : 1'bz;  // Controlled_Inverter controlled_inverter_250
  assign pull_resistor_161_node = xor_48_out[10] ? ~xor_48_out[10] : 1'bz;  // Controlled_Inverter controlled_inverter_251
  assign pull_resistor_161_node = xor_48_out[11] ? ~xor_48_out[11] : 1'bz;  // Controlled_Inverter controlled_inverter_252
  assign pull_resistor_161_node = xor_48_out[12] ? ~xor_48_out[12] : 1'bz;  // Controlled_Inverter controlled_inverter_253
  assign pull_resistor_161_node = xor_48_out[13] ? ~xor_48_out[13] : 1'bz;  // Controlled_Inverter controlled_inverter_254
  assign pull_resistor_161_node = xor_48_out[14] ? ~xor_48_out[14] : 1'bz;  // Controlled_Inverter controlled_inverter_255
  assign pull_resistor_161_node = xor_48_out[15] ? ~xor_48_out[15] : 1'bz;  // Controlled_Inverter controlled_inverter_256
  assign controlled_buffer_683_out = pull_resistor_161_node ? pull_resistor_161_node : 1'bz;  // Controlled_Buffer controlled_buffer_689
  assign out_10 = and_205_out ? out_6 : 8'bz;  // Controlled_Buffer controlled_buffer_690
  assign pull_resistor_1_node = and_205_out ? out_7 : 16'bz;  // Controlled_Buffer controlled_buffer_691
  assign not_148_out = ~{controlled_buffer_1_out_2, controlled_buffer_1_out};  // NOT_Gate not_148, 8 bits wide
  assign out_8 = not_148_out[0] ? ~not_148_out[0] : 1'bz;  // Controlled_Inverter controlled_inverter_257
  assign out_8 = not_148_out[1] ? ~not_148_out[1] : 1'bz;  // Controlled_Inverter controlled_inverter_258
  assign out_8 = not_148_out[2] ? ~not_148_out[2] : 1'bz;  // Controlled_Inverter controlled_inverter_259
  assign out_8 = not_148_out[3] ? ~not_148_out[3] : 1'bz;  // Controlled_Inverter controlled_inverter_260
  Pull_Resistor #(.pull(1)) pull_resistor_163 (.node(out_8));
  assign out_8 = not_148_out[4] ? ~not_148_out[4] : 1'bz;  // Controlled_Inverter controlled_inverter_261
  assign out_8 = not_148_out[5] ? ~not_148_out[5] : 1'bz;  // Controlled_Inverter controlled_inverter_262
  assign out_8 = not_148_out[6] ? ~not_148_out[6] : 1'bz;  // Controlled_Inverter controlled_inverter_263
  assign out_8 = not_148_out[7] ? ~not_148_out[7] : 1'bz;  // Controlled_Inverter controlled_inverter_264
endmodule

module CO8 (
  input  [7:0] in_1,
  output [2:0] out_2
);

  Pull_Resistor pull_resistor_1 (.node(out_2));
  assign out_2 = in_1[0] ? 3'b000 : 3'bz;  // Controlled_Buffer controlled_buffer_1
  assign out_2 = in_1[1] ? 3'b001 : 3'bz;  // Controlled_Buffer controlled_buffer_2
  assign out_2 = in_1[2] ? 3'b010 : 3'bz;  // Controlled_Buffer controlled_buffer_3
  assign out_2 = in_1[3] ? 3'b011 : 3'bz;  // Controlled_Buffer controlled_buffer_4
  assign out_2 = in_1[4] ? 3'b100 : 3'bz;  // Controlled_Buffer controlled_buffer_5
  assign out_2 = in_1[5] ? 3'b101 : 3'bz;  // Controlled_Buffer controlled_buffer_6
  assign out_2 = in_1[6] ? 3'b110 : 3'bz;  // Controlled_Buffer controlled_buffer_7
  assign out_2 = in_1[7] ? 3'b111 : 3'bz;  // Controlled_Buffer controlled_buffer_8
endmodule

module R5 (
  input  in_1,
  input  in_2,
  input  [3:0] in_3,
  input  [31:0] in_4,
  input  [3:0] in_5,
  input  [15:0] in_6,
  output [7:0] out_7
);

  wire controlled_buffer_2_out, controlled_buffer_12_out, controlled_buffer_23_out, controlled_buffer_34_out,
       controlled_buffer_46_out, controlled_buffer_56_out, controlled_buffer_67_out,
       controlled_buffer_78_out, controlled_buffer_90_out, controlled_buffer_100_out,
       controlled_buffer_111_out, controlled_buffer_122_out, controlled_buffer_134_out,
       controlled_buffer_144_out, controlled_buffer_155_out, controlled_buffer_166_out, decoder_1_out0,
       decoder_1_out1, decoder_1_out2, decoder_1_out3, decoder_1_out4, decoder_1_out5, decoder_1_out6,
       decoder_1_out7, decoder_1_out8, decoder_1_out9, decoder_1_out10, decoder_1_out11, decoder_1_out12,
       decoder_1_out13, decoder_1_out14, decoder_1_out15, decoder_2_out0, decoder_2_out1, decoder_2_out2,
       decoder_2_out3, decoder_2_out4, decoder_2_out5, decoder_2_out6, decoder_2_out7, decoder_2_out8,
       decoder_2_out9, decoder_2_out10, decoder_2_out11, decoder_2_out12, decoder_2_out13, decoder_2_out14,
       decoder_2_out15, decoder_3_out0, decoder_3_out1, decoder_3_out2, decoder_3_out3, decoder_3_out4,
       decoder_3_out5, decoder_3_out6, decoder_3_out7, decoder_3_out8, decoder_3_out9, decoder_3_out10,
       decoder_3_out11, decoder_3_out12, decoder_3_out13, decoder_3_out14, decoder_3_out15, decoder_4_out0,
       decoder_4_out1, decoder_4_out2, decoder_4_out3, decoder_4_out4, decoder_4_out5, decoder_4_out6,
       decoder_4_out7, decoder_4_out8, decoder_4_out9, decoder_4_out10, decoder_4_out11, decoder_4_out12,
       decoder_4_out13, decoder_4_out14, decoder_4_out15, decoder_5_out0, decoder_5_out1, decoder_5_out2,
       decoder_5_out3, decoder_5_out4, decoder_5_out5, decoder_5_out6, decoder_5_out7, decoder_5_out8,
       decoder_5_out9, decoder_5_out10, decoder_5_out11, decoder_5_out12, decoder_5_out13, decoder_5_out14,
       decoder_5_out15;
  wire [7:0] and_1_out, and_2_out, and_3_out, and_4_out, and_5_out, and_6_out, and_7_out, and_8_out,
       and_9_out, and_10_out, and_11_out, and_12_out, and_13_out, and_14_out, and_15_out, and_16_out,
       and_17_out, and_18_out, and_19_out, and_20_out, and_21_out, and_22_out, and_23_out, and_24_out,
       and_25_out, and_26_out, and_27_out, and_28_out, and_29_out, and_30_out, and_31_out, and_32_out,
       buffer_1_out, buffer_2_out, buffer_3_out, buffer_4_out, buffer_5_out, buffer_6_out, buffer_7_out,
       buffer_8_out, buffer_9_out, buffer_10_out, buffer_11_out, buffer_12_out, buffer_13_out, buffer_14_out,
       buffer_15_out, buffer_16_out, controlled_buffer_1_out, controlled_buffer_3_out,
       controlled_buffer_14_out, controlled_buffer_16_out, controlled_buffer_24_out,
       controlled_buffer_27_out, controlled_buffer_35_out, controlled_buffer_39_out,
       controlled_buffer_45_out, controlled_buffer_47_out, controlled_buffer_58_out,
       controlled_buffer_60_out, controlled_buffer_68_out, controlled_buffer_71_out,
       controlled_buffer_79_out, controlled_buffer_83_out, controlled_buffer_89_out,
       controlled_buffer_91_out, controlled_buffer_102_out, controlled_buffer_104_out,
       controlled_buffer_112_out, controlled_buffer_115_out, controlled_buffer_123_out,
       controlled_buffer_127_out, controlled_buffer_133_out, controlled_buffer_135_out,
       controlled_buffer_146_out, controlled_buffer_148_out, controlled_buffer_156_out,
       controlled_buffer_159_out, controlled_buffer_167_out, controlled_buffer_171_out, nor_1_out, nor_2_out,
       nor_3_out, nor_4_out, nor_5_out, nor_6_out, nor_7_out, nor_8_out, nor_9_out, nor_10_out, nor_11_out,
       nor_12_out, nor_13_out, nor_14_out, nor_15_out, nor_16_out, nor_17_out, nor_18_out, nor_19_out,
       nor_20_out, nor_21_out, nor_22_out, nor_23_out, nor_24_out, nor_25_out, nor_26_out, nor_27_out,
       nor_28_out, nor_29_out, nor_30_out, nor_31_out, nor_32_out, not_1_out, not_2_out, not_3_out,
       not_4_out, not_5_out, not_6_out, not_7_out, not_8_out, not_9_out, not_10_out, not_11_out, not_12_out,
       not_13_out, not_14_out, not_15_out, not_16_out;

  assign controlled_buffer_1_out = decoder_4_out0 ? in_4[31:24] : 8'bz;  // Controlled_Buffer controlled_buffer_1
  assign controlled_buffer_2_out = in_1 ? in_1 : 1'bz;  // Controlled_Buffer controlled_buffer_2
  assign controlled_buffer_3_out = controlled_buffer_2_out ? {8{1'b1}} : 8'bz;  // Controlled_Buffer controlled_buffer_3
  Pull_Resistor pull_resistor_1 (.node(controlled_buffer_2_out));
  assign controlled_buffer_2_out = decoder_4_out0 ? decoder_4_out0 : 1'bz;  // Controlled_Buffer controlled_buffer_4
  assign controlled_buffer_2_out = decoder_3_out0 ? decoder_3_out0 : 1'bz;  // Controlled_Buffer controlled_buffer_5
  assign controlled_buffer_2_out = decoder_2_out0 ? decoder_2_out0 : 1'bz;  // Controlled_Buffer controlled_buffer_6
  assign controlled_buffer_2_out = decoder_1_out0 ? decoder_1_out0 : 1'bz;  // Controlled_Buffer controlled_buffer_7
  assign controlled_buffer_1_out = decoder_3_out0 ? in_4[23:16] : 8'bz;  // Controlled_Buffer controlled_buffer_8
  assign controlled_buffer_1_out = decoder_2_out0 ? in_4[15:8] : 8'bz;  // Controlled_Buffer controlled_buffer_9
  assign controlled_buffer_1_out = decoder_1_out0 ? in_4[7:0] : 8'bz;  // Controlled_Buffer controlled_buffer_10
  Decoder #(.select(4)) decoder_1 (
    .out0(decoder_1_out0), .out1(decoder_1_out1), .out2(decoder_1_out2), .out3(decoder_1_out3),
    .out4(decoder_1_out4), .out5(decoder_1_out5), .out6(decoder_1_out6), .out7(decoder_1_out7),
    .out8(decoder_1_out8), .out9(decoder_1_out9), .out10(decoder_1_out10), .out11(decoder_1_out11),
    .out12(decoder_1_out12), .out13(decoder_1_out13), .out14(decoder_1_out14), .out15(decoder_1_out15),
    .sel(in_6[3:0]), .en(in_5[0]));
  Decoder #(.select(4)) decoder_2 (
    .out0(decoder_2_out0), .out1(decoder_2_out1), .out2(decoder_2_out2), .out3(decoder_2_out3),
    .out4(decoder_2_out4), .out5(decoder_2_out5), .out6(decoder_2_out6), .out7(decoder_2_out7),
    .out8(decoder_2_out8), .out9(decoder_2_out9), .out10(decoder_2_out10), .out11(decoder_2_out11),
    .out12(decoder_2_out12), .out13(decoder_2_out13), .out14(decoder_2_out14), .out15(decoder_2_out15),
    .sel(in_6[7:4]), .en(in_5[1]));
  Decoder #(.select(4)) decoder_3 (
    .out0(decoder_3_out0), .out1(decoder_3_out1), .out2(decoder_3_out2), .out3(decoder_3_out3),
    .out4(decoder_3_out4), .out5(decoder_3_out5), .out6(decoder_3_out6), .out7(decoder_3_out7),
    .out8(decoder_3_out8), .out9(decoder_3_out9), .out10(decoder_3_out10), .out11(decoder_3_out11),
    .out12(decoder_3_out12), .out13(decoder_3_out13), .out14(decoder_3_out14), .out15(decoder_3_out15),
    .sel(in_6[11:8]), .en(in_5[2]));
  Decoder #(.select(4)) decoder_4 (
    .out0(decoder_4_out0), .out1(decoder_4_out1), .out2(decoder_4_out2), .out3(decoder_4_out3),
    .out4(decoder_4_out4), .out5(decoder_4_out5), .out6(decoder_4_out6), .out7(decoder_4_out7),
    .out8(decoder_4_out8), .out9(decoder_4_out9), .out10(decoder_4_out10), .out11(decoder_4_out11),
    .out12(decoder_4_out12), .out13(decoder_4_out13), .out14(decoder_4_out14), .out15(decoder_4_out15),
    .sel(in_6[15:12]), .en(in_5[3]));
  assign not_1_out = ~controlled_buffer_1_out;  // NOT_Gate not_1, 8 bits wide
  assign and_1_out = not_1_out & controlled_buffer_3_out;  // AND_Gate and_1, 8 bits wide
  assign and_2_out = controlled_buffer_3_out & buffer_1_out;  // AND_Gate and_2, 8 bits wide
  assign buffer_1_out = controlled_buffer_1_out;  // Buffer buffer_1, 8 bits wide
  Pull_Resistor pull_resistor_2 (.node(controlled_buffer_3_out));
  Pull_Resistor pull_resistor_3 (.node(controlled_buffer_1_out));
  Decoder #(.select(4)) decoder_5 (
    .out0(decoder_5_out0), .out1(decoder_5_out1), .out2(decoder_5_out2), .out3(decoder_5_out3),
    .out4(decoder_5_out4), .out5(decoder_5_out5), .out6(decoder_5_out6), .out7(decoder_5_out7),
    .out8(decoder_5_out8), .out9(decoder_5_out9), .out10(decoder_5_out10), .out11(decoder_5_out11),
    .out12(decoder_5_out12), .out13(decoder_5_out13), .out14(decoder_5_out14), .out15(decoder_5_out15),
    .sel(in_3), .en(in_2));
  assign out_7 = decoder_5_out0 ? nor_1_out : 8'bz;  // Controlled_Buffer controlled_buffer_11
  assign nor_1_out = ~(and_1_out | nor_2_out);  // NOR_Gate nor_1, 8 bits wide
  assign controlled_buffer_12_out = in_1 ? in_1 : 1'bz;  // Controlled_Buffer controlled_buffer_12
  assign nor_2_out = ~(nor_1_out | and_2_out);  // NOR_Gate nor_2, 8 bits wide
  Pull_Resistor pull_resistor_4 (.node(controlled_buffer_12_out));
  assign controlled_buffer_12_out = decoder_4_out1 ? decoder_4_out1 : 1'bz;  // Controlled_Buffer controlled_buffer_13
  assign controlled_buffer_14_out = decoder_4_out1 ? in_4[31:24] : 8'bz;  // Controlled_Buffer controlled_buffer_14
  assign controlled_buffer_14_out = decoder_3_out1 ? in_4[23:16] : 8'bz;  // Controlled_Buffer controlled_buffer_15
  assign not_2_out = ~controlled_buffer_14_out;  // NOT_Gate not_2, 8 bits wide
  assign controlled_buffer_16_out = controlled_buffer_12_out ? {8{1'b1}} : 8'bz;  // Controlled_Buffer controlled_buffer_16
  assign buffer_2_out = controlled_buffer_14_out;  // Buffer buffer_2, 8 bits wide
  Pull_Resistor pull_resistor_5 (.node(controlled_buffer_16_out));
  assign controlled_buffer_12_out = decoder_3_out1 ? decoder_3_out1 : 1'bz;  // Controlled_Buffer controlled_buffer_17
  assign controlled_buffer_12_out = decoder_2_out1 ? decoder_2_out1 : 1'bz;  // Controlled_Buffer controlled_buffer_18
  assign controlled_buffer_12_out = decoder_1_out1 ? decoder_1_out1 : 1'bz;  // Controlled_Buffer controlled_buffer_19
  Pull_Resistor pull_resistor_6 (.node(controlled_buffer_14_out));
  assign controlled_buffer_14_out = decoder_2_out1 ? in_4[15:8] : 8'bz;  // Controlled_Buffer controlled_buffer_20
  assign controlled_buffer_14_out = decoder_1_out1 ? in_4[7:0] : 8'bz;  // Controlled_Buffer controlled_buffer_21
  assign out_7 = decoder_5_out1 ? nor_3_out : 8'bz;  // Controlled_Buffer controlled_buffer_22
  assign and_3_out = not_2_out & controlled_buffer_16_out;  // AND_Gate and_3, 8 bits wide
  assign nor_3_out = ~(and_3_out | nor_4_out);  // NOR_Gate nor_3, 8 bits wide
  assign nor_4_out = ~(nor_3_out | and_4_out);  // NOR_Gate nor_4, 8 bits wide
  assign and_4_out = controlled_buffer_16_out & buffer_2_out;  // AND_Gate and_4, 8 bits wide
  assign controlled_buffer_23_out = in_1 ? in_1 : 1'bz;  // Controlled_Buffer controlled_buffer_23
  assign controlled_buffer_24_out = controlled_buffer_23_out ? {8{1'b1}} : 8'bz;  // Controlled_Buffer controlled_buffer_24
  Pull_Resistor pull_resistor_7 (.node(controlled_buffer_23_out));
  assign controlled_buffer_23_out = decoder_4_out2 ? decoder_4_out2 : 1'bz;  // Controlled_Buffer controlled_buffer_25
  assign controlled_buffer_23_out = decoder_3_out2 ? decoder_3_out2 : 1'bz;  // Controlled_Buffer controlled_buffer_26
  assign controlled_buffer_27_out = decoder_4_out2 ? in_4[31:24] : 8'bz;  // Controlled_Buffer controlled_buffer_27
  assign controlled_buffer_27_out = decoder_3_out2 ? in_4[23:16] : 8'bz;  // Controlled_Buffer controlled_buffer_28
  assign controlled_buffer_27_out = decoder_2_out2 ? in_4[15:8] : 8'bz;  // Controlled_Buffer controlled_buffer_29
  assign not_3_out = ~controlled_buffer_27_out;  // NOT_Gate not_3, 8 bits wide
  assign buffer_3_out = controlled_buffer_27_out;  // Buffer buffer_3, 8 bits wide
  Pull_Resistor pull_resistor_8 (.node(controlled_buffer_24_out));
  assign controlled_buffer_23_out = decoder_2_out2 ? decoder_2_out2 : 1'bz;  // Controlled_Buffer controlled_buffer_30
  assign controlled_buffer_23_out = decoder_1_out2 ? decoder_1_out2 : 1'bz;  // Controlled_Buffer controlled_buffer_31
  Pull_Resistor pull_resistor_9 (.node(controlled_buffer_27_out));
  assign controlled_buffer_27_out = decoder_1_out2 ? in_4[7:0] : 8'bz;  // Controlled_Buffer controlled_buffer_32
  assign out_7 = decoder_5_out2 ? nor_5_out : 8'bz;  // Controlled_Buffer controlled_buffer_33
  assign and_5_out = not_3_out & controlled_buffer_24_out;  // AND_Gate and_5, 8 bits wide
  assign nor_5_out = ~(and_5_out | nor_6_out);  // NOR_Gate nor_5, 8 bits wide
  assign nor_6_out = ~(nor_5_out | and_6_out);  // NOR_Gate nor_6, 8 bits wide
  assign and_6_out = controlled_buffer_24_out & buffer_3_out;  // AND_Gate and_6, 8 bits wide
  assign controlled_buffer_34_out = in_1 ? in_1 : 1'bz;  // Controlled_Buffer controlled_buffer_34
  assign controlled_buffer_35_out = controlled_buffer_34_out ? {8{1'b1}} : 8'bz;  // Controlled_Buffer controlled_buffer_35
  Pull_Resistor pull_resistor_10 (.node(controlled_buffer_34_out));
  assign controlled_buffer_34_out = decoder_4_out3 ? decoder_4_out3 : 1'bz;  // Controlled_Buffer controlled_buffer_36
  assign controlled_buffer_34_out = decoder_3_out3 ? decoder_3_out3 : 1'bz;  // Controlled_Buffer controlled_buffer_37
  assign controlled_buffer_34_out = decoder_2_out3 ? decoder_2_out3 : 1'bz;  // Controlled_Buffer controlled_buffer_38
  assign controlled_buffer_39_out = decoder_4_out3 ? in_4[31:24] : 8'bz;  // Controlled_Buffer controlled_buffer_39
  assign controlled_buffer_39_out = decoder_3_out3 ? in_4[23:16] : 8'bz;  // Controlled_Buffer controlled_buffer_40
  assign controlled_buffer_39_out = decoder_2_out3 ? in_4[15:8] : 8'bz;  // Controlled_Buffer controlled_buffer_41
  assign controlled_buffer_39_out = decoder_1_out3 ? in_4[7:0] : 8'bz;  // Controlled_Buffer controlled_buffer_42
  assign not_4_out = ~controlled_buffer_39_out;  // NOT_Gate not_4, 8 bits wide
  assign and_7_out = not_4_out & controlled_buffer_35_out;  // AND_Gate and_7, 8 bits wide
  assign and_8_out = controlled_buffer_35_out & buffer_4_out;  // AND_Gate and_8, 8 bits wide
  assign buffer_4_out = controlled_buffer_39_out;  // Buffer buffer_4, 8 bits wide
  Pull_Resistor pull_resistor_11 (.node(controlled_buffer_35_out));
  assign controlled_buffer_34_out = decoder_1_out3 ? decoder_1_out3 : 1'bz;  // Controlled_Buffer controlled_buffer_43
  Pull_Resistor pull_resistor_12 (.node(controlled_buffer_39_out));
  assign out_7 = decoder_5_out3 ? nor_7_out : 8'bz;  // Controlled_Buffer controlled_buffer_44
  assign nor_7_out = ~(and_7_out | nor_8_out);  // NOR_Gate nor_7, 8 bits wide
  assign nor_8_out = ~(nor_7_out | and_8_out);  // NOR_Gate nor_8, 8 bits wide
  assign controlled_buffer_45_out = decoder_4_out4 ? in_4[31:24] : 8'bz;  // Controlled_Buffer controlled_buffer_45
  assign controlled_buffer_46_out = in_1 ? in_1 : 1'bz;  // Controlled_Buffer controlled_buffer_46
  assign controlled_buffer_47_out = controlled_buffer_46_out ? {8{1'b1}} : 8'bz;  // Controlled_Buffer controlled_buffer_47
  Pull_Resistor pull_resistor_13 (.node(controlled_buffer_46_out));
  assign controlled_buffer_46_out = decoder_4_out4 ? decoder_4_out4 : 1'bz;  // Controlled_Buffer controlled_buffer_48
  assign controlled_buffer_46_out = decoder_3_out4 ? decoder_3_out4 : 1'bz;  // Controlled_Buffer controlled_buffer_49
  assign controlled_buffer_46_out = decoder_2_out4 ? decoder_2_out4 : 1'bz;  // Controlled_Buffer controlled_buffer_50
  assign controlled_buffer_46_out = decoder_1_out4 ? decoder_1_out4 : 1'bz;  // Controlled_Buffer controlled_buffer_51
  assign controlled_buffer_45_out = decoder_3_out4 ? in_4[23:16] : 8'bz;  // Controlled_Buffer controlled_buffer_52
  assign controlled_buffer_45_out = decoder_2_out4 ? in_4[15:8] : 8'bz;  // Controlled_Buffer controlled_buffer_53
  assign controlled_buffer_45_out = decoder_1_out4 ? in_4[7:0] : 8'bz;  // Controlled_Buffer controlled_buffer_54
  assign not_5_out = ~controlled_buffer_45_out;  // NOT_Gate not_5, 8 bits wide
  assign and_9_out = not_5_out & controlled_buffer_47_out;  // AND_Gate and_9, 8 bits wide
  assign and_10_out = controlled_buffer_47_out & buffer_5_out;  // AND_Gate and_10, 8 bits wide
  assign buffer_5_out = controlled_buffer_45_out;  // Buffer buffer_5, 8 bits wide
  Pull_Resistor pull_resistor_14 (.node(controlled_buffer_47_out));
  Pull_Resistor pull_resistor_15 (.node(controlled_buffer_45_out));
  assign out_7 = decoder_5_out4 ? nor_9_out : 8'bz;  // Controlled_Buffer controlled_buffer_55
  assign nor_9_out = ~(and_9_out | nor_10_out);  // NOR_Gate nor_9, 8 bits wide
  assign controlled_buffer_56_out = in_1 ? in_1 : 1'bz;  // Controlled_Buffer controlled_buffer_56
  assign nor_10_out = ~(nor_9_out | and_10_out);  // NOR_Gate nor_10, 8 bits wide
  Pull_Resistor pull_resistor_16 (.node(controlled_buffer_56_out));
  assign controlled_buffer_56_out = decoder_4_out5 ? decoder_4_out5 : 1'bz;  // Controlled_Buffer controlled_buffer_57
  assign controlled_buffer_58_out = decoder_4_out5 ? in_4[31:24] : 8'bz;  // Controlled_Buffer controlled_buffer_58
  assign controlled_buffer_58_out = decoder_3_out5 ? in_4[23:16] : 8'bz;  // Controlled_Buffer controlled_buffer_59
  assign not_6_out = ~controlled_buffer_58_out;  // NOT_Gate not_6, 8 bits wide
  assign controlled_buffer_60_out = controlled_buffer_56_out ? {8{1'b1}} : 8'bz;  // Controlled_Buffer controlled_buffer_60
  assign buffer_6_out = controlled_buffer_58_out;  // Buffer buffer_6, 8 bits wide
  Pull_Resistor pull_resistor_17 (.node(controlled_buffer_60_out));
  assign controlled_buffer_56_out = decoder_3_out5 ? decoder_3_out5 : 1'bz;  // Controlled_Buffer controlled_buffer_61
  assign controlled_buffer_56_out = decoder_2_out5 ? decoder_2_out5 : 1'bz;  // Controlled_Buffer controlled_buffer_62
  assign controlled_buffer_56_out = decoder_1_out5 ? decoder_1_out5 : 1'bz;  // Controlled_Buffer controlled_buffer_63
  Pull_Resistor pull_resistor_18 (.node(controlled_buffer_58_out));
  assign controlled_buffer_58_out = decoder_2_out5 ? in_4[15:8] : 8'bz;  // Controlled_Buffer controlled_buffer_64
  assign controlled_buffer_58_out = decoder_1_out5 ? in_4[7:0] : 8'bz;  // Controlled_Buffer controlled_buffer_65
  assign out_7 = decoder_5_out5 ? nor_11_out : 8'bz;  // Controlled_Buffer controlled_buffer_66
  assign and_11_out = not_6_out & controlled_buffer_60_out;  // AND_Gate and_11, 8 bits wide
  assign nor_11_out = ~(and_11_out | nor_12_out);  // NOR_Gate nor_11, 8 bits wide
  assign nor_12_out = ~(nor_11_out | and_12_out);  // NOR_Gate nor_12, 8 bits wide
  assign and_12_out = controlled_buffer_60_out & buffer_6_out;  // AND_Gate and_12, 8 bits wide
  assign controlled_buffer_67_out = in_1 ? in_1 : 1'bz;  // Controlled_Buffer controlled_buffer_67
  assign controlled_buffer_68_out = controlled_buffer_67_out ? {8{1'b1}} : 8'bz;  // Controlled_Buffer controlled_buffer_68
  Pull_Resistor pull_resistor_19 (.node(controlled_buffer_67_out));
  assign controlled_buffer_67_out = decoder_4_out6 ? decoder_4_out6 : 1'bz;  // Controlled_Buffer controlled_buffer_69
  assign controlled_buffer_67_out = decoder_3_out6 ? decoder_3_out6 : 1'bz;  // Controlled_Buffer controlled_buffer_70
  assign controlled_buffer_71_out = decoder_4_out6 ? in_4[31:24] : 8'bz;  // Controlled_Buffer controlled_buffer_71
  assign controlled_buffer_71_out = decoder_3_out6 ? in_4[23:16] : 8'bz;  // Controlled_Buffer controlled_buffer_72
  assign controlled_buffer_71_out = decoder_2_out6 ? in_4[15:8] : 8'bz;  // Controlled_Buffer controlled_buffer_73
  assign not_7_out = ~controlled_buffer_71_out;  // NOT_Gate not_7, 8 bits wide
  assign buffer_7_out = controlled_buffer_71_out;  // Buffer buffer_7, 8 bits wide
  Pull_Resistor pull_resistor_20 (.node(controlled_buffer_68_out));
  assign controlled_buffer_67_out = decoder_2_out6 ? decoder_2_out6 : 1'bz;  // Controlled_Buffer controlled_buffer_74
  assign controlled_buffer_67_out = decoder_1_out6 ? decoder_1_out6 : 1'bz;  // Controlled_Buffer controlled_buffer_75
  Pull_Resistor pull_resistor_21 (.node(controlled_buffer_71_out));
  assign controlled_buffer_71_out = decoder_1_out6 ? in_4[7:0] : 8'bz;  // Controlled_Buffer controlled_buffer_76
  assign out_7 = decoder_5_out6 ? nor_13_out : 8'bz;  // Controlled_Buffer controlled_buffer_77
  assign and_13_out = not_7_out & controlled_buffer_68_out;  // AND_Gate and_13, 8 bits wide
  assign nor_13_out = ~(and_13_out | nor_14_out);  // NOR_Gate nor_13, 8 bits wide
  assign nor_14_out = ~(nor_13_out | and_14_out);  // NOR_Gate nor_14, 8 bits wide
  assign and_14_out = controlled_buffer_68_out & buffer_7_out;  // AND_Gate and_14, 8 bits wide
  assign controlled_buffer_78_out = in_1 ? in_1 : 1'bz;  // Controlled_Buffer controlled_buffer_78
  assign controlled_buffer_79_out = controlled_buffer_78_out ? {8{1'b1}} : 8'bz;  // Controlled_Buffer controlled_buffer_79
  Pull_Resistor pull_resistor_22 (.node(controlled_buffer_78_out));
  assign controlled_buffer_78_out = decoder_4_out7 ? decoder_4_out7 : 1'bz;  // Controlled_Buffer controlled_buffer_80
  assign controlled_buffer_78_out = decoder_3_out7 ? decoder_3_out7 : 1'bz;  // Controlled_Buffer controlled_buffer_81
  assign controlled_buffer_78_out = decoder_2_out7 ? decoder_2_out7 : 1'bz;  // Controlled_Buffer controlled_buffer_82
  assign controlled_buffer_83_out = decoder_4_out7 ? in_4[31:24] : 8'bz;  // Controlled_Buffer controlled_buffer_83
  assign controlled_buffer_83_out = decoder_3_out7 ? in_4[23:16] : 8'bz;  // Controlled_Buffer controlled_buffer_84
  assign controlled_buffer_83_out = decoder_2_out7 ? in_4[15:8] : 8'bz;  // Controlled_Buffer controlled_buffer_85
  assign controlled_buffer_83_out = decoder_1_out7 ? in_4[7:0] : 8'bz;  // Controlled_Buffer controlled_buffer_86
  assign not_8_out = ~controlled_buffer_83_out;  // NOT_Gate not_8, 8 bits wide
  assign and_15_out = not_8_out & controlled_buffer_79_out;  // AND_Gate and_15, 8 bits wide
  assign and_16_out = controlled_buffer_79_out & buffer_8_out;  // AND_Gate and_16, 8 bits wide
  assign buffer_8_out = controlled_buffer_83_out;  // Buffer buffer_8, 8 bits wide
  Pull_Resistor pull_resistor_23 (.node(controlled_buffer_79_out));
  assign controlled_buffer_78_out = decoder_1_out7 ? decoder_1_out7 : 1'bz;  // Controlled_Buffer controlled_buffer_87
  Pull_Resistor pull_resistor_24 (.node(controlled_buffer_83_out));
  assign out_7 = decoder_5_out7 ? nor_15_out : 8'bz;  // Controlled_Buffer controlled_buffer_88
  assign nor_15_out = ~(and_15_out | nor_16_out);  // NOR_Gate nor_15, 8 bits wide
  assign nor_16_out = ~(nor_15_out | and_16_out);  // NOR_Gate nor_16, 8 bits wide
  assign controlled_buffer_89_out = decoder_4_out8 ? in_4[31:24] : 8'bz;  // Controlled_Buffer controlled_buffer_89
  assign controlled_buffer_90_out = in_1 ? in_1 : 1'bz;  // Controlled_Buffer controlled_buffer_90
  assign controlled_buffer_91_out = controlled_buffer_90_out ? {8{1'b1}} : 8'bz;  // Controlled_Buffer controlled_buffer_91
  Pull_Resistor pull_resistor_25 (.node(controlled_buffer_90_out));
  assign controlled_buffer_90_out = decoder_4_out8 ? decoder_4_out8 : 1'bz;  // Controlled_Buffer controlled_buffer_92
  assign controlled_buffer_90_out = decoder_3_out8 ? decoder_3_out8 : 1'bz;  // Controlled_Buffer controlled_buffer_93
  assign controlled_buffer_90_out = decoder_2_out8 ? decoder_2_out8 : 1'bz;  // Controlled_Buffer controlled_buffer_94
  assign controlled_buffer_90_out = decoder_1_out8 ? decoder_1_out8 : 1'bz;  // Controlled_Buffer controlled_buffer_95
  assign controlled_buffer_89_out = decoder_3_out8 ? in_4[23:16] : 8'bz;  // Controlled_Buffer controlled_buffer_96
  assign controlled_buffer_89_out = decoder_2_out8 ? in_4[15:8] : 8'bz;  // Controlled_Buffer controlled_buffer_97
  assign controlled_buffer_89_out = decoder_1_out8 ? in_4[7:0] : 8'bz;  // Controlled_Buffer controlled_buffer_98
  assign not_9_out = ~controlled_buffer_89_out;  // NOT_Gate not_9, 8 bits wide
  assign and_17_out = not_9_out & controlled_buffer_91_out;  // AND_Gate and_17, 8 bits wide
  assign and_18_out = controlled_buffer_91_out & buffer_9_out;  // AND_Gate and_18, 8 bits wide
  assign buffer_9_out = controlled_buffer_89_out;  // Buffer buffer_9, 8 bits wide
  Pull_Resistor pull_resistor_26 (.node(controlled_buffer_91_out));
  Pull_Resistor pull_resistor_27 (.node(controlled_buffer_89_out));
  assign out_7 = decoder_5_out8 ? nor_17_out : 8'bz;  // Controlled_Buffer controlled_buffer_99
  assign nor_17_out = ~(and_17_out | nor_18_out);  // NOR_Gate nor_17, 8 bits wide
  assign controlled_buffer_100_out = in_1 ? in_1 : 1'bz;  // Controlled_Buffer controlled_buffer_100
  assign nor_18_out = ~(nor_17_out | and_18_out);  // NOR_Gate nor_18, 8 bits wide
  Pull_Resistor pull_resistor_28 (.node(controlled_buffer_100_out));
  assign controlled_buffer_100_out = decoder_4_out9 ? decoder_4_out9 : 1'bz;  // Controlled_Buffer controlled_buffer_101
  assign controlled_buffer_102_out = decoder_4_out9 ? in_4[31:24] : 8'bz;  // Controlled_Buffer controlled_buffer_102
  assign controlled_buffer_102_out = decoder_3_out9 ? in_4[23:16] : 8'bz;  // Controlled_Buffer controlled_buffer_103
  assign not_10_out = ~controlled_buffer_102_out;  // NOT_Gate not_10, 8 bits wide
  assign controlled_buffer_104_out = controlled_buffer_100_out ? {8{1'b1}} : 8'bz;  // Controlled_Buffer controlled_buffer_104
  assign buffer_10_out = controlled_buffer_102_out;  // Buffer buffer_10, 8 bits wide
  Pull_Resistor pull_resistor_29 (.node(controlled_buffer_104_out));
  assign controlled_buffer_100_out = decoder_3_out9 ? decoder_3_out9 : 1'bz;  // Controlled_Buffer controlled_buffer_105
  assign controlled_buffer_100_out = decoder_2_out9 ? decoder_2_out9 : 1'bz;  // Controlled_Buffer controlled_buffer_106
  assign controlled_buffer_100_out = decoder_1_out9 ? decoder_1_out9 : 1'bz;  // Controlled_Buffer controlled_buffer_107
  Pull_Resistor pull_resistor_30 (.node(controlled_buffer_102_out));
  assign controlled_buffer_102_out = decoder_2_out9 ? in_4[15:8] : 8'bz;  // Controlled_Buffer controlled_buffer_108
  assign controlled_buffer_102_out = decoder_1_out9 ? in_4[7:0] : 8'bz;  // Controlled_Buffer controlled_buffer_109
  assign out_7 = decoder_5_out9 ? nor_19_out : 8'bz;  // Controlled_Buffer controlled_buffer_110
  assign and_19_out = not_10_out & controlled_buffer_104_out;  // AND_Gate and_19, 8 bits wide
  assign nor_19_out = ~(and_19_out | nor_20_out);  // NOR_Gate nor_19, 8 bits wide
  assign nor_20_out = ~(nor_19_out | and_20_out);  // NOR_Gate nor_20, 8 bits wide
  assign and_20_out = controlled_buffer_104_out & buffer_10_out;  // AND_Gate and_20, 8 bits wide
  assign controlled_buffer_111_out = in_1 ? in_1 : 1'bz;  // Controlled_Buffer controlled_buffer_111
  assign controlled_buffer_112_out = controlled_buffer_111_out ? {8{1'b1}} : 8'bz;  // Controlled_Buffer controlled_buffer_112
  Pull_Resistor pull_resistor_31 (.node(controlled_buffer_111_out));
  assign controlled_buffer_111_out = decoder_4_out10 ? decoder_4_out10 : 1'bz;  // Controlled_Buffer controlled_buffer_113
  assign controlled_buffer_111_out = decoder_3_out10 ? decoder_3_out10 : 1'bz;  // Controlled_Buffer controlled_buffer_114
  assign controlled_buffer_115_out = decoder_4_out10 ? in_4[31:24] : 8'bz;  // Controlled_Buffer controlled_buffer_115
  assign controlled_buffer_115_out = decoder_3_out10 ? in_4[23:16] : 8'bz;  // Controlled_Buffer controlled_buffer_116
  assign controlled_buffer_115_out = decoder_2_out10 ? in_4[15:8] : 8'bz;  // Controlled_Buffer controlled_buffer_117
  assign not_11_out = ~controlled_buffer_115_out;  // NOT_Gate not_11, 8 bits wide
  assign buffer_11_out = controlled_buffer_115_out;  // Buffer buffer_11, 8 bits wide
  Pull_Resistor pull_resistor_32 (.node(controlled_buffer_112_out));
  assign controlled_buffer_111_out = decoder_2_out10 ? decoder_2_out10 : 1'bz;  // Controlled_Buffer controlled_buffer_118
  assign controlled_buffer_111_out = decoder_1_out10 ? decoder_1_out10 : 1'bz;  // Controlled_Buffer controlled_buffer_119
  Pull_Resistor pull_resistor_33 (.node(controlled_buffer_115_out));
  assign controlled_buffer_115_out = decoder_1_out10 ? in_4[7:0] : 8'bz;  // Controlled_Buffer controlled_buffer_120
  assign out_7 = decoder_5_out10 ? nor_21_out : 8'bz;  // Controlled_Buffer controlled_buffer_121
  assign and_21_out = not_11_out & controlled_buffer_112_out;  // AND_Gate and_21, 8 bits wide
  assign nor_21_out = ~(and_21_out | nor_22_out);  // NOR_Gate nor_21, 8 bits wide
  assign nor_22_out = ~(nor_21_out | and_22_out);  // NOR_Gate nor_22, 8 bits wide
  assign and_22_out = controlled_buffer_112_out & buffer_11_out;  // AND_Gate and_22, 8 bits wide
  assign controlled_buffer_122_out = in_1 ? in_1 : 1'bz;  // Controlled_Buffer controlled_buffer_122
  assign controlled_buffer_123_out = controlled_buffer_122_out ? {8{1'b1}} : 8'bz;  // Controlled_Buffer controlled_buffer_123
  Pull_Resistor pull_resistor_34 (.node(controlled_buffer_122_out));
  assign controlled_buffer_122_out = decoder_4_out11 ? decoder_4_out11 : 1'bz;  // Controlled_Buffer controlled_buffer_124
  assign controlled_buffer_122_out = decoder_3_out11 ? decoder_3_out11 : 1'bz;  // Controlled_Buffer controlled_buffer_125
  assign controlled_buffer_122_out = decoder_2_out11 ? decoder_2_out11 : 1'bz;  // Controlled_Buffer controlled_buffer_126
  assign controlled_buffer_127_out = decoder_4_out11 ? in_4[31:24] : 8'bz;  // Controlled_Buffer controlled_buffer_127
  assign controlled_buffer_127_out = decoder_3_out11 ? in_4[23:16] : 8'bz;  // Controlled_Buffer controlled_buffer_128
  assign controlled_buffer_127_out = decoder_2_out11 ? in_4[15:8] : 8'bz;  // Controlled_Buffer controlled_buffer_129
  assign controlled_buffer_127_out = decoder_1_out11 ? in_4[7:0] : 8'bz;  // Controlled_Buffer controlled_buffer_130
  assign not_12_out = ~controlled_buffer_127_out;  // NOT_Gate not_12, 8 bits wide
  assign and_23_out = not_12_out & controlled_buffer_123_out;  // AND_Gate and_23, 8 bits wide
  assign and_24_out = controlled_buffer_123_out & buffer_12_out;  // AND_Gate and_24, 8 bits wide
  assign buffer_12_out = controlled_buffer_127_out;  // Buffer buffer_12, 8 bits wide
  Pull_Resistor pull_resistor_35 (.node(controlled_buffer_123_out));
  assign controlled_buffer_122_out = decoder_1_out11 ? decoder_1_out11 : 1'bz;  // Controlled_Buffer controlled_buffer_131
  Pull_Resistor pull_resistor_36 (.node(controlled_buffer_127_out));
  assign out_7 = decoder_5_out11 ? nor_23_out : 8'bz;  // Controlled_Buffer controlled_buffer_132
  assign nor_23_out = ~(and_23_out | nor_24_out);  // NOR_Gate nor_23, 8 bits wide
  assign nor_24_out = ~(nor_23_out | and_24_out);  // NOR_Gate nor_24, 8 bits wide
  assign controlled_buffer_133_out = decoder_4_out12 ? in_4[31:24] : 8'bz;  // Controlled_Buffer controlled_buffer_133
  assign controlled_buffer_134_out = in_1 ? in_1 : 1'bz;  // Controlled_Buffer controlled_buffer_134
  assign controlled_buffer_135_out = controlled_buffer_134_out ? {8{1'b1}} : 8'bz;  // Controlled_Buffer controlled_buffer_135
  Pull_Resistor pull_resistor_37 (.node(controlled_buffer_134_out));
  assign controlled_buffer_134_out = decoder_4_out12 ? decoder_4_out12 : 1'bz;  // Controlled_Buffer controlled_buffer_136
  assign controlled_buffer_134_out = decoder_3_out12 ? decoder_3_out12 : 1'bz;  // Controlled_Buffer controlled_buffer_137
  assign controlled_buffer_134_out = decoder_2_out12 ? decoder_2_out12 : 1'bz;  // Controlled_Buffer controlled_buffer_138
  assign controlled_buffer_134_out = decoder_1_out12 ? decoder_1_out12 : 1'bz;  // Controlled_Buffer controlled_buffer_139
  assign controlled_buffer_133_out = decoder_3_out12 ? in_4[23:16] : 8'bz;  // Controlled_Buffer controlled_buffer_140
  assign controlled_buffer_133_out = decoder_2_out12 ? in_4[15:8] : 8'bz;  // Controlled_Buffer controlled_buffer_141
  assign controlled_buffer_133_out = decoder_1_out12 ? in_4[7:0] : 8'bz;  // Controlled_Buffer controlled_buffer_142
  assign not_13_out = ~controlled_buffer_133_out;  // NOT_Gate not_13, 8 bits wide
  assign and_25_out = not_13_out & controlled_buffer_135_out;  // AND_Gate and_25, 8 bits wide
  assign and_26_out = controlled_buffer_135_out & buffer_13_out;  // AND_Gate and_26, 8 bits wide
  assign buffer_13_out = controlled_buffer_133_out;  // Buffer buffer_13, 8 bits wide
  Pull_Resistor pull_resistor_38 (.node(controlled_buffer_135_out));
  Pull_Resistor pull_resistor_39 (.node(controlled_buffer_133_out));
  assign out_7 = decoder_5_out12 ? nor_25_out : 8'bz;  // Controlled_Buffer controlled_buffer_143
  assign nor_25_out = ~(and_25_out | nor_26_out);  // NOR_Gate nor_25, 8 bits wide
  assign controlled_buffer_144_out = in_1 ? in_1 : 1'bz;  // Controlled_Buffer controlled_buffer_144
  assign nor_26_out = ~(nor_25_out | and_26_out);  // NOR_Gate nor_26, 8 bits wide
  Pull_Resistor pull_resistor_40 (.node(controlled_buffer_144_out));
  assign controlled_buffer_144_out = decoder_4_out13 ? decoder_4_out13 : 1'bz;  // Controlled_Buffer controlled_buffer_145
  assign controlled_buffer_146_out = decoder_4_out13 ? in_4[31:24] : 8'bz;  // Controlled_Buffer controlled_buffer_146
  assign controlled_buffer_146_out = decoder_3_out13 ? in_4[23:16] : 8'bz;  // Controlled_Buffer controlled_buffer_147
  assign not_14_out = ~controlled_buffer_146_out;  // NOT_Gate not_14, 8 bits wide
  assign controlled_buffer_148_out = controlled_buffer_144_out ? {8{1'b1}} : 8'bz;  // Controlled_Buffer controlled_buffer_148
  assign buffer_14_out = controlled_buffer_146_out;  // Buffer buffer_14, 8 bits wide
  Pull_Resistor pull_resistor_41 (.node(controlled_buffer_148_out));
  assign controlled_buffer_144_out = decoder_3_out13 ? decoder_3_out13 : 1'bz;  // Controlled_Buffer controlled_buffer_149
  assign controlled_buffer_144_out = decoder_2_out13 ? decoder_2_out13 : 1'bz;  // Controlled_Buffer controlled_buffer_150
  assign controlled_buffer_144_out = decoder_1_out13 ? decoder_1_out13 : 1'bz;  // Controlled_Buffer controlled_buffer_151
  Pull_Resistor pull_resistor_42 (.node(controlled_buffer_146_out));
  assign controlled_buffer_146_out = decoder_2_out13 ? in_4[15:8] : 8'bz;  // Controlled_Buffer controlled_buffer_152
  assign controlled_buffer_146_out = decoder_1_out13 ? in_4[7:0] : 8'bz;  // Controlled_Buffer controlled_buffer_153
  assign out_7 = decoder_5_out13 ? nor_27_out : 8'bz;  // Controlled_Buffer controlled_buffer_154
  assign and_27_out = not_14_out & controlled_buffer_148_out;  // AND_Gate and_27, 8 bits wide
  assign nor_27_out = ~(and_27_out | nor_28_out);  // NOR_Gate nor_27, 8 bits wide
  assign nor_28_out = ~(nor_27_out | and_28_out);  // NOR_Gate nor_28, 8 bits wide
  assign and_28_out = controlled_buffer_148_out & buffer_14_out;  // AND_Gate and_28, 8 bits wide
  assign controlled_buffer_155_out = in_1 ? in_1 : 1'bz;  // Controlled_Buffer controlled_buffer_155
  assign controlled_buffer_156_out = controlled_buffer_155_out ? {8{1'b1}} : 8'bz;  // Controlled_Buffer controlled_buffer_156
  Pull_Resistor pull_resistor_43 (.node(controlled_buffer_155_out));
  assign controlled_buffer_155_out = decoder_4_out14 ? decoder_4_out14 : 1'bz;  // Controlled_Buffer controlled_buffer_157
  assign controlled_buffer_155_out = decoder_3_out14 ? decoder_3_out14 : 1'bz;  // Controlled_Buffer controlled_buffer_158
  assign controlled_buffer_159_out = decoder_4_out14 ? in_4[31:24] : 8'bz;  // Controlled_Buffer controlled_buffer_159
  assign controlled_buffer_159_out = decoder_3_out14 ? in_4[23:16] : 8'bz;  // Controlled_Buffer controlled_buffer_160
  assign controlled_buffer_159_out = decoder_2_out14 ? in_4[15:8] : 8'bz;  // Controlled_Buffer controlled_buffer_161
  assign not_15_out = ~controlled_buffer_159_out;  // NOT_Gate not_15, 8 bits wide
  assign buffer_15_out = controlled_buffer_159_out;  // Buffer buffer_15, 8 bits wide
  Pull_Resistor pull_resistor_44 (.node(controlled_buffer_156_out));
  assign controlled_buffer_155_out = decoder_2_out14 ? decoder_2_out14 : 1'bz;  // Controlled_Buffer controlled_buffer_162
  assign controlled_buffer_155_out = decoder_1_out14 ? decoder_1_out14 : 1'bz;  // Controlled_Buffer controlled_buffer_163
  Pull_Resistor pull_resistor_45 (.node(controlled_buffer_159_out));
  assign controlled_buffer_159_out = decoder_1_out14 ? in_4[7:0] : 8'bz;  // Controlled_Buffer controlled_buffer_164
  assign out_7 = decoder_5_out14 ? nor_29_out : 8'bz;  // Controlled_Buffer controlled_buffer_165
  assign and_29_out = not_15_out & controlled_buffer_156_out;  // AND_Gate and_29, 8 bits wide
  assign nor_29_out = ~(and_29_out | nor_30_out);  // NOR_Gate nor_29, 8 bits wide
  assign nor_30_out = ~(nor_29_out | and_30_out);  // NOR_Gate nor_30, 8 bits wide
  assign and_30_out = controlled_buffer_156_out & buffer_15_out;  // AND_Gate and_30, 8 bits wide
  assign controlled_buffer_166_out = in_1 ? in_1 : 1'bz;  // Controlled_Buffer controlled_buffer_166
  assign controlled_buffer_167_out = controlled_buffer_166_out ? {8{1'b1}} : 8'bz;  // Controlled_Buffer controlled_buffer_167
  Pull_Resistor pull_resistor_46 (.node(controlled_buffer_166_out));
  assign controlled_buffer_166_out = decoder_4_out15 ? decoder_4_out15 : 1'bz;  // Controlled_Buffer controlled_buffer_168
  assign controlled_buffer_166_out = decoder_3_out15 ? decoder_3_out15 : 1'bz;  // Controlled_Buffer controlled_buffer_169
  assign controlled_buffer_166_out = decoder_2_out15 ? decoder_2_out15 : 1'bz;  // Controlled_Buffer controlled_buffer_170
  assign controlled_buffer_171_out = decoder_4_out15 ? in_4[31:24] : 8'bz;  // Controlled_Buffer controlled_buffer_171
  assign controlled_buffer_171_out = decoder_3_out15 ? in_4[23:16] : 8'bz;  // Controlled_Buffer controlled_buffer_172
  assign controlled_buffer_171_out = decoder_2_out15 ? in_4[15:8] : 8'bz;  // Controlled_Buffer controlled_buffer_173
  assign controlled_buffer_171_out = decoder_1_out15 ? in_4[7:0] : 8'bz;  // Controlled_Buffer controlled_buffer_174
  assign not_16_out = ~controlled_buffer_171_out;  // NOT_Gate not_16, 8 bits wide
  assign and_31_out = not_16_out & controlled_buffer_167_out;  // AND_Gate and_31, 8 bits wide
  assign and_32_out = controlled_buffer_167_out & buffer_16_out;  // AND_Gate and_32, 8 bits wide
  assign buffer_16_out = controlled_buffer_171_out;  // Buffer buffer_16, 8 bits wide
  Pull_Resistor pull_resistor_47 (.node(controlled_buffer_167_out));
  assign controlled_buffer_166_out = decoder_1_out15 ? decoder_1_out15 : 1'bz;  // Controlled_Buffer controlled_buffer_175
  Pull_Resistor pull_resistor_48 (.node(controlled_buffer_171_out));
  assign out_7 = decoder_5_out15 ? nor_31_out : 8'bz;  // Controlled_Buffer controlled_buffer_176
  assign nor_31_out = ~(and_31_out | nor_32_out);  // NOR_Gate nor_31, 8 bits wide
  assign nor_32_out = ~(nor_31_out | and_32_out);  // NOR_Gate nor_32, 8 bits wide
endmodule

module R7 (
  input  [31:0] in_1,
  input  [47:0] in_2,
  input  [3:0] in_3,
  input  [11:0] in_4,
  input  in_5,
  input  in_6,
  output [7:0] out_7
);

  wire decoder_5_out0, decoder_5_out1, decoder_5_out2, decoder_5_out3, decoder_5_out4, decoder_5_out5,
       decoder_5_out6, decoder_5_out7, decoder_5_out8, decoder_5_out9, decoder_5_out10, decoder_5_out11,
       decoder_5_out12, decoder_5_out13, decoder_5_out14, decoder_5_out15;
  wire [3:0] decoder_1_out0, decoder_1_out1, decoder_1_out2, decoder_1_out3, decoder_1_out4, decoder_1_out5,
       decoder_1_out6, decoder_1_out7, decoder_1_out8, decoder_1_out9, decoder_1_out10, decoder_1_out11,
       decoder_1_out12, decoder_1_out13, decoder_1_out14, decoder_1_out15;

  Decoder #(.select(4)) decoder_1 (
    .out0(decoder_1_out0[0]), .out1(decoder_1_out1[0]), .out2(decoder_1_out2[0]), .out3(decoder_1_out3[0]),
    .out4(decoder_1_out4[0]), .out5(decoder_1_out5[0]), .out6(decoder_1_out6[0]), .out7(decoder_1_out7[0]),
    .out8(decoder_1_out8[0]), .out9(decoder_1_out9[0]), .out10(decoder_1_out10[0]),
    .out11(decoder_1_out11[0]), .out12(decoder_1_out12[0]), .out13(decoder_1_out13[0]),
    .out14(decoder_1_out14[0]), .out15(decoder_1_out15[0]), .sel(in_2[3:0]), .en(in_3[0]));
  Decoder #(.select(4)) decoder_2 (
    .out0(decoder_1_out0[1]), .out1(decoder_1_out1[1]), .out2(decoder_1_out2[1]), .out3(decoder_1_out3[1]),
    .out4(decoder_1_out4[1]), .out5(decoder_1_out5[1]), .out6(decoder_1_out6[1]), .out7(decoder_1_out7[1]),
    .out8(decoder_1_out8[1]), .out9(decoder_1_out9[1]), .out10(decoder_1_out10[1]),
    .out11(decoder_1_out11[1]), .out12(decoder_1_out12[1]), .out13(decoder_1_out13[1]),
    .out14(decoder_1_out14[1]), .out15(decoder_1_out15[1]), .sel(in_2[15:12]), .en(in_3[1]));
  Decoder #(.select(4)) decoder_3 (
    .out0(decoder_1_out0[2]), .out1(decoder_1_out1[2]), .out2(decoder_1_out2[2]), .out3(decoder_1_out3[2]),
    .out4(decoder_1_out4[2]), .out5(decoder_1_out5[2]), .out6(decoder_1_out6[2]), .out7(decoder_1_out7[2]),
    .out8(decoder_1_out8[2]), .out9(decoder_1_out9[2]), .out10(decoder_1_out10[2]),
    .out11(decoder_1_out11[2]), .out12(decoder_1_out12[2]), .out13(decoder_1_out13[2]),
    .out14(decoder_1_out14[2]), .out15(decoder_1_out15[2]), .sel(in_2[27:24]), .en(in_3[2]));
  Decoder #(.select(4)) decoder_4 (
    .out0(decoder_1_out0[3]), .out1(decoder_1_out1[3]), .out2(decoder_1_out2[3]), .out3(decoder_1_out3[3]),
    .out4(decoder_1_out4[3]), .out5(decoder_1_out5[3]), .out6(decoder_1_out6[3]), .out7(decoder_1_out7[3]),
    .out8(decoder_1_out8[3]), .out9(decoder_1_out9[3]), .out10(decoder_1_out10[3]),
    .out11(decoder_1_out11[3]), .out12(decoder_1_out12[3]), .out13(decoder_1_out13[3]),
    .out14(decoder_1_out14[3]), .out15(decoder_1_out15[3]), .sel(in_2[39:36]), .en(in_3[3]));
  Decoder #(.select(4)) decoder_5 (
    .out0(decoder_5_out0), .out1(decoder_5_out1), .out2(decoder_5_out2), .out3(decoder_5_out3),
    .out4(decoder_5_out4), .out5(decoder_5_out5), .out6(decoder_5_out6), .out7(decoder_5_out7),
    .out8(decoder_5_out8), .out9(decoder_5_out9), .out10(decoder_5_out10), .out11(decoder_5_out11),
    .out12(decoder_5_out12), .out13(decoder_5_out13), .out14(decoder_5_out14), .out15(decoder_5_out15),
    .sel(in_4[3:0]), .en(in_5));
  R6 r6_1 (
    .in_1(in_1), .in_2({in_2[47:40], in_2[35:28], in_2[23:16], in_2[11:4]}), .in_3(decoder_1_out0),
    .in_4(in_4[11:4]), .in_5(decoder_5_out0), .in_6(in_6), .out_7(out_7));
  R6 r6_2 (
    .in_1(in_1), .in_2({in_2[47:40], in_2[35:28], in_2[23:16], in_2[11:4]}), .in_3(decoder_1_out1),
    .in_4(in_4[11:4]), .in_5(decoder_5_out1), .in_6(in_6), .out_7(out_7));
  R6 r6_3 (
    .in_1(in_1), .in_2({in_2[47:40], in_2[35:28], in_2[23:16], in_2[11:4]}), .in_3(decoder_1_out2),
    .in_4(in_4[11:4]), .in_5(decoder_5_out2), .in_6(in_6), .out_7(out_7));
  R6 r6_4 (
    .in_1(in_1), .in_2({in_2[47:40], in_2[35:28], in_2[23:16], in_2[11:4]}), .in_3(decoder_1_out3),
    .in_4(in_4[11:4]), .in_5(decoder_5_out3), .in_6(in_6), .out_7(out_7));
  R6 r6_5 (
    .in_1(in_1), .in_2({in_2[47:40], in_2[35:28], in_2[23:16], in_2[11:4]}), .in_3(decoder_1_out4),
    .in_4(in_4[11:4]), .in_5(decoder_5_out4), .in_6(in_6), .out_7(out_7));
  R6 r6_6 (
    .in_1(in_1), .in_2({in_2[47:40], in_2[35:28], in_2[23:16], in_2[11:4]}), .in_3(decoder_1_out5),
    .in_4(in_4[11:4]), .in_5(decoder_5_out5), .in_6(in_6), .out_7(out_7));
  R6 r6_7 (
    .in_1(in_1), .in_2({in_2[47:40], in_2[35:28], in_2[23:16], in_2[11:4]}), .in_3(decoder_1_out6),
    .in_4(in_4[11:4]), .in_5(decoder_5_out6), .in_6(in_6), .out_7(out_7));
  R6 r6_8 (
    .in_1(in_1), .in_2({in_2[47:40], in_2[35:28], in_2[23:16], in_2[11:4]}), .in_3(decoder_1_out7),
    .in_4(in_4[11:4]), .in_5(decoder_5_out7), .in_6(in_6), .out_7(out_7));
  R6 r6_9 (
    .in_1(in_1), .in_2({in_2[47:40], in_2[35:28], in_2[23:16], in_2[11:4]}), .in_3(decoder_1_out8),
    .in_4(in_4[11:4]), .in_5(decoder_5_out8), .in_6(in_6), .out_7(out_7));
  R6 r6_10 (
    .in_1(in_1), .in_2({in_2[47:40], in_2[35:28], in_2[23:16], in_2[11:4]}), .in_3(decoder_1_out9),
    .in_4(in_4[11:4]), .in_5(decoder_5_out9), .in_6(in_6), .out_7(out_7));
  R6 r6_11 (
    .in_1(in_1), .in_2({in_2[47:40], in_2[35:28], in_2[23:16], in_2[11:4]}), .in_3(decoder_1_out10),
    .in_4(in_4[11:4]), .in_5(decoder_5_out10), .in_6(in_6), .out_7(out_7));
  R6 r6_12 (
    .in_1(in_1), .in_2({in_2[47:40], in_2[35:28], in_2[23:16], in_2[11:4]}), .in_3(decoder_1_out11),
    .in_4(in_4[11:4]), .in_5(decoder_5_out11), .in_6(in_6), .out_7(out_7));
  R6 r6_13 (
    .in_1(in_1), .in_2({in_2[47:40], in_2[35:28], in_2[23:16], in_2[11:4]}), .in_3(decoder_1_out12),
    .in_4(in_4[11:4]), .in_5(decoder_5_out12), .in_6(in_6), .out_7(out_7));
  R6 r6_14 (
    .in_1(in_1), .in_2({in_2[47:40], in_2[35:28], in_2[23:16], in_2[11:4]}), .in_3(decoder_1_out13),
    .in_4(in_4[11:4]), .in_5(decoder_5_out13), .in_6(in_6), .out_7(out_7));
  R6 r6_15 (
    .in_1(in_1), .in_2({in_2[47:40], in_2[35:28], in_2[23:16], in_2[11:4]}), .in_3(decoder_1_out14),
    .in_4(in_4[11:4]), .in_5(decoder_5_out14), .in_6(in_6), .out_7(out_7));
  R6 r6_16 (
    .in_1(in_1), .in_2({in_2[47:40], in_2[35:28], in_2[23:16], in_2[11:4]}), .in_3(decoder_1_out15),
    .in_4(in_4[11:4]), .in_5(decoder_5_out15), .in_6(in_6), .out_7(out_7));
endmodule

module R6 (
  input  [31:0] in_1,
  input  [31:0] in_2,
  input  [3:0] in_3,
  input  [7:0] in_4,
  input  in_5,
  input  in_6,
  output [7:0] out_7
);

  wire clock_1_out, d1_1_out_3, decoder_5_out0, decoder_5_out1, decoder_5_out2, decoder_5_out3,
       decoder_5_out4, decoder_5_out5, decoder_5_out6, decoder_5_out7, decoder_5_out8, decoder_5_out9,
       decoder_5_out10, decoder_5_out11, decoder_5_out12, decoder_5_out13, decoder_5_out14, decoder_5_out15;
  wire [3:0] d4_1_out_3, d8_1_out_3, d8_1_out_3_2, decoder_1_out0, decoder_1_out1, decoder_1_out2,
       decoder_1_out3, decoder_1_out4, decoder_1_out5, decoder_1_out6, decoder_1_out7, decoder_1_out8,
       decoder_1_out9, decoder_1_out10, decoder_1_out11, decoder_1_out12, decoder_1_out13, decoder_1_out14,
       decoder_1_out15;
  wire [31:0] d32_1_out_3, d32_2_out_3;

  Decoder #(.select(4)) decoder_1 (
    .out0(decoder_1_out0[0]), .out1(decoder_1_out1[0]), .out2(decoder_1_out2[0]), .out3(decoder_1_out3[0]),
    .out4(decoder_1_out4[0]), .out5(decoder_1_out5[0]), .out6(decoder_1_out6[0]), .out7(decoder_1_out7[0]),
    .out8(decoder_1_out8[0]), .out9(decoder_1_out9[0]), .out10(decoder_1_out10[0]),
    .out11(decoder_1_out11[0]), .out12(decoder_1_out12[0]), .out13(decoder_1_out13[0]),
    .out14(decoder_1_out14[0]), .out15(decoder_1_out15[0]), .sel(d32_2_out_3[3:0]), .en(d4_1_out_3[0]));
  Decoder #(.select(4)) decoder_2 (
    .out0(decoder_1_out0[1]), .out1(decoder_1_out1[1]), .out2(decoder_1_out2[1]), .out3(decoder_1_out3[1]),
    .out4(decoder_1_out4[1]), .out5(decoder_1_out5[1]), .out6(decoder_1_out6[1]), .out7(decoder_1_out7[1]),
    .out8(decoder_1_out8[1]), .out9(decoder_1_out9[1]), .out10(decoder_1_out10[1]),
    .out11(decoder_1_out11[1]), .out12(decoder_1_out12[1]), .out13(decoder_1_out13[1]),
    .out14(decoder_1_out14[1]), .out15(decoder_1_out15[1]), .sel(d32_2_out_3[11:8]), .en(d4_1_out_3[1]));
  Decoder #(.select(4)) decoder_3 (
    .out0(decoder_1_out0[2]), .out1(decoder_1_out1[2]), .out2(decoder_1_out2[2]), .out3(decoder_1_out3[2]),
    .out4(decoder_1_out4[2]), .out5(decoder_1_out5[2]), .out6(decoder_1_out6[2]), .out7(decoder_1_out7[2]),
    .out8(decoder_1_out8[2]), .out9(decoder_1_out9[2]), .out10(decoder_1_out10[2]),
    .out11(decoder_1_out11[2]), .out12(decoder_1_out12[2]), .out13(decoder_1_out13[2]),
    .out14(decoder_1_out14[2]), .out15(decoder_1_out15[2]), .sel(d32_2_out_3[19:16]), .en(d4_1_out_3[2]));
  Decoder #(.select(4)) decoder_4 (
    .out0(decoder_1_out0[3]), .out1(decoder_1_out1[3]), .out2(decoder_1_out2[3]), .out3(decoder_1_out3[3]),
    .out4(decoder_1_out4[3]), .out5(decoder_1_out5[3]), .out6(decoder_1_out6[3]), .out7(decoder_1_out7[3]),
    .out8(decoder_1_out8[3]), .out9(decoder_1_out9[3]), .out10(decoder_1_out10[3]),
    .out11(decoder_1_out11[3]), .out12(decoder_1_out12[3]), .out13(decoder_1_out13[3]),
    .out14(decoder_1_out14[3]), .out15(decoder_1_out15[3]), .sel(d32_2_out_3[27:24]), .en(d4_1_out_3[3]));
  Decoder #(.select(4)) decoder_5 (
    .out0(decoder_5_out0), .out1(decoder_5_out1), .out2(decoder_5_out2), .out3(decoder_5_out3),
    .out4(decoder_5_out4), .out5(decoder_5_out5), .out6(decoder_5_out6), .out7(decoder_5_out7),
    .out8(decoder_5_out8), .out9(decoder_5_out9), .out10(decoder_5_out10), .out11(decoder_5_out11),
    .out12(decoder_5_out12), .out13(decoder_5_out13), .out14(decoder_5_out14), .out15(decoder_5_out15),
    .sel(d8_1_out_3), .en(d1_1_out_3));
  Clock clock_1 (.out(clock_1_out));
  D32 d32_1 (.in_2(in_1), .in_1(clock_1_out), .out_3(d32_1_out_3));
  D32 d32_2 (.in_2(in_2), .in_1(clock_1_out), .out_3(d32_2_out_3));
  D4 d4_1 (.in_2(in_3), .in_1(clock_1_out), .out_3(d4_1_out_3));
  D8 d8_1 (.in_2(in_4), .in_1(clock_1_out), .out_3({d8_1_out_3_2, d8_1_out_3}));
  D1 d1_1 (.in_2(in_5), .in_1(clock_1_out), .out_3(d1_1_out_3));
  R5 r5_1 (
    .in_2(decoder_5_out0), .in_3(d8_1_out_3_2), .in_5(decoder_1_out0), .in_1(in_6),
    .in_6({d32_2_out_3[31:28], d32_2_out_3[23:20], d32_2_out_3[15:12], d32_2_out_3[7:4]}),
    .in_4(d32_1_out_3), .out_7(out_7));
  R5 r5_2 (
    .in_2(decoder_5_out1), .in_3(d8_1_out_3_2), .in_5(decoder_1_out1), .in_1(in_6),
    .in_6({d32_2_out_3[31:28], d32_2_out_3[23:20], d32_2_out_3[15:12], d32_2_out_3[7:4]}),
    .in_4(d32_1_out_3), .out_7(out_7));
  R5 r5_3 (
    .in_2(decoder_5_out2), .in_3(d8_1_out_3_2), .in_5(decoder_1_out2), .in_1(in_6),
    .in_6({d32_2_out_3[31:28], d32_2_out_3[23:20], d32_2_out_3[15:12], d32_2_out_3[7:4]}),
    .in_4(d32_1_out_3), .out_7(out_7));
  R5 r5_4 (
    .in_2(decoder_5_out3), .in_3(d8_1_out_3_2), .in_5(decoder_1_out3), .in_1(in_6),
    .in_6({d32_2_out_3[31:28], d32_2_out_3[23:20], d32_2_out_3[15:12], d32_2_out_3[7:4]}),
    .in_4(d32_1_out_3), .out_7(out_7));
  R5 r5_5 (
    .in_2(decoder_5_out4), .in_3(d8_1_out_3_2), .in_5(decoder_1_out4), .in_1(in_6),
    .in_6({d32_2_out_3[31:28], d32_2_out_3[23:20], d32_2_out_3[15:12], d32_2_out_3[7:4]}),
    .in_4(d32_1_out_3), .out_7(out_7));
  R5 r5_6 (
    .in_2(decoder_5_out5), .in_3(d8_1_out_3_2), .in_5(decoder_1_out5), .in_1(in_6),
    .in_6({d32_2_out_3[31:28], d32_2_out_3[23:20], d32_2_out_3[15:12], d32_2_out_3[7:4]}),
    .in_4(d32_1_out_3), .out_7(out_7));
  R5 r5_7 (
    .in_2(decoder_5_out6), .in_3(d8_1_out_3_2), .in_5(decoder_1_out6), .in_1(in_6),
    .in_6({d32_2_out_3[31:28], d32_2_out_3[23:20], d32_2_out_3[15:12], d32_2_out_3[7:4]}),
    .in_4(d32_1_out_3), .out_7(out_7));
  R5 r5_8 (
    .in_2(decoder_5_out7), .in_3(d8_1_out_3_2), .in_5(decoder_1_out7), .in_1(in_6),
    .in_6({d32_2_out_3[31:28], d32_2_out_3[23:20], d32_2_out_3[15:12], d32_2_out_3[7:4]}),
    .in_4(d32_1_out_3), .out_7(out_7));
  R5 r5_9 (
    .in_2(decoder_5_out8), .in_3(d8_1_out_3_2), .in_5(decoder_1_out8), .in_1(in_6),
    .in_6({d32_2_out_3[31:28], d32_2_out_3[23:20], d32_2_out_3[15:12], d32_2_out_3[7:4]}),
    .in_4(d32_1_out_3), .out_7(out_7));
  R5 r5_10 (
    .in_2(decoder_5_out9), .in_3(d8_1_out_3_2), .in_5(decoder_1_out9), .in_1(in_6),
    .in_6({d32_2_out_3[31:28], d32_2_out_3[23:20], d32_2_out_3[15:12], d32_2_out_3[7:4]}),
    .in_4(d32_1_out_3), .out_7(out_7));
  R5 r5_11 (
    .in_2(decoder_5_out10), .in_3(d8_1_out_3_2), .in_5(decoder_1_out10), .in_1(in_6),
    .in_6({d32_2_out_3[31:28], d32_2_out_3[23:20], d32_2_out_3[15:12], d32_2_out_3[7:4]}),
    .in_4(d32_1_out_3), .out_7(out_7));
  R5 r5_12 (
    .in_2(decoder_5_out11), .in_3(d8_1_out_3_2), .in_5(decoder_1_out11), .in_1(in_6),
    .in_6({d32_2_out_3[31:28], d32_2_out_3[23:20], d32_2_out_3[15:12], d32_2_out_3[7:4]}),
    .in_4(d32_1_out_3), .out_7(out_7));
  R5 r5_13 (
    .in_2(decoder_5_out12), .in_3(d8_1_out_3_2), .in_5(decoder_1_out12), .in_1(in_6),
    .in_6({d32_2_out_3[31:28], d32_2_out_3[23:20], d32_2_out_3[15:12], d32_2_out_3[7:4]}),
    .in_4(d32_1_out_3), .out_7(out_7));
  R5 r5_14 (
    .in_2(decoder_5_out13), .in_3(d8_1_out_3_2), .in_5(decoder_1_out13), .in_1(in_6),
    .in_6({d32_2_out_3[31:28], d32_2_out_3[23:20], d32_2_out_3[15:12], d32_2_out_3[7:4]}),
    .in_4(d32_1_out_3), .out_7(out_7));
  R5 r5_15 (
    .in_2(decoder_5_out14), .in_3(d8_1_out_3_2), .in_5(decoder_1_out14), .in_1(in_6),
    .in_6({d32_2_out_3[31:28], d32_2_out_3[23:20], d32_2_out_3[15:12], d32_2_out_3[7:4]}),
    .in_4(d32_1_out_3), .out_7(out_7));
  R5 r5_16 (
    .in_2(decoder_5_out15), .in_3(d8_1_out_3_2), .in_5(decoder_1_out15), .in_1(in_6),
    .in_6({d32_2_out_3[31:28], d32_2_out_3[23:20], d32_2_out_3[15:12], d32_2_out_3[7:4]}),
    .in_4(d32_1_out_3), .out_7(out_7));
endmodule

module R2 (
  input  [31:0] in_1,
  input  [31:0] in_2,
  input  [3:0] in_3,
  input  [7:0] in_4,
  input  in_5,
  input  in_6,
  output [7:0] out_7
);

  wire clock_1_out, d1_1_out_3, decoder_5_out0, decoder_5_out1, decoder_5_out2, decoder_5_out3,
       decoder_5_out4, decoder_5_out5, decoder_5_out6, decoder_5_out7, decoder_5_out8, decoder_5_out9,
       decoder_5_out10, decoder_5_out11, decoder_5_out12, decoder_5_out13, decoder_5_out14, decoder_5_out15;
  wire [3:0] d4_1_out_3, d8_1_out_3, d8_1_out_3_2, d32_2_out_3, d32_2_out_3_2, d32_2_out_3_3, d32_2_out_3_4,
       d32_2_out_3_5, d32_2_out_3_6, d32_2_out_3_7, d32_2_out_3_8, decoder_1_out0, decoder_1_out1,
       decoder_1_out2, decoder_1_out3, decoder_1_out4, decoder_1_out5, decoder_1_out6, decoder_1_out7,
       decoder_1_out8, decoder_1_out9, decoder_1_out10, decoder_1_out11, decoder_1_out12, decoder_1_out13,
       decoder_1_out14, decoder_1_out15;
  wire [31:0] d32_1_out_3;

  Decoder #(.select(4)) decoder_1 (
    .out0(decoder_1_out0[0]), .out1(decoder_1_out1[0]), .out2(decoder_1_out2[0]), .out3(decoder_1_out3[0]),
    .out4(decoder_1_out4[0]), .out5(decoder_1_out5[0]), .out6(decoder_1_out6[0]), .out7(decoder_1_out7[0]),
    .out8(decoder_1_out8[0]), .out9(decoder_1_out9[0]), .out10(decoder_1_out10[0]),
    .out11(decoder_1_out11[0]), .out12(decoder_1_out12[0]), .out13(decoder_1_out13[0]),
    .out14(decoder_1_out14[0]), .out15(decoder_1_out15[0]), .sel(d32_2_out_3), .en(d4_1_out_3[0]));
  Decoder #(.select(4)) decoder_2 (
    .out0(decoder_1_out0[1]), .out1(decoder_1_out1[1]), .out2(decoder_1_out2[1]), .out3(decoder_1_out3[1]),
    .out4(decoder_1_out4[1]), .out5(decoder_1_out5[1]), .out6(decoder_1_out6[1]), .out7(decoder_1_out7[1]),
    .out8(decoder_1_out8[1]), .out9(decoder_1_out9[1]), .out10(decoder_1_out10[1]),
    .out11(decoder_1_out11[1]), .out12(decoder_1_out12[1]), .out13(decoder_1_out13[1]),
    .out14(decoder_1_out14[1]), .out15(decoder_1_out15[1]), .sel(d32_2_out_3_2), .en(d4_1_out_3[1]));
  Decoder #(.select(4)) decoder_3 (
    .out0(decoder_1_out0[2]), .out1(decoder_1_out1[2]), .out2(decoder_1_out2[2]), .out3(decoder_1_out3[2]),
    .out4(decoder_1_out4[2]), .out5(decoder_1_out5[2]), .out6(decoder_1_out6[2]), .out7(decoder_1_out7[2]),
    .out8(decoder_1_out8[2]), .out9(decoder_1_out9[2]), .out10(decoder_1_out10[2]),
    .out11(decoder_1_out11[2]), .out12(decoder_1_out12[2]), .out13(decoder_1_out13[2]),
    .out14(decoder_1_out14[2]), .out15(decoder_1_out15[2]), .sel(d32_2_out_3_3), .en(d4_1_out_3[2]));
  Decoder #(.select(4)) decoder_4 (
    .out0(decoder_1_out0[3]), .out1(decoder_1_out1[3]), .out2(decoder_1_out2[3]), .out3(decoder_1_out3[3]),
    .out4(decoder_1_out4[3]), .out5(decoder_1_out5[3]), .out6(decoder_1_out6[3]), .out7(decoder_1_out7[3]),
    .out8(decoder_1_out8[3]), .out9(decoder_1_out9[3]), .out10(decoder_1_out10[3]),
    .out11(decoder_1_out11[3]), .out12(decoder_1_out12[3]), .out13(decoder_1_out13[3]),
    .out14(decoder_1_out14[3]), .out15(decoder_1_out15[3]), .sel(d32_2_out_3_4), .en(d4_1_out_3[3]));
  Decoder #(.select(4)) decoder_5 (
    .out0(decoder_5_out0), .out1(decoder_5_out1), .out2(decoder_5_out2), .out3(decoder_5_out3),
    .out4(decoder_5_out4), .out5(decoder_5_out5), .out6(decoder_5_out6), .out7(decoder_5_out7),
    .out8(decoder_5_out8), .out9(decoder_5_out9), .out10(decoder_5_out10), .out11(decoder_5_out11),
    .out12(decoder_5_out12), .out13(decoder_5_out13), .out14(decoder_5_out14), .out15(decoder_5_out15),
    .sel(d8_1_out_3), .en(d1_1_out_3));
  Clock clock_1 (.out(clock_1_out));
  D32 d32_1 (.in_2(in_1), .in_1(clock_1_out), .out_3(d32_1_out_3));
  D32 d32_2 (
    .in_2(in_2), .in_1(clock_1_out),
    .out_3({d32_2_out_3_8, d32_2_out_3_4, d32_2_out_3_7, d32_2_out_3_3, d32_2_out_3_6, d32_2_out_3_2, d32_2_out_3_5, d32_2_out_3}));
  D4 d4_1 (.in_2(in_3), .in_1(clock_1_out), .out_3(d4_1_out_3));
  D8 d8_1 (.in_2(in_4), .in_1(clock_1_out), .out_3({d8_1_out_3_2, d8_1_out_3}));
  D1 d1_1 (.in_2(in_5), .in_1(clock_1_out), .out_3(d1_1_out_3));
  R5 r5_1 (
    .in_2(decoder_5_out1), .in_3(d8_1_out_3_2), .in_5(decoder_1_out1), .in_1(in_6),
    .in_6({d32_2_out_3_8, d32_2_out_3_7, d32_2_out_3_6, d32_2_out_3_5}), .in_4(d32_1_out_3), .out_7(out_7));
  R5 r5_2 (
    .in_2(decoder_5_out2), .in_3(d8_1_out_3_2), .in_5(decoder_1_out2), .in_1(in_6),
    .in_6({d32_2_out_3_8, d32_2_out_3_7, d32_2_out_3_6, d32_2_out_3_5}), .in_4(d32_1_out_3), .out_7(out_7));
  R5 r5_3 (
    .in_2(decoder_5_out3), .in_3(d8_1_out_3_2), .in_5(decoder_1_out3), .in_1(in_6),
    .in_6({d32_2_out_3_8, d32_2_out_3_7, d32_2_out_3_6, d32_2_out_3_5}), .in_4(d32_1_out_3), .out_7(out_7));
  R5 r5_4 (
    .in_2(decoder_5_out4), .in_3(d8_1_out_3_2), .in_5(decoder_1_out4), .in_1(in_6),
    .in_6({d32_2_out_3_8, d32_2_out_3_7, d32_2_out_3_6, d32_2_out_3_5}), .in_4(d32_1_out_3), .out_7(out_7));
  R5 r5_5 (
    .in_2(decoder_5_out5), .in_3(d8_1_out_3_2), .in_5(decoder_1_out5), .in_1(in_6),
    .in_6({d32_2_out_3_8, d32_2_out_3_7, d32_2_out_3_6, d32_2_out_3_5}), .in_4(d32_1_out_3), .out_7(out_7));
  R5 r5_6 (
    .in_2(decoder_5_out6), .in_3(d8_1_out_3_2), .in_5(decoder_1_out6), .in_1(in_6),
    .in_6({d32_2_out_3_8, d32_2_out_3_7, d32_2_out_3_6, d32_2_out_3_5}), .in_4(d32_1_out_3), .out_7(out_7));
  R5 r5_7 (
    .in_2(decoder_5_out7), .in_3(d8_1_out_3_2), .in_5(decoder_1_out7), .in_1(in_6),
    .in_6({d32_2_out_3_8, d32_2_out_3_7, d32_2_out_3_6, d32_2_out_3_5}), .in_4(d32_1_out_3), .out_7(out_7));
  R5 r5_8 (
    .in_2(decoder_5_out8), .in_3(d8_1_out_3_2), .in_5(decoder_1_out8), .in_1(in_6),
    .in_6({d32_2_out_3_8, d32_2_out_3_7, d32_2_out_3_6, d32_2_out_3_5}), .in_4(d32_1_out_3), .out_7(out_7));
  R5 r5_9 (
    .in_2(decoder_5_out9), .in_3(d8_1_out_3_2), .in_5(decoder_1_out9), .in_1(in_6),
    .in_6({d32_2_out_3_8, d32_2_out_3_7, d32_2_out_3_6, d32_2_out_3_5}), .in_4(d32_1_out_3), .out_7(out_7));
  R5 r5_10 (
    .in_2(decoder_5_out10), .in_3(d8_1_out_3_2), .in_5(decoder_1_out10), .in_1(in_6),
    .in_6({d32_2_out_3_8, d32_2_out_3_7, d32_2_out_3_6, d32_2_out_3_5}), .in_4(d32_1_out_3), .out_7(out_7));
  R5 r5_11 (
    .in_2(decoder_5_out11), .in_3(d8_1_out_3_2), .in_5(decoder_1_out11), .in_1(in_6),
    .in_6({d32_2_out_3_8, d32_2_out_3_7, d32_2_out_3_6, d32_2_out_3_5}), .in_4(d32_1_out_3), .out_7(out_7));
  R5 r5_12 (
    .in_2(decoder_5_out12), .in_3(d8_1_out_3_2), .in_5(decoder_1_out12), .in_1(in_6),
    .in_6({d32_2_out_3_8, d32_2_out_3_7, d32_2_out_3_6, d32_2_out_3_5}), .in_4(d32_1_out_3), .out_7(out_7));
  R5 r5_13 (
    .in_2(decoder_5_out13), .in_3(d8_1_out_3_2), .in_5(decoder_1_out13), .in_1(in_6),
    .in_6({d32_2_out_3_8, d32_2_out_3_7, d32_2_out_3_6, d32_2_out_3_5}), .in_4(d32_1_out_3), .out_7(out_7));
  R5 r5_14 (
    .in_2(decoder_5_out14), .in_3(d8_1_out_3_2), .in_5(decoder_1_out14), .in_1(in_6),
    .in_6({d32_2_out_3_8, d32_2_out_3_7, d32_2_out_3_6, d32_2_out_3_5}), .in_4(d32_1_out_3), .out_7(out_7));
  R5 r5_15 (
    .in_2(decoder_5_out15), .in_3(d8_1_out_3_2), .in_5(decoder_1_out15), .in_1(in_6),
    .in_6({d32_2_out_3_8, d32_2_out_3_7, d32_2_out_3_6, d32_2_out_3_5}), .in_4(d32_1_out_3), .out_7(out_7));
  R1 r1_1 ();  // open: ReadEnable, ReadAddress, WriteEnable, reset, WriteAddress, WriteData, ReadOut
endmodule
module R1 (
  input  reset,
  input  ReadEnable,
  input  [3:0] ReadAddress,
  input  [31:0] WriteData,
  input  [3:0] WriteEnable,
  input  [15:0] WriteAddress,
  output [7:0] ReadOut
);

  wire controlled_buffer_2_out, controlled_buffer_12_out, controlled_buffer_23_out, controlled_buffer_34_out,
       controlled_buffer_46_out, controlled_buffer_56_out, controlled_buffer_67_out,
       controlled_buffer_78_out, controlled_buffer_90_out, controlled_buffer_100_out,
       controlled_buffer_111_out, controlled_buffer_122_out, controlled_buffer_134_out,
       controlled_buffer_144_out, controlled_buffer_155_out, controlled_buffer_166_out, decoder_1_out0,
       decoder_1_out1, decoder_1_out2, decoder_1_out3, decoder_1_out4, decoder_1_out5, decoder_1_out6,
       decoder_1_out7, decoder_1_out8, decoder_1_out9, decoder_1_out10, decoder_1_out11, decoder_1_out12,
       decoder_1_out13, decoder_1_out14, decoder_1_out15, decoder_2_out0, decoder_2_out1, decoder_2_out2,
       decoder_2_out3, decoder_2_out4, decoder_2_out5, decoder_2_out6, decoder_2_out7, decoder_2_out8,
       decoder_2_out9, decoder_2_out10, decoder_2_out11, decoder_2_out12, decoder_2_out13, decoder_2_out14,
       decoder_2_out15, decoder_3_out0, decoder_3_out1, decoder_3_out2, decoder_3_out3, decoder_3_out4,
       decoder_3_out5, decoder_3_out6, decoder_3_out7, decoder_3_out8, decoder_3_out9, decoder_3_out10,
       decoder_3_out11, decoder_3_out12, decoder_3_out13, decoder_3_out14, decoder_3_out15, decoder_4_out0,
       decoder_4_out1, decoder_4_out2, decoder_4_out3, decoder_4_out4, decoder_4_out5, decoder_4_out6,
       decoder_4_out7, decoder_4_out8, decoder_4_out9, decoder_4_out10, decoder_4_out11, decoder_4_out12,
       decoder_4_out13, decoder_4_out14, decoder_4_out15, decoder_5_out0, decoder_5_out1, decoder_5_out2,
       decoder_5_out3, decoder_5_out4, decoder_5_out5, decoder_5_out6, decoder_5_out7, decoder_5_out8,
       decoder_5_out9, decoder_5_out10, decoder_5_out11, decoder_5_out12, decoder_5_out13, decoder_5_out14,
       decoder_5_out15;
  wire [7:0] and_1_out, and_2_out, and_3_out, and_4_out, and_5_out, and_6_out, and_7_out, and_8_out,
       and_9_out, and_10_out, and_11_out, and_12_out, and_13_out, and_14_out, and_15_out, and_16_out,
       and_17_out, and_18_out, and_19_out, and_20_out, and_21_out, and_22_out, and_23_out, and_24_out,
       and_25_out, and_26_out, and_27_out, and_28_out, and_29_out, and_30_out, and_31_out, and_32_out,
       buffer_1_out, buffer_2_out, buffer_3_out, buffer_4_out, buffer_5_out, buffer_6_out, buffer_7_out,
       buffer_8_out, buffer_9_out, buffer_10_out, buffer_11_out, buffer_12_out, buffer_13_out, buffer_14_out,
       buffer_15_out, buffer_16_out, controlled_buffer_1_out, controlled_buffer_3_out,
       controlled_buffer_14_out, controlled_buffer_16_out, controlled_buffer_24_out,
       controlled_buffer_27_out, controlled_buffer_35_out, controlled_buffer_39_out,
       controlled_buffer_45_out, controlled_buffer_47_out, controlled_buffer_58_out,
       controlled_buffer_60_out, controlled_buffer_68_out, controlled_buffer_71_out,
       controlled_buffer_79_out, controlled_buffer_83_out, controlled_buffer_89_out,
       controlled_buffer_91_out, controlled_buffer_102_out, controlled_buffer_104_out,
       controlled_buffer_112_out, controlled_buffer_115_out, controlled_buffer_123_out,
       controlled_buffer_127_out, controlled_buffer_133_out, controlled_buffer_135_out,
       controlled_buffer_146_out, controlled_buffer_148_out, controlled_buffer_156_out,
       controlled_buffer_159_out, controlled_buffer_167_out, controlled_buffer_171_out, nor_1_out, nor_2_out,
       nor_3_out, nor_4_out, nor_5_out, nor_6_out, nor_7_out, nor_8_out, nor_9_out, nor_10_out, nor_11_out,
       nor_12_out, nor_13_out, nor_14_out, nor_15_out, nor_16_out, nor_17_out, nor_18_out, nor_19_out,
       nor_20_out, nor_21_out, nor_22_out, nor_23_out, nor_24_out, nor_25_out, nor_26_out, nor_27_out,
       nor_28_out, nor_29_out, nor_30_out, nor_31_out, nor_32_out, not_1_out, not_2_out, not_3_out,
       not_4_out, not_5_out, not_6_out, not_7_out, not_8_out, not_9_out, not_10_out, not_11_out, not_12_out,
       not_13_out, not_14_out, not_15_out, not_16_out;

  assign controlled_buffer_1_out = decoder_4_out0 ? WriteData[31:24] : 8'bz;  // Controlled_Buffer controlled_buffer_1
  assign controlled_buffer_2_out = reset ? reset : 1'bz;  // Controlled_Buffer controlled_buffer_2
  assign controlled_buffer_3_out = controlled_buffer_2_out ? {8{1'b1}} : 8'bz;  // Controlled_Buffer controlled_buffer_3
  Pull_Resistor pull_resistor_1 (.node(controlled_buffer_2_out));
  assign controlled_buffer_2_out = decoder_4_out0 ? decoder_4_out0 : 1'bz;  // Controlled_Buffer controlled_buffer_4
  assign controlled_buffer_2_out = decoder_3_out0 ? decoder_3_out0 : 1'bz;  // Controlled_Buffer controlled_buffer_5
  assign controlled_buffer_2_out = decoder_2_out0 ? decoder_2_out0 : 1'bz;  // Controlled_Buffer controlled_buffer_6
  assign controlled_buffer_2_out = decoder_1_out0 ? decoder_1_out0 : 1'bz;  // Controlled_Buffer controlled_buffer_7
  assign controlled_buffer_1_out = decoder_3_out0 ? WriteData[23:16] : 8'bz;  // Controlled_Buffer controlled_buffer_8
  assign controlled_buffer_1_out = decoder_2_out0 ? WriteData[15:8] : 8'bz;  // Controlled_Buffer controlled_buffer_9
  assign controlled_buffer_1_out = decoder_1_out0 ? WriteData[7:0] : 8'bz;  // Controlled_Buffer controlled_buffer_10
  Decoder #(.select(4)) decoder_1 (
    .out0(decoder_1_out0), .out1(decoder_1_out1), .out2(decoder_1_out2), .out3(decoder_1_out3),
    .out4(decoder_1_out4), .out5(decoder_1_out5), .out6(decoder_1_out6), .out7(decoder_1_out7),
    .out8(decoder_1_out8), .out9(decoder_1_out9), .out10(decoder_1_out10), .out11(decoder_1_out11),
    .out12(decoder_1_out12), .out13(decoder_1_out13), .out14(decoder_1_out14), .out15(decoder_1_out15),
    .sel(WriteAddress[3:0]), .en(WriteEnable[0]));
  Decoder #(.select(4)) decoder_2 (
    .out0(decoder_2_out0), .out1(decoder_2_out1), .out2(decoder_2_out2), .out3(decoder_2_out3),
    .out4(decoder_2_out4), .out5(decoder_2_out5), .out6(decoder_2_out6), .out7(decoder_2_out7),
    .out8(decoder_2_out8), .out9(decoder_2_out9), .out10(decoder_2_out10), .out11(decoder_2_out11),
    .out12(decoder_2_out12), .out13(decoder_2_out13), .out14(decoder_2_out14), .out15(decoder_2_out15),
    .sel(WriteAddress[7:4]), .en(WriteEnable[1]));
  Decoder #(.select(4)) decoder_3 (
    .out0(decoder_3_out0), .out1(decoder_3_out1), .out2(decoder_3_out2), .out3(decoder_3_out3),
    .out4(decoder_3_out4), .out5(decoder_3_out5), .out6(decoder_3_out6), .out7(decoder_3_out7),
    .out8(decoder_3_out8), .out9(decoder_3_out9), .out10(decoder_3_out10), .out11(decoder_3_out11),
    .out12(decoder_3_out12), .out13(decoder_3_out13), .out14(decoder_3_out14), .out15(decoder_3_out15),
    .sel(WriteAddress[11:8]), .en(WriteEnable[2]));
  Decoder #(.select(4)) decoder_4 (
    .out0(decoder_4_out0), .out1(decoder_4_out1), .out2(decoder_4_out2), .out3(decoder_4_out3),
    .out4(decoder_4_out4), .out5(decoder_4_out5), .out6(decoder_4_out6), .out7(decoder_4_out7),
    .out8(decoder_4_out8), .out9(decoder_4_out9), .out10(decoder_4_out10), .out11(decoder_4_out11),
    .out12(decoder_4_out12), .out13(decoder_4_out13), .out14(decoder_4_out14), .out15(decoder_4_out15),
    .sel(WriteAddress[15:12]), .en(WriteEnable[3]));
  assign not_1_out = ~controlled_buffer_1_out;  // NOT_Gate not_1, 8 bits wide
  assign and_1_out = not_1_out & controlled_buffer_3_out;  // AND_Gate and_1, 8 bits wide
  assign and_2_out = controlled_buffer_3_out & buffer_1_out;  // AND_Gate and_2, 8 bits wide
  assign buffer_1_out = controlled_buffer_1_out;  // Buffer buffer_1, 8 bits wide
  Pull_Resistor pull_resistor_2 (.node(controlled_buffer_3_out));
  Pull_Resistor pull_resistor_3 (.node(controlled_buffer_1_out));
  Decoder #(.select(4)) decoder_5 (
    .out0(decoder_5_out0), .out1(decoder_5_out1), .out2(decoder_5_out2), .out3(decoder_5_out3),
    .out4(decoder_5_out4), .out5(decoder_5_out5), .out6(decoder_5_out6), .out7(decoder_5_out7),
    .out8(decoder_5_out8), .out9(decoder_5_out9), .out10(decoder_5_out10), .out11(decoder_5_out11),
    .out12(decoder_5_out12), .out13(decoder_5_out13), .out14(decoder_5_out14), .out15(decoder_5_out15),
    .sel(ReadAddress), .en(ReadEnable));
  assign ReadOut = decoder_5_out0 ? nor_1_out : 8'bz;  // Controlled_Buffer controlled_buffer_11
  assign nor_1_out = ~(and_1_out | nor_2_out);  // NOR_Gate nor_1, 8 bits wide
  assign controlled_buffer_12_out = reset ? reset : 1'bz;  // Controlled_Buffer controlled_buffer_12
  assign nor_2_out = ~(nor_1_out | and_2_out);  // NOR_Gate nor_2, 8 bits wide
  Pull_Resistor pull_resistor_4 (.node(controlled_buffer_12_out));
  assign controlled_buffer_12_out = decoder_4_out1 ? decoder_4_out1 : 1'bz;  // Controlled_Buffer controlled_buffer_13
  assign controlled_buffer_14_out = decoder_4_out1 ? WriteData[31:24] : 8'bz;  // Controlled_Buffer controlled_buffer_14
  assign controlled_buffer_14_out = decoder_3_out1 ? WriteData[23:16] : 8'bz;  // Controlled_Buffer controlled_buffer_15
  assign not_2_out = ~controlled_buffer_14_out;  // NOT_Gate not_2, 8 bits wide
  assign controlled_buffer_16_out = controlled_buffer_12_out ? {8{1'b1}} : 8'bz;  // Controlled_Buffer controlled_buffer_16
  assign buffer_2_out = controlled_buffer_14_out;  // Buffer buffer_2, 8 bits wide
  Pull_Resistor pull_resistor_5 (.node(controlled_buffer_16_out));
  assign controlled_buffer_12_out = decoder_3_out1 ? decoder_3_out1 : 1'bz;  // Controlled_Buffer controlled_buffer_17
  assign controlled_buffer_12_out = decoder_2_out1 ? decoder_2_out1 : 1'bz;  // Controlled_Buffer controlled_buffer_18
  assign controlled_buffer_12_out = decoder_1_out1 ? decoder_1_out1 : 1'bz;  // Controlled_Buffer controlled_buffer_19
  Pull_Resistor pull_resistor_6 (.node(controlled_buffer_14_out));
  assign controlled_buffer_14_out = decoder_2_out1 ? WriteData[15:8] : 8'bz;  // Controlled_Buffer controlled_buffer_20
  assign controlled_buffer_14_out = decoder_1_out1 ? WriteData[7:0] : 8'bz;  // Controlled_Buffer controlled_buffer_21
  assign ReadOut = decoder_5_out1 ? nor_3_out : 8'bz;  // Controlled_Buffer controlled_buffer_22
  assign and_3_out = not_2_out & controlled_buffer_16_out;  // AND_Gate and_3, 8 bits wide
  assign nor_3_out = ~(and_3_out | nor_4_out);  // NOR_Gate nor_3, 8 bits wide
  assign nor_4_out = ~(nor_3_out | and_4_out);  // NOR_Gate nor_4, 8 bits wide
  assign and_4_out = controlled_buffer_16_out & buffer_2_out;  // AND_Gate and_4, 8 bits wide
  assign controlled_buffer_23_out = reset ? reset : 1'bz;  // Controlled_Buffer controlled_buffer_23
  assign controlled_buffer_24_out = controlled_buffer_23_out ? {8{1'b1}} : 8'bz;  // Controlled_Buffer controlled_buffer_24
  Pull_Resistor pull_resistor_7 (.node(controlled_buffer_23_out));
  assign controlled_buffer_23_out = decoder_4_out2 ? decoder_4_out2 : 1'bz;  // Controlled_Buffer controlled_buffer_25
  assign controlled_buffer_23_out = decoder_3_out2 ? decoder_3_out2 : 1'bz;  // Controlled_Buffer controlled_buffer_26
  assign controlled_buffer_27_out = decoder_4_out2 ? WriteData[31:24] : 8'bz;  // Controlled_Buffer controlled_buffer_27
  assign controlled_buffer_27_out = decoder_3_out2 ? WriteData[23:16] : 8'bz;  // Controlled_Buffer controlled_buffer_28
  assign controlled_buffer_27_out = decoder_2_out2 ? WriteData[15:8] : 8'bz;  // Controlled_Buffer controlled_buffer_29
  assign not_3_out = ~controlled_buffer_27_out;  // NOT_Gate not_3, 8 bits wide
  assign buffer_3_out = controlled_buffer_27_out;  // Buffer buffer_3, 8 bits wide
  Pull_Resistor pull_resistor_8 (.node(controlled_buffer_24_out));
  assign controlled_buffer_23_out = decoder_2_out2 ? decoder_2_out2 : 1'bz;  // Controlled_Buffer controlled_buffer_30
  assign controlled_buffer_23_out = decoder_1_out2 ? decoder_1_out2 : 1'bz;  // Controlled_Buffer controlled_buffer_31
  Pull_Resistor pull_resistor_9 (.node(controlled_buffer_27_out));
  assign controlled_buffer_27_out = decoder_1_out2 ? WriteData[7:0] : 8'bz;  // Controlled_Buffer controlled_buffer_32
  assign ReadOut = decoder_5_out2 ? nor_5_out : 8'bz;  // Controlled_Buffer controlled_buffer_33
  assign and_5_out = not_3_out & controlled_buffer_24_out;  // AND_Gate and_5, 8 bits wide
  assign nor_5_out = ~(and_5_out | nor_6_out);  // NOR_Gate nor_5, 8 bits wide
  assign nor_6_out = ~(nor_5_out | and_6_out);  // NOR_Gate nor_6, 8 bits wide
  assign and_6_out = controlled_buffer_24_out & buffer_3_out;  // AND_Gate and_6, 8 bits wide
  assign controlled_buffer_34_out = reset ? reset : 1'bz;  // Controlled_Buffer controlled_buffer_34
  assign controlled_buffer_35_out = controlled_buffer_34_out ? {8{1'b1}} : 8'bz;  // Controlled_Buffer controlled_buffer_35
  Pull_Resistor pull_resistor_10 (.node(controlled_buffer_34_out));
  assign controlled_buffer_34_out = decoder_4_out3 ? decoder_4_out3 : 1'bz;  // Controlled_Buffer controlled_buffer_36
  assign controlled_buffer_34_out = decoder_3_out3 ? decoder_3_out3 : 1'bz;  // Controlled_Buffer controlled_buffer_37
  assign controlled_buffer_34_out = decoder_2_out3 ? decoder_2_out3 : 1'bz;  // Controlled_Buffer controlled_buffer_38
  assign controlled_buffer_39_out = decoder_4_out3 ? WriteData[31:24] : 8'bz;  // Controlled_Buffer controlled_buffer_39
  assign controlled_buffer_39_out = decoder_3_out3 ? WriteData[23:16] : 8'bz;  // Controlled_Buffer controlled_buffer_40
  assign controlled_buffer_39_out = decoder_2_out3 ? WriteData[15:8] : 8'bz;  // Controlled_Buffer controlled_buffer_41
  assign controlled_buffer_39_out = decoder_1_out3 ? WriteData[7:0] : 8'bz;  // Controlled_Buffer controlled_buffer_42
  assign not_4_out = ~controlled_buffer_39_out;  // NOT_Gate not_4, 8 bits wide
  assign and_7_out = not_4_out & controlled_buffer_35_out;  // AND_Gate and_7, 8 bits wide
  assign and_8_out = controlled_buffer_35_out & buffer_4_out;  // AND_Gate and_8, 8 bits wide
  assign buffer_4_out = controlled_buffer_39_out;  // Buffer buffer_4, 8 bits wide
  Pull_Resistor pull_resistor_11 (.node(controlled_buffer_35_out));
  assign controlled_buffer_34_out = decoder_1_out3 ? decoder_1_out3 : 1'bz;  // Controlled_Buffer controlled_buffer_43
  Pull_Resistor pull_resistor_12 (.node(controlled_buffer_39_out));
  assign ReadOut = decoder_5_out3 ? nor_7_out : 8'bz;  // Controlled_Buffer controlled_buffer_44
  assign nor_7_out = ~(and_7_out | nor_8_out);  // NOR_Gate nor_7, 8 bits wide
  assign nor_8_out = ~(nor_7_out | and_8_out);  // NOR_Gate nor_8, 8 bits wide
  assign controlled_buffer_45_out = decoder_4_out4 ? WriteData[31:24] : 8'bz;  // Controlled_Buffer controlled_buffer_45
  assign controlled_buffer_46_out = reset ? reset : 1'bz;  // Controlled_Buffer controlled_buffer_46
  assign controlled_buffer_47_out = controlled_buffer_46_out ? {8{1'b1}} : 8'bz;  // Controlled_Buffer controlled_buffer_47
  Pull_Resistor pull_resistor_13 (.node(controlled_buffer_46_out));
  assign controlled_buffer_46_out = decoder_4_out4 ? decoder_4_out4 : 1'bz;  // Controlled_Buffer controlled_buffer_48
  assign controlled_buffer_46_out = decoder_3_out4 ? decoder_3_out4 : 1'bz;  // Controlled_Buffer controlled_buffer_49
  assign controlled_buffer_46_out = decoder_2_out4 ? decoder_2_out4 : 1'bz;  // Controlled_Buffer controlled_buffer_50
  assign controlled_buffer_46_out = decoder_1_out4 ? decoder_1_out4 : 1'bz;  // Controlled_Buffer controlled_buffer_51
  assign controlled_buffer_45_out = decoder_3_out4 ? WriteData[23:16] : 8'bz;  // Controlled_Buffer controlled_buffer_52
  assign controlled_buffer_45_out = decoder_2_out4 ? WriteData[15:8] : 8'bz;  // Controlled_Buffer controlled_buffer_53
  assign controlled_buffer_45_out = decoder_1_out4 ? WriteData[7:0] : 8'bz;  // Controlled_Buffer controlled_buffer_54
  assign not_5_out = ~controlled_buffer_45_out;  // NOT_Gate not_5, 8 bits wide
  assign and_9_out = not_5_out & controlled_buffer_47_out;  // AND_Gate and_9, 8 bits wide
  assign and_10_out = controlled_buffer_47_out & buffer_5_out;  // AND_Gate and_10, 8 bits wide
  assign buffer_5_out = controlled_buffer_45_out;  // Buffer buffer_5, 8 bits wide
  Pull_Resistor pull_resistor_14 (.node(controlled_buffer_47_out));
  Pull_Resistor pull_resistor_15 (.node(controlled_buffer_45_out));
  assign ReadOut = decoder_5_out4 ? nor_9_out : 8'bz;  // Controlled_Buffer controlled_buffer_55
  assign nor_9_out = ~(and_9_out | nor_10_out);  // NOR_Gate nor_9, 8 bits wide
  assign controlled_buffer_56_out = reset ? reset : 1'bz;  // Controlled_Buffer controlled_buffer_56
  assign nor_10_out = ~(nor_9_out | and_10_out);  // NOR_Gate nor_10, 8 bits wide
  Pull_Resistor pull_resistor_16 (.node(controlled_buffer_56_out));
  assign controlled_buffer_56_out = decoder_4_out5 ? decoder_4_out5 : 1'bz;  // Controlled_Buffer controlled_buffer_57
  assign controlled_buffer_58_out = decoder_4_out5 ? WriteData[31:24] : 8'bz;  // Controlled_Buffer controlled_buffer_58
  assign controlled_buffer_58_out = decoder_3_out5 ? WriteData[23:16] : 8'bz;  // Controlled_Buffer controlled_buffer_59
  assign not_6_out = ~controlled_buffer_58_out;  // NOT_Gate not_6, 8 bits wide
  assign controlled_buffer_60_out = controlled_buffer_56_out ? {8{1'b1}} : 8'bz;  // Controlled_Buffer controlled_buffer_60
  assign buffer_6_out = controlled_buffer_58_out;  // Buffer buffer_6, 8 bits wide
  Pull_Resistor pull_resistor_17 (.node(controlled_buffer_60_out));
  assign controlled_buffer_56_out = decoder_3_out5 ? decoder_3_out5 : 1'bz;  // Controlled_Buffer controlled_buffer_61
  assign controlled_buffer_56_out = decoder_2_out5 ? decoder_2_out5 : 1'bz;  // Controlled_Buffer controlled_buffer_62
  assign controlled_buffer_56_out = decoder_1_out5 ? decoder_1_out5 : 1'bz;  // Controlled_Buffer controlled_buffer_63
  Pull_Resistor pull_resistor_18 (.node(controlled_buffer_58_out));
  assign controlled_buffer_58_out = decoder_2_out5 ? WriteData[15:8] : 8'bz;  // Controlled_Buffer controlled_buffer_64
  assign controlled_buffer_58_out = decoder_1_out5 ? WriteData[7:0] : 8'bz;  // Controlled_Buffer controlled_buffer_65
  assign ReadOut = decoder_5_out5 ? nor_11_out : 8'bz;  // Controlled_Buffer controlled_buffer_66
  assign and_11_out = not_6_out & controlled_buffer_60_out;  // AND_Gate and_11, 8 bits wide
  assign nor_11_out = ~(and_11_out | nor_12_out);  // NOR_Gate nor_11, 8 bits wide
  assign nor_12_out = ~(nor_11_out | and_12_out);  // NOR_Gate nor_12, 8 bits wide
  assign and_12_out = controlled_buffer_60_out & buffer_6_out;  // AND_Gate and_12, 8 bits wide
  assign controlled_buffer_67_out = reset ? reset : 1'bz;  // Controlled_Buffer controlled_buffer_67
  assign controlled_buffer_68_out = controlled_buffer_67_out ? {8{1'b1}} : 8'bz;  // Controlled_Buffer controlled_buffer_68
  Pull_Resistor pull_resistor_19 (.node(controlled_buffer_67_out));
  assign controlled_buffer_67_out = decoder_4_out6 ? decoder_4_out6 : 1'bz;  // Controlled_Buffer controlled_buffer_69
  assign controlled_buffer_67_out = decoder_3_out6 ? decoder_3_out6 : 1'bz;  // Controlled_Buffer controlled_buffer_70
  assign controlled_buffer_71_out = decoder_4_out6 ? WriteData[31:24] : 8'bz;  // Controlled_Buffer controlled_buffer_71
  assign controlled_buffer_71_out = decoder_3_out6 ? WriteData[23:16] : 8'bz;  // Controlled_Buffer controlled_buffer_72
  assign controlled_buffer_71_out = decoder_2_out6 ? WriteData[15:8] : 8'bz;  // Controlled_Buffer controlled_buffer_73
  assign not_7_out = ~controlled_buffer_71_out;  // NOT_Gate not_7, 8 bits wide
  assign buffer_7_out = controlled_buffer_71_out;  // Buffer buffer_7, 8 bits wide
  Pull_Resistor pull_resistor_20 (.node(controlled_buffer_68_out));
  assign controlled_buffer_67_out = decoder_2_out6 ? decoder_2_out6 : 1'bz;  // Controlled_Buffer controlled_buffer_74
  assign controlled_buffer_67_out = decoder_1_out6 ? decoder_1_out6 : 1'bz;  // Controlled_Buffer controlled_buffer_75
  Pull_Resistor pull_resistor_21 (.node(controlled_buffer_71_out));
  assign controlled_buffer_71_out = decoder_1_out6 ? WriteData[7:0] : 8'bz;  // Controlled_Buffer controlled_buffer_76
  assign ReadOut = decoder_5_out6 ? nor_13_out : 8'bz;  // Controlled_Buffer controlled_buffer_77
  assign and_13_out = not_7_out & controlled_buffer_68_out;  // AND_Gate and_13, 8 bits wide
  assign nor_13_out = ~(and_13_out | nor_14_out);  // NOR_Gate nor_13, 8 bits wide
  assign nor_14_out = ~(nor_13_out | and_14_out);  // NOR_Gate nor_14, 8 bits wide
  assign and_14_out = controlled_buffer_68_out & buffer_7_out;  // AND_Gate and_14, 8 bits wide
  assign controlled_buffer_78_out = reset ? reset : 1'bz;  // Controlled_Buffer controlled_buffer_78
  assign controlled_buffer_79_out = controlled_buffer_78_out ? {8{1'b1}} : 8'bz;  // Controlled_Buffer controlled_buffer_79
  Pull_Resistor pull_resistor_22 (.node(controlled_buffer_78_out));
  assign controlled_buffer_78_out = decoder_4_out7 ? decoder_4_out7 : 1'bz;  // Controlled_Buffer controlled_buffer_80
  assign controlled_buffer_78_out = decoder_3_out7 ? decoder_3_out7 : 1'bz;  // Controlled_Buffer controlled_buffer_81
  assign controlled_buffer_78_out = decoder_2_out7 ? decoder_2_out7 : 1'bz;  // Controlled_Buffer controlled_buffer_82
  assign controlled_buffer_83_out = decoder_4_out7 ? WriteData[31:24] : 8'bz;  // Controlled_Buffer controlled_buffer_83
  assign controlled_buffer_83_out = decoder_3_out7 ? WriteData[23:16] : 8'bz;  // Controlled_Buffer controlled_buffer_84
  assign controlled_buffer_83_out = decoder_2_out7 ? WriteData[15:8] : 8'bz;  // Controlled_Buffer controlled_buffer_85
  assign controlled_buffer_83_out = decoder_1_out7 ? WriteData[7:0] : 8'bz;  // Controlled_Buffer controlled_buffer_86
  assign not_8_out = ~controlled_buffer_83_out;  // NOT_Gate not_8, 8 bits wide
  assign and_15_out = not_8_out & controlled_buffer_79_out;  // AND_Gate and_15, 8 bits wide
  assign and_16_out = controlled_buffer_79_out & buffer_8_out;  // AND_Gate and_16, 8 bits wide
  assign buffer_8_out = controlled_buffer_83_out;  // Buffer buffer_8, 8 bits wide
  Pull_Resistor pull_resistor_23 (.node(controlled_buffer_79_out));
  assign controlled_buffer_78_out = decoder_1_out7 ? decoder_1_out7 : 1'bz;  // Controlled_Buffer controlled_buffer_87
  Pull_Resistor pull_resistor_24 (.node(controlled_buffer_83_out));
  assign ReadOut = decoder_5_out7 ? nor_15_out : 8'bz;  // Controlled_Buffer controlled_buffer_88
  assign nor_15_out = ~(and_15_out | nor_16_out);  // NOR_Gate nor_15, 8 bits wide
  assign nor_16_out = ~(nor_15_out | and_16_out);  // NOR_Gate nor_16, 8 bits wide
  assign controlled_buffer_89_out = decoder_4_out8 ? WriteData[31:24] : 8'bz;  // Controlled_Buffer controlled_buffer_89
  assign controlled_buffer_90_out = reset ? reset : 1'bz;  // Controlled_Buffer controlled_buffer_90
  assign controlled_buffer_91_out = controlled_buffer_90_out ? {8{1'b1}} : 8'bz;  // Controlled_Buffer controlled_buffer_91
  Pull_Resistor pull_resistor_25 (.node(controlled_buffer_90_out));
  assign controlled_buffer_90_out = decoder_4_out8 ? decoder_4_out8 : 1'bz;  // Controlled_Buffer controlled_buffer_92
  assign controlled_buffer_90_out = decoder_3_out8 ? decoder_3_out8 : 1'bz;  // Controlled_Buffer controlled_buffer_93
  assign controlled_buffer_90_out = decoder_2_out8 ? decoder_2_out8 : 1'bz;  // Controlled_Buffer controlled_buffer_94
  assign controlled_buffer_90_out = decoder_1_out8 ? decoder_1_out8 : 1'bz;  // Controlled_Buffer controlled_buffer_95
  assign controlled_buffer_89_out = decoder_3_out8 ? WriteData[23:16] : 8'bz;  // Controlled_Buffer controlled_buffer_96
  assign controlled_buffer_89_out = decoder_2_out8 ? WriteData[15:8] : 8'bz;  // Controlled_Buffer controlled_buffer_97
  assign controlled_buffer_89_out = decoder_1_out8 ? WriteData[7:0] : 8'bz;  // Controlled_Buffer controlled_buffer_98
  assign not_9_out = ~controlled_buffer_89_out;  // NOT_Gate not_9, 8 bits wide
  assign and_17_out = not_9_out & controlled_buffer_91_out;  // AND_Gate and_17, 8 bits wide
  assign and_18_out = controlled_buffer_91_out & buffer_9_out;  // AND_Gate and_18, 8 bits wide
  assign buffer_9_out = controlled_buffer_89_out;  // Buffer buffer_9, 8 bits wide
  Pull_Resistor pull_resistor_26 (.node(controlled_buffer_91_out));
  Pull_Resistor pull_resistor_27 (.node(controlled_buffer_89_out));
  assign ReadOut = decoder_5_out8 ? nor_17_out : 8'bz;  // Controlled_Buffer controlled_buffer_99
  assign nor_17_out = ~(and_17_out | nor_18_out);  // NOR_Gate nor_17, 8 bits wide
  assign controlled_buffer_100_out = reset ? reset : 1'bz;  // Controlled_Buffer controlled_buffer_100
  assign nor_18_out = ~(nor_17_out | and_18_out);  // NOR_Gate nor_18, 8 bits wide
  Pull_Resistor pull_resistor_28 (.node(controlled_buffer_100_out));
  assign controlled_buffer_100_out = decoder_4_out9 ? decoder_4_out9 : 1'bz;  // Controlled_Buffer controlled_buffer_101
  assign controlled_buffer_102_out = decoder_4_out9 ? WriteData[31:24] : 8'bz;  // Controlled_Buffer controlled_buffer_102
  assign controlled_buffer_102_out = decoder_3_out9 ? WriteData[23:16] : 8'bz;  // Controlled_Buffer controlled_buffer_103
  assign not_10_out = ~controlled_buffer_102_out;  // NOT_Gate not_10, 8 bits wide
  assign controlled_buffer_104_out = controlled_buffer_100_out ? {8{1'b1}} : 8'bz;  // Controlled_Buffer controlled_buffer_104
  assign buffer_10_out = controlled_buffer_102_out;  // Buffer buffer_10, 8 bits wide
  Pull_Resistor pull_resistor_29 (.node(controlled_buffer_104_out));
  assign controlled_buffer_100_out = decoder_3_out9 ? decoder_3_out9 : 1'bz;  // Controlled_Buffer controlled_buffer_105
  assign controlled_buffer_100_out = decoder_2_out9 ? decoder_2_out9 : 1'bz;  // Controlled_Buffer controlled_buffer_106
  assign controlled_buffer_100_out = decoder_1_out9 ? decoder_1_out9 : 1'bz;  // Controlled_Buffer controlled_buffer_107
  Pull_Resistor pull_resistor_30 (.node(controlled_buffer_102_out));
  assign controlled_buffer_102_out = decoder_2_out9 ? WriteData[15:8] : 8'bz;  // Controlled_Buffer controlled_buffer_108
  assign controlled_buffer_102_out = decoder_1_out9 ? WriteData[7:0] : 8'bz;  // Controlled_Buffer controlled_buffer_109
  assign ReadOut = decoder_5_out9 ? nor_19_out : 8'bz;  // Controlled_Buffer controlled_buffer_110
  assign and_19_out = not_10_out & controlled_buffer_104_out;  // AND_Gate and_19, 8 bits wide
  assign nor_19_out = ~(and_19_out | nor_20_out);  // NOR_Gate nor_19, 8 bits wide
  assign nor_20_out = ~(nor_19_out | and_20_out);  // NOR_Gate nor_20, 8 bits wide
  assign and_20_out = controlled_buffer_104_out & buffer_10_out;  // AND_Gate and_20, 8 bits wide
  assign controlled_buffer_111_out = reset ? reset : 1'bz;  // Controlled_Buffer controlled_buffer_111
  assign controlled_buffer_112_out = controlled_buffer_111_out ? {8{1'b1}} : 8'bz;  // Controlled_Buffer controlled_buffer_112
  Pull_Resistor pull_resistor_31 (.node(controlled_buffer_111_out));
  assign controlled_buffer_111_out = decoder_4_out10 ? decoder_4_out10 : 1'bz;  // Controlled_Buffer controlled_buffer_113
  assign controlled_buffer_111_out = decoder_3_out10 ? decoder_3_out10 : 1'bz;  // Controlled_Buffer controlled_buffer_114
  assign controlled_buffer_115_out = decoder_4_out10 ? WriteData[31:24] : 8'bz;  // Controlled_Buffer controlled_buffer_115
  assign controlled_buffer_115_out = decoder_3_out10 ? WriteData[23:16] : 8'bz;  // Controlled_Buffer controlled_buffer_116
  assign controlled_buffer_115_out = decoder_2_out10 ? WriteData[15:8] : 8'bz;  // Controlled_Buffer controlled_buffer_117
  assign not_11_out = ~controlled_buffer_115_out;  // NOT_Gate not_11, 8 bits wide
  assign buffer_11_out = controlled_buffer_115_out;  // Buffer buffer_11, 8 bits wide
  Pull_Resistor pull_resistor_32 (.node(controlled_buffer_112_out));
  assign controlled_buffer_111_out = decoder_2_out10 ? decoder_2_out10 : 1'bz;  // Controlled_Buffer controlled_buffer_118
  assign controlled_buffer_111_out = decoder_1_out10 ? decoder_1_out10 : 1'bz;  // Controlled_Buffer controlled_buffer_119
  Pull_Resistor pull_resistor_33 (.node(controlled_buffer_115_out));
  assign controlled_buffer_115_out = decoder_1_out10 ? WriteData[7:0] : 8'bz;  // Controlled_Buffer controlled_buffer_120
  assign ReadOut = decoder_5_out10 ? nor_21_out : 8'bz;  // Controlled_Buffer controlled_buffer_121
  assign and_21_out = not_11_out & controlled_buffer_112_out;  // AND_Gate and_21, 8 bits wide
  assign nor_21_out = ~(and_21_out | nor_22_out);  // NOR_Gate nor_21, 8 bits wide
  assign nor_22_out = ~(nor_21_out | and_22_out);  // NOR_Gate nor_22, 8 bits wide
  assign and_22_out = controlled_buffer_112_out & buffer_11_out;  // AND_Gate and_22, 8 bits wide
  assign controlled_buffer_122_out = reset ? reset : 1'bz;  // Controlled_Buffer controlled_buffer_122
  assign controlled_buffer_123_out = controlled_buffer_122_out ? {8{1'b1}} : 8'bz;  // Controlled_Buffer controlled_buffer_123
  Pull_Resistor pull_resistor_34 (.node(controlled_buffer_122_out));
  assign controlled_buffer_122_out = decoder_4_out11 ? decoder_4_out11 : 1'bz;  // Controlled_Buffer controlled_buffer_124
  assign controlled_buffer_122_out = decoder_3_out11 ? decoder_3_out11 : 1'bz;  // Controlled_Buffer controlled_buffer_125
  assign controlled_buffer_122_out = decoder_2_out11 ? decoder_2_out11 : 1'bz;  // Controlled_Buffer controlled_buffer_126
  assign controlled_buffer_127_out = decoder_4_out11 ? WriteData[31:24] : 8'bz;  // Controlled_Buffer controlled_buffer_127
  assign controlled_buffer_127_out = decoder_3_out11 ? WriteData[23:16] : 8'bz;  // Controlled_Buffer controlled_buffer_128
  assign controlled_buffer_127_out = decoder_2_out11 ? WriteData[15:8] : 8'bz;  // Controlled_Buffer controlled_buffer_129
  assign controlled_buffer_127_out = decoder_1_out11 ? WriteData[7:0] : 8'bz;  // Controlled_Buffer controlled_buffer_130
  assign not_12_out = ~controlled_buffer_127_out;  // NOT_Gate not_12, 8 bits wide
  assign and_23_out = not_12_out & controlled_buffer_123_out;  // AND_Gate and_23, 8 bits wide
  assign and_24_out = controlled_buffer_123_out & buffer_12_out;  // AND_Gate and_24, 8 bits wide
  assign buffer_12_out = controlled_buffer_127_out;  // Buffer buffer_12, 8 bits wide
  Pull_Resistor pull_resistor_35 (.node(controlled_buffer_123_out));
  assign controlled_buffer_122_out = decoder_1_out11 ? decoder_1_out11 : 1'bz;  // Controlled_Buffer controlled_buffer_131
  Pull_Resistor pull_resistor_36 (.node(controlled_buffer_127_out));
  assign ReadOut = decoder_5_out11 ? nor_23_out : 8'bz;  // Controlled_Buffer controlled_buffer_132
  assign nor_23_out = ~(and_23_out | nor_24_out);  // NOR_Gate nor_23, 8 bits wide
  assign nor_24_out = ~(nor_23_out | and_24_out);  // NOR_Gate nor_24, 8 bits wide
  assign controlled_buffer_133_out = decoder_4_out12 ? WriteData[31:24] : 8'bz;  // Controlled_Buffer controlled_buffer_133
  assign controlled_buffer_134_out = reset ? reset : 1'bz;  // Controlled_Buffer controlled_buffer_134
  assign controlled_buffer_135_out = controlled_buffer_134_out ? {8{1'b1}} : 8'bz;  // Controlled_Buffer controlled_buffer_135
  Pull_Resistor pull_resistor_37 (.node(controlled_buffer_134_out));
  assign controlled_buffer_134_out = decoder_4_out12 ? decoder_4_out12 : 1'bz;  // Controlled_Buffer controlled_buffer_136
  assign controlled_buffer_134_out = decoder_3_out12 ? decoder_3_out12 : 1'bz;  // Controlled_Buffer controlled_buffer_137
  assign controlled_buffer_134_out = decoder_2_out12 ? decoder_2_out12 : 1'bz;  // Controlled_Buffer controlled_buffer_138
  assign controlled_buffer_134_out = decoder_1_out12 ? decoder_1_out12 : 1'bz;  // Controlled_Buffer controlled_buffer_139
  assign controlled_buffer_133_out = decoder_3_out12 ? WriteData[23:16] : 8'bz;  // Controlled_Buffer controlled_buffer_140
  assign controlled_buffer_133_out = decoder_2_out12 ? WriteData[15:8] : 8'bz;  // Controlled_Buffer controlled_buffer_141
  assign controlled_buffer_133_out = decoder_1_out12 ? WriteData[7:0] : 8'bz;  // Controlled_Buffer controlled_buffer_142
  assign not_13_out = ~controlled_buffer_133_out;  // NOT_Gate not_13, 8 bits wide
  assign and_25_out = not_13_out & controlled_buffer_135_out;  // AND_Gate and_25, 8 bits wide
  assign and_26_out = controlled_buffer_135_out & buffer_13_out;  // AND_Gate and_26, 8 bits wide
  assign buffer_13_out = controlled_buffer_133_out;  // Buffer buffer_13, 8 bits wide
  Pull_Resistor pull_resistor_38 (.node(controlled_buffer_135_out));
  Pull_Resistor pull_resistor_39 (.node(controlled_buffer_133_out));
  assign ReadOut = decoder_5_out12 ? nor_25_out : 8'bz;  // Controlled_Buffer controlled_buffer_143
  assign nor_25_out = ~(and_25_out | nor_26_out);  // NOR_Gate nor_25, 8 bits wide
  assign controlled_buffer_144_out = reset ? reset : 1'bz;  // Controlled_Buffer controlled_buffer_144
  assign nor_26_out = ~(nor_25_out | and_26_out);  // NOR_Gate nor_26, 8 bits wide
  Pull_Resistor pull_resistor_40 (.node(controlled_buffer_144_out));
  assign controlled_buffer_144_out = decoder_4_out13 ? decoder_4_out13 : 1'bz;  // Controlled_Buffer controlled_buffer_145
  assign controlled_buffer_146_out = decoder_4_out13 ? WriteData[31:24] : 8'bz;  // Controlled_Buffer controlled_buffer_146
  assign controlled_buffer_146_out = decoder_3_out13 ? WriteData[23:16] : 8'bz;  // Controlled_Buffer controlled_buffer_147
  assign not_14_out = ~controlled_buffer_146_out;  // NOT_Gate not_14, 8 bits wide
  assign controlled_buffer_148_out = controlled_buffer_144_out ? {8{1'b1}} : 8'bz;  // Controlled_Buffer controlled_buffer_148
  assign buffer_14_out = controlled_buffer_146_out;  // Buffer buffer_14, 8 bits wide
  Pull_Resistor pull_resistor_41 (.node(controlled_buffer_148_out));
  assign controlled_buffer_144_out = decoder_3_out13 ? decoder_3_out13 : 1'bz;  // Controlled_Buffer controlled_buffer_149
  assign controlled_buffer_144_out = decoder_2_out13 ? decoder_2_out13 : 1'bz;  // Controlled_Buffer controlled_buffer_150
  assign controlled_buffer_144_out = decoder_1_out13 ? decoder_1_out13 : 1'bz;  // Controlled_Buffer controlled_buffer_151
  Pull_Resistor pull_resistor_42 (.node(controlled_buffer_146_out));
  assign controlled_buffer_146_out = decoder_2_out13 ? WriteData[15:8] : 8'bz;  // Controlled_Buffer controlled_buffer_152
  assign controlled_buffer_146_out = decoder_1_out13 ? WriteData[7:0] : 8'bz;  // Controlled_Buffer controlled_buffer_153
  assign ReadOut = decoder_5_out13 ? nor_27_out : 8'bz;  // Controlled_Buffer controlled_buffer_154
  assign and_27_out = not_14_out & controlled_buffer_148_out;  // AND_Gate and_27, 8 bits wide
  assign nor_27_out = ~(and_27_out | nor_28_out);  // NOR_Gate nor_27, 8 bits wide
  assign nor_28_out = ~(nor_27_out | and_28_out);  // NOR_Gate nor_28, 8 bits wide
  assign and_28_out = controlled_buffer_148_out & buffer_14_out;  // AND_Gate and_28, 8 bits wide
  assign controlled_buffer_155_out = reset ? reset : 1'bz;  // Controlled_Buffer controlled_buffer_155
  assign controlled_buffer_156_out = controlled_buffer_155_out ? {8{1'b1}} : 8'bz;  // Controlled_Buffer controlled_buffer_156
  Pull_Resistor pull_resistor_43 (.node(controlled_buffer_155_out));
  assign controlled_buffer_155_out = decoder_4_out14 ? decoder_4_out14 : 1'bz;  // Controlled_Buffer controlled_buffer_157
  assign controlled_buffer_155_out = decoder_3_out14 ? decoder_3_out14 : 1'bz;  // Controlled_Buffer controlled_buffer_158
  assign controlled_buffer_159_out = decoder_4_out14 ? WriteData[31:24] : 8'bz;  // Controlled_Buffer controlled_buffer_159
  assign controlled_buffer_159_out = decoder_3_out14 ? WriteData[23:16] : 8'bz;  // Controlled_Buffer controlled_buffer_160
  assign controlled_buffer_159_out = decoder_2_out14 ? WriteData[15:8] : 8'bz;  // Controlled_Buffer controlled_buffer_161
  assign not_15_out = ~controlled_buffer_159_out;  // NOT_Gate not_15, 8 bits wide
  assign buffer_15_out = controlled_buffer_159_out;  // Buffer buffer_15, 8 bits wide
  Pull_Resistor pull_resistor_44 (.node(controlled_buffer_156_out));
  assign controlled_buffer_155_out = decoder_2_out14 ? decoder_2_out14 : 1'bz;  // Controlled_Buffer controlled_buffer_162
  assign controlled_buffer_155_out = decoder_1_out14 ? decoder_1_out14 : 1'bz;  // Controlled_Buffer controlled_buffer_163
  Pull_Resistor pull_resistor_45 (.node(controlled_buffer_159_out));
  assign controlled_buffer_159_out = decoder_1_out14 ? WriteData[7:0] : 8'bz;  // Controlled_Buffer controlled_buffer_164
  assign ReadOut = decoder_5_out14 ? nor_29_out : 8'bz;  // Controlled_Buffer controlled_buffer_165
  assign and_29_out = not_15_out & controlled_buffer_156_out;  // AND_Gate and_29, 8 bits wide
  assign nor_29_out = ~(and_29_out | nor_30_out);  // NOR_Gate nor_29, 8 bits wide
  assign nor_30_out = ~(nor_29_out | and_30_out);  // NOR_Gate nor_30, 8 bits wide
  assign and_30_out = controlled_buffer_156_out & buffer_15_out;  // AND_Gate and_30, 8 bits wide
  assign controlled_buffer_166_out = reset ? reset : 1'bz;  // Controlled_Buffer controlled_buffer_166
  assign controlled_buffer_167_out = controlled_buffer_166_out ? {8{1'b1}} : 8'bz;  // Controlled_Buffer controlled_buffer_167
  Pull_Resistor pull_resistor_46 (.node(controlled_buffer_166_out));
  assign controlled_buffer_166_out = decoder_4_out15 ? decoder_4_out15 : 1'bz;  // Controlled_Buffer controlled_buffer_168
  assign controlled_buffer_166_out = decoder_3_out15 ? decoder_3_out15 : 1'bz;  // Controlled_Buffer controlled_buffer_169
  assign controlled_buffer_166_out = decoder_2_out15 ? decoder_2_out15 : 1'bz;  // Controlled_Buffer controlled_buffer_170
  assign controlled_buffer_171_out = decoder_4_out15 ? WriteData[31:24] : 8'bz;  // Controlled_Buffer controlled_buffer_171
  assign controlled_buffer_171_out = decoder_3_out15 ? WriteData[23:16] : 8'bz;  // Controlled_Buffer controlled_buffer_172
  assign controlled_buffer_171_out = decoder_2_out15 ? WriteData[15:8] : 8'bz;  // Controlled_Buffer controlled_buffer_173
  assign controlled_buffer_171_out = decoder_1_out15 ? WriteData[7:0] : 8'bz;  // Controlled_Buffer controlled_buffer_174
  assign not_16_out = ~controlled_buffer_171_out;  // NOT_Gate not_16, 8 bits wide
  assign and_31_out = not_16_out & controlled_buffer_167_out;  // AND_Gate and_31, 8 bits wide
  assign and_32_out = controlled_buffer_167_out & buffer_16_out;  // AND_Gate and_32, 8 bits wide
  assign buffer_16_out = controlled_buffer_171_out;  // Buffer buffer_16, 8 bits wide
  Pull_Resistor pull_resistor_47 (.node(controlled_buffer_167_out));
  assign controlled_buffer_166_out = decoder_1_out15 ? decoder_1_out15 : 1'bz;  // Controlled_Buffer controlled_buffer_175
  Pull_Resistor pull_resistor_48 (.node(controlled_buffer_171_out));
  assign ReadOut = decoder_5_out15 ? nor_31_out : 8'bz;  // Controlled_Buffer controlled_buffer_176
  assign nor_31_out = ~(and_31_out | nor_32_out);  // NOR_Gate nor_31, 8 bits wide
  assign nor_32_out = ~(nor_31_out | and_32_out);  // NOR_Gate nor_32, 8 bits wide
endmodule

module R3 (
  input  [31:0] in_1,
  input  [47:0] in_2,
  input  [3:0] in_3,
  input  [11:0] in_4,
  input  in_5,
  input  in_6,
  output [7:0] out_7
);

  wire decoder_5_out0, decoder_5_out1, decoder_5_out2, decoder_5_out3, decoder_5_out4, decoder_5_out5,
       decoder_5_out6, decoder_5_out7, decoder_5_out8, decoder_5_out9, decoder_5_out10, decoder_5_out11,
       decoder_5_out12, decoder_5_out13, decoder_5_out14, decoder_5_out15;
  wire [3:0] decoder_1_out0, decoder_1_out1, decoder_1_out2, decoder_1_out3, decoder_1_out4, decoder_1_out5,
       decoder_1_out6, decoder_1_out7, decoder_1_out8, decoder_1_out9, decoder_1_out10, decoder_1_out11,
       decoder_1_out12, decoder_1_out13, decoder_1_out14, decoder_1_out15;

  Decoder #(.select(4)) decoder_1 (
    .out0(decoder_1_out0[0]), .out1(decoder_1_out1[0]), .out2(decoder_1_out2[0]), .out3(decoder_1_out3[0]),
    .out4(decoder_1_out4[0]), .out5(decoder_1_out5[0]), .out6(decoder_1_out6[0]), .out7(decoder_1_out7[0]),
    .out8(decoder_1_out8[0]), .out9(decoder_1_out9[0]), .out10(decoder_1_out10[0]),
    .out11(decoder_1_out11[0]), .out12(decoder_1_out12[0]), .out13(decoder_1_out13[0]),
    .out14(decoder_1_out14[0]), .out15(decoder_1_out15[0]), .sel(in_2[3:0]), .en(in_3[0]));
  Decoder #(.select(4)) decoder_2 (
    .out0(decoder_1_out0[1]), .out1(decoder_1_out1[1]), .out2(decoder_1_out2[1]), .out3(decoder_1_out3[1]),
    .out4(decoder_1_out4[1]), .out5(decoder_1_out5[1]), .out6(decoder_1_out6[1]), .out7(decoder_1_out7[1]),
    .out8(decoder_1_out8[1]), .out9(decoder_1_out9[1]), .out10(decoder_1_out10[1]),
    .out11(decoder_1_out11[1]), .out12(decoder_1_out12[1]), .out13(decoder_1_out13[1]),
    .out14(decoder_1_out14[1]), .out15(decoder_1_out15[1]), .sel(in_2[15:12]), .en(in_3[1]));
  Decoder #(.select(4)) decoder_3 (
    .out0(decoder_1_out0[2]), .out1(decoder_1_out1[2]), .out2(decoder_1_out2[2]), .out3(decoder_1_out3[2]),
    .out4(decoder_1_out4[2]), .out5(decoder_1_out5[2]), .out6(decoder_1_out6[2]), .out7(decoder_1_out7[2]),
    .out8(decoder_1_out8[2]), .out9(decoder_1_out9[2]), .out10(decoder_1_out10[2]),
    .out11(decoder_1_out11[2]), .out12(decoder_1_out12[2]), .out13(decoder_1_out13[2]),
    .out14(decoder_1_out14[2]), .out15(decoder_1_out15[2]), .sel(in_2[27:24]), .en(in_3[2]));
  Decoder #(.select(4)) decoder_4 (
    .out0(decoder_1_out0[3]), .out1(decoder_1_out1[3]), .out2(decoder_1_out2[3]), .out3(decoder_1_out3[3]),
    .out4(decoder_1_out4[3]), .out5(decoder_1_out5[3]), .out6(decoder_1_out6[3]), .out7(decoder_1_out7[3]),
    .out8(decoder_1_out8[3]), .out9(decoder_1_out9[3]), .out10(decoder_1_out10[3]),
    .out11(decoder_1_out11[3]), .out12(decoder_1_out12[3]), .out13(decoder_1_out13[3]),
    .out14(decoder_1_out14[3]), .out15(decoder_1_out15[3]), .sel(in_2[39:36]), .en(in_3[3]));
  Decoder #(.select(4)) decoder_5 (
    .out0(decoder_5_out0), .out1(decoder_5_out1), .out2(decoder_5_out2), .out3(decoder_5_out3),
    .out4(decoder_5_out4), .out5(decoder_5_out5), .out6(decoder_5_out6), .out7(decoder_5_out7),
    .out8(decoder_5_out8), .out9(decoder_5_out9), .out10(decoder_5_out10), .out11(decoder_5_out11),
    .out12(decoder_5_out12), .out13(decoder_5_out13), .out14(decoder_5_out14), .out15(decoder_5_out15),
    .sel(in_4[3:0]), .en(in_5));
  R2 r2_1 (
    .in_1(in_1), .in_2({in_2[47:40], in_2[35:28], in_2[23:16], in_2[11:4]}), .in_3(decoder_1_out0),
    .in_4(in_4[11:4]), .in_5(decoder_5_out0), .in_6(in_6), .out_7(out_7));
  R6 r6_1 (
    .in_1(in_1), .in_2({in_2[47:40], in_2[35:28], in_2[23:16], in_2[11:4]}), .in_3(decoder_1_out1),
    .in_4(in_4[11:4]), .in_5(decoder_5_out1), .in_6(in_6), .out_7(out_7));
  R6 r6_2 (
    .in_1(in_1), .in_2({in_2[47:40], in_2[35:28], in_2[23:16], in_2[11:4]}), .in_3(decoder_1_out2),
    .in_4(in_4[11:4]), .in_5(decoder_5_out2), .in_6(in_6), .out_7(out_7));
  R6 r6_3 (
    .in_1(in_1), .in_2({in_2[47:40], in_2[35:28], in_2[23:16], in_2[11:4]}), .in_3(decoder_1_out3),
    .in_4(in_4[11:4]), .in_5(decoder_5_out3), .in_6(in_6), .out_7(out_7));
  R6 r6_4 (
    .in_1(in_1), .in_2({in_2[47:40], in_2[35:28], in_2[23:16], in_2[11:4]}), .in_3(decoder_1_out4),
    .in_4(in_4[11:4]), .in_5(decoder_5_out4), .in_6(in_6), .out_7(out_7));
  R6 r6_5 (
    .in_1(in_1), .in_2({in_2[47:40], in_2[35:28], in_2[23:16], in_2[11:4]}), .in_3(decoder_1_out5),
    .in_4(in_4[11:4]), .in_5(decoder_5_out5), .in_6(in_6), .out_7(out_7));
  R6 r6_6 (
    .in_1(in_1), .in_2({in_2[47:40], in_2[35:28], in_2[23:16], in_2[11:4]}), .in_3(decoder_1_out6),
    .in_4(in_4[11:4]), .in_5(decoder_5_out6), .in_6(in_6), .out_7(out_7));
  R6 r6_7 (
    .in_1(in_1), .in_2({in_2[47:40], in_2[35:28], in_2[23:16], in_2[11:4]}), .in_3(decoder_1_out7),
    .in_4(in_4[11:4]), .in_5(decoder_5_out7), .in_6(in_6), .out_7(out_7));
  R6 r6_8 (
    .in_1(in_1), .in_2({in_2[47:40], in_2[35:28], in_2[23:16], in_2[11:4]}), .in_3(decoder_1_out8),
    .in_4(in_4[11:4]), .in_5(decoder_5_out8), .in_6(in_6), .out_7(out_7));
  R6 r6_9 (
    .in_1(in_1), .in_2({in_2[47:40], in_2[35:28], in_2[23:16], in_2[11:4]}), .in_3(decoder_1_out9),
    .in_4(in_4[11:4]), .in_5(decoder_5_out9), .in_6(in_6), .out_7(out_7));
  R6 r6_10 (
    .in_1(in_1), .in_2({in_2[47:40], in_2[35:28], in_2[23:16], in_2[11:4]}), .in_3(decoder_1_out10),
    .in_4(in_4[11:4]), .in_5(decoder_5_out10), .in_6(in_6), .out_7(out_7));
  R6 r6_11 (
    .in_1(in_1), .in_2({in_2[47:40], in_2[35:28], in_2[23:16], in_2[11:4]}), .in_3(decoder_1_out11),
    .in_4(in_4[11:4]), .in_5(decoder_5_out11), .in_6(in_6), .out_7(out_7));
  R6 r6_12 (
    .in_1(in_1), .in_2({in_2[47:40], in_2[35:28], in_2[23:16], in_2[11:4]}), .in_3(decoder_1_out12),
    .in_4(in_4[11:4]), .in_5(decoder_5_out12), .in_6(in_6), .out_7(out_7));
  R6 r6_13 (
    .in_1(in_1), .in_2({in_2[47:40], in_2[35:28], in_2[23:16], in_2[11:4]}), .in_3(decoder_1_out13),
    .in_4(in_4[11:4]), .in_5(decoder_5_out13), .in_6(in_6), .out_7(out_7));
  R6 r6_14 (
    .in_1(in_1), .in_2({in_2[47:40], in_2[35:28], in_2[23:16], in_2[11:4]}), .in_3(decoder_1_out14),
    .in_4(in_4[11:4]), .in_5(decoder_5_out14), .in_6(in_6), .out_7(out_7));
  R6 r6_15 (
    .in_1(in_1), .in_2({in_2[47:40], in_2[35:28], in_2[23:16], in_2[11:4]}), .in_3(decoder_1_out15),
    .in_4(in_4[11:4]), .in_5(decoder_5_out15), .in_6(in_6), .out_7(out_7));
endmodule

module R4 (
  input  [31:0] in_1,
  input  [63:0] in_2,
  input  [3:0] in_3,
  input  [15:0] in_4,
  input  in_5,
  input  in_6,
  output [7:0] out_7
);

  wire clock_1_out, d1_1_out_3, decoder_5_out0, decoder_5_out1, decoder_5_out2, decoder_5_out3,
       decoder_5_out4, decoder_5_out5, decoder_5_out6, decoder_5_out7, decoder_5_out8, decoder_5_out9,
       decoder_5_out10, decoder_5_out11, decoder_5_out12, decoder_5_out13, decoder_5_out14, decoder_5_out15;
  wire [3:0] d4_1_out_3, d16_1_out_3, d64_1_out_3, d64_1_out_3_2, d64_1_out_3_3, d64_1_out_3_4,
       decoder_1_out0, decoder_1_out1, decoder_1_out2, decoder_1_out3, decoder_1_out4, decoder_1_out5,
       decoder_1_out6, decoder_1_out7, decoder_1_out8, decoder_1_out9, decoder_1_out10, decoder_1_out11,
       decoder_1_out12, decoder_1_out13, decoder_1_out14, decoder_1_out15;
  wire [11:0] d16_1_out_3_2, d64_1_out_3_5, d64_1_out_3_6, d64_1_out_3_7, d64_1_out_3_8;
  wire [31:0] d32_1_out_3;

  Decoder #(.select(4)) decoder_1 (
    .out0(decoder_1_out0[0]), .out1(decoder_1_out1[0]), .out2(decoder_1_out2[0]), .out3(decoder_1_out3[0]),
    .out4(decoder_1_out4[0]), .out5(decoder_1_out5[0]), .out6(decoder_1_out6[0]), .out7(decoder_1_out7[0]),
    .out8(decoder_1_out8[0]), .out9(decoder_1_out9[0]), .out10(decoder_1_out10[0]),
    .out11(decoder_1_out11[0]), .out12(decoder_1_out12[0]), .out13(decoder_1_out13[0]),
    .out14(decoder_1_out14[0]), .out15(decoder_1_out15[0]), .sel(d64_1_out_3), .en(d4_1_out_3[0]));
  Decoder #(.select(4)) decoder_2 (
    .out0(decoder_1_out0[1]), .out1(decoder_1_out1[1]), .out2(decoder_1_out2[1]), .out3(decoder_1_out3[1]),
    .out4(decoder_1_out4[1]), .out5(decoder_1_out5[1]), .out6(decoder_1_out6[1]), .out7(decoder_1_out7[1]),
    .out8(decoder_1_out8[1]), .out9(decoder_1_out9[1]), .out10(decoder_1_out10[1]),
    .out11(decoder_1_out11[1]), .out12(decoder_1_out12[1]), .out13(decoder_1_out13[1]),
    .out14(decoder_1_out14[1]), .out15(decoder_1_out15[1]), .sel(d64_1_out_3_2), .en(d4_1_out_3[1]));
  Decoder #(.select(4)) decoder_3 (
    .out0(decoder_1_out0[2]), .out1(decoder_1_out1[2]), .out2(decoder_1_out2[2]), .out3(decoder_1_out3[2]),
    .out4(decoder_1_out4[2]), .out5(decoder_1_out5[2]), .out6(decoder_1_out6[2]), .out7(decoder_1_out7[2]),
    .out8(decoder_1_out8[2]), .out9(decoder_1_out9[2]), .out10(decoder_1_out10[2]),
    .out11(decoder_1_out11[2]), .out12(decoder_1_out12[2]), .out13(decoder_1_out13[2]),
    .out14(decoder_1_out14[2]), .out15(decoder_1_out15[2]), .sel(d64_1_out_3_3), .en(d4_1_out_3[2]));
  Decoder #(.select(4)) decoder_4 (
    .out0(decoder_1_out0[3]), .out1(decoder_1_out1[3]), .out2(decoder_1_out2[3]), .out3(decoder_1_out3[3]),
    .out4(decoder_1_out4[3]), .out5(decoder_1_out5[3]), .out6(decoder_1_out6[3]), .out7(decoder_1_out7[3]),
    .out8(decoder_1_out8[3]), .out9(decoder_1_out9[3]), .out10(decoder_1_out10[3]),
    .out11(decoder_1_out11[3]), .out12(decoder_1_out12[3]), .out13(decoder_1_out13[3]),
    .out14(decoder_1_out14[3]), .out15(decoder_1_out15[3]), .sel(d64_1_out_3_4), .en(d4_1_out_3[3]));
  Decoder #(.select(4)) decoder_5 (
    .out0(decoder_5_out0), .out1(decoder_5_out1), .out2(decoder_5_out2), .out3(decoder_5_out3),
    .out4(decoder_5_out4), .out5(decoder_5_out5), .out6(decoder_5_out6), .out7(decoder_5_out7),
    .out8(decoder_5_out8), .out9(decoder_5_out9), .out10(decoder_5_out10), .out11(decoder_5_out11),
    .out12(decoder_5_out12), .out13(decoder_5_out13), .out14(decoder_5_out14), .out15(decoder_5_out15),
    .sel(d16_1_out_3), .en(d1_1_out_3));
  Clock clock_1 (.out(clock_1_out));
  D32 d32_1 (.in_2(in_1), .in_1(clock_1_out), .out_3(d32_1_out_3));
  D64 d64_1 (
    .in_2(in_2), .in_1(clock_1_out),
    .out_3({d64_1_out_3_8, d64_1_out_3_4, d64_1_out_3_7, d64_1_out_3_3, d64_1_out_3_6, d64_1_out_3_2, d64_1_out_3_5, d64_1_out_3}));
  D4 d4_1 (.in_2(in_3), .in_1(clock_1_out), .out_3(d4_1_out_3));
  D16 d16_1 (.in_2(in_4), .in_1(clock_1_out), .out_3({d16_1_out_3_2, d16_1_out_3}));
  D1 d1_1 (.in_2(in_5), .in_1(clock_1_out), .out_3(d1_1_out_3));
  R3 r3_1 (
    .in_1(d32_1_out_3), .in_2({d64_1_out_3_8, d64_1_out_3_7, d64_1_out_3_6, d64_1_out_3_5}),
    .in_3(decoder_1_out0), .in_4(d16_1_out_3_2), .in_5(decoder_5_out0), .in_6(in_6), .out_7(out_7));
  R7 r7_1 (
    .in_1(d32_1_out_3), .in_2({d64_1_out_3_8, d64_1_out_3_7, d64_1_out_3_6, d64_1_out_3_5}),
    .in_3(decoder_1_out1), .in_4(d16_1_out_3_2), .in_5(decoder_5_out1), .in_6(in_6), .out_7(out_7));
  R7 r7_2 (
    .in_1(d32_1_out_3), .in_2({d64_1_out_3_8, d64_1_out_3_7, d64_1_out_3_6, d64_1_out_3_5}),
    .in_3(decoder_1_out2), .in_4(d16_1_out_3_2), .in_5(decoder_5_out2), .in_6(in_6), .out_7(out_7));
  R7 r7_3 (
    .in_1(d32_1_out_3), .in_2({d64_1_out_3_8, d64_1_out_3_7, d64_1_out_3_6, d64_1_out_3_5}),
    .in_3(decoder_1_out3), .in_4(d16_1_out_3_2), .in_5(decoder_5_out3), .in_6(in_6), .out_7(out_7));
  R7 r7_4 (
    .in_1(d32_1_out_3), .in_2({d64_1_out_3_8, d64_1_out_3_7, d64_1_out_3_6, d64_1_out_3_5}),
    .in_3(decoder_1_out4), .in_4(d16_1_out_3_2), .in_5(decoder_5_out4), .in_6(in_6), .out_7(out_7));
  R7 r7_5 (
    .in_1(d32_1_out_3), .in_2({d64_1_out_3_8, d64_1_out_3_7, d64_1_out_3_6, d64_1_out_3_5}),
    .in_3(decoder_1_out5), .in_4(d16_1_out_3_2), .in_5(decoder_5_out5), .in_6(in_6), .out_7(out_7));
  R7 r7_6 (
    .in_1(d32_1_out_3), .in_2({d64_1_out_3_8, d64_1_out_3_7, d64_1_out_3_6, d64_1_out_3_5}),
    .in_3(decoder_1_out6), .in_4(d16_1_out_3_2), .in_5(decoder_5_out6), .in_6(in_6), .out_7(out_7));
  R7 r7_7 (
    .in_1(d32_1_out_3), .in_2({d64_1_out_3_8, d64_1_out_3_7, d64_1_out_3_6, d64_1_out_3_5}),
    .in_3(decoder_1_out7), .in_4(d16_1_out_3_2), .in_5(decoder_5_out7), .in_6(in_6), .out_7(out_7));
  R7 r7_8 (
    .in_1(d32_1_out_3), .in_2({d64_1_out_3_8, d64_1_out_3_7, d64_1_out_3_6, d64_1_out_3_5}),
    .in_3(decoder_1_out8), .in_4(d16_1_out_3_2), .in_5(decoder_5_out8), .in_6(in_6), .out_7(out_7));
  R7 r7_9 (
    .in_1(d32_1_out_3), .in_2({d64_1_out_3_8, d64_1_out_3_7, d64_1_out_3_6, d64_1_out_3_5}),
    .in_3(decoder_1_out9), .in_4(d16_1_out_3_2), .in_5(decoder_5_out9), .in_6(in_6), .out_7(out_7));
  R7 r7_10 (
    .in_1(d32_1_out_3), .in_2({d64_1_out_3_8, d64_1_out_3_7, d64_1_out_3_6, d64_1_out_3_5}),
    .in_3(decoder_1_out10), .in_4(d16_1_out_3_2), .in_5(decoder_5_out10), .in_6(in_6), .out_7(out_7));
  R7 r7_11 (
    .in_1(d32_1_out_3), .in_2({d64_1_out_3_8, d64_1_out_3_7, d64_1_out_3_6, d64_1_out_3_5}),
    .in_3(decoder_1_out11), .in_4(d16_1_out_3_2), .in_5(decoder_5_out11), .in_6(in_6), .out_7(out_7));
  R7 r7_12 (
    .in_1(d32_1_out_3), .in_2({d64_1_out_3_8, d64_1_out_3_7, d64_1_out_3_6, d64_1_out_3_5}),
    .in_3(decoder_1_out12), .in_4(d16_1_out_3_2), .in_5(decoder_5_out12), .in_6(in_6), .out_7(out_7));
  R7 r7_13 (
    .in_1(d32_1_out_3), .in_2({d64_1_out_3_8, d64_1_out_3_7, d64_1_out_3_6, d64_1_out_3_5}),
    .in_3(decoder_1_out13), .in_4(d16_1_out_3_2), .in_5(decoder_5_out13), .in_6(in_6), .out_7(out_7));
  R7 r7_14 (
    .in_1(d32_1_out_3), .in_2({d64_1_out_3_8, d64_1_out_3_7, d64_1_out_3_6, d64_1_out_3_5}),
    .in_3(decoder_1_out14), .in_4(d16_1_out_3_2), .in_5(decoder_5_out14), .in_6(in_6), .out_7(out_7));
  R7 r7_15 (
    .in_1(d32_1_out_3), .in_2({d64_1_out_3_8, d64_1_out_3_7, d64_1_out_3_6, d64_1_out_3_5}),
    .in_3(decoder_1_out15), .in_4(d16_1_out_3_2), .in_5(decoder_5_out15), .in_6(in_6), .out_7(out_7));
endmodule

module D1 (
  input  in_1,
  input  in_2,
  output out_3
);

  wire and_1_out, buffer_1_out, buffer_2_out, controlled_buffer_1_out, nor_1_out, not_1_out, not_2_out,
       not_3_out, not_4_out;

  and and_1 (and_1_out, in_1, not_1_out);
  buf buffer_1 (buffer_1_out, and_1_out);
  assign controlled_buffer_1_out = buffer_1_out ? in_2 : 1'bz;  // Controlled_Buffer controlled_buffer_1
  not not_1 (not_1_out, in_1);
  not not_2 (not_2_out, and_1_out);
  assign controlled_buffer_1_out = not_2_out ? controlled_buffer_1_out : 1'bz;  // Controlled_Buffer controlled_buffer_2
  not not_3 (not_3_out, in_1);
  nor nor_1 (nor_1_out, not_3_out, in_1);
  buf buffer_2 (buffer_2_out, nor_1_out);
  assign out_3 = buffer_2_out ? controlled_buffer_1_out : 1'bz;  // Controlled_Buffer controlled_buffer_3
  not not_4 (not_4_out, nor_1_out);
  assign out_3 = not_4_out ? out_3 : 1'bz;  // Controlled_Buffer controlled_buffer_4

  // Notes on the sheet:
  //   out_3: pull=down
endmodule

module D4 (
  input  in_1,
  input  [3:0] in_2,
  output [3:0] out_3
);

  wire and_1_out, buffer_1_out, buffer_2_out, nor_1_out, not_1_out, not_2_out, not_3_out, not_4_out;
  wire [3:0] controlled_buffer_1_out;

  not not_1 (not_1_out, in_1);
  and and_1 (and_1_out, in_1, not_1_out);
  buf buffer_1 (buffer_1_out, and_1_out);
  assign controlled_buffer_1_out = buffer_1_out ? in_2 : 4'bz;  // Controlled_Buffer controlled_buffer_1
  not not_2 (not_2_out, and_1_out);
  assign controlled_buffer_1_out = not_2_out ? controlled_buffer_1_out : 4'bz;  // Controlled_Buffer controlled_buffer_2
  Pull_Resistor pull_resistor_1 (.node(controlled_buffer_1_out));
  not not_3 (not_3_out, in_1);
  nor nor_1 (nor_1_out, not_3_out, in_1);
  buf buffer_2 (buffer_2_out, nor_1_out);
  not not_4 (not_4_out, nor_1_out);
  assign out_3 = buffer_2_out ? controlled_buffer_1_out : 4'bz;  // Controlled_Buffer controlled_buffer_3
  assign out_3 = not_4_out ? out_3 : 4'bz;  // Controlled_Buffer controlled_buffer_4
  Pull_Resistor pull_resistor_2 (.node(out_3));

  // Notes on the sheet:
  //   out_3: pull=down
endmodule

module D8 (
  input  in_1,
  input  [7:0] in_2,
  output [7:0] out_3
);

  wire and_1_out, buffer_1_out, buffer_2_out, nor_1_out, not_1_out, not_2_out, not_3_out, not_4_out;
  wire [7:0] controlled_buffer_1_out;

  not not_1 (not_1_out, in_1);
  and and_1 (and_1_out, in_1, not_1_out);
  buf buffer_1 (buffer_1_out, and_1_out);
  assign controlled_buffer_1_out = buffer_1_out ? in_2 : 8'bz;  // Controlled_Buffer controlled_buffer_1
  not not_2 (not_2_out, and_1_out);
  assign controlled_buffer_1_out = not_2_out ? controlled_buffer_1_out : 8'bz;  // Controlled_Buffer controlled_buffer_2
  not not_3 (not_3_out, in_1);
  nor nor_1 (nor_1_out, not_3_out, in_1);
  buf buffer_2 (buffer_2_out, nor_1_out);
  not not_4 (not_4_out, nor_1_out);
  assign out_3 = buffer_2_out ? controlled_buffer_1_out : 8'bz;  // Controlled_Buffer controlled_buffer_3
  assign out_3 = not_4_out ? out_3 : 8'bz;  // Controlled_Buffer controlled_buffer_4

  // Notes on the sheet:
  //   out_3: pull=down
endmodule

module D12 (
  input  in_1,
  input  [11:0] in_2,
  output [11:0] out_3
);

  wire and_1_out, buffer_1_out, buffer_2_out, nor_1_out, not_1_out, not_2_out, not_3_out, not_4_out;
  wire [11:0] controlled_buffer_1_out;

  buf buffer_1 (buffer_1_out, and_1_out);
  assign controlled_buffer_1_out = buffer_1_out ? in_2 : 12'bz;  // Controlled_Buffer controlled_buffer_1
  not not_1 (not_1_out, in_1);
  and and_1 (and_1_out, in_1, not_1_out);
  not not_2 (not_2_out, and_1_out);
  assign controlled_buffer_1_out = not_2_out ? controlled_buffer_1_out : 12'bz;  // Controlled_Buffer controlled_buffer_2
  buf buffer_2 (buffer_2_out, nor_1_out);
  assign out_3 = buffer_2_out ? controlled_buffer_1_out : 12'bz;  // Controlled_Buffer controlled_buffer_3
  not not_3 (not_3_out, in_1);
  nor nor_1 (nor_1_out, not_3_out, in_1);
  not not_4 (not_4_out, nor_1_out);
  assign out_3 = not_4_out ? out_3 : 12'bz;  // Controlled_Buffer controlled_buffer_4

  // Notes on the sheet:
  //   out_3: pull=down
endmodule

module D16 (
  input  in_1,
  input  [15:0] in_2,
  output [15:0] out_3
);

  wire and_1_out, buffer_1_out, buffer_2_out, nor_1_out, not_1_out, not_2_out, not_3_out, not_4_out;
  wire [15:0] controlled_buffer_1_out;

  and and_1 (and_1_out, in_1, not_1_out);
  buf buffer_1 (buffer_1_out, and_1_out);
  assign controlled_buffer_1_out = buffer_1_out ? in_2 : 16'bz;  // Controlled_Buffer controlled_buffer_1
  not not_1 (not_1_out, in_1);
  not not_2 (not_2_out, and_1_out);
  assign controlled_buffer_1_out = not_2_out ? controlled_buffer_1_out : 16'bz;  // Controlled_Buffer controlled_buffer_2
  not not_3 (not_3_out, in_1);
  nor nor_1 (nor_1_out, not_3_out, in_1);
  buf buffer_2 (buffer_2_out, nor_1_out);
  assign out_3 = buffer_2_out ? controlled_buffer_1_out : 16'bz;  // Controlled_Buffer controlled_buffer_3
  not not_4 (not_4_out, nor_1_out);
  assign out_3 = not_4_out ? out_3 : 16'bz;  // Controlled_Buffer controlled_buffer_4

  // Notes on the sheet:
  //   out_3: pull=down
endmodule

module D24 (
  input  in_1,
  input  [23:0] in_2,
  output [23:0] out_3
);

  wire and_1_out, buffer_1_out, buffer_2_out, nor_1_out, not_1_out, not_2_out, not_3_out, not_4_out;
  wire [23:0] controlled_buffer_1_out;

  not not_1 (not_1_out, in_1);
  and and_1 (and_1_out, in_1, not_1_out);
  buf buffer_1 (buffer_1_out, and_1_out);
  assign controlled_buffer_1_out = buffer_1_out ? in_2 : 24'bz;  // Controlled_Buffer controlled_buffer_1
  not not_2 (not_2_out, and_1_out);
  assign controlled_buffer_1_out = not_2_out ? controlled_buffer_1_out : 24'bz;  // Controlled_Buffer controlled_buffer_2
  not not_3 (not_3_out, in_1);
  nor nor_1 (nor_1_out, not_3_out, in_1);
  buf buffer_2 (buffer_2_out, nor_1_out);
  assign out_3 = buffer_2_out ? controlled_buffer_1_out : 24'bz;  // Controlled_Buffer controlled_buffer_3
  not not_4 (not_4_out, nor_1_out);
  assign out_3 = not_4_out ? out_3 : 24'bz;  // Controlled_Buffer controlled_buffer_4

  // Notes on the sheet:
  //   out_3: pull=down
endmodule

module D32 (
  input  in_1,
  input  [31:0] in_2,
  output [31:0] out_3
);

  wire and_1_out, buffer_1_out, buffer_2_out, nor_1_out, not_1_out, not_2_out, not_3_out, not_4_out;
  wire [31:0] controlled_buffer_1_out;

  and and_1 (and_1_out, in_1, not_1_out);
  buf buffer_1 (buffer_1_out, and_1_out);
  assign controlled_buffer_1_out = buffer_1_out ? in_2 : 32'bz;  // Controlled_Buffer controlled_buffer_1
  not not_1 (not_1_out, in_1);
  not not_2 (not_2_out, and_1_out);
  assign controlled_buffer_1_out = not_2_out ? controlled_buffer_1_out : 32'bz;  // Controlled_Buffer controlled_buffer_2
  not not_3 (not_3_out, in_1);
  nor nor_1 (nor_1_out, not_3_out, in_1);
  buf buffer_2 (buffer_2_out, nor_1_out);
  assign out_3 = buffer_2_out ? controlled_buffer_1_out : 32'bz;  // Controlled_Buffer controlled_buffer_3
  not not_4 (not_4_out, nor_1_out);
  assign out_3 = not_4_out ? out_3 : 32'bz;  // Controlled_Buffer controlled_buffer_4

  // Notes on the sheet:
  //   out_3: pull=down
endmodule

module D48 (
  input  in_1,
  input  [47:0] in_2,
  output [47:0] out_3
);

  wire and_1_out, buffer_1_out, buffer_2_out, nor_1_out, not_1_out, not_2_out, not_3_out, not_4_out;
  wire [47:0] controlled_buffer_1_out;

  not not_1 (not_1_out, in_1);
  and and_1 (and_1_out, in_1, not_1_out);
  buf buffer_1 (buffer_1_out, and_1_out);
  assign controlled_buffer_1_out = buffer_1_out ? in_2 : 48'bz;  // Controlled_Buffer controlled_buffer_1
  not not_2 (not_2_out, and_1_out);
  assign controlled_buffer_1_out = not_2_out ? controlled_buffer_1_out : 48'bz;  // Controlled_Buffer controlled_buffer_2
  not not_3 (not_3_out, in_1);
  nor nor_1 (nor_1_out, not_3_out, in_1);
  buf buffer_2 (buffer_2_out, nor_1_out);
  assign out_3 = buffer_2_out ? controlled_buffer_1_out : 48'bz;  // Controlled_Buffer controlled_buffer_3
  not not_4 (not_4_out, nor_1_out);
  assign out_3 = not_4_out ? out_3 : 48'bz;  // Controlled_Buffer controlled_buffer_4

  // Notes on the sheet:
  //   out_3: pull=down
endmodule

module D64 (
  input  in_1,
  input  [63:0] in_2,
  output [63:0] out_3
);

  wire and_1_out, buffer_1_out, buffer_2_out, nor_1_out, not_1_out, not_2_out, not_3_out, not_4_out;
  wire [63:0] controlled_buffer_1_out;

  not not_1 (not_1_out, in_1);
  and and_1 (and_1_out, in_1, not_1_out);
  buf buffer_1 (buffer_1_out, and_1_out);
  assign controlled_buffer_1_out = buffer_1_out ? in_2 : 64'bz;  // Controlled_Buffer controlled_buffer_1
  not not_2 (not_2_out, and_1_out);
  assign controlled_buffer_1_out = not_2_out ? controlled_buffer_1_out : 64'bz;  // Controlled_Buffer controlled_buffer_2
  not not_3 (not_3_out, in_1);
  nor nor_1 (nor_1_out, not_3_out, in_1);
  buf buffer_2 (buffer_2_out, nor_1_out);
  assign out_3 = buffer_2_out ? controlled_buffer_1_out : 64'bz;  // Controlled_Buffer controlled_buffer_3
  not not_4 (not_4_out, nor_1_out);
  assign out_3 = not_4_out ? out_3 : 64'bz;  // Controlled_Buffer controlled_buffer_4

  // Notes on the sheet:
  //   out_3: pull=down
endmodule
